// Logisim project cpu.circ as structural Verilog: 26 circuits, main circuit ◇单周期MIPS
module \单周期MIPS  (
  input  IR1,
  input  IR2,
  input  IR3,
  output RegWrite,
  output MemWrite,
  output [31:0] PC,
  output [31:0] IR,
  output [31:0] RDin,
  output [31:0] MDin,
  output [31:0] LedData
);

  wire and_1_out, and_2_out, and_3_out, BLEZ, Branch, CLK, clock_2_out, comparator_1_eq, comparator_2_eq,
       comparator_3_eq, comparator_3_lt, d_ff_1_q, Go, halt, IR1_t, IR2_t, IR3_t, IRA, IRB, IRC, JAL, LBU,
       LedOut, mips_alu_1_equal, nand_1_out, not_1_out, not_2_out, or_1_out, or_5_out, RST, SignedExt, SLLV,
       Syscall, W1, W2, W3, \单周期硬布线控制器_1_alu_src , \单周期硬布线控制器_1_beq , \单周期硬布线控制器_1_bne , \单周期硬布线控制器_1_jmp ,
       \单周期硬布线控制器_1_jr , \单周期硬布线控制器_1_memtoreg , \单周期硬布线控制器_1_regdst ;
  wire [3:0] adder_1_out, \单周期硬布线控制器_1_alu_op ;
  wire [4:0] mips_probe_1_p2, multiplexer_5_out, multiplexer_6_out, multiplexer_7_out, multiplexer_11_out;
  wire [7:0] multiplexer_13_out;
  wire [12:0] CNT_num;
  wire [15:0] \总周期数 ;
  wire [27:0] adder_1_out_2;
  wire [31:0] adder_2_out, bit_extender_1_out, bit_extender_2_out, bit_extender_3_out, mips_alu_1_result,
       mips_regifile_1_r1, multiplexer_1_out, multiplexer_2_out, multiplexer_3_out, multiplexer_8_out,
       multiplexer_9_out, multiplexer_10_out, multiplexer_12_out, multiplexer_14_out, ram_1_data,
       shifter_1_out;

  Clock clock_1 ();  // open: out
  Button _1 (.out(IRA));
  Button _2 (.out(IRB));
  Button _3 (.out(IRC));
  Button \u_继续运行  (.out(Go));
  LED led_1 (.in(W1));
  LED led_2 (.in(W2));
  LED led_3 (.in(W3));
  Multiplexer #(.width(32), .enable("false")) multiplexer_1 (
    .in0({adder_1_out, adder_1_out_2}), .in1(adder_2_out), .out(multiplexer_1_out), .sel(Branch));
  Hex_Digit_Display hex_digit_display_1 (.value(LedData[31:28]));  // open: dp
  Multiplexer #(.width(32), .enable("false")) multiplexer_2 (
    .in0(multiplexer_1_out), .in1({adder_1_out, IR[25:0], 2'b00}), .out(multiplexer_2_out),
    .sel(\单周期硬布线控制器_1_jmp ));
  Hex_Digit_Display hex_digit_display_2 (.value(LedData[23:20]));  // open: dp
  Hex_Digit_Display hex_digit_display_3 (.value(LedData[27:24]));  // open: dp
  Button button_1 (.out(RST));
  Multiplexer #(.width(32), .enable("false")) multiplexer_3 (
    .in0(multiplexer_2_out), .in1(mips_regifile_1_r1), .out(multiplexer_3_out), .sel(\单周期硬布线控制器_1_jr ));
  or or_1 (or_1_out, not_1_out, Go);
  not not_1 (not_1_out, halt);
  Hex_Digit_Display hex_digit_display_4 (.value(LedData[15:12]));  // open: dp
  Hex_Digit_Display hex_digit_display_5 (.value(LedData[19:16]));  // open: dp
  not not_2 (not_2_out, halt);
  Register #(.width(32), .Select("low")) u_PC (.D(multiplexer_3_out), .en(or_1_out), .Q(PC), .clk(CLK), .clr(RST));
  Hex_Digit_Display hex_digit_display_6 (.value(LedData[7:4]));  // open: dp
  Hex_Digit_Display hex_digit_display_7 (.value(LedData[11:8]));  // open: dp
  // Probe on \总周期数 
  Counter #(.width(16), .max('hffff)) counter_1 (
    .count(not_2_out), .Q(\总周期数 ), .clk(CLK), .clr(RST));  // open: load, D, carry, preset, down
  Adder #(.width(32)) adder_1 (.a(PC), .b(32'h4), .out({adder_1_out, adder_1_out_2}));  // open: cin, cout
  Hex_Digit_Display hex_digit_display_8 (.value(LedData[3:0]));  // open: dp
  // Probe on IR[5:0]
  // Probe on IR[31:26]
  // Mips_Probe mips_probe_1: pin names not known; wires that end beside it: IR, mips_probe_1_p2
  ROM #(.addrWidth(10), .dataWidth(32), .Select("high")) rom_1 (.addr(PC[11:2]), .data(IR));
  or or_2 (IR1_t, IR1, IRA);
  or or_3 (IR2_t, IR2, IRB);
  assign bit_extender_1_out = {{16{1'b0}}, IR[15:0]};  // Bit_Extender bit_extender_1
  assign bit_extender_2_out = {{16{IR[15]}}, IR[15:0]};  // Bit_Extender bit_extender_2
  \单周期硬布线控制器  \u_单周期硬布线控制器_1  (
    .Func(IR[5:0]), .OP(IR[31:26]), .ALU_OP(\单周期硬布线控制器_1_alu_op ), .MemToReg(\单周期硬布线控制器_1_memtoreg ),
    .MemWrite(MemWrite), .ALU_SRC(\单周期硬布线控制器_1_alu_src ), .RegWrite(RegWrite), .SysCALL(Syscall),
    .SignedExt(SignedExt), .RegDst(\单周期硬布线控制器_1_regdst ), .JR(\单周期硬布线控制器_1_jr ), .JMP(\单周期硬布线控制器_1_jmp ),
    .Beq(\单周期硬布线控制器_1_beq ), .JAL(JAL), .Bne(\单周期硬布线控制器_1_bne ), .SLLV(SLLV), .BLEZ(BLEZ), .LBU(LBU));  // open: ERET, MFC0, MTC0, MF
  Multiplexer #(.width(5), .enable("false")) multiplexer_4 (
    .in0(IR[25:21]), .in1(5'b00010), .out(mips_probe_1_p2), .sel(Syscall));
  Multiplexer #(.width(5), .enable("false")) multiplexer_5 (
    .in0(IR[20:16]), .in1(5'b00100), .out(multiplexer_5_out), .sel(Syscall));
  Multiplexer #(.width(5), .enable("false")) multiplexer_6 (
    .in0(IR[20:16]), .in1(IR[15:11]), .out(multiplexer_6_out), .sel(\单周期硬布线控制器_1_regdst ));
  Multiplexer #(.width(5), .enable("false")) multiplexer_7 (
    .in0(multiplexer_6_out), .in1({5{1'b1}}), .out(multiplexer_7_out), .sel(JAL));
  Multiplexer #(.width(32), .enable("false")) multiplexer_8 (
    .in0(bit_extender_1_out), .in1(bit_extender_2_out), .out(multiplexer_8_out), .sel(SignedExt));
  or or_4 (IR3_t, IR3, IRC);
  Shifter #(.width(32)) shifter_1 (.in(bit_extender_2_out), .\dist (5'b00010), .out(shifter_1_out));
  MIPS_Regifile mips_regifile_1 (
    .Din(RDin), .Clk(CLK), .R1(mips_regifile_1_r1), .R2(MDin), .WE(RegWrite), .W_num(multiplexer_7_out),
    .R1_num(mips_probe_1_p2), .R2_num(multiplexer_5_out));
  Adder #(.width(32)) adder_2 (
    .a(shifter_1_out), .b({adder_1_out, adder_1_out_2}), .out(adder_2_out));  // open: cin, cout
  Multiplexer #(.width(32), .enable("false")) multiplexer_9 (
    .in0(MDin), .in1(multiplexer_8_out), .out(multiplexer_9_out), .sel(\单周期硬布线控制器_1_alu_src ));
  Multiplexer #(.width(32), .enable("false")) multiplexer_10 (
    .in0(multiplexer_9_out), .in1({32{1'b0}}), .out(multiplexer_10_out), .sel(BLEZ));
  Multiplexer #(.width(5), .enable("false")) multiplexer_11 (
    .in0(IR[10:6]), .in1(mips_regifile_1_r1[4:0]), .out(multiplexer_11_out), .sel(SLLV));
  MIPS_ALU mips_alu_1 (
    .X(mips_regifile_1_r1), .Y(multiplexer_10_out), .AluOP(\单周期硬布线控制器_1_alu_op ), .Equal(mips_alu_1_equal),
    .Result(mips_alu_1_result), .shamt(multiplexer_11_out));  // open: Result_2
  // Probe on mips_alu_1_result
  // Probe on multiplexer_11_out
  or or_5 (or_5_out, mips_alu_1_equal, comparator_1_eq);
  Comparator #(.width(32)) comparator_1 (.a(32'h1), .b(mips_alu_1_result), .eq(comparator_1_eq));  // open: gt, lt
  Comparator #(.width(32)) comparator_2 (.a(32'h22), .b(mips_regifile_1_r1), .eq(comparator_2_eq));  // open: gt, lt
  Register #(.width(32), .Select("low")) LedReg (.D(MDin), .en(LedOut), .Q(LedData), .clk(CLK), .clr(RST));
  D_Flip_Flop #(.trigger("high"), .Pre_Clr_Positions("LEGACY"), .enable("true"), .NewFFLayout("false")) d_ff_1 (.Q(d_ff_1_q));  // open: clk, D, Qn, preset, en, reset
  // Probe on 13'h10
  and and_1 (and_1_out, or_5_out, BLEZ);
  and and_2 (and_2_out, mips_alu_1_equal, \单周期硬布线控制器_1_beq );
  and and_3 (and_3_out, ~mips_alu_1_equal, \单周期硬布线控制器_1_bne );  // AND_Gate
  and and_4 (halt, Syscall, ~comparator_2_eq);  // AND_Gate
  and and_5 (LedOut, Syscall, comparator_2_eq);
  Comparator #(.width(13)) comparator_3 (
    .a(CNT_num), .b(13'h10), .eq(comparator_3_eq), .lt(comparator_3_lt));  // open: gt
  Clock clock_2 (.out(clock_2_out));
  or or_6 (Branch, and_1_out, and_2_out, and_3_out);
  RAM #(.addrWidth(10), .dataWidth(32), .bus("separate"), .Select("high")) ram_1 (
    .addr(mips_alu_1_result[11:2]), .din(MDin), .data(ram_1_data), .str(MemWrite), .clk(CLK), .clr(RST));  // open: sel, ld
  nand nand_1 (nand_1_out, d_ff_1_q, comparator_3_eq);
  Counter #(.width(13), .max('h1fff), .ongoal("stay"), .behavior("old")) counter_2 (
    .count(comparator_3_lt), .Q(CNT_num), .clk(clock_2_out));  // open: load, D, carry, clr, preset
  Multiplexer #(.width(32), .enable("false")) multiplexer_12 (
    .in0(mips_alu_1_result), .in1(ram_1_data), .out(multiplexer_12_out), .sel(\单周期硬布线控制器_1_memtoreg ));
  assign CLK = nand_1_out ? clock_2_out : 1'bz;  // Controlled_Buffer controlled_buffer_1
  Multiplexer #(.select(2), .width(8), .enable("false")) multiplexer_13 (
    .in0(multiplexer_12_out[7:0]), .in1(multiplexer_12_out[15:8]), .in2(multiplexer_12_out[23:16]),
    .in3(multiplexer_12_out[31:24]), .out(multiplexer_13_out), .sel(mips_alu_1_result[1:0]));
  Pull_Resistor #(.pull(1)) pull_resistor_1 (.node(CLK));
  Multiplexer #(.width(32), .enable("false")) multiplexer_14 (
    .in0(multiplexer_12_out), .in1(bit_extender_3_out), .out(multiplexer_14_out), .sel(LBU));
  assign bit_extender_3_out = {{24{1'b0}}, multiplexer_13_out};  // Bit_Extender bit_extender_3
  Multiplexer #(.width(32), .enable("false")) multiplexer_15 (
    .in0(multiplexer_14_out), .in1({adder_1_out, adder_1_out_2}), .out(RDin), .sel(JAL));

  // Other names for the same wires on the sheet: OP[5:0] = IR[31:26]

  // Notes on the sheet:
  //   中断源
  //   中断等待指示
  //   总复位信号应将除ROM以外所有存储组件全部清零
  //   jump
  //   jr
  //   数码管输出
  //   数码管输出应该用寄存器锁存，否则显示数据只能一闪而过
  //   指令存储器
  //   指令字
  //   contents of rom_1 (hex, n*v repeats v):
  //   20110001 8000c05 20110001 20120002 20130003 8000c09 20110001 20120002 20130003 8000c0d 20110001
  //   20120002 20130003 8000c11 20110001 20120002 20130003 c000cf6 20100001 20110001 118fc0 112020
  //   20020022 c 118882 12200001 8000c15 112020 20020022 c 20110001 118880 112020 20020022 c 12200001
  //   8000c1f 20110001 118fc0 112020 20020022 c 1188c3 112020 20020022 c 118903 112020 20020022 c 118903
  //   112020 20020022 c 118903 112020 20020022 c 118903 112020 20020022 c 118903 112020 20020022 c 118903
  //   112020 20020022 c 118903 112020 20020022 c 20100001 109fc0 139fc3 8021 2012000c 24160003 26100001
  //   3210000f 20080008 20090001 139900 2709825 132020 20020022 c 1094022 1500fff9 22100001 2018000f
  //   2188024 108700 20080008 20090001 139902 2709825 132021 20020022 c 1094022 1500fff9 108702 2c9b022
  //   12c00001 8000c50 4020 1084027 84400 3508ffff 82021 20020022 c 2010ffff 20110000 ae300000 22100001
  //   22310004 ae300000 22100001 22310004 ae300000 22100001 22310004 ae300000 22100001 22310004 ae300000
  //   22100001 22310004 ae300000 22100001 22310004 ae300000 22100001 22310004 ae300000 22100001 22310004
  //   ae300000 22100001 22310004 ae300000 22100001 22310004 ae300000 22100001 22310004 ae300000 22100001
  //   22310004 ae300000 22100001 22310004 ae300000 22100001 22310004 ae300000 22100001 22310004 ae300000
  //   22100001 22310004 22100001 8020 2011003c 8e130000 8e340000 274402a 11000002 ae330000 ae140000
  //   2231fffc 1611fff8 102020 20020022 c 22100004 2011003c 1611fff2 20020032 c 20080001 20090003 20110876
  //   112020 20020022 c 200b0008 1118804 1318804 112020 20020022 c 216bffff 1560fff9 2002000a c 2008ffff
  //   20117777 112020 20020022 c 200b0010 3a31ffff 112020 20020022 c 216bffff 1560fffa 2002000a c 20090000
  //   200b0010 34118483 20120404 118c00 129400 36318281 22520404 ad310000 2328820 21290004 216bffff
  //   1560fffb 200b0020 20090000 91310000 112020 20020022 c 21290001 216bffff 1560fff9 2002000a c 2011fff1
  //   112020 20020022 c 22310001 1a20fffb 2002000a c 20100000 22100001 102020 20020022 c 22100002 102020
  //   20020022 c 22100003 102020 20020022 c 22100004 102020 20020022 c 22100005 102020 20020022 c 22100006
  //   102020 20020022 c 22100007 102020 20020022 c 22100008 102020 20020022 20020022 c 3e00008
  //   imm26
  //   OP
  //   Func
  //   rs
  //   rt
  //   rd
  //   shamt
  //   imm16
  //   JMP
  //   JR
  //   OP
  //   Func
  //   Syscall
  //   Beq
  //   Bne
  //   MemToReg
  //   MemWrite
  //   AluOP
  //   AluSrcB
  //   RegWrite
  //   JAL
  //   RegDst
  //   PC+4+imm16<<2
  //   为方便自动评测，需要输出PC，IR，寄存器堆写如数据RDin
  //   RAM写使能MemWrite、RAM写入数据MDin等信号
  //   控制位
  //   暂停节拍，不能为0
  //   用这个时钟源需要去掉电路中的其他时钟源
  //   戳工具置1进入计数暂停模式，ctrl+k时钟自动运行到对应节拍暂停
  //   ctrl+k关闭时钟连续运行，将控制位置零，进入单步调试模式调试
  //   可计数暂停的时钟源
endmodule

// 单周期硬布线控制器
module \单周期硬布线控制器  (
  input  [5:0] OP,
  input  [5:0] Func,
  input  [4:0] MF,
  output [3:0] ALU_OP,
  output MemToReg,
  output LBU,
  output MemWrite,
  output ALU_SRC,
  output SysCALL,
  output SignedExt,
  output RegDst,
  output Beq,
  output Bne,
  output JR,
  output JMP,
  output JAL,
  output SLLV,
  output BLEZ,
  output ERET,
  output RegWrite,
  output MFC0,
  output MTC0
);

  wire comparator_1_eq, comparator_2_eq, comparator_3_eq, comparator_4_eq, \控制信号自动生成_1_regwrite ;

  \运算控制器自动生成  \u_运算控制器自动生成_1  (
    .OP0(OP[0]), .OP1(OP[1]), .OP2(OP[2]), .OP3(OP[3]), .OP4(OP[4]), .OP5(OP[5]), .F0(Func[0]), .F1(Func[1]),
    .F2(Func[2]), .F3(Func[3]), .F4(Func[4]), .F5(Func[5]), .S0(ALU_OP[0]), .S1(ALU_OP[1]), .S2(ALU_OP[2]),
    .S3(ALU_OP[3]));
  \控制信号自动生成  \u_控制信号自动生成_1  (
    .OP0(OP[0]), .OP1(OP[1]), .OP2(OP[2]), .OP3(OP[3]), .OP4(OP[4]), .OP5(OP[5]), .F0(Func[0]), .F1(Func[1]),
    .F2(Func[2]), .F3(Func[3]), .F4(Func[4]), .F5(Func[5]), .MemtoReg(MemToReg), .LBU(LBU),
    .MemWrite(MemWrite), .ALU_SRC(ALU_SRC), .RegWrite(\控制信号自动生成_1_regwrite ), .SYSCALL(SysCALL),
    .SignedExt(SignedExt), .RegDst(RegDst), .BEQ(Beq), .BNE(Bne), .JR(JR), .JMP(JMP), .JAL(JAL), .SLLV(SLLV),
    .BLEZ(BLEZ));
  Comparator #(.width(6)) comparator_1 (.a(OP), .b(6'b010000), .eq(comparator_1_eq));  // open: gt, lt
  Comparator #(.width(6)) comparator_2 (.a(Func), .b(6'b011000), .eq(comparator_2_eq));  // open: gt, lt
  Comparator #(.width(5)) comparator_3 (.a(MF), .b({5{1'b0}}), .eq(comparator_3_eq));  // open: gt, lt
  Comparator #(.width(5)) comparator_4 (.a(MF), .b(5'b00100), .eq(comparator_4_eq));  // open: gt, lt
  and and_1 (ERET, comparator_1_eq, comparator_2_eq);
  and and_2 (MFC0, comparator_3_eq, comparator_1_eq);
  and and_3 (MTC0, comparator_4_eq, comparator_1_eq);
  or or_1 (RegWrite, \控制信号自动生成_1_regwrite , MFC0);

  // Other names for the same wires on the sheet: OP_CODE[5:0] = OP

  // Notes on the sheet:
  //   运算器控制器，根据指令生成运算器功能选择信号
  //   控制信号生成，产生数据通路需要的其他控制信号
endmodule

// 运算器控制器
module \运算控制器自动生成  (
  input  OP0,
  input  OP1,
  input  OP2,
  input  OP3,
  input  OP4,
  input  OP5,
  input  F0,
  input  F1,
  input  F2,
  input  F3,
  input  F4,
  input  F5,
  output S0,
  output S1,
  output S2,
  output S3
);

  wire and_1_out, and_2_out, and_3_out, and_4_out, and_5_out, and_6_out, and_7_out, and_8_out, and_9_out,
       and_10_out, and_11_out, and_12_out, and_13_out, and_14_out, and_15_out, and_16_out, and_17_out,
       and_18_out, and_19_out, and_20_out, and_21_out, and_22_out, and_23_out, and_24_out, and_25_out,
       and_26_out, and_27_out, and_28_out, and_29_out, and_30_out, and_31_out, and_32_out, and_33_out,
       and_34_out, and_35_out, and_36_out, and_37_out, and_38_out, and_39_out, and_40_out, and_41_out,
       and_42_out, and_43_out, and_44_out, and_45_out, and_46_out, and_47_out, not_1_out, not_2_out,
       not_3_out, not_4_out, not_5_out, not_6_out, not_7_out, not_8_out, not_9_out, not_10_out, not_11_out,
       not_12_out, not_13_out, not_14_out, not_15_out, not_16_out, not_17_out, not_18_out, not_19_out,
       not_20_out, not_21_out, not_22_out, not_23_out, not_24_out, not_25_out, not_26_out, not_27_out,
       not_28_out, not_29_out, not_30_out, not_31_out, not_32_out, not_33_out, not_34_out, not_35_out,
       not_36_out, not_37_out, not_38_out, not_39_out, not_40_out, not_41_out, not_42_out, not_43_out,
       not_44_out, not_45_out, not_46_out, not_47_out, not_48_out, not_49_out, not_50_out, not_51_out,
       not_52_out, not_53_out, not_54_out, not_55_out, not_56_out, not_57_out, not_58_out, not_59_out,
       not_60_out, not_61_out, not_62_out, not_63_out, not_64_out, not_65_out, not_66_out, not_67_out,
       not_68_out, not_69_out, not_70_out, not_71_out, not_72_out, not_73_out, not_74_out, not_75_out,
       not_76_out, not_77_out, not_78_out, not_79_out, not_80_out, not_81_out, not_82_out, not_83_out,
       not_84_out, not_85_out, not_86_out, not_87_out, not_88_out, not_89_out, not_90_out, not_91_out,
       not_92_out, not_93_out, not_94_out, not_95_out, not_96_out, not_97_out, not_98_out, not_99_out,
       not_100_out, not_101_out, not_102_out, not_103_out, not_104_out, not_105_out, not_106_out,
       not_107_out, not_108_out, not_109_out, not_110_out, not_111_out, not_112_out, not_113_out,
       not_114_out, not_115_out, not_116_out, not_117_out, not_118_out, not_119_out, not_120_out,
       not_121_out, not_122_out, not_123_out, not_124_out, not_125_out, not_126_out, not_127_out,
       not_128_out, not_129_out, not_130_out, not_131_out, not_132_out, not_133_out, not_134_out,
       not_135_out, not_136_out, not_137_out, not_138_out, not_139_out, not_140_out, not_141_out,
       not_142_out, not_143_out, not_144_out, not_145_out, not_146_out, not_147_out, not_148_out,
       not_149_out, not_150_out, not_151_out, not_152_out, not_153_out, not_154_out, not_155_out,
       not_156_out, not_157_out, not_158_out, not_159_out, not_160_out, not_161_out, not_162_out,
       not_163_out, not_164_out, not_165_out, not_166_out, not_167_out, not_168_out, not_169_out,
       not_170_out, not_171_out, not_172_out, not_173_out, not_174_out, not_175_out, not_176_out,
       not_177_out, not_178_out, not_179_out, not_180_out, not_181_out, not_182_out, not_183_out,
       not_184_out, not_185_out, not_186_out, not_187_out, not_188_out, not_189_out, not_190_out,
       not_191_out, not_192_out, not_193_out, not_194_out, not_195_out, not_196_out, not_197_out,
       not_198_out, not_199_out, not_200_out, not_201_out, not_202_out, not_203_out, not_204_out,
       not_205_out, not_206_out, not_207_out, not_208_out, not_209_out, not_210_out, not_211_out,
       not_212_out, not_213_out, not_214_out, not_215_out, not_216_out, not_217_out, not_218_out,
       not_219_out, not_220_out, not_221_out, not_222_out, not_223_out, not_224_out, not_225_out,
       not_226_out, not_227_out, not_228_out, not_229_out, not_230_out, not_231_out, not_232_out,
       not_233_out, not_234_out, not_235_out, not_236_out, not_237_out, not_238_out, not_239_out,
       not_240_out, not_241_out, not_242_out, not_243_out, not_244_out, not_245_out, not_246_out,
       not_247_out, not_248_out, not_249_out, not_250_out, not_251_out, not_252_out, not_253_out,
       not_254_out, not_255_out, not_256_out, not_257_out, not_258_out, not_259_out, not_260_out,
       not_261_out, not_262_out, not_263_out, not_264_out, not_265_out, not_266_out, not_267_out,
       not_268_out, not_269_out, not_270_out, not_271_out, not_272_out, not_273_out, not_274_out,
       not_275_out, not_276_out, not_277_out, not_278_out, not_279_out, not_280_out, not_281_out,
       not_282_out, not_283_out, not_284_out, not_285_out, not_286_out, not_287_out, not_288_out, not_289_out;

  not not_1 (not_1_out, OP5);
  not not_2 (not_2_out, OP4);
  not not_3 (not_3_out, OP3);
  not not_4 (not_4_out, OP2);
  not not_5 (not_5_out, OP1);
  not not_6 (not_6_out, OP0);
  not not_7 (not_7_out, F5);
  not not_8 (not_8_out, F4);
  not not_9 (not_9_out, F3);
  not not_10 (not_10_out, F2);
  not not_11 (not_11_out, OP5);
  not not_12 (not_12_out, OP4);
  not not_13 (not_13_out, OP3);
  not not_14 (not_14_out, OP2);
  not not_15 (not_15_out, OP1);
  not not_16 (not_16_out, OP0);
  not not_17 (not_17_out, F4);
  not not_18 (not_18_out, F3);
  not not_19 (not_19_out, F2);
  not not_20 (not_20_out, F1);
  not not_21 (not_21_out, F0);
  not not_22 (not_22_out, OP5);
  not not_23 (not_23_out, OP4);
  not not_24 (not_24_out, OP3);
  not not_25 (not_25_out, OP2);
  not not_26 (not_26_out, OP1);
  not not_27 (not_27_out, OP0);
  not not_28 (not_28_out, F4);
  not not_29 (not_29_out, F3);
  not not_30 (not_30_out, F2);
  not not_31 (not_31_out, F1);
  not not_32 (not_32_out, OP5);
  not not_33 (not_33_out, OP4);
  not not_34 (not_34_out, OP3);
  not not_35 (not_35_out, OP2);
  not not_36 (not_36_out, OP1);
  not not_37 (not_37_out, OP0);
  not not_38 (not_38_out, F4);
  not not_39 (not_39_out, F3);
  not not_40 (not_40_out, F1);
  not not_41 (not_41_out, F0);
  not not_42 (not_42_out, OP5);
  not not_43 (not_43_out, OP4);
  not not_44 (not_44_out, OP3);
  not not_45 (not_45_out, OP2);
  not not_46 (not_46_out, OP1);
  not not_47 (not_47_out, OP0);
  not not_48 (not_48_out, F4);
  not not_49 (not_49_out, F2);
  not not_50 (not_50_out, F0);
  not not_51 (not_51_out, OP5);
  not not_52 (not_52_out, OP4);
  not not_53 (not_53_out, OP3);
  not not_54 (not_54_out, OP1);
  not not_55 (not_55_out, OP0);
  not not_56 (not_56_out, OP5);
  not not_57 (not_57_out, OP4);
  not not_58 (not_58_out, OP3);
  not not_59 (not_59_out, OP1);
  not not_60 (not_60_out, OP5);
  not not_61 (not_61_out, OP4);
  not not_62 (not_62_out, OP2);
  not not_63 (not_63_out, OP1);
  not not_64 (not_64_out, OP0);
  not not_65 (not_65_out, OP5);
  not not_66 (not_66_out, OP4);
  not not_67 (not_67_out, OP1);
  not not_68 (not_68_out, OP0);
  not not_69 (not_69_out, OP5);
  not not_70 (not_70_out, OP4);
  not not_71 (not_71_out, OP2);
  not not_72 (not_72_out, OP1);
  not not_73 (not_73_out, OP5);
  not not_74 (not_74_out, OP4);
  not not_75 (not_75_out, OP2);
  not not_76 (not_76_out, OP0);
  not not_77 (not_77_out, OP4);
  not not_78 (not_78_out, OP3);
  not not_79 (not_79_out, OP2);
  not not_80 (not_80_out, OP4);
  not not_81 (not_81_out, OP2);
  not not_82 (not_82_out, OP5);
  not not_83 (not_83_out, OP4);
  not not_84 (not_84_out, OP3);
  not not_85 (not_85_out, OP0);
  not not_86 (not_86_out, OP5);
  not not_87 (not_87_out, OP4);
  not not_88 (not_88_out, OP0);
  not not_89 (not_89_out, OP4);
  not not_90 (not_90_out, OP3);
  not not_91 (not_91_out, OP1);
  not not_92 (not_92_out, OP0);
  not not_93 (not_93_out, OP5);
  not not_94 (not_94_out, OP4);
  not not_95 (not_95_out, OP3);
  not not_96 (not_96_out, OP2);
  not not_97 (not_97_out, OP1);
  not not_98 (not_98_out, OP0);
  not not_99 (not_99_out, F5);
  not not_100 (not_100_out, F4);
  not not_101 (not_101_out, F3);
  not not_102 (not_102_out, F2);
  not not_103 (not_103_out, F0);
  not not_104 (not_104_out, OP5);
  not not_105 (not_105_out, OP4);
  not not_106 (not_106_out, OP3);
  not not_107 (not_107_out, OP2);
  not not_108 (not_108_out, OP1);
  not not_109 (not_109_out, OP0);
  not not_110 (not_110_out, F4);
  not not_111 (not_111_out, F3);
  not not_112 (not_112_out, F2);
  not not_113 (not_113_out, F0);
  not not_114 (not_114_out, OP5);
  not not_115 (not_115_out, OP4);
  not not_116 (not_116_out, OP3);
  not not_117 (not_117_out, OP2);
  not not_118 (not_118_out, OP1);
  not not_119 (not_119_out, OP0);
  not not_120 (not_120_out, F4);
  not not_121 (not_121_out, F3);
  not not_122 (not_122_out, F1);
  not not_123 (not_123_out, F0);
  not not_124 (not_124_out, OP5);
  not not_125 (not_125_out, OP4);
  not not_126 (not_126_out, OP3);
  not not_127 (not_127_out, OP2);
  not not_128 (not_128_out, OP1);
  not not_129 (not_129_out, OP0);
  not not_130 (not_130_out, F4);
  not not_131 (not_131_out, F3);
  not not_132 (not_132_out, OP5);
  not not_133 (not_133_out, OP4);
  not not_134 (not_134_out, OP3);
  not not_135 (not_135_out, OP2);
  not not_136 (not_136_out, OP1);
  not not_137 (not_137_out, OP0);
  not not_138 (not_138_out, F4);
  not not_139 (not_139_out, F2);
  not not_140 (not_140_out, F0);
  not not_141 (not_141_out, OP5);
  not not_142 (not_142_out, OP4);
  not not_143 (not_143_out, OP3);
  not not_144 (not_144_out, OP1);
  not not_145 (not_145_out, OP0);
  not not_146 (not_146_out, OP5);
  not not_147 (not_147_out, OP4);
  not not_148 (not_148_out, OP3);
  not not_149 (not_149_out, OP1);
  not not_150 (not_150_out, OP5);
  not not_151 (not_151_out, OP4);
  not not_152 (not_152_out, OP1);
  not not_153 (not_153_out, OP0);
  not not_154 (not_154_out, OP5);
  not not_155 (not_155_out, OP4);
  not not_156 (not_156_out, OP2);
  not not_157 (not_157_out, OP0);
  not not_158 (not_158_out, OP5);
  not not_159 (not_159_out, OP4);
  not not_160 (not_160_out, OP3);
  not not_161 (not_161_out, OP0);
  not not_162 (not_162_out, OP5);
  not not_163 (not_163_out, OP4);
  not not_164 (not_164_out, OP3);
  not not_165 (not_165_out, OP2);
  not not_166 (not_166_out, OP1);
  not not_167 (not_167_out, OP0);
  not not_168 (not_168_out, F4);
  not not_169 (not_169_out, F3);
  not not_170 (not_170_out, F2);
  not not_171 (not_171_out, F1);
  not not_172 (not_172_out, F0);
  not not_173 (not_173_out, OP5);
  not not_174 (not_174_out, OP4);
  not not_175 (not_175_out, OP3);
  not not_176 (not_176_out, OP2);
  not not_177 (not_177_out, OP1);
  not not_178 (not_178_out, OP0);
  not not_179 (not_179_out, F4);
  not not_180 (not_180_out, F3);
  not not_181 (not_181_out, F2);
  not not_182 (not_182_out, F1);
  not not_183 (not_183_out, OP5);
  not not_184 (not_184_out, OP4);
  not not_185 (not_185_out, OP3);
  not not_186 (not_186_out, OP2);
  not not_187 (not_187_out, OP1);
  not not_188 (not_188_out, OP0);
  not not_189 (not_189_out, F4);
  not not_190 (not_190_out, F3);
  not not_191 (not_191_out, F2);
  not not_192 (not_192_out, F0);
  not not_193 (not_193_out, OP5);
  not not_194 (not_194_out, OP4);
  not not_195 (not_195_out, OP3);
  not not_196 (not_196_out, OP2);
  not not_197 (not_197_out, OP1);
  not not_198 (not_198_out, OP0);
  not not_199 (not_199_out, F4);
  not not_200 (not_200_out, F3);
  not not_201 (not_201_out, F1);
  not not_202 (not_202_out, F0);
  not not_203 (not_203_out, OP5);
  not not_204 (not_204_out, OP4);
  not not_205 (not_205_out, OP3);
  not not_206 (not_206_out, OP2);
  not not_207 (not_207_out, OP1);
  not not_208 (not_208_out, OP0);
  not not_209 (not_209_out, F4);
  not not_210 (not_210_out, F2);
  not not_211 (not_211_out, OP5);
  not not_212 (not_212_out, OP4);
  not not_213 (not_213_out, OP2);
  not not_214 (not_214_out, OP1);
  not not_215 (not_215_out, OP0);
  not not_216 (not_216_out, OP5);
  not not_217 (not_217_out, OP4);
  not not_218 (not_218_out, OP1);
  not not_219 (not_219_out, OP0);
  not not_220 (not_220_out, OP5);
  not not_221 (not_221_out, OP4);
  not not_222 (not_222_out, OP2);
  not not_223 (not_223_out, OP1);
  not not_224 (not_224_out, OP4);
  not not_225 (not_225_out, OP3);
  not not_226 (not_226_out, OP2);
  not not_227 (not_227_out, OP4);
  not not_228 (not_228_out, OP2);
  not not_229 (not_229_out, OP4);
  not not_230 (not_230_out, OP3);
  not not_231 (not_231_out, OP1);
  not not_232 (not_232_out, OP0);
  not not_233 (not_233_out, OP5);
  not not_234 (not_234_out, OP4);
  not not_235 (not_235_out, OP3);
  not not_236 (not_236_out, OP2);
  not not_237 (not_237_out, OP1);
  not not_238 (not_238_out, OP0);
  not not_239 (not_239_out, F4);
  not not_240 (not_240_out, F3);
  not not_241 (not_241_out, F1);
  not not_242 (not_242_out, OP5);
  not not_243 (not_243_out, OP4);
  not not_244 (not_244_out, OP3);
  not not_245 (not_245_out, OP2);
  not not_246 (not_246_out, OP1);
  not not_247 (not_247_out, OP0);
  not not_248 (not_248_out, F4);
  not not_249 (not_249_out, F3);
  not not_250 (not_250_out, OP5);
  not not_251 (not_251_out, OP4);
  not not_252 (not_252_out, OP3);
  not not_253 (not_253_out, OP2);
  not not_254 (not_254_out, OP1);
  not not_255 (not_255_out, OP0);
  not not_256 (not_256_out, F4);
  not not_257 (not_257_out, F2);
  not not_258 (not_258_out, F0);
  not not_259 (not_259_out, OP5);
  not not_260 (not_260_out, OP4);
  not not_261 (not_261_out, OP3);
  not not_262 (not_262_out, OP2);
  not not_263 (not_263_out, OP1);
  not not_264 (not_264_out, OP0);
  not not_265 (not_265_out, F4);
  not not_266 (not_266_out, F2);
  not not_267 (not_267_out, OP5);
  not not_268 (not_268_out, OP4);
  not not_269 (not_269_out, OP3);
  not not_270 (not_270_out, OP1);
  not not_271 (not_271_out, OP0);
  not not_272 (not_272_out, OP5);
  not not_273 (not_273_out, OP4);
  not not_274 (not_274_out, OP3);
  not not_275 (not_275_out, OP1);
  not not_276 (not_276_out, OP5);
  not not_277 (not_277_out, OP4);
  not not_278 (not_278_out, OP2);
  not not_279 (not_279_out, OP0);
  not not_280 (not_280_out, OP5);
  not not_281 (not_281_out, OP4);
  not not_282 (not_282_out, OP1);
  not not_283 (not_283_out, OP5);
  not not_284 (not_284_out, OP4);
  not not_285 (not_285_out, OP3);
  not not_286 (not_286_out, OP0);
  not not_287 (not_287_out, OP5);
  not not_288 (not_288_out, OP4);
  not not_289 (not_289_out, OP0);
  and and_1 (and_1_out, not_1_out, not_2_out, not_3_out, not_4_out, not_5_out, not_6_out, not_7_out, not_8_out, not_9_out, not_10_out, F1, F0);
  and and_2 (and_2_out, not_11_out, not_12_out, not_13_out, not_14_out, not_15_out, not_16_out, F5, not_17_out, not_18_out, not_19_out, not_20_out, not_21_out);
  and and_3 (and_3_out, not_22_out, not_23_out, not_24_out, not_25_out, not_26_out, not_27_out, F5, not_28_out, not_29_out, not_30_out, not_31_out, F0);
  and and_4 (and_4_out, not_32_out, not_33_out, not_34_out, not_35_out, not_36_out, not_37_out, F5, not_38_out, not_39_out, F2, not_40_out, not_41_out);
  and and_5 (and_5_out, not_42_out, not_43_out, not_44_out, not_45_out, not_46_out, not_47_out, F5, not_48_out, F3, not_49_out, F1, not_50_out);
  and and_6 (and_6_out, not_51_out, not_52_out, not_53_out, OP2, not_54_out, not_55_out);
  and and_7 (and_7_out, not_56_out, not_57_out, not_58_out, OP2, not_59_out, OP0);
  and and_8 (and_8_out, not_60_out, not_61_out, OP3, not_62_out, not_63_out, not_64_out);
  and and_9 (and_9_out, not_65_out, not_66_out, OP3, OP2, not_67_out, not_68_out);
  and and_10 (and_10_out, not_69_out, not_70_out, OP3, not_71_out, not_72_out, OP0);
  and and_11 (and_11_out, not_73_out, not_74_out, OP3, not_75_out, OP1, not_76_out);
  and and_12 (and_12_out, OP5, not_77_out, not_78_out, not_79_out, OP1, OP0);
  and and_13 (and_13_out, OP5, not_80_out, OP3, not_81_out, OP1, OP0);
  and and_14 (and_14_out, not_82_out, not_83_out, not_84_out, OP2, OP1, not_85_out);
  and and_15 (and_15_out, not_86_out, not_87_out, OP3, OP2, OP1, not_88_out);
  and and_16 (and_16_out, OP5, not_89_out, not_90_out, OP2, not_91_out, not_92_out);
  and and_17 (and_17_out, not_93_out, not_94_out, not_95_out, not_96_out, not_97_out, not_98_out, not_99_out, not_100_out, not_101_out, not_102_out, F1, not_103_out);
  and and_18 (and_18_out, not_104_out, not_105_out, not_106_out, not_107_out, not_108_out, not_109_out, F5, not_110_out, not_111_out, not_112_out, F1, not_113_out);
  and and_19 (and_19_out, not_114_out, not_115_out, not_116_out, not_117_out, not_118_out, not_119_out, F5, not_120_out, not_121_out, F2, not_122_out, not_123_out);
  and and_20 (and_20_out, not_124_out, not_125_out, not_126_out, not_127_out, not_128_out, not_129_out, F5, not_130_out, not_131_out, F2, F1, F0);
  and and_21 (and_21_out, not_132_out, not_133_out, not_134_out, not_135_out, not_136_out, not_137_out, F5, not_138_out, F3, not_139_out, F1, not_140_out);
  and and_22 (and_22_out, not_141_out, not_142_out, not_143_out, OP2, not_144_out, not_145_out);
  and and_23 (and_23_out, not_146_out, not_147_out, not_148_out, OP2, not_149_out, OP0);
  and and_24 (and_24_out, not_150_out, not_151_out, OP3, OP2, not_152_out, not_153_out);
  and and_25 (and_25_out, not_154_out, not_155_out, OP3, not_156_out, OP1, not_157_out);
  and and_26 (and_26_out, not_158_out, not_159_out, not_160_out, OP2, OP1, not_161_out);
  and and_27 (and_27_out, not_162_out, not_163_out, not_164_out, not_165_out, not_166_out, not_167_out, F5, not_168_out, not_169_out, not_170_out, not_171_out, not_172_out);
  and and_28 (and_28_out, not_173_out, not_174_out, not_175_out, not_176_out, not_177_out, not_178_out, F5, not_179_out, not_180_out, not_181_out, not_182_out, F0);
  and and_29 (and_29_out, not_183_out, not_184_out, not_185_out, not_186_out, not_187_out, not_188_out, F5, not_189_out, not_190_out, not_191_out, F1, not_192_out);
  and and_30 (and_30_out, not_193_out, not_194_out, not_195_out, not_196_out, not_197_out, not_198_out, F5, not_199_out, not_200_out, F2, not_201_out, not_202_out);
  and and_31 (and_31_out, not_203_out, not_204_out, not_205_out, not_206_out, not_207_out, not_208_out, F5, not_209_out, F3, not_210_out, F1, F0);
  and and_32 (and_32_out, not_211_out, not_212_out, OP3, not_213_out, not_214_out, not_215_out);
  and and_33 (and_33_out, not_216_out, not_217_out, OP3, OP2, not_218_out, not_219_out);
  and and_34 (and_34_out, not_220_out, not_221_out, OP3, not_222_out, not_223_out, OP0);
  and and_35 (and_35_out, OP5, not_224_out, not_225_out, not_226_out, OP1, OP0);
  and and_36 (and_36_out, OP5, not_227_out, OP3, not_228_out, OP1, OP0);
  and and_37 (and_37_out, OP5, not_229_out, not_230_out, OP2, not_231_out, not_232_out);
  and and_38 (and_38_out, not_233_out, not_234_out, not_235_out, not_236_out, not_237_out, not_238_out, F5, not_239_out, not_240_out, F2, not_241_out, F0);
  and and_39 (and_39_out, not_242_out, not_243_out, not_244_out, not_245_out, not_246_out, not_247_out, F5, not_248_out, not_249_out, F2, F1, F0);
  and and_40 (and_40_out, not_250_out, not_251_out, not_252_out, not_253_out, not_254_out, not_255_out, F5, not_256_out, F3, not_257_out, F1, not_258_out);
  and and_41 (and_41_out, not_259_out, not_260_out, not_261_out, not_262_out, not_263_out, not_264_out, F5, not_265_out, F3, not_266_out, F1, F0);
  and and_42 (and_42_out, not_267_out, not_268_out, not_269_out, OP2, not_270_out, not_271_out);
  and and_43 (and_43_out, not_272_out, not_273_out, not_274_out, OP2, not_275_out, OP0);
  and and_44 (and_44_out, not_276_out, not_277_out, OP3, not_278_out, OP1, not_279_out);
  and and_45 (and_45_out, not_280_out, not_281_out, OP3, OP2, not_282_out, OP0);
  and and_46 (and_46_out, not_283_out, not_284_out, not_285_out, OP2, OP1, not_286_out);
  and and_47 (and_47_out, not_287_out, not_288_out, OP3, OP2, OP1, not_289_out);
  or or_1 (S1, and_17_out, and_18_out, and_19_out, and_20_out, and_21_out, and_22_out, and_23_out, and_24_out, and_25_out, and_26_out);
  or or_2 (S2, and_27_out, and_28_out, and_29_out, and_30_out, and_31_out, and_32_out, and_33_out, and_34_out, and_35_out, and_36_out, and_37_out);
  or or_3 (S3, and_38_out, and_39_out, and_40_out, and_41_out, and_42_out, and_43_out, and_44_out, and_45_out, and_46_out, and_47_out);
  or or_4 (S0, and_1_out, and_2_out, and_3_out, and_4_out, and_5_out, and_6_out, and_7_out, and_8_out, and_9_out, and_10_out, and_11_out, and_12_out, and_13_out, and_14_out, and_15_out, and_16_out);
endmodule

// 控制信号生成
module \控制信号自动生成  (
  input  OP0,
  input  OP1,
  input  OP2,
  input  OP3,
  input  OP4,
  input  OP5,
  input  F0,
  input  F1,
  input  F2,
  input  F3,
  input  F4,
  input  F5,
  output MemtoReg,
  output LBU,
  output MemWrite,
  output ALU_SRC,
  output RegWrite,
  output SYSCALL,
  output SignedExt,
  output RegDst,
  output BEQ,
  output BNE,
  output JR,
  output JMP,
  output JAL,
  output SLLV,
  output BLEZ
);

  wire and_1_out, and_2_out, and_5_out, and_6_out, and_7_out, and_8_out, and_9_out, and_10_out, and_11_out,
       and_12_out, and_13_out, and_14_out, and_15_out, and_16_out, and_17_out, and_18_out, and_20_out,
       and_21_out, and_22_out, and_23_out, and_24_out, and_25_out, and_26_out, and_27_out, and_28_out,
       and_29_out, and_30_out, and_31_out, and_32_out, and_36_out, and_37_out, not_1_out, not_2_out,
       not_3_out, not_4_out, not_5_out, not_6_out, not_7_out, not_8_out, not_9_out, not_10_out, not_11_out,
       not_12_out, not_13_out, not_14_out, not_15_out, not_16_out, not_17_out, not_18_out, not_19_out,
       not_20_out, not_21_out, not_22_out, not_23_out, not_24_out, not_25_out, not_26_out, not_27_out,
       not_28_out, not_29_out, not_30_out, not_31_out, not_32_out, not_33_out, not_34_out, not_35_out,
       not_36_out, not_37_out, not_38_out, not_39_out, not_40_out, not_41_out, not_42_out, not_43_out,
       not_44_out, not_45_out, not_46_out, not_47_out, not_48_out, not_49_out, not_50_out, not_51_out,
       not_52_out, not_53_out, not_54_out, not_55_out, not_56_out, not_57_out, not_58_out, not_59_out,
       not_60_out, not_61_out, not_62_out, not_63_out, not_64_out, not_65_out, not_66_out, not_67_out,
       not_68_out, not_69_out, not_70_out, not_71_out, not_72_out, not_73_out, not_74_out, not_75_out,
       not_76_out, not_77_out, not_78_out, not_79_out, not_80_out, not_81_out, not_82_out, not_83_out,
       not_84_out, not_85_out, not_86_out, not_87_out, not_88_out, not_89_out, not_90_out, not_91_out,
       not_92_out, not_93_out, not_94_out, not_95_out, not_96_out, not_97_out, not_98_out, not_99_out,
       not_100_out, not_101_out, not_102_out, not_103_out, not_104_out, not_105_out, not_106_out,
       not_107_out, not_108_out, not_109_out, not_110_out, not_111_out, not_112_out, not_113_out,
       not_114_out, not_115_out, not_116_out, not_117_out, not_118_out, not_119_out, not_120_out,
       not_121_out, not_122_out, not_123_out, not_124_out, not_125_out, not_126_out, not_127_out,
       not_128_out, not_129_out, not_130_out, not_131_out, not_132_out, not_133_out, not_134_out,
       not_135_out, not_136_out, not_137_out, not_138_out, not_139_out, not_140_out, not_141_out,
       not_142_out, not_143_out, not_144_out, not_145_out, not_146_out, not_147_out, not_148_out,
       not_149_out, not_150_out, not_151_out, not_152_out, not_153_out, not_154_out, not_155_out,
       not_156_out, not_157_out, not_158_out, not_159_out, not_160_out, not_161_out, not_162_out,
       not_163_out, not_164_out, not_165_out, not_166_out, not_167_out, not_168_out, not_169_out,
       not_170_out, not_171_out, not_172_out, not_173_out, not_174_out, not_175_out, not_176_out,
       not_177_out, not_178_out, not_179_out, not_180_out, not_181_out, not_182_out, not_183_out,
       not_184_out, not_185_out, not_186_out, not_187_out, not_188_out, not_189_out, not_190_out,
       not_191_out, not_192_out, not_193_out, not_194_out, not_195_out, not_196_out, not_197_out,
       not_198_out, not_199_out, not_200_out, not_201_out, not_202_out, not_203_out, not_204_out,
       not_205_out, not_206_out, not_207_out, not_208_out, not_209_out, not_210_out, not_211_out,
       not_212_out, not_213_out, not_214_out, not_215_out, not_216_out, not_217_out, not_218_out,
       not_219_out, not_220_out, not_221_out, not_222_out, not_223_out, not_224_out, not_225_out,
       not_226_out, not_227_out, not_228_out, not_229_out, not_230_out, not_231_out, not_232_out,
       not_233_out, not_234_out, not_235_out, not_236_out, not_237_out, not_238_out;

  not not_1 (not_1_out, OP0);
  not not_2 (not_2_out, OP1);
  not not_3 (not_3_out, OP3);
  not not_4 (not_4_out, OP4);
  not not_5 (not_5_out, OP2);
  not not_6 (not_6_out, OP3);
  not not_7 (not_7_out, OP4);
  not not_8 (not_8_out, OP4);
  not not_9 (not_9_out, OP3);
  not not_10 (not_10_out, OP1);
  not not_11 (not_11_out, OP0);
  not not_12 (not_12_out, OP2);
  not not_13 (not_13_out, OP4);
  not not_14 (not_14_out, OP0);
  not not_15 (not_15_out, OP4);
  not not_16 (not_16_out, OP5);
  not not_17 (not_17_out, OP1);
  not not_18 (not_18_out, OP4);
  not not_19 (not_19_out, OP5);
  not not_20 (not_20_out, OP0);
  not not_21 (not_21_out, OP1);
  not not_22 (not_22_out, OP3);
  not not_23 (not_23_out, OP4);
  not not_24 (not_24_out, OP2);
  not not_25 (not_25_out, OP4);
  not not_26 (not_26_out, OP0);
  not not_27 (not_27_out, OP1);
  not not_28 (not_28_out, OP2);
  not not_29 (not_29_out, OP4);
  not not_30 (not_30_out, OP5);
  not not_31 (not_31_out, F0);
  not not_32 (not_32_out, F1);
  not not_33 (not_33_out, F3);
  not not_34 (not_34_out, F4);
  not not_35 (not_35_out, OP0);
  not not_36 (not_36_out, OP1);
  not not_37 (not_37_out, OP2);
  not not_38 (not_38_out, OP4);
  not not_39 (not_39_out, OP5);
  not not_40 (not_40_out, F0);
  not not_41 (not_41_out, F2);
  not not_42 (not_42_out, F3);
  not not_43 (not_43_out, F4);
  not not_44 (not_44_out, OP0);
  not not_45 (not_45_out, OP1);
  not not_46 (not_46_out, OP2);
  not not_47 (not_47_out, OP4);
  not not_48 (not_48_out, OP5);
  not not_49 (not_49_out, F1);
  not not_50 (not_50_out, F3);
  not not_51 (not_51_out, F4);
  not not_52 (not_52_out, OP0);
  not not_53 (not_53_out, OP1);
  not not_54 (not_54_out, OP2);
  not not_55 (not_55_out, OP4);
  not not_56 (not_56_out, OP5);
  not not_57 (not_57_out, F2);
  not not_58 (not_58_out, F3);
  not not_59 (not_59_out, F4);
  not not_60 (not_60_out, F5);
  not not_61 (not_61_out, OP0);
  not not_62 (not_62_out, OP1);
  not not_63 (not_63_out, OP2);
  not not_64 (not_64_out, OP4);
  not not_65 (not_65_out, OP5);
  not not_66 (not_66_out, F2);
  not not_67 (not_67_out, F4);
  not not_68 (not_68_out, OP0);
  not not_69 (not_69_out, OP1);
  not not_70 (not_70_out, OP2);
  not not_71 (not_71_out, OP4);
  not not_72 (not_72_out, OP5);
  not not_73 (not_73_out, F3);
  not not_74 (not_74_out, F4);
  not not_75 (not_75_out, OP0);
  not not_76 (not_76_out, OP4);
  not not_77 (not_77_out, OP5);
  not not_78 (not_78_out, OP1);
  not not_79 (not_79_out, OP4);
  not not_80 (not_80_out, OP5);
  not not_81 (not_81_out, OP0);
  not not_82 (not_82_out, OP1);
  not not_83 (not_83_out, OP3);
  not not_84 (not_84_out, OP4);
  not not_85 (not_85_out, OP2);
  not not_86 (not_86_out, OP3);
  not not_87 (not_87_out, OP4);
  not not_88 (not_88_out, OP0);
  not not_89 (not_89_out, OP1);
  not not_90 (not_90_out, OP2);
  not not_91 (not_91_out, OP3);
  not not_92 (not_92_out, OP4);
  not not_93 (not_93_out, OP5);
  not not_94 (not_94_out, F0);
  not not_95 (not_95_out, F1);
  not not_96 (not_96_out, F4);
  not not_97 (not_97_out, F5);
  not not_98 (not_98_out, OP0);
  not not_99 (not_99_out, OP2);
  not not_100 (not_100_out, OP4);
  not not_101 (not_101_out, OP5);
  not not_102 (not_102_out, OP1);
  not not_103 (not_103_out, OP2);
  not not_104 (not_104_out, OP4);
  not not_105 (not_105_out, OP5);
  not not_106 (not_106_out, OP0);
  not not_107 (not_107_out, OP1);
  not not_108 (not_108_out, OP3);
  not not_109 (not_109_out, OP4);
  not not_110 (not_110_out, OP0);
  not not_111 (not_111_out, OP3);
  not not_112 (not_112_out, OP4);
  not not_113 (not_113_out, OP5);
  not not_114 (not_114_out, OP1);
  not not_115 (not_115_out, OP3);
  not not_116 (not_116_out, OP4);
  not not_117 (not_117_out, OP5);
  not not_118 (not_118_out, OP2);
  not not_119 (not_119_out, OP4);
  not not_120 (not_120_out, OP0);
  not not_121 (not_121_out, OP1);
  not not_122 (not_122_out, OP2);
  not not_123 (not_123_out, OP3);
  not not_124 (not_124_out, OP4);
  not not_125 (not_125_out, OP5);
  not not_126 (not_126_out, F0);
  not not_127 (not_127_out, F1);
  not not_128 (not_128_out, F2);
  not not_129 (not_129_out, F4);
  not not_130 (not_130_out, F5);
  not not_131 (not_131_out, OP0);
  not not_132 (not_132_out, OP1);
  not not_133 (not_133_out, OP2);
  not not_134 (not_134_out, OP3);
  not not_135 (not_135_out, OP4);
  not not_136 (not_136_out, OP5);
  not not_137 (not_137_out, F0);
  not not_138 (not_138_out, F1);
  not not_139 (not_139_out, F3);
  not not_140 (not_140_out, F4);
  not not_141 (not_141_out, OP0);
  not not_142 (not_142_out, OP1);
  not not_143 (not_143_out, OP2);
  not not_144 (not_144_out, OP3);
  not not_145 (not_145_out, OP4);
  not not_146 (not_146_out, OP5);
  not not_147 (not_147_out, F0);
  not not_148 (not_148_out, F2);
  not not_149 (not_149_out, F3);
  not not_150 (not_150_out, F4);
  not not_151 (not_151_out, OP0);
  not not_152 (not_152_out, OP1);
  not not_153 (not_153_out, OP2);
  not not_154 (not_154_out, OP3);
  not not_155 (not_155_out, OP4);
  not not_156 (not_156_out, OP5);
  not not_157 (not_157_out, F1);
  not not_158 (not_158_out, F3);
  not not_159 (not_159_out, F4);
  not not_160 (not_160_out, OP0);
  not not_161 (not_161_out, OP1);
  not not_162 (not_162_out, OP2);
  not not_163 (not_163_out, OP3);
  not not_164 (not_164_out, OP4);
  not not_165 (not_165_out, OP5);
  not not_166 (not_166_out, F2);
  not not_167 (not_167_out, F3);
  not not_168 (not_168_out, F4);
  not not_169 (not_169_out, F5);
  not not_170 (not_170_out, OP0);
  not not_171 (not_171_out, OP1);
  not not_172 (not_172_out, OP2);
  not not_173 (not_173_out, OP3);
  not not_174 (not_174_out, OP4);
  not not_175 (not_175_out, OP5);
  not not_176 (not_176_out, F2);
  not not_177 (not_177_out, F4);
  not not_178 (not_178_out, OP0);
  not not_179 (not_179_out, OP1);
  not not_180 (not_180_out, OP2);
  not not_181 (not_181_out, OP3);
  not not_182 (not_182_out, OP4);
  not not_183 (not_183_out, OP5);
  not not_184 (not_184_out, F3);
  not not_185 (not_185_out, F4);
  not not_186 (not_186_out, OP0);
  not not_187 (not_187_out, OP1);
  not not_188 (not_188_out, OP3);
  not not_189 (not_189_out, OP4);
  not not_190 (not_190_out, OP5);
  not not_191 (not_191_out, OP1);
  not not_192 (not_192_out, OP3);
  not not_193 (not_193_out, OP4);
  not not_194 (not_194_out, OP5);
  not not_195 (not_195_out, OP0);
  not not_196 (not_196_out, OP1);
  not not_197 (not_197_out, OP2);
  not not_198 (not_198_out, OP3);
  not not_199 (not_199_out, OP4);
  not not_200 (not_200_out, OP5);
  not not_201 (not_201_out, F0);
  not not_202 (not_202_out, F1);
  not not_203 (not_203_out, F2);
  not not_204 (not_204_out, F4);
  not not_205 (not_205_out, F5);
  not not_206 (not_206_out, OP0);
  not not_207 (not_207_out, OP2);
  not not_208 (not_208_out, OP3);
  not not_209 (not_209_out, OP4);
  not not_210 (not_210_out, OP5);
  not not_211 (not_211_out, F0);
  not not_212 (not_212_out, F1);
  not not_213 (not_213_out, F2);
  not not_214 (not_214_out, F4);
  not not_215 (not_215_out, F5);
  not not_216 (not_216_out, OP2);
  not not_217 (not_217_out, OP3);
  not not_218 (not_218_out, OP4);
  not not_219 (not_219_out, OP5);
  not not_220 (not_220_out, OP2);
  not not_221 (not_221_out, OP3);
  not not_222 (not_222_out, OP4);
  not not_223 (not_223_out, OP5);
  not not_224 (not_224_out, OP0);
  not not_225 (not_225_out, OP1);
  not not_226 (not_226_out, OP2);
  not not_227 (not_227_out, OP3);
  not not_228 (not_228_out, OP4);
  not not_229 (not_229_out, OP5);
  not not_230 (not_230_out, F0);
  not not_231 (not_231_out, F1);
  not not_232 (not_232_out, F3);
  not not_233 (not_233_out, F4);
  not not_234 (not_234_out, F5);
  not not_235 (not_235_out, OP0);
  not not_236 (not_236_out, OP3);
  not not_237 (not_237_out, OP4);
  not not_238 (not_238_out, OP5);
  and and_1 (and_1_out, not_1_out, not_2_out, OP2, not_3_out, not_4_out, OP5);
  and and_2 (and_2_out, OP0, OP1, not_5_out, not_6_out, not_7_out, OP5);
  and and_3 (LBU, OP5, not_8_out, not_9_out, OP2, not_10_out, not_11_out);
  and and_4 (MemWrite, OP0, OP1, not_12_out, OP3, not_13_out, OP5);
  and and_5 (and_5_out, not_14_out, OP3, not_15_out, not_16_out);
  and and_6 (and_6_out, not_17_out, OP3, not_18_out, not_19_out);
  and and_7 (and_7_out, not_20_out, not_21_out, OP2, not_22_out, not_23_out, OP5);
  and and_8 (and_8_out, OP0, OP1, not_24_out, not_25_out, OP5);
  and and_9 (and_9_out, not_26_out, not_27_out, not_28_out, not_29_out, not_30_out, not_31_out, not_32_out, not_33_out, not_34_out);
  and and_10 (and_10_out, not_35_out, not_36_out, not_37_out, not_38_out, not_39_out, not_40_out, not_41_out, not_42_out, not_43_out);
  and and_11 (and_11_out, not_44_out, not_45_out, not_46_out, not_47_out, not_48_out, not_49_out, not_50_out, not_51_out, F5);
  and and_12 (and_12_out, not_52_out, not_53_out, not_54_out, not_55_out, not_56_out, F1, not_57_out, not_58_out, not_59_out, not_60_out);
  and and_13 (and_13_out, not_61_out, not_62_out, not_63_out, not_64_out, not_65_out, F1, not_66_out, F3, not_67_out, F5);
  and and_14 (and_14_out, not_68_out, not_69_out, not_70_out, not_71_out, not_72_out, F0, F2, not_73_out, not_74_out, F5);
  and and_15 (and_15_out, not_75_out, OP3, not_76_out, not_77_out);
  and and_16 (and_16_out, not_78_out, OP3, not_79_out, not_80_out);
  and and_17 (and_17_out, not_81_out, not_82_out, OP2, not_83_out, not_84_out, OP5);
  and and_18 (and_18_out, OP0, OP1, not_85_out, not_86_out, not_87_out);
  and and_19 (SYSCALL, not_88_out, not_89_out, not_90_out, not_91_out, not_92_out, not_93_out, not_94_out, not_95_out, F2, F3, not_96_out, not_97_out);
  and and_20 (and_20_out, not_98_out, not_99_out, OP3, not_100_out, not_101_out);
  and and_21 (and_21_out, not_102_out, not_103_out, OP3, not_104_out, not_105_out);
  and and_22 (and_22_out, not_106_out, not_107_out, OP2, not_108_out, not_109_out);
  and and_23 (and_23_out, not_110_out, OP2, not_111_out, not_112_out, not_113_out);
  and and_24 (and_24_out, not_114_out, OP2, not_115_out, not_116_out, not_117_out);
  and and_25 (and_25_out, OP0, OP1, not_118_out, not_119_out, OP5);
  and and_26 (and_26_out, not_120_out, not_121_out, not_122_out, not_123_out, not_124_out, not_125_out, not_126_out, not_127_out, not_128_out, not_129_out, not_130_out);
  and and_27 (and_27_out, not_131_out, not_132_out, not_133_out, not_134_out, not_135_out, not_136_out, not_137_out, not_138_out, not_139_out, not_140_out);
  and and_28 (and_28_out, not_141_out, not_142_out, not_143_out, not_144_out, not_145_out, not_146_out, not_147_out, not_148_out, not_149_out, not_150_out);
  and and_29 (and_29_out, not_151_out, not_152_out, not_153_out, not_154_out, not_155_out, not_156_out, not_157_out, not_158_out, not_159_out, F5);
  and and_30 (and_30_out, not_160_out, not_161_out, not_162_out, not_163_out, not_164_out, not_165_out, F1, not_166_out, not_167_out, not_168_out, not_169_out);
  and and_31 (and_31_out, not_170_out, not_171_out, not_172_out, not_173_out, not_174_out, not_175_out, F1, not_176_out, F3, not_177_out, F5);
  and and_32 (and_32_out, not_178_out, not_179_out, not_180_out, not_181_out, not_182_out, not_183_out, F0, F2, not_184_out, not_185_out, F5);
  and and_33 (BEQ, not_186_out, not_187_out, OP2, not_188_out, not_189_out, not_190_out);
  and and_34 (BNE, OP0, not_191_out, OP2, not_192_out, not_193_out, not_194_out);
  and and_35 (JR, not_195_out, not_196_out, not_197_out, not_198_out, not_199_out, not_200_out, not_201_out, not_202_out, not_203_out, F3, not_204_out, not_205_out);
  and and_36 (and_36_out, not_206_out, not_207_out, not_208_out, not_209_out, not_210_out, not_211_out, not_212_out, not_213_out, F3, not_214_out, not_215_out);
  and and_37 (and_37_out, OP1, not_216_out, not_217_out, not_218_out, not_219_out);
  and and_38 (JAL, OP0, OP1, not_220_out, not_221_out, not_222_out, not_223_out);
  and and_39 (SLLV, not_224_out, not_225_out, not_226_out, not_227_out, not_228_out, not_229_out, not_230_out, not_231_out, F2, not_232_out, not_233_out, not_234_out);
  and and_40 (BLEZ, not_235_out, OP1, OP2, not_236_out, not_237_out, not_238_out);
  or or_1 (MemtoReg, and_1_out, and_2_out);
  or or_2 (ALU_SRC, and_5_out, and_6_out, and_7_out, and_8_out);
  or or_3 (RegWrite, and_9_out, and_10_out, and_11_out, and_12_out, and_13_out, and_14_out, and_15_out, and_16_out, and_17_out, and_18_out);
  or or_4 (SignedExt, and_20_out, and_21_out, and_22_out, and_23_out, and_24_out, and_25_out);
  or or_5 (RegDst, and_26_out, and_27_out, and_28_out, and_29_out, and_30_out, and_31_out, and_32_out);
  or or_6 (JMP, and_36_out, and_37_out);
endmodule

module \理想流水线  (
  output RegWrite,
  output MemWrite,
  output [31:0] IF_PC,
  output [31:0] ID_PC,
  output [31:0] EX_PC,
  output [31:0] M_PC,
  output [31:0] WB_PC,
  output [31:0] RDin,
  output [31:0] MDin,
  output [31:0] LedData
);

  wire and_1_out, and_2_out, and_3_out, and_4_out, Branch, CLK, clock_1_out, clock_2_out, comparator_1_eq,
       comparator_1_lt, d_ff_1_q, Equal, ex_mem_1_halt_out, ex_mem_1_jal_out, ex_mem_1_memtoreg_out,
       ex_mem_1_regdst_out, ex_mem_1_regwtire_out, ex_mem_1_syscall_out, Go, Halt, id_ex_1_alusrcb_out,
       id_ex_1_beq_out, id_ex_1_bne_out, id_ex_1_halt_out, id_ex_1_jal_out, id_ex_1_memtogeg_out,
       id_ex_1_memwrite_out, id_ex_1_regdst_out, id_ex_1_regwrite_out, id_ex_1_syscall_out, IR1, IR2, IR3,
       JAL, JMP, JR, mem_wb_1_halt_out, MemtoReg, mips_alu_1_equal, nand_1_out, or_1_out, or_2_out, RegDst,
       RST, SignedExt, sys, Syscall, W1, W2, W3, \单周期硬布线控制器_1_alu_src , \单周期硬布线控制器_1_beq , \单周期硬布线控制器_1_bne ,
       \单周期硬布线控制器_1_jal , \单周期硬布线控制器_1_jmp , \单周期硬布线控制器_1_jr , \单周期硬布线控制器_1_memtoreg ,
       \单周期硬布线控制器_1_memwrite , \单周期硬布线控制器_1_regdst , \单周期硬布线控制器_1_regwrite ;
  wire [3:0] id_ex_1_aluop_out, \单周期硬布线控制器_1_alu_op ;
  wire [4:0] id_ex_1_shamt_in_2, multiplexer_2_out, multiplexer_3_out, multiplexer_7_out, multiplexer_8_out;
  wire [12:0] CNT_num;
  wire [15:0] \LoadUse次数 , \总周期数 , \插入气泡数 , \无条件分支数 , \条件分支成功数 ;
  wire [31:0] a0, adder_1_out, adder_2_out, bit_extender_1_out, bit_extender_2_out, EX_IR,
       ex_mem_1_aluresult_out, ex_mem_1_ir_out, EX_PC2, id_ex_1_address_out, id_ex_1_eimm_out,
       id_ex_1_ir_out, id_ex_1_r1_out, id_ex_1_r2_out, ID_IR, ID_PC2, if_id_1_ir_out, IF_IR, MEM_IR, MEM_PC2,
       mem_wb_1_aluresult_out, mem_wb_1_ir_out, mem_wb_1_memd_out, mem_wb_1_pc_out, mips_alu_1_result,
       mips_regifile_1_r2, multiplexer_1_out, multiplexer_4_out, multiplexer_5_out, multiplexer_6_out,
       ram_1_data, rom_1_data, shifter_1_out, WB_IR;

  Button \u_总复位  (.out(RST));
  Button _1 (.out(IR1));
  Button _2 (.out(IR2));
  Button _3 (.out(IR3));
  // Probe on \总周期数 
  // Probe on \总周期数 
  Button \u_继续运行  (.out(Go));
  LED led_1 (.in(W1));
  LED led_2 (.in(W2));
  LED led_3 (.in(W3));
  or or_1 (or_1_out, Halt, Go);
  Hex_Digit_Display hex_digit_display_1 (.value(LedData[31:28]));  // open: dp
  // Probe on IF_PC[19:0]
  // Mips_Probe mips_probe_1: pin names not known; wires that end beside it: IF_IR
  Counter #(.width(16), .max('hffff)) counter_1 (
    .Q(\总周期数 ), .clk(CLK), .clr(RST), .down(or_1_out));  // open: load, D, count, carry, preset
  Multiplexer #(.select(3), .width(32), .enable("false")) multiplexer_1 (
    .in0(adder_1_out), .in1({32{1'b0}}), .in2(id_ex_1_address_out), .in3(id_ex_1_r1_out), .in4(adder_2_out),
    .in5({32{1'b0}}), .in6({32{1'b0}}), .in7({32{1'b0}}), .out(multiplexer_1_out), .sel({Branch, JMP, JR}));
  Hex_Digit_Display hex_digit_display_2 (.value(LedData[23:20]));  // open: dp
  Hex_Digit_Display hex_digit_display_3 (.value(LedData[27:24]));  // open: dp
  // Probe on ID_PC[19:0]
  // Mips_Probe mips_probe_2: pin names not known; wires that end beside it: ID_IR
  // Probe on multiplexer_1_out
  Register #(.width(32), .Select("low")) PC (.D(multiplexer_1_out), .en(or_2_out), .Q(IF_PC), .clk(CLK), .clr(RST));
  or or_2 (or_2_out, Halt, Go);
  Hex_Digit_Display hex_digit_display_4 (.value(LedData[19:16]));  // open: dp
  Hex_Digit_Display hex_digit_display_5 (.value(LedData[15:12]));  // open: dp
  Hex_Digit_Display hex_digit_display_6 (.value(LedData[11:8]));  // open: dp
  Hex_Digit_Display hex_digit_display_7 (.value(LedData[7:4]));  // open: dp
  Clock clock_1 (.out(clock_1_out));
  // Probe on EX_PC[19:0]
  // Mips_Probe mips_probe_3: pin names not known; wires that end beside it: clock_1_out, EX_IR, CLK
  and and_1 (and_1_out, Equal, Syscall);
  Adder #(.width(32)) adder_1 (.a(IF_PC), .b(32'h4), .out(adder_1_out));  // open: cin, cout
  Hex_Digit_Display hex_digit_display_8 (.value(LedData[3:0]));  // open: dp
  Register #(.width(32), .Select("low")) register_1 (.D(a0), .en(and_1_out), .Q(LedData), .clk(CLK), .clr(RST));
  // Probe on rom_1_data
  ROM #(.addrWidth(10), .dataWidth(32), .Select("high")) rom_1 (.addr(IF_PC[11:2]), .data(rom_1_data));
  // Probe on \总周期数 
  // Probe on M_PC[19:0]
  // Mips_Probe mips_probe_4: pin names not known; wires that end beside it: MEM_IR
  IF_ID if_id_1 (
    .ir_in(rom_1_data), .pcr_in(IF_PC), .pc_in(adder_1_out), .ir_out(if_id_1_ir_out), .pcr_out(ID_PC),
    .pc_out(ID_PC2), .Reset(RST), .CLK(CLK), .Enable(Halt));
  // Probe on \总周期数 
  // Probe on \无条件分支数 
  // Probe on \条件分支成功数 
  // Probe on \插入气泡数 
  // Probe on \LoadUse次数 
  // Probe on if_id_1_ir_out
  // Probe on IF_PC[11:0]
  // Probe on WB_PC[19:0]
  // Mips_Probe mips_probe_5: pin names not known; wires that end beside it: WB_IR
  // Probe on EX_PC[11:0]
  // Probe on ID_PC[11:0]
  // Probe on if_id_1_ir_out[15:11]
  // Probe on M_PC[11:0]
  D_Flip_Flop #(.trigger("high"), .Pre_Clr_Positions("LEGACY"), .enable("true"), .NewFFLayout("false")) d_ff_1 (.Q(d_ff_1_q));  // open: clk, D, Qn, preset, en, reset
  // Probe on 13'hc
  \单周期硬布线控制器  \u_单周期硬布线控制器_1  (
    .Func(if_id_1_ir_out[5:0]), .OP(if_id_1_ir_out[31:26]), .ALU_OP(\单周期硬布线控制器_1_alu_op ),
    .MemToReg(\单周期硬布线控制器_1_memtoreg ), .MemWrite(\单周期硬布线控制器_1_memwrite ), .ALU_SRC(\单周期硬布线控制器_1_alu_src ),
    .RegWrite(\单周期硬布线控制器_1_regwrite ), .SysCALL(Syscall), .SignedExt(SignedExt),
    .RegDst(\单周期硬布线控制器_1_regdst ), .JR(\单周期硬布线控制器_1_jr ), .JMP(\单周期硬布线控制器_1_jmp ), .Beq(\单周期硬布线控制器_1_beq ),
    .JAL(\单周期硬布线控制器_1_jal ), .Bne(\单周期硬布线控制器_1_bne ));  // open: SLLV, BLEZ, LBU, ERET, MFC0, MTC0, MF
  Multiplexer #(.width(5), .enable("false")) multiplexer_2 (
    .in0(if_id_1_ir_out[25:21]), .in1(5'b00100), .out(multiplexer_2_out), .sel(Syscall));
  Multiplexer #(.width(5), .enable("false")) multiplexer_3 (
    .in0(if_id_1_ir_out[20:16]), .in1(5'b00010), .out(multiplexer_3_out), .sel(Syscall));
  assign bit_extender_1_out = {{16{1'b0}}, if_id_1_ir_out[15:0]};  // Bit_Extender bit_extender_1
  Multiplexer #(.width(32), .enable("false")) multiplexer_4 (
    .in0(bit_extender_1_out), .in1(bit_extender_2_out), .out(multiplexer_4_out), .sel(SignedExt));
  assign bit_extender_2_out = {{16{if_id_1_ir_out[15]}}, if_id_1_ir_out[15:0]};  // Bit_Extender bit_extender_2
  // Probe on WB_PC[11:0]
  Comparator #(.width(13)) comparator_1 (
    .a(CNT_num), .b(13'hc), .eq(comparator_1_eq), .lt(comparator_1_lt));  // open: gt
  Clock clock_2 (.out(clock_2_out));
  nand nand_1 (nand_1_out, d_ff_1_q, comparator_1_eq);
  Counter #(.width(13), .max('h1fff), .ongoal("stay"), .behavior("old")) counter_2 (
    .count(comparator_1_lt), .Q(CNT_num), .clk(clock_2_out));  // open: load, D, carry, clr, preset
  MIPS_Regifile mips_regifile_1 (
    .Din(RDin), .Clk(CLK), .R1(a0), .R2(mips_regifile_1_r2), .WE(RegWrite), .W_num(multiplexer_8_out),
    .R1_num(multiplexer_2_out), .R2_num(multiplexer_3_out));
  and and_2 (and_2_out, ~Equal, Syscall);  // AND_Gate
  assign CLK = nand_1_out ? clock_2_out : 1'bz;  // Controlled_Buffer controlled_buffer_1
  Comparator #(.width(32)) comparator_2 (.a(mips_regifile_1_r2), .b(32'h22), .eq(Equal));  // open: gt, lt
  // Probe on multiplexer_4_out
  Pull_Resistor #(.pull(1)) pull_resistor_1 (.node(CLK));
  ID_EX id_ex_1 (
    .jr_in(\单周期硬布线控制器_1_jr ), .R1_in(a0), .Eimm_in(multiplexer_4_out), .jmp_in(\单周期硬布线控制器_1_jmp ),
    .beq_in(\单周期硬布线控制器_1_beq ), .R2_in(mips_regifile_1_r2), .bne_in(\单周期硬布线控制器_1_bne ),
    .Address_in({ID_PC2[31:28], if_id_1_ir_out[25:0], 2'b00}), .memtogeg_in(\单周期硬布线控制器_1_memtoreg ),
    .memwrite_in(\单周期硬布线控制器_1_memwrite ), .pcr_in(ID_PC), .shamt_in(if_id_1_ir_out[10:6]),
    .AluOp_in(\单周期硬布线控制器_1_alu_op ), .AluSrcB_in(\单周期硬布线控制器_1_alu_src ),
    .RegWrite_in(\单周期硬布线控制器_1_regwrite ), .pc_in(ID_PC2), .JAL_in(\单周期硬布线控制器_1_jal ),
    .RegDst_in(\单周期硬布线控制器_1_regdst ), .ir_in(if_id_1_ir_out), .Eimm_out(id_ex_1_eimm_out),
    .R2_out(id_ex_1_r2_out), .Address_out(id_ex_1_address_out), .pcr_out(EX_PC),
    .shamt_in_2(id_ex_1_shamt_in_2), .pc_out(EX_PC2), .ir_out(id_ex_1_ir_out), .Rest(RST), .CLK(CLK),
    .Enable(Halt), .halt_in(and_2_out), .syscall_in(Syscall), .jr_out(JR), .jmp_out(JMP),
    .beq_out(id_ex_1_beq_out), .bne_out(id_ex_1_bne_out), .memtogeg_out(id_ex_1_memtogeg_out),
    .memwrite_out(id_ex_1_memwrite_out), .AluOp_out(id_ex_1_aluop_out), .AluSrcB_out(id_ex_1_alusrcb_out),
    .RegWrite_out(id_ex_1_regwrite_out), .JAL_out(id_ex_1_jal_out), .RegDst_out(id_ex_1_regdst_out),
    .halt_out(id_ex_1_halt_out), .syscall_out(id_ex_1_syscall_out), .R1_out(id_ex_1_r1_out));  // open: W__in, W__IN_2, SLLV_in, SLLV_out, BLEZ_in, BLEZ_out, LBU_in, LBU_out
  Multiplexer #(.width(32), .enable("false")) multiplexer_5 (
    .in0(id_ex_1_r2_out), .in1(id_ex_1_eimm_out), .out(multiplexer_5_out), .sel(id_ex_1_alusrcb_out));
  or or_3 (Branch, and_3_out, and_4_out);
  and and_3 (and_3_out, id_ex_1_beq_out, mips_alu_1_equal);
  Shifter #(.width(32)) shifter_1 (.in(id_ex_1_eimm_out), .\dist (5'b00010), .out(shifter_1_out));
  and and_4 (and_4_out, id_ex_1_bne_out, ~mips_alu_1_equal);  // AND_Gate
  MIPS_ALU mips_alu_1 (
    .X(id_ex_1_r1_out), .Y(multiplexer_5_out), .AluOP(id_ex_1_aluop_out), .Equal(mips_alu_1_equal),
    .Result(mips_alu_1_result), .shamt(id_ex_1_shamt_in_2));  // open: Result_2
  Adder #(.width(32)) adder_2 (.a(shifter_1_out), .b(EX_PC2), .out(adder_2_out));  // open: cin, cout
  EX_MEM ex_mem_1 (
    .MemtoReg_in(id_ex_1_memtogeg_out), .AluResult_in(mips_alu_1_result),
    .MemWrite_int(id_ex_1_memwrite_out), .R2_in(id_ex_1_r2_out), .RegWtire_in(id_ex_1_regwrite_out),
    .PCr_in(EX_PC), .JAL_in(id_ex_1_jal_out), .RegDst_in(id_ex_1_regdst_out), .IR_in(id_ex_1_ir_out),
    .syscall_in(id_ex_1_syscall_out), .PC_in(EX_PC2), .halt_in(id_ex_1_halt_out),
    .MemtoReg_out(ex_mem_1_memtoreg_out), .AluResult_out(ex_mem_1_aluresult_out), .MemWrite_out(MemWrite),
    .R2_out(MDin), .RegWtire_out(ex_mem_1_regwtire_out), .PCr_out(M_PC), .JAL_out(ex_mem_1_jal_out),
    .RegDst_out(ex_mem_1_regdst_out), .IR_out(ex_mem_1_ir_out), .syscall_out(ex_mem_1_syscall_out),
    .PC_out(MEM_PC2), .halt_out(ex_mem_1_halt_out), .Reset(RST), .CLK(CLK), .Enable(Halt));  // open: W__in, W__IN_2, LBU_in, LBU_out
  RAM #(.addrWidth(10), .dataWidth(32), .bus("separate"), .Select("high")) ram_1 (
    .addr(ex_mem_1_aluresult_out[11:2]), .din(MDin), .data(ram_1_data), .str(MemWrite), .clk(CLK), .clr(RST));  // open: sel, ld
  MEM_WB mem_wb_1 (
    .AluResult_in(ex_mem_1_aluresult_out), .MemtoReg_in(ex_mem_1_memtoreg_out), .MemD_in(ram_1_data),
    .RegWtire_in(ex_mem_1_regwtire_out), .PCr_in(M_PC), .JAL_in(ex_mem_1_jal_out),
    .RegDst_in(ex_mem_1_regdst_out), .IR_in(ex_mem_1_ir_out), .syscall_in(ex_mem_1_syscall_out),
    .PC_in(MEM_PC2), .halt_in(ex_mem_1_halt_out), .AluResult_out(mem_wb_1_aluresult_out),
    .MemtoReg_out(MemtoReg), .MemD_out(mem_wb_1_memd_out), .RegWtire_out(RegWrite), .PCr_out(WB_PC),
    .JAL_out(JAL), .RegDst_out(RegDst), .IR_out(mem_wb_1_ir_out), .syscall_out(sys),
    .PC_out(mem_wb_1_pc_out), .halt_out(mem_wb_1_halt_out), .Reset(RST), .CLK(CLK), .Enable(Halt));  // open: W__in, W__IN_2, LBU_in, LBU_out, go
  not not_1 (Halt, mem_wb_1_halt_out);
  Multiplexer #(.width(32), .enable("false")) multiplexer_6 (
    .in0(mem_wb_1_aluresult_out), .in1(mem_wb_1_memd_out), .out(multiplexer_6_out), .sel(MemtoReg));
  Multiplexer #(.width(5), .enable("false")) multiplexer_7 (
    .in0(mem_wb_1_ir_out[20:16]), .in1(mem_wb_1_ir_out[15:11]), .out(multiplexer_7_out), .sel(RegDst));
  Multiplexer #(.width(5), .enable("false")) multiplexer_8 (
    .in0(multiplexer_7_out), .in1({5{1'b1}}), .out(multiplexer_8_out), .sel(JAL));
  Multiplexer #(.width(32), .enable("false")) multiplexer_9 (
    .in0(multiplexer_6_out), .in1(mem_wb_1_pc_out), .out(RDin), .sel(JAL));

  // Other names for the same wires on the sheet: MEM_PC[31:0] = M_PC

  // Notes on the sheet:
  //   中断源
  //   时空图监测，可删除
  //   中断等待指示
  //   数码管输出
  //   指令字
  //   contents of rom_1 (hex, n*v repeats v):
  //   20100000 20110000 20120000 20130000 36100000 36310001 36520002 36730003 ae100000 ae110004 ae120008
  //   ae13000c 2002000a 20110000 20120000 20130000 c
  //   OP
  //   rs
  //   rt
  //   rd
  //   shamt
  //   imm16
  //   控制位
  //   Func
  //   (PC+4)U4+imm26<<2
  //   流水调试日志用
  //   暂停节拍，不能为0
  //   JMP
  //   JR
  //   OP
  //   Func
  //   Syscall
  //   戳工具置1进入计数暂停模式，ctrl+k时钟自动运行到对应节拍暂停
  //   ctrl+k关闭时钟连续运行，将控制位置零，进入单步调试模式调试
  //   用这个时钟源需要去掉电路中的其他时钟源
  //   Beq
  //   Bne
  //   MemToReg
  //   MemWrite
  //   AluOP
  //   AluSrcB
  //   RegWrite
  //   JAL
  //   RegDst
  //   可计数暂停的时钟源
  //   为方便自动评测，需要输出流水线各段保存的PC值，注意是PC不是PC+4，另外ID段寄存器写入信息，Mem段内存写入信息也要输出
  //   rt
  //   rd
endmodule

module \分支流水线  (
  output RegWrite,
  output MemWrite,
  output [31:0] IF_PC,
  output [31:0] ID_PC,
  output [31:0] EX_PC,
  output [31:0] M_PC,
  output [31:0] WB_PC,
  output [31:0] RDin,
  output [31:0] MDin,
  output [31:0] LedData
);

  wire and_1_out, and_2_out, and_3_out, and_4_out, Branch, CLK, clock_1_out, clock_2_out, comparator_1_eq,
       comparator_1_lt, d_ff_1_q, Equal, ex_mem_1_halt_out, ex_mem_1_jal_out, ex_mem_1_memtoreg_out,
       ex_mem_1_regdst_out, ex_mem_1_regwtire_out, ex_mem_1_syscall_out, Go, Halt, id_ex_1_alusrcb_out,
       id_ex_1_beq_out, id_ex_1_bne_out, id_ex_1_halt_out, id_ex_1_jal_out, id_ex_1_memtogeg_out,
       id_ex_1_memwrite_out, id_ex_1_regdst_out, id_ex_1_regwrite_out, id_ex_1_syscall_out, IR1, IR2, IR3,
       JAL, JMP, JR, mem_wb_1_halt_out, MemtoReg, mips_alu_1_equal, nand_1_out, nop, or_1_out, or_2_out,
       or_3_out, or_4_out, RegDst, RST, SignedExt, sys, Syscall, W1, W2, W3, \单周期硬布线控制器_1_alu_src ,
       \单周期硬布线控制器_1_beq , \单周期硬布线控制器_1_bne , \单周期硬布线控制器_1_jal , \单周期硬布线控制器_1_jmp , \单周期硬布线控制器_1_jr ,
       \单周期硬布线控制器_1_memtoreg , \单周期硬布线控制器_1_memwrite , \单周期硬布线控制器_1_regdst , \单周期硬布线控制器_1_regwrite ;
  wire [3:0] id_ex_1_aluop_out, \单周期硬布线控制器_1_alu_op ;
  wire [4:0] id_ex_1_shamt_in_2, multiplexer_2_out, multiplexer_3_out, multiplexer_7_out, multiplexer_8_out;
  wire [12:0] CNT_num;
  wire [15:0] \LoadUse次数 , \总周期数 , \插入气泡数 , \无条件分支数 , \条件分支成功数 ;
  wire [25:0] if_id_1_ir_out_2;
  wire [31:0] a0, adder_1_out, adder_2_out, bit_extender_1_out, bit_extender_2_out, EX_IR,
       ex_mem_1_aluresult_out, ex_mem_1_ir_out, EX_PC2, id_ex_1_address_out, id_ex_1_eimm_out,
       id_ex_1_ir_out, id_ex_1_r1_out, id_ex_1_r2_out, ID_IR, ID_PC2, IF_IR, MEM_IR, MEM_PC2,
       mem_wb_1_aluresult_out, mem_wb_1_ir_out, mem_wb_1_memd_out, mem_wb_1_pc_out, mips_alu_1_result,
       mips_regifile_1_r2, multiplexer_1_out, multiplexer_4_out, multiplexer_5_out, multiplexer_6_out,
       ram_1_data, rom_1_data, shifter_1_out, WB_IR;
  wire [31:26] if_id_1_ir_out;

  Button \u_总复位  (.out(RST));
  Button _1 (.out(IR1));
  Button _2 (.out(IR2));
  Button _3 (.out(IR3));
  // Probe on \总周期数 
  // Probe on \总周期数 
  Button \u_继续运行  (.out(Go));
  LED led_1 (.in(W1));
  LED led_2 (.in(W2));
  LED led_3 (.in(W3));
  Hex_Digit_Display hex_digit_display_1 (.value(LedData[31:28]));  // open: dp
  // Probe on IF_PC[19:0]
  // Mips_Probe mips_probe_1: pin names not known; wires that end beside it: IF_IR
  Multiplexer #(.select(3), .width(32), .enable("false")) multiplexer_1 (
    .in0(adder_1_out), .in1({32{1'b0}}), .in2(id_ex_1_address_out), .in3(id_ex_1_r1_out), .in4(adder_2_out),
    .in5({32{1'b0}}), .in6({32{1'b0}}), .in7({32{1'b0}}), .out(multiplexer_1_out), .sel({Branch, JMP, JR}));
  Hex_Digit_Display hex_digit_display_2 (.value(LedData[27:24]));  // open: dp
  Hex_Digit_Display hex_digit_display_3 (.value(LedData[23:20]));  // open: dp
  // Probe on ID_PC[19:0]
  // Mips_Probe mips_probe_2: pin names not known; wires that end beside it: ID_IR
  // Probe on multiplexer_1_out
  Register #(.width(32), .Select("low")) PC (.D(multiplexer_1_out), .en(or_1_out), .Q(IF_PC), .clk(CLK), .clr(RST));
  or or_1 (or_1_out, Halt, Go);
  Hex_Digit_Display hex_digit_display_4 (.value(LedData[15:12]));  // open: dp
  Hex_Digit_Display hex_digit_display_5 (.value(LedData[19:16]));  // open: dp
  Hex_Digit_Display hex_digit_display_6 (.value(LedData[7:4]));  // open: dp
  Hex_Digit_Display hex_digit_display_7 (.value(LedData[11:8]));  // open: dp
  Clock clock_1 (.out(clock_1_out));
  // Probe on EX_PC[19:0]
  // Mips_Probe mips_probe_3: pin names not known; wires that end beside it: clock_1_out, EX_IR, CLK
  Adder #(.width(32)) adder_1 (.a(IF_PC), .b(32'h4), .out(adder_1_out));  // open: cin, cout
  Hex_Digit_Display hex_digit_display_8 (.value(LedData[3:0]));  // open: dp
  // Probe on rom_1_data
  ROM #(.addrWidth(10), .dataWidth(32), .Select("high")) rom_1 (.addr(IF_PC[11:2]), .data(rom_1_data));
  // Probe on \总周期数 
  // Probe on M_PC[19:0]
  // Mips_Probe mips_probe_4: pin names not known; wires that end beside it: MEM_IR
  or or_2 (or_2_out, RST, nop);
  IF_ID if_id_1 (
    .ir_in(rom_1_data), .pcr_in(IF_PC), .pc_in(adder_1_out), .ir_out({if_id_1_ir_out, if_id_1_ir_out_2}),
    .pcr_out(ID_PC), .pc_out(ID_PC2), .Reset(or_2_out), .CLK(CLK), .Enable(Halt));
  // Probe on \总周期数 
  // Probe on \无条件分支数 
  // Probe on \条件分支成功数 
  // Probe on \插入气泡数 
  // Probe on \LoadUse次数 
  // Probe on {if_id_1_ir_out, if_id_1_ir_out_2}
  // Probe on IF_PC[11:0]
  // Probe on WB_PC[19:0]
  // Mips_Probe mips_probe_5: pin names not known; wires that end beside it: WB_IR
  // Probe on ID_PC[11:0]
  // Probe on EX_PC[11:0]
  // Probe on if_id_1_ir_out_2[15:11]
  // Probe on M_PC[11:0]
  D_Flip_Flop #(.trigger("high"), .Pre_Clr_Positions("LEGACY"), .enable("true"), .NewFFLayout("false")) d_ff_1 (.Q(d_ff_1_q));  // open: clk, D, Qn, preset, en, reset
  // Probe on 13'hc
  \单周期硬布线控制器  \u_单周期硬布线控制器_1  (
    .Func(if_id_1_ir_out_2[5:0]), .OP(if_id_1_ir_out), .ALU_OP(\单周期硬布线控制器_1_alu_op ),
    .MemToReg(\单周期硬布线控制器_1_memtoreg ), .MemWrite(\单周期硬布线控制器_1_memwrite ), .ALU_SRC(\单周期硬布线控制器_1_alu_src ),
    .RegWrite(\单周期硬布线控制器_1_regwrite ), .SysCALL(Syscall), .SignedExt(SignedExt),
    .RegDst(\单周期硬布线控制器_1_regdst ), .JR(\单周期硬布线控制器_1_jr ), .JMP(\单周期硬布线控制器_1_jmp ), .Beq(\单周期硬布线控制器_1_beq ),
    .JAL(\单周期硬布线控制器_1_jal ), .Bne(\单周期硬布线控制器_1_bne ));  // open: SLLV, BLEZ, LBU, ERET, MFC0, MTC0, MF
  Multiplexer #(.width(5), .enable("false")) multiplexer_2 (
    .in0(if_id_1_ir_out_2[25:21]), .in1(5'b00100), .out(multiplexer_2_out), .sel(Syscall));
  Multiplexer #(.width(5), .enable("false")) multiplexer_3 (
    .in0(if_id_1_ir_out_2[20:16]), .in1(5'b00010), .out(multiplexer_3_out), .sel(Syscall));
  assign bit_extender_1_out = {{16{1'b0}}, if_id_1_ir_out_2[15:0]};  // Bit_Extender bit_extender_1
  Multiplexer #(.width(32), .enable("false")) multiplexer_4 (
    .in0(bit_extender_1_out), .in1(bit_extender_2_out), .out(multiplexer_4_out), .sel(SignedExt));
  assign bit_extender_2_out = {{16{if_id_1_ir_out_2[15]}}, if_id_1_ir_out_2[15:0]};  // Bit_Extender bit_extender_2
  // Probe on WB_PC[11:0]
  Comparator #(.width(13)) comparator_1 (
    .a(CNT_num), .b(13'hc), .eq(comparator_1_eq), .lt(comparator_1_lt));  // open: gt
  Clock clock_2 (.out(clock_2_out));
  nand nand_1 (nand_1_out, d_ff_1_q, comparator_1_eq);
  Counter #(.width(13), .max('h1fff), .ongoal("stay"), .behavior("old")) counter_1 (
    .count(comparator_1_lt), .Q(CNT_num), .clk(clock_2_out));  // open: load, D, carry, clr, preset
  MIPS_Regifile mips_regifile_1 (
    .Din(RDin), .Clk(CLK), .R1(a0), .R2(mips_regifile_1_r2), .WE(RegWrite), .W_num(multiplexer_8_out),
    .R1_num(multiplexer_2_out), .R2_num(multiplexer_3_out));
  and and_1 (and_1_out, ~Equal, Syscall);  // AND_Gate
  assign CLK = nand_1_out ? clock_2_out : 1'bz;  // Controlled_Buffer controlled_buffer_1
  Comparator #(.width(32)) comparator_2 (.a(mips_regifile_1_r2), .b(32'h22), .eq(Equal));  // open: gt, lt
  // Probe on multiplexer_4_out
  Pull_Resistor #(.pull(1)) pull_resistor_1 (.node(CLK));
  or or_3 (or_3_out, RST, nop);
  ID_EX id_ex_1 (
    .jr_in(\单周期硬布线控制器_1_jr ), .R1_in(a0), .Eimm_in(multiplexer_4_out), .jmp_in(\单周期硬布线控制器_1_jmp ),
    .beq_in(\单周期硬布线控制器_1_beq ), .R2_in(mips_regifile_1_r2), .bne_in(\单周期硬布线控制器_1_bne ),
    .Address_in({ID_PC2[31:28], if_id_1_ir_out_2, 2'b00}), .memtogeg_in(\单周期硬布线控制器_1_memtoreg ),
    .memwrite_in(\单周期硬布线控制器_1_memwrite ), .pcr_in(ID_PC), .shamt_in(if_id_1_ir_out_2[10:6]),
    .AluOp_in(\单周期硬布线控制器_1_alu_op ), .AluSrcB_in(\单周期硬布线控制器_1_alu_src ),
    .RegWrite_in(\单周期硬布线控制器_1_regwrite ), .pc_in(ID_PC2), .JAL_in(\单周期硬布线控制器_1_jal ),
    .RegDst_in(\单周期硬布线控制器_1_regdst ), .ir_in({if_id_1_ir_out, if_id_1_ir_out_2}),
    .Eimm_out(id_ex_1_eimm_out), .R2_out(id_ex_1_r2_out), .Address_out(id_ex_1_address_out), .pcr_out(EX_PC),
    .shamt_in_2(id_ex_1_shamt_in_2), .pc_out(EX_PC2), .ir_out(id_ex_1_ir_out), .Rest(or_3_out), .CLK(CLK),
    .Enable(Halt), .halt_in(and_1_out), .syscall_in(Syscall), .jr_out(JR), .jmp_out(JMP),
    .beq_out(id_ex_1_beq_out), .bne_out(id_ex_1_bne_out), .memtogeg_out(id_ex_1_memtogeg_out),
    .memwrite_out(id_ex_1_memwrite_out), .AluOp_out(id_ex_1_aluop_out), .AluSrcB_out(id_ex_1_alusrcb_out),
    .RegWrite_out(id_ex_1_regwrite_out), .JAL_out(id_ex_1_jal_out), .RegDst_out(id_ex_1_regdst_out),
    .halt_out(id_ex_1_halt_out), .syscall_out(id_ex_1_syscall_out), .R1_out(id_ex_1_r1_out));  // open: W__in, W__IN_2, SLLV_in, SLLV_out, BLEZ_in, BLEZ_out, LBU_in, LBU_out
  or or_4 (or_4_out, Halt, Go);
  Counter #(.width(16), .max('hffff), .behavior("old")) counter_2 (
    .count(or_4_out), .Q(\总周期数 ), .clk(CLK), .clr(RST));  // open: load, D, carry, preset
  Multiplexer #(.width(32), .enable("false")) multiplexer_5 (
    .in0(id_ex_1_r2_out), .in1(id_ex_1_eimm_out), .out(multiplexer_5_out), .sel(id_ex_1_alusrcb_out));
  or or_5 (Branch, and_2_out, and_3_out);
  and and_2 (and_2_out, id_ex_1_beq_out, mips_alu_1_equal);
  Shifter #(.width(32)) shifter_1 (.in(id_ex_1_eimm_out), .\dist (5'b00010), .out(shifter_1_out));
  and and_3 (and_3_out, id_ex_1_bne_out, ~mips_alu_1_equal);  // AND_Gate
  MIPS_ALU mips_alu_1 (
    .X(id_ex_1_r1_out), .Y(multiplexer_5_out), .AluOP(id_ex_1_aluop_out), .Equal(mips_alu_1_equal),
    .Result(mips_alu_1_result), .shamt(id_ex_1_shamt_in_2));  // open: Result_2
  Adder #(.width(32)) adder_2 (.a(shifter_1_out), .b(EX_PC2), .out(adder_2_out));  // open: cin, cout
  and and_4 (and_4_out, Equal, Syscall);
  or or_6 (nop, Branch, JR, JMP);
  Register #(.width(32), .Select("low")) register_1 (.D(a0), .en(and_4_out), .Q(LedData), .clk(CLK), .clr(RST));
  EX_MEM ex_mem_1 (
    .MemtoReg_in(id_ex_1_memtogeg_out), .AluResult_in(mips_alu_1_result),
    .MemWrite_int(id_ex_1_memwrite_out), .R2_in(id_ex_1_r2_out), .RegWtire_in(id_ex_1_regwrite_out),
    .PCr_in(EX_PC), .JAL_in(id_ex_1_jal_out), .RegDst_in(id_ex_1_regdst_out), .IR_in(id_ex_1_ir_out),
    .syscall_in(id_ex_1_syscall_out), .PC_in(EX_PC2), .halt_in(id_ex_1_halt_out),
    .MemtoReg_out(ex_mem_1_memtoreg_out), .AluResult_out(ex_mem_1_aluresult_out), .MemWrite_out(MemWrite),
    .R2_out(MDin), .RegWtire_out(ex_mem_1_regwtire_out), .PCr_out(M_PC), .JAL_out(ex_mem_1_jal_out),
    .RegDst_out(ex_mem_1_regdst_out), .IR_out(ex_mem_1_ir_out), .syscall_out(ex_mem_1_syscall_out),
    .PC_out(MEM_PC2), .halt_out(ex_mem_1_halt_out), .Reset(RST), .CLK(CLK), .Enable(Halt));  // open: W__in, W__IN_2, LBU_in, LBU_out
  RAM #(.addrWidth(10), .dataWidth(32), .bus("separate"), .Select("high")) ram_1 (
    .addr(ex_mem_1_aluresult_out[11:2]), .din(MDin), .data(ram_1_data), .str(MemWrite), .clk(CLK), .clr(RST));  // open: sel, ld
  MEM_WB mem_wb_1 (
    .AluResult_in(ex_mem_1_aluresult_out), .MemtoReg_in(ex_mem_1_memtoreg_out), .MemD_in(ram_1_data),
    .RegWtire_in(ex_mem_1_regwtire_out), .PCr_in(M_PC), .JAL_in(ex_mem_1_jal_out),
    .RegDst_in(ex_mem_1_regdst_out), .IR_in(ex_mem_1_ir_out), .syscall_in(ex_mem_1_syscall_out),
    .PC_in(MEM_PC2), .halt_in(ex_mem_1_halt_out), .AluResult_out(mem_wb_1_aluresult_out),
    .MemtoReg_out(MemtoReg), .MemD_out(mem_wb_1_memd_out), .RegWtire_out(RegWrite), .PCr_out(WB_PC),
    .JAL_out(JAL), .RegDst_out(RegDst), .IR_out(mem_wb_1_ir_out), .syscall_out(sys),
    .PC_out(mem_wb_1_pc_out), .halt_out(mem_wb_1_halt_out), .Reset(RST), .CLK(CLK), .Enable(Halt));  // open: W__in, W__IN_2, LBU_in, LBU_out, go
  not not_1 (Halt, mem_wb_1_halt_out);
  Multiplexer #(.width(32), .enable("false")) multiplexer_6 (
    .in0(mem_wb_1_aluresult_out), .in1(mem_wb_1_memd_out), .out(multiplexer_6_out), .sel(MemtoReg));
  Multiplexer #(.width(5), .enable("false")) multiplexer_7 (
    .in0(mem_wb_1_ir_out[20:16]), .in1(mem_wb_1_ir_out[15:11]), .out(multiplexer_7_out), .sel(RegDst));
  Multiplexer #(.width(5), .enable("false")) multiplexer_8 (
    .in0(multiplexer_7_out), .in1({5{1'b1}}), .out(multiplexer_8_out), .sel(JAL));
  Multiplexer #(.width(32), .enable("false")) multiplexer_9 (
    .in0(multiplexer_6_out), .in1(mem_wb_1_pc_out), .out(RDin), .sel(JAL));

  // Other names for the same wires on the sheet: MEM_PC[31:0] = M_PC

  // Notes on the sheet:
  //   中断源
  //   时空图监测，可删除
  //   中断等待指示
  //   数码管输出
  //   指令字
  //   contents of rom_1 (hex, n*v repeats v):
  //   20110001 8000c05 20110001 20120002 20130003 8000c09 20110001 20120002 20130003 8000c0d 20110001
  //   20120002 20130003 8000c11 20110001 20120002 20130003 c000cb8 20100001 20110001 118fc0 112020
  //   20020022 c 118882 12200001 8000c15 112020 20020022 c 20110001 118880 112020 20020022 c 12200001
  //   8000c1f 20110001 118fc0 112020 20020022 c 1188c3 112020 20020022 c 118903 112020 20020022 c 118903
  //   112020 20020022 c 118903 112020 20020022 c 118903 112020 20020022 c 118903 112020 20020022 c 118903
  //   112020 20020022 c 118903 112020 20020022 c 20100001 109fc0 139fc3 8021 2012000c 24160003 26100001
  //   3210000f 20080008 20090001 139900 2709825 132020 20020022 c 1094022 1500fff9 22100001 2018000f
  //   2188024 108700 20080008 20090001 139902 2709825 132021 20020022 c 1094022 1500fff9 108702 2c9b022
  //   12c00001 8000c50 4020 1084027 84400 3508ffff 82021 20020022 c 2010ffff 20110000 ae300000 22100001
  //   22310004 ae300000 22100001 22310004 ae300000 22100001 22310004 ae300000 22100001 22310004 ae300000
  //   22100001 22310004 ae300000 22100001 22310004 ae300000 22100001 22310004 ae300000 22100001 22310004
  //   ae300000 22100001 22310004 ae300000 22100001 22310004 ae300000 22100001 22310004 ae300000 22100001
  //   22310004 ae300000 22100001 22310004 ae300000 22100001 22310004 ae300000 22100001 22310004 ae300000
  //   22100001 22310004 22100001 8020 2011003c 8e130000 8e340000 274402a 11000002 ae330000 ae140000
  //   2231fffc 1611fff8 102020 20020022 c 22100004 2011003c 1611fff2 20020032 c 20100000 22100001 102020
  //   20020022 c 22100002 102020 20020022 c 22100003 102020 20020022 c 22100004 102020 20020022 c 22100005
  //   102020 20020022 c 22100006 102020 20020022 c 22100007 102020 20020022 c 22100008 102020 20020022
  //   20020022 c 3e00008
  //   OP
  //   rs
  //   rt
  //   rd
  //   shamt
  //   imm16
  //   控制位
  //   Func
  //   (PC+4)U4+imm26<<2
  //   流水调试日志用
  //   暂停节拍，不能为0
  //   JMP
  //   JR
  //   OP
  //   Func
  //   Syscall
  //   Beq
  //   Bne
  //   MemToReg
  //   MemWrite
  //   AluOP
  //   AluSrcB
  //   RegWrite
  //   JAL
  //   RegDst
  //   可计数暂停的时钟源
  //   为方便自动评测，需要输出流水线各段保存的PC值，注意是PC不是PC+4，另外ID段寄存器写入信息，Mem段内存写入信息也要输出
  //   rt
  //   rd
  //   戳工具置1进入计数暂停模式，ctrl+k时钟自动运行到对应节拍暂停
  //   ctrl+k关闭时钟连续运行，将控制位置零，进入单步调试模式调试
  //   用这个时钟源需要去掉电路中的其他时钟源
endmodule

// ALU
module MIPS_ALU (
  input  [4:0] shamt,
  input  [31:0] X,
  input  [31:0] Y,
  input  [3:0] AluOP,
  output Equal,
  output [31:0] Result,
  output [31:0] Result_2
);

  wire [0:0] comparator_1_lt, comparator_2_lt;
  wire [31:0] adder_1_out, AND_out, divider_1_out, divider_1_rem, multiplier_1_cout, multiplier_1_out,
       NOR_out, OR_out, shifter_1_out, shifter_2_out, shifter_3_out, subtractor_1_out, XOR_out;

  assign AND_out = X & Y;  // AND_Gate AND, 32 bits wide
  assign OR_out = X | Y;  // OR_Gate OR, 32 bits wide
  Shifter #(.width(32)) shifter_1 (.in(Y), .\dist (shamt), .out(shifter_1_out));
  Shifter #(.width(32), .shift("ar")) shifter_2 (.in(Y), .\dist (shamt), .out(shifter_2_out));
  Shifter #(.width(32), .shift("lr")) shifter_3 (.in(Y), .\dist (shamt), .out(shifter_3_out));
  Multiplier #(.width(32)) multiplier_1 (.a(X), .b(Y), .out(multiplier_1_out), .cout(multiplier_1_cout));  // open: cin
  Divider #(.width(32)) divider_1 (.a(X), .b(Y), .out(divider_1_out), .rem(divider_1_rem));  // open: upper
  Adder #(.width(32)) adder_1 (.a(X), .b(Y), .out(adder_1_out));  // open: cin, cout
  Subtractor #(.width(32)) subtractor_1 (.a(X), .b(Y), .out(subtractor_1_out));  // open: bin, bout
  assign XOR_out = X ^ Y;  // XOR_Gate XOR, 32 bits wide
  assign NOR_out = ~(X | Y);  // NOR_Gate NOR, 32 bits wide
  Comparator #(.width(32)) comparator_1 (.a(X), .b(Y), .eq(Equal), .lt(comparator_1_lt[0]));  // open: gt
  Comparator #(.width(32), .mode("unsigned")) comparator_2 (.a(X), .b(Y), .lt(comparator_2_lt[0]));  // open: gt, eq
  Multiplexer #(.select(4), .width(32), .enable("false")) multiplexer_1 (
    .in0(shifter_1_out), .in1(shifter_2_out), .in2(shifter_3_out), .in3(multiplier_1_out),
    .in4(divider_1_out), .in5(adder_1_out), .in6(subtractor_1_out), .in7(AND_out), .in8(OR_out),
    .in9(XOR_out), .in10(NOR_out), .in11({{31{1'b0}}, comparator_1_lt[0]}),
    .in12({{31{1'b0}}, comparator_2_lt[0]}), .in13({32{1'b0}}), .in14({32{1'b0}}), .in15({32{1'b0}}),
    .out(Result), .sel(AluOP));
  Multiplexer #(.select(4), .width(32), .enable("false")) multiplexer_2 (
    .in0({32{1'b0}}), .in1({32{1'b0}}), .in2({32{1'b0}}), .in3(multiplier_1_cout), .in4(divider_1_rem),
    .in5({32{1'b0}}), .in6({32{1'b0}}), .in7({32{1'b0}}), .in8({32{1'b0}}), .in9({32{1'b0}}),
    .in10({32{1'b0}}), .in11({32{1'b0}}), .in12({32{1'b0}}), .in13({32{1'b0}}), .in14({32{1'b0}}),
    .in15({32{1'b0}}), .out(Result_2), .sel(AluOP));

  // Other names for the same wires on the sheet: Result2[31:0] = Result_2; S[3:0] = AluOP

  // Notes on the sheet:
  //   不要改变此引脚区域内容，也不要改变ALU封装形式
  //   输入引脚
  //   输出引脚
endmodule

module MIPS_Regifile (
  input  [31:0] Din,
  input  Clk,
  input  WE,
  input  [4:0] R1_num,
  input  [4:0] W_num,
  input  [4:0] R2_num,
  output [31:0] R1,
  output [31:0] R2
);

  // RegisterFile registerfile_1: pin names not known; wires that end beside it: Din, Clk, WE, W_num, R1_num, R2_num, R1, R2
endmodule

module \气泡流水线  (
  output RegWrite,
  output MemWrite,
  output [31:0] IF_PC,
  output [31:0] ID_PC,
  output [31:0] EX_PC,
  output [31:0] M_PC,
  output [31:0] WB_PC,
  output [31:0] RDin,
  output [31:0] MDin,
  output [31:0] LedData
);

  wire and_1_out, and_2_out, and_3_out, and_4_out, and_5_out, and_6_out, and_7_out, and_8_out, BLEZ_O,
       Branch, CLK, clock_1_out, clock_2_out, comparator_1_eq, comparator_1_lt, comparator_3_eq, d_ff_1_q,
       DataConflict, Equal, ex_mem_1_halt_out, ex_mem_1_jal_out, ex_mem_1_memtoreg_out, ex_mem_1_regdst_out,
       ex_mem_1_syscall_out, EX_RegWrite, Go, id_ex_1_alusrcb_out, id_ex_1_beq_out, id_ex_1_bne_out,
       id_ex_1_jal_out, id_ex_1_memtogeg_out, id_ex_1_memwrite_out, id_ex_1_regdst_out, ID_RegDst, IR1, IR2,
       IR3, JAL, JMP, JR, LBU_M, LBU_O, LBU_W, MEM_RegWrite, mem_wb_1_halt_out, MemtoReg, mips_alu_1_equal,
       nand_1_out, nop, or_1_out, or_2_out, or_3_out, or_4_out, or_7_out, RegDst, RST, run, SignedExt,
       SLLV_O, sys, Syscall, W1, W2, W3, \单周期硬布线控制器_1_alu_src , \单周期硬布线控制器_1_beq , \单周期硬布线控制器_1_blez ,
       \单周期硬布线控制器_1_bne , \单周期硬布线控制器_1_jal , \单周期硬布线控制器_1_jmp , \单周期硬布线控制器_1_jr , \单周期硬布线控制器_1_lbu ,
       \单周期硬布线控制器_1_memtoreg , \单周期硬布线控制器_1_memwrite , \单周期硬布线控制器_1_regwrite , \单周期硬布线控制器_1_sllv ,
       \单周期硬布线控制器_1_syscall ;
  wire [1:0] undriven;
  wire [3:0] id_ex_1_aluop_out, \单周期硬布线控制器_1_alu_op ;
  wire [4:0] EX_WriteReg_num, id_ex_1_shamt_in_2, ID_R1_num, ID_R2_num, MEM_WriteReg_num, multiplexer_2_out,
       multiplexer_5_out, multiplexer_9_out, multiplexer_13_out, multiplexer_14_out;
  wire [5:0] Func;
  wire [7:0] multiplexer_10_out, multiplexer_15_out;
  wire [12:0] CNT_num;
  wire [15:0] \LoadUse次数 , \总周期数 , \插入气泡数 , \无条件分支数 , \条件分支成功数 ;
  wire [31:0] a0, a0_t, adder_1_out, adder_2_out, bit_extender_1_out, bit_extender_2_out, bit_extender_3_out,
       bit_extender_4_out, EX_IR, ex_mem_1_aluresult_out, EX_PC2, id_ex_1_address_out, id_ex_1_eimm_out,
       id_ex_1_r2_out, ID_PC2, IF_IR, MEM_IR, MEM_PC2, mem_wb_1_aluresult_out, mem_wb_1_memd_out,
       mem_wb_1_pc_out, mips_alu_1_result, mips_regifile_1_r1, multiplexer_1_out, multiplexer_6_out,
       multiplexer_7_out, multiplexer_8_out, multiplexer_11_out, multiplexer_12_out, multiplexer_16_out,
       ram_1_data, shifter_1_out, undriven_2, WB_IR;
  wire [31:6] ID_IR;

  Button \u_总复位  (.out(RST));
  Button _1 (.out(IR1));
  Button _2 (.out(IR2));
  Button _3 (.out(IR3));
  // Probe on \总周期数 
  // Probe on \总周期数 
  Button \u_继续运行  (.out(Go));
  LED led_1 (.in(W1));
  LED led_2 (.in(W2));
  LED led_3 (.in(W3));
  Hex_Digit_Display hex_digit_display_1 (.value(LedData[31:28]));  // open: dp
  // Probe on IF_PC[19:0]
  // Mips_Probe mips_probe_1: pin names not known; wires that end beside it: IF_IR
  Multiplexer #(.select(3), .width(32), .enable("false")) multiplexer_1 (
    .in0(adder_1_out), .in1({32{1'b0}}), .in2(id_ex_1_address_out), .in3(a0_t), .in4(adder_2_out),
    .in5({32{1'b0}}), .in6({32{1'b0}}), .in7({32{1'b0}}), .out(multiplexer_1_out), .sel({Branch, JMP, JR}));
  or or_1 (or_1_out, run, Go);
  // Probe on adder_2_out
  Hex_Digit_Display hex_digit_display_2 (.value(LedData[27:24]));  // open: dp
  Hex_Digit_Display hex_digit_display_3 (.value(LedData[23:20]));  // open: dp
  // Probe on ID_PC[19:0]
  // Mips_Probe mips_probe_2: pin names not known; wires that end beside it: {ID_IR, Func}
  // Probe on multiplexer_1_out
  Register #(.width(32), .Select("low")) PC (.D(multiplexer_1_out), .en(and_1_out), .Q(IF_PC), .clk(CLK), .clr(RST));
  and and_1 (and_1_out, or_1_out, ~DataConflict);  // AND_Gate
  Hex_Digit_Display hex_digit_display_4 (.value(LedData[15:12]));  // open: dp
  Hex_Digit_Display hex_digit_display_5 (.value(LedData[19:16]));  // open: dp
  // Probe on IF_PC
  // Probe on IF_PC
  Hex_Digit_Display hex_digit_display_6 (.value(LedData[7:4]));  // open: dp
  Hex_Digit_Display hex_digit_display_7 (.value(LedData[11:8]));  // open: dp
  Clock clock_1 (.out(clock_1_out));
  // Probe on EX_PC[19:0]
  // Mips_Probe mips_probe_3: pin names not known; wires that end beside it: clock_1_out, EX_IR, CLK
  // Probe on ID_PC
  Adder #(.width(32)) adder_1 (.a(IF_PC), .b(32'h4), .out(adder_1_out));  // open: cin, cout
  Hex_Digit_Display hex_digit_display_8 (.value(LedData[3:0]));  // open: dp
  // Probe on EX_PC
  // Probe on IF_IR
  ROM #(.addrWidth(10), .dataWidth(32), .Select("high")) rom_1 (.addr(IF_PC[11:2]), .data(IF_IR));
  and and_2 (and_2_out, ~DataConflict, run);  // AND_Gate
  // Probe on \总周期数 
  // Probe on M_PC[19:0]
  // Mips_Probe mips_probe_4: pin names not known; wires that end beside it: MEM_IR
  // Probe on M_PC
  or or_2 (or_2_out, RST, nop);
  IF_ID if_id_1 (
    .ir_in(IF_IR), .pcr_in(IF_PC), .pc_in(adder_1_out), .ir_out({ID_IR, Func}), .pcr_out(ID_PC),
    .pc_out(ID_PC2), .Reset(or_2_out), .CLK(CLK), .Enable(and_2_out));
  // Probe on \总周期数 
  // Probe on \无条件分支数 
  // Probe on \条件分支成功数 
  // Probe on \插入气泡数 
  // Probe on \LoadUse次数 
  // Probe on WB_PC
  // Probe on {ID_IR, Func}
  // Probe on IF_PC[11:0]
  // Probe on WB_PC[19:0]
  // Mips_Probe mips_probe_5: pin names not known; wires that end beside it: WB_IR
  // Probe on ID_PC[11:0]
  // Probe on EX_PC[11:0]
  Multiplexer #(.width(5), .enable("false")) multiplexer_2 (
    .in0(ID_IR[20:16]), .in1(ID_IR[15:11]), .out(multiplexer_2_out), .sel(ID_RegDst));
  assign bit_extender_1_out = {{16{1'b0}}, {ID_IR[15:6], Func}};  // Bit_Extender bit_extender_1
  assign bit_extender_2_out = {{16{ID_IR[15]}}, {ID_IR[15:6], Func}};  // Bit_Extender bit_extender_2
  // Probe on M_PC[11:0]
  D_Flip_Flop #(.trigger("high"), .Pre_Clr_Positions("LEGACY"), .enable("true"), .NewFFLayout("false")) d_ff_1 (.Q(d_ff_1_q));  // open: clk, D, Qn, preset, en, reset
  // Probe on 13'h10
  \单周期硬布线控制器  \u_单周期硬布线控制器_1  (
    .Func(Func), .OP(ID_IR[31:26]), .ALU_OP(\单周期硬布线控制器_1_alu_op ), .MemToReg(\单周期硬布线控制器_1_memtoreg ),
    .MemWrite(\单周期硬布线控制器_1_memwrite ), .ALU_SRC(\单周期硬布线控制器_1_alu_src ), .RegWrite(\单周期硬布线控制器_1_regwrite ),
    .SysCALL(\单周期硬布线控制器_1_syscall ), .SignedExt(SignedExt), .RegDst(ID_RegDst), .JR(\单周期硬布线控制器_1_jr ),
    .JMP(\单周期硬布线控制器_1_jmp ), .Beq(\单周期硬布线控制器_1_beq ), .JAL(\单周期硬布线控制器_1_jal ), .Bne(\单周期硬布线控制器_1_bne ),
    .SLLV(\单周期硬布线控制器_1_sllv ), .BLEZ(\单周期硬布线控制器_1_blez ), .LBU(\单周期硬布线控制器_1_lbu ));  // open: ERET, MFC0, MTC0, MF
  Multiplexer #(.width(5), .enable("false")) multiplexer_3 (
    .in0(ID_IR[25:21]), .in1(5'b00100), .out(ID_R1_num), .sel(\单周期硬布线控制器_1_syscall ));
  Multiplexer #(.width(5), .enable("false")) multiplexer_4 (
    .in0(ID_IR[20:16]), .in1(5'b00010), .out(ID_R2_num), .sel(\单周期硬布线控制器_1_syscall ));
  Multiplexer #(.width(5), .enable("false")) multiplexer_5 (
    .in0(multiplexer_2_out), .in1({5{1'b1}}), .out(multiplexer_5_out), .sel(\单周期硬布线控制器_1_jal ));
  Multiplexer #(.width(32), .enable("false")) multiplexer_6 (
    .in0(bit_extender_1_out), .in1(bit_extender_2_out), .out(multiplexer_6_out), .sel(SignedExt));
  // Probe on WB_PC[11:0]
  Comparator #(.width(13)) comparator_1 (
    .a(CNT_num), .b(13'h10), .eq(comparator_1_eq), .lt(comparator_1_lt));  // open: gt
  Clock clock_2 (.out(clock_2_out));
  \气泡数据相关检测  \u_气泡数据相关检测_1  (
    .ID_OP(ID_IR[31:26]), .ID_FUNC(Func), .ID_R1_num(ID_R1_num), .ID_R2_num(ID_R2_num),
    .EX_WriteReg_num(EX_WriteReg_num), .MEM_WriteReg_num(MEM_WriteReg_num), .EX_RegWrite(EX_RegWrite),
    .MEM_RegWrite(MEM_RegWrite), .DataConflict(DataConflict));
  // Probe on multiplexer_6_out
  nand nand_1 (nand_1_out, d_ff_1_q, comparator_1_eq);
  Counter #(.width(13), .max('h1fff), .ongoal("stay"), .behavior("old")) counter_1 (
    .count(comparator_1_lt), .Q(CNT_num), .clk(clock_2_out), .clr(RST));  // open: load, D, carry, preset
  MIPS_Regifile mips_regifile_1 (
    .Din(RDin), .Clk(CLK), .R1(mips_regifile_1_r1), .R2(a0), .WE(RegWrite), .W_num(multiplexer_14_out),
    .R1_num(ID_R1_num), .R2_num(ID_R2_num));
  // Probe on multiplexer_6_out
  assign CLK = nand_1_out ? clock_2_out : 1'bz;  // Controlled_Buffer controlled_buffer_1
  Pull_Resistor #(.pull(1)) pull_resistor_1 (.node(CLK));
  or or_3 (or_3_out, RST, DataConflict, nop);
  ID_EX id_ex_1 (
    .jr_in(\单周期硬布线控制器_1_jr ), .R1_in(mips_regifile_1_r1), .Eimm_in(multiplexer_6_out),
    .jmp_in(\单周期硬布线控制器_1_jmp ), .beq_in(\单周期硬布线控制器_1_beq ), .R2_in(a0), .bne_in(\单周期硬布线控制器_1_bne ),
    .Address_in({ID_PC2[31:28], ID_IR[25:6], Func, 2'b00}), .memtogeg_in(\单周期硬布线控制器_1_memtoreg ),
    .memwrite_in(\单周期硬布线控制器_1_memwrite ), .pcr_in(ID_PC), .shamt_in(ID_IR[10:6]),
    .AluOp_in(\单周期硬布线控制器_1_alu_op ), .AluSrcB_in(\单周期硬布线控制器_1_alu_src ),
    .RegWrite_in(\单周期硬布线控制器_1_regwrite ), .pc_in(ID_PC2), .JAL_in(\单周期硬布线控制器_1_jal ), .RegDst_in(ID_RegDst),
    .ir_in({ID_IR, Func}), .Eimm_out(id_ex_1_eimm_out), .R2_out(id_ex_1_r2_out),
    .Address_out(id_ex_1_address_out), .pcr_out(EX_PC), .shamt_in_2(id_ex_1_shamt_in_2), .pc_out(EX_PC2),
    .ir_out(EX_IR), .Rest(or_3_out), .CLK(CLK), .Enable(run), .syscall_in(\单周期硬布线控制器_1_syscall ),
    .jr_out(JR), .jmp_out(JMP), .beq_out(id_ex_1_beq_out), .bne_out(id_ex_1_bne_out),
    .memtogeg_out(id_ex_1_memtogeg_out), .memwrite_out(id_ex_1_memwrite_out), .AluOp_out(id_ex_1_aluop_out),
    .AluSrcB_out(id_ex_1_alusrcb_out), .RegWrite_out(EX_RegWrite), .JAL_out(id_ex_1_jal_out),
    .RegDst_out(id_ex_1_regdst_out), .syscall_out(Syscall), .R1_out(a0_t), .W__in(multiplexer_5_out),
    .W__IN_2(EX_WriteReg_num), .SLLV_in(\单周期硬布线控制器_1_sllv ), .SLLV_out(SLLV_O), .BLEZ_in(\单周期硬布线控制器_1_blez ),
    .BLEZ_out(BLEZ_O), .LBU_in(\单周期硬布线控制器_1_lbu ), .LBU_out(LBU_O));  // open: halt_in, halt_out
  or or_4 (or_4_out, run, Go);
  and and_3 (and_3_out, DataConflict, run);
  Comparator #(.width(32)) comparator_2 (.a(id_ex_1_r2_out), .b(32'h22), .eq(Equal));  // open: gt, lt
  Counter #(.width(16), .max('hffff), .behavior("old")) counter_2 (
    .count(or_4_out), .Q(\总周期数 ), .clk(CLK), .clr(RST));  // open: load, D, carry, preset
  Counter #(.width(16), .max('hffff), .behavior("old")) counter_3 (
    .count(and_3_out), .Q(\插入气泡数 ), .clk(CLK), .clr(RST));  // open: load, D, carry, preset
  Multiplexer #(.width(32), .enable("false")) multiplexer_7 (
    .in0(id_ex_1_r2_out), .in1(id_ex_1_eimm_out), .out(multiplexer_7_out), .sel(id_ex_1_alusrcb_out));
  // Probe on EX_PC2
  or or_5 (Branch, and_4_out, and_6_out, and_8_out);
  and and_4 (and_4_out, id_ex_1_beq_out, mips_alu_1_equal);
  MIPS_ALU mips_alu_1 (
    .X(a0_t), .Y(multiplexer_8_out), .AluOP(id_ex_1_aluop_out), .Equal(mips_alu_1_equal),
    .Result(mips_alu_1_result), .shamt(multiplexer_9_out));  // open: Result_2
  Multiplexer #(.width(32), .enable("false")) multiplexer_8 (
    .in0(multiplexer_7_out), .in1({32{1'b0}}), .out(multiplexer_8_out), .sel(BLEZ_O));
  Multiplexer #(.width(5), .enable("false")) multiplexer_9 (
    .in0(id_ex_1_shamt_in_2), .in1(a0_t[4:0]), .out(multiplexer_9_out), .sel(SLLV_O));
  Shifter #(.width(32)) shifter_1 (.in(id_ex_1_eimm_out), .\dist (5'b00010), .out(shifter_1_out));
  and and_5 (and_5_out, Equal, Syscall);
  and and_6 (and_6_out, id_ex_1_bne_out, ~mips_alu_1_equal);  // AND_Gate
  Adder #(.width(32)) adder_2 (.a(shifter_1_out), .b(EX_PC2), .out(adder_2_out));  // open: cin, cout
  // Probe on adder_2_out
  Register #(.width(32), .Select("low")) register_1 (.D(a0_t), .en(and_5_out), .Q(LedData), .clk(CLK), .clr(RST));
  or or_6 (nop, Branch, JR, JMP);
  Comparator #(.width(32)) comparator_3 (.a(32'h1), .b(mips_alu_1_result), .eq(comparator_3_eq));  // open: gt, lt
  or or_7 (or_7_out, comparator_3_eq, mips_alu_1_equal);
  and and_7 (and_7_out, ~Equal, Syscall);  // AND_Gate
  and and_8 (and_8_out, BLEZ_O, or_7_out);
  EX_MEM ex_mem_1 (
    .MemtoReg_in(id_ex_1_memtogeg_out), .AluResult_in(mips_alu_1_result),
    .MemWrite_int(id_ex_1_memwrite_out), .R2_in(id_ex_1_r2_out), .RegWtire_in(EX_RegWrite), .PCr_in(EX_PC),
    .JAL_in(id_ex_1_jal_out), .RegDst_in(id_ex_1_regdst_out), .IR_in(EX_IR), .syscall_in(Syscall),
    .PC_in(EX_PC2), .halt_in(and_7_out), .MemtoReg_out(ex_mem_1_memtoreg_out),
    .AluResult_out(ex_mem_1_aluresult_out), .MemWrite_out(MemWrite), .R2_out(MDin),
    .RegWtire_out(MEM_RegWrite), .PCr_out(M_PC), .JAL_out(ex_mem_1_jal_out),
    .RegDst_out(ex_mem_1_regdst_out), .IR_out(MEM_IR), .syscall_out(ex_mem_1_syscall_out), .PC_out(MEM_PC2),
    .halt_out(ex_mem_1_halt_out), .Reset(RST), .CLK(CLK), .Enable(run), .W__in(EX_WriteReg_num),
    .W__IN_2(MEM_WriteReg_num), .LBU_in(LBU_O), .LBU_out(LBU_M));
  Counter #(.width(16), .max('hffff), .behavior("old")) counter_4 (
    .count(JMP), .Q(\无条件分支数 ), .clk(CLK), .clr(RST));  // open: load, D, carry, preset
  Counter #(.width(16), .max('hffff), .behavior("old")) counter_5 (
    .count(Branch), .Q(\条件分支成功数 ), .clk(CLK), .clr(RST));  // open: load, D, carry, preset
  RAM #(.addrWidth(10), .dataWidth(32), .bus("separate"), .Select("high")) ram_1 (
    .addr(ex_mem_1_aluresult_out[11:2]), .din(MDin), .data(ram_1_data), .str(MemWrite), .clk(CLK), .clr(RST));  // open: sel, ld
  Multiplexer #(.select(2), .width(8), .enable("false")) multiplexer_10 (
    .in0(ram_1_data[7:0]), .in1(ram_1_data[15:8]), .in2(ram_1_data[23:16]), .in3(ram_1_data[31:24]),
    .out(multiplexer_10_out), .sel(ex_mem_1_aluresult_out[1:0]));
  MEM_WB mem_wb_1 (
    .AluResult_in(ex_mem_1_aluresult_out), .MemtoReg_in(ex_mem_1_memtoreg_out), .MemD_in(multiplexer_11_out),
    .RegWtire_in(MEM_RegWrite), .PCr_in(M_PC), .JAL_in(ex_mem_1_jal_out), .RegDst_in(ex_mem_1_regdst_out),
    .IR_in(MEM_IR), .syscall_in(ex_mem_1_syscall_out), .PC_in(MEM_PC2), .halt_in(ex_mem_1_halt_out),
    .AluResult_out(mem_wb_1_aluresult_out), .MemtoReg_out(MemtoReg), .MemD_out(mem_wb_1_memd_out),
    .RegWtire_out(RegWrite), .PCr_out(WB_PC), .JAL_out(JAL), .RegDst_out(RegDst), .IR_out(WB_IR),
    .syscall_out(sys), .PC_out(mem_wb_1_pc_out), .halt_out(mem_wb_1_halt_out), .Reset(RST), .CLK(CLK),
    .Enable(run), .W__in(MEM_WriteReg_num), .LBU_in(LBU_M), .LBU_out(LBU_W));  // open: W__IN_2, go
  Multiplexer #(.width(32), .enable("false")) multiplexer_11 (
    .in0(ram_1_data), .in1(bit_extender_3_out), .out(multiplexer_11_out), .sel(LBU_M));
  assign bit_extender_3_out = {{24{1'b0}}, multiplexer_10_out};  // Bit_Extender bit_extender_3
  not not_1 (run, mem_wb_1_halt_out);
  Multiplexer #(.width(32), .enable("false")) multiplexer_12 (
    .in0(mem_wb_1_aluresult_out), .in1(mem_wb_1_memd_out), .out(multiplexer_12_out), .sel(MemtoReg));
  Multiplexer #(.width(5), .enable("false")) multiplexer_13 (
    .in0(WB_IR[20:16]), .in1(WB_IR[15:11]), .out(multiplexer_13_out), .sel(RegDst));
  // Probe on multiplexer_14_out
  Multiplexer #(.width(5), .enable("false")) multiplexer_14 (
    .in0(multiplexer_13_out), .in1({5{1'b1}}), .out(multiplexer_14_out), .sel(JAL));
  assign bit_extender_4_out = {{24{1'b0}}, multiplexer_15_out};  // Bit_Extender bit_extender_4
  Multiplexer #(.select(2), .width(8), .enable("false")) multiplexer_15 (
    .in0(undriven_2[7:0]), .in1(undriven_2[15:8]), .in2(undriven_2[23:16]), .in3(undriven_2[31:24]),
    .out(multiplexer_15_out), .sel(undriven));
  Multiplexer #(.width(32), .enable("false")) multiplexer_16 (
    .in1(bit_extender_4_out), .out(multiplexer_16_out), .sel(LBU_W));  // open: in0
  Multiplexer #(.width(32), .enable("false")) multiplexer_17 (
    .in0(multiplexer_12_out), .in1(mem_wb_1_pc_out), .out(RDin), .sel(JAL));

  // Other names for the same wires on the sheet: ID_IR[5:0] = Func; OP[5:0] = ID_IR[31:26]; MEM_PC[31:0] = M_PC

  // Notes on the sheet:
  //   中断源
  //   时空图监测，可删除
  //   中断等待指示
  //   数码管输出
  //   指令字
  //   contents of rom_1 (hex, n*v repeats v):
  //   20110001 8000c05 20110001 20120002 20130003 8000c09 20110001 20120002 20130003 8000c0d 20110001
  //   20120002 20130003 8000c11 20110001 20120002 20130003 c000cf6 20100001 20110001 118fc0 112020
  //   20020022 c 118882 12200001 8000c15 112020 20020022 c 20110001 118880 112020 20020022 c 12200001
  //   8000c1f 20110001 118fc0 112020 20020022 c 1188c3 112020 20020022 c 118903 112020 20020022 c 118903
  //   112020 20020022 c 118903 112020 20020022 c 118903 112020 20020022 c 118903 112020 20020022 c 118903
  //   112020 20020022 c 118903 112020 20020022 c 20100001 109fc0 139fc3 8021 2012000c 24160003 26100001
  //   3210000f 20080008 20090001 139900 2709825 132020 20020022 c 1094022 1500fff9 22100001 2018000f
  //   2188024 108700 20080008 20090001 139902 2709825 132021 20020022 c 1094022 1500fff9 108702 2c9b022
  //   12c00001 8000c50 4020 1084027 84400 3508ffff 82021 20020022 c 2010ffff 20110000 ae300000 22100001
  //   22310004 ae300000 22100001 22310004 ae300000 22100001 22310004 ae300000 22100001 22310004 ae300000
  //   22100001 22310004 ae300000 22100001 22310004 ae300000 22100001 22310004 ae300000 22100001 22310004
  //   ae300000 22100001 22310004 ae300000 22100001 22310004 ae300000 22100001 22310004 ae300000 22100001
  //   22310004 ae300000 22100001 22310004 ae300000 22100001 22310004 ae300000 22100001 22310004 ae300000
  //   22100001 22310004 22100001 8020 2011003c 8e130000 8e340000 274402a 11000002 ae330000 ae140000
  //   2231fffc 1611fff8 102020 20020022 c 22100004 2011003c 1611fff2 20020032 c 20080001 20090003 20110876
  //   112020 20020022 c 200b0008 1118804 1318804 112020 20020022 c 216bffff 1560fff9 2002000a c 2008ffff
  //   20117777 112020 20020022 c 200b0010 3a31ffff 112020 20020022 c 216bffff 1560fffa 2002000a c 20090000
  //   200b0010 34118483 20120404 118c00 129400 36318281 22520404 ad310000 2328820 21290004 216bffff
  //   1560fffb 200b0020 20090000 91310000 112020 20020022 c 21290001 216bffff 1560fff9 2002000a c 2011fff1
  //   112020 20020022 c 22310001 1a20fffb 2002000a c 20100000 22100001 102020 20020022 c 22100002 102020
  //   20020022 c 22100003 102020 20020022 c 22100004 102020 20020022 c 22100005 102020 20020022 c 22100006
  //   102020 20020022 c 22100007 102020 20020022 c 22100008 102020 20020022 20020022 c 3e00008
  //   OP
  //   Func
  //   rs
  //   rt
  //   rd
  //   shamt
  //   imm16
  //   控制位
  //   (PC+4)U4+imm26<<2
  //   流水调试日志用
  //   暂停节拍，不能为0
  //   Beq
  //   JMP
  //   JR
  //   Bne
  //   OP
  //   JAL
  //   Func
  //   Syscall
  //   戳工具置1进入计数暂停模式，ctrl+k时钟自动运行到对应节拍暂停
  //   ctrl+k关闭时钟连续运行，将控制位置零，进入单步调试模式调试
  //   MemToReg
  //   MemWrite
  //   AluOP
  //   AluSrcB
  //   RegWrite
  //   RegDst
  //   可计数暂停的时钟源
  //   为方便自动评测，需要输出流水线各段保存的PC值，注意是PC不是PC+4，另外ID段寄存器写入信息，Mem段内存写入信息也要输出
  //   rt
  //   rd
endmodule
module \重定向流水线  (
  output RegWrite,
  output MemWrite,
  output [31:0] IF_PC,
  output [31:0] ID_PC,
  output [31:0] EX_PC,
  output [31:0] M_PC,
  output [31:0] WB_PC,
  output [31:0] RDin,
  output [31:0] MDin,
  output [31:0] LedData
);

  wire and_1_out, and_2_out, and_3_out, and_4_out, and_5_out, and_6_out, and_7_out, and_8_out, BLEZ_EX,
       Branch, CLK, clock_2_out, comparator_1_eq, comparator_1_lt, comparator_2_eq, d_ff_1_q, Equal,
       ex_mem_1_halt_out, ex_mem_1_jal_out, ex_mem_1_memtoreg_out, ex_mem_1_regdst_out, ex_mem_1_syscall_out,
       EX_RegWrite, Go, id_ex_1_alusrcb_out, id_ex_1_beq_out, id_ex_1_bne_out, id_ex_1_halt_out,
       id_ex_1_jal_out, id_ex_1_memtogeg_out, id_ex_1_memwrite_out, id_ex_1_regdst_out, ID_RegDst, IR1, IR2,
       IR3, JAL, JMP, JR, LBU_EX, LBU_M, LBU_W, LoadUse, MEM_RegWrite, mem_wb_1_halt_out, MemtoReg,
       mips_alu_1_equal, nand_1_out, nop, or_1_out, or_2_out, or_4_out, or_5_out, or_8_out, RegDst, RST, run,
       SignedExt, SLLV_EX, sys, Syscall, undriven, W1, W2, W3, \单周期硬布线控制器_1_alu_src , \单周期硬布线控制器_1_beq ,
       \单周期硬布线控制器_1_blez , \单周期硬布线控制器_1_bne , \单周期硬布线控制器_1_jal , \单周期硬布线控制器_1_jmp , \单周期硬布线控制器_1_jr ,
       \单周期硬布线控制器_1_lbu , \单周期硬布线控制器_1_memtoreg , \单周期硬布线控制器_1_memwrite , \单周期硬布线控制器_1_regwrite ,
       \单周期硬布线控制器_1_sllv , \单周期硬布线控制器_1_syscall , \重定向数据相关检测_1_loaduse ;
  wire [1:0] R1_Forward, R2_Forward, undriven_3, \重定向数据相关检测_1_r1_forward , \重定向数据相关检测_1_r2_forward ;
  wire [3:0] id_ex_1_aluop_out, \单周期硬布线控制器_1_alu_op ;
  wire [4:0] EX_WriteReg_num, id_ex_1_shamt_in_2, ID_R1_num, ID_R2_num, MEM_WriteReg_num, multiplexer_2_out,
       multiplexer_5_out, multiplexer_11_out, multiplexer_15_out, multiplexer_16_out;
  wire [5:0] ID_Func;
  wire [7:0] multiplexer_12_out, multiplexer_17_out, ram_1_data, ram_1_data_2, ram_1_data_3, ram_1_data_4;
  wire [12:0] CNT_num;
  wire [15:0] adder_3_out, \LoadUse次数 , multiplier_1_out, \总周期数 , \插入气泡数 , \无条件分支数 , \条件分支成功数 ;
  wire [31:0] a0, adder_1_out, adder_2_out, bit_extender_1_out, bit_extender_2_out, bit_extender_3_out,
       bit_extender_4_out, EX_IR, EX_PC2, id_ex_1_address_out, id_ex_1_eimm_out, id_ex_1_r1_out,
       id_ex_1_r2_out, ID_PC2, IF_IR, MEM_Alu, MEM_IR, MEM_PC2, mem_wb_1_pc_out, mips_alu_1_result,
       mips_regifile_1_r1, mips_regifile_1_r2, multiplexer_1_out, multiplexer_6_out, multiplexer_8_out,
       multiplexer_9_out, multiplexer_10_out, multiplexer_13_out, multiplexer_14_out, shifter_1_out,
       undriven_2, WB_Alu, WB_IR, WB_MD;
  wire [31:6] ID_IR;

  Button \u_总复位  (.out(RST));
  Button _1 (.out(IR1));
  Button _2 (.out(IR2));
  Button _3 (.out(IR3));
  // Probe on \总周期数 
  // Probe on \总周期数 
  Button \u_继续运行  (.out(Go));
  LED led_1 (.in(W1));
  LED led_2 (.in(W2));
  LED led_3 (.in(W3));
  Hex_Digit_Display hex_digit_display_1 (.value(LedData[31:28]));  // open: dp
  // Probe on IF_PC[19:0]
  // Mips_Probe mips_probe_1: pin names not known; wires that end beside it: IF_IR
  Multiplexer #(.select(3), .width(32), .enable("false")) multiplexer_1 (
    .in0(adder_1_out), .in1({32{1'b0}}), .in2(id_ex_1_address_out), .in3(id_ex_1_r1_out), .in4(adder_2_out),
    .in5({32{1'b0}}), .in6({32{1'b0}}), .in7({32{1'b0}}), .out(multiplexer_1_out), .sel({Branch, JMP, JR}));
  or or_1 (or_1_out, run, Go);
  Hex_Digit_Display hex_digit_display_2 (.value(LedData[27:24]));  // open: dp
  Hex_Digit_Display hex_digit_display_3 (.value(LedData[23:20]));  // open: dp
  // Probe on ID_PC[19:0]
  // Mips_Probe mips_probe_2: pin names not known; wires that end beside it: {ID_IR, ID_Func}
  Register #(.width(32), .Select("low")) PC (.D(multiplexer_1_out), .en(and_1_out), .Q(IF_PC), .clk(CLK), .clr(RST));
  and and_1 (and_1_out, or_1_out, ~LoadUse);  // AND_Gate
  Hex_Digit_Display hex_digit_display_4 (.value(LedData[15:12]));  // open: dp
  Hex_Digit_Display hex_digit_display_5 (.value(LedData[19:16]));  // open: dp
  // Probe on IF_PC
  Hex_Digit_Display hex_digit_display_6 (.value(LedData[7:4]));  // open: dp
  Hex_Digit_Display hex_digit_display_7 (.value(LedData[11:8]));  // open: dp
  Clock clock_1 (.out(CLK));
  // Probe on EX_PC[19:0]
  // Mips_Probe mips_probe_3: pin names not known; wires that end beside it: EX_IR
  // Probe on ID_PC
  Adder #(.width(32)) adder_1 (.a(IF_PC), .b(32'h4), .out(adder_1_out));  // open: cin, cout
  Hex_Digit_Display hex_digit_display_8 (.value(LedData[3:0]));  // open: dp
  // Probe on EX_PC
  ROM #(.addrWidth(10), .dataWidth(32), .Select("high")) rom_1 (.addr(IF_PC[11:2]), .data(IF_IR));
  and and_2 (and_2_out, ~LoadUse, run);  // AND_Gate
  // Probe on \总周期数 
  // Probe on M_PC[19:0]
  // Mips_Probe mips_probe_4: pin names not known; wires that end beside it: MEM_IR
  // Probe on M_PC
  \重定向数据相关检测  \u_重定向数据相关检测_1  (
    .ID_OP(ID_IR[31:26]), .ID_FUNC(ID_Func), .ID_R1_num(ID_R1_num), .ID_R2_num(ID_R2_num),
    .EX_WriteReg_num(EX_WriteReg_num), .MEM_WriteReg_num(MEM_WriteReg_num), .EX_RegWrite(EX_RegWrite),
    .MEM_RegWrite(MEM_RegWrite), .EX_OP(EX_IR[31:26]), .MEM_OP(MEM_IR[31:26]),
    .LoadUse(\重定向数据相关检测_1_loaduse ), .R1_Forward(\重定向数据相关检测_1_r1_forward ),
    .R2_Forward(\重定向数据相关检测_1_r2_forward ));
  or or_2 (or_2_out, RST, nop);
  IF_ID if_id_1 (
    .ir_in(IF_IR), .pcr_in(IF_PC), .pc_in(adder_1_out), .ir_out({ID_IR, ID_Func}), .pcr_out(ID_PC),
    .pc_out(ID_PC2), .Reset(or_2_out), .CLK(CLK), .Enable(and_2_out));
  // Probe on \总周期数 
  // Probe on \无条件分支数 
  // Probe on \条件分支成功数 
  // Probe on \插入气泡数 
  // Probe on \LoadUse次数 
  // Probe on WB_PC
  // Probe on IF_PC[11:0]
  // Probe on WB_PC[19:0]
  // Mips_Probe mips_probe_5: pin names not known; wires that end beside it: WB_IR
  Register #(.width(2), .Select("low")) register_1 (
    .D(\重定向数据相关检测_1_r1_forward ), .Q(R1_Forward), .clk(CLK), .clr(RST));  // open: en
  Register #(.width(2), .Select("low")) register_2 (
    .D(\重定向数据相关检测_1_r2_forward ), .Q(R2_Forward), .clk(CLK), .clr(RST));  // open: en
  // Probe on EX_PC[11:0]
  // Probe on ID_PC[11:0]
  Multiplexer #(.width(5), .enable("false")) multiplexer_2 (
    .in0(ID_IR[20:16]), .in1(ID_IR[15:11]), .out(multiplexer_2_out), .sel(ID_RegDst));
  assign bit_extender_1_out = {{16{1'b0}}, {ID_IR[15:6], ID_Func}};  // Bit_Extender bit_extender_1
  assign bit_extender_2_out = {{16{ID_IR[15]}}, {ID_IR[15:6], ID_Func}};  // Bit_Extender bit_extender_2
  // Probe on M_PC[11:0]
  D_Flip_Flop #(.trigger("high"), .Pre_Clr_Positions("LEGACY"), .enable("true"), .NewFFLayout("false")) d_ff_1 (.Q(d_ff_1_q));  // open: clk, D, Qn, preset, en, reset
  // Probe on 13'h340
  or or_3 (LoadUse, LBU_M, LBU_EX, \重定向数据相关检测_1_loaduse );
  \单周期硬布线控制器  \u_单周期硬布线控制器_1  (
    .Func(ID_Func), .OP(ID_IR[31:26]), .ALU_OP(\单周期硬布线控制器_1_alu_op ), .MemToReg(\单周期硬布线控制器_1_memtoreg ),
    .MemWrite(\单周期硬布线控制器_1_memwrite ), .ALU_SRC(\单周期硬布线控制器_1_alu_src ), .RegWrite(\单周期硬布线控制器_1_regwrite ),
    .SysCALL(\单周期硬布线控制器_1_syscall ), .SignedExt(SignedExt), .RegDst(ID_RegDst), .JR(\单周期硬布线控制器_1_jr ),
    .JMP(\单周期硬布线控制器_1_jmp ), .Beq(\单周期硬布线控制器_1_beq ), .JAL(\单周期硬布线控制器_1_jal ), .Bne(\单周期硬布线控制器_1_bne ),
    .SLLV(\单周期硬布线控制器_1_sllv ), .BLEZ(\单周期硬布线控制器_1_blez ), .LBU(\单周期硬布线控制器_1_lbu ));  // open: ERET, MFC0, MTC0, MF
  Multiplexer #(.width(5), .enable("false")) multiplexer_3 (
    .in0(ID_IR[25:21]), .in1(5'b00100), .out(ID_R1_num), .sel(\单周期硬布线控制器_1_syscall ));
  Multiplexer #(.width(5), .enable("false")) multiplexer_4 (
    .in0(ID_IR[20:16]), .in1(5'b00010), .out(ID_R2_num), .sel(\单周期硬布线控制器_1_syscall ));
  Multiplexer #(.width(5), .enable("false")) multiplexer_5 (
    .in0(multiplexer_2_out), .in1({5{1'b1}}), .out(multiplexer_5_out), .sel(\单周期硬布线控制器_1_jal ));
  Multiplexer #(.width(32), .enable("false")) multiplexer_6 (
    .in0(bit_extender_1_out), .in1(bit_extender_2_out), .out(multiplexer_6_out), .sel(SignedExt));
  // Probe on WB_PC[11:0]
  Comparator #(.width(13)) comparator_1 (
    .a(CNT_num), .b(13'h340), .eq(comparator_1_eq), .lt(comparator_1_lt));  // open: gt
  Clock clock_2 (.out(clock_2_out));
  // Probe on multiplexer_6_out
  nand nand_1 (nand_1_out, d_ff_1_q, comparator_1_eq);
  Counter #(.width(13), .max('h1fff), .ongoal("stay"), .behavior("old")) counter_1 (
    .count(comparator_1_lt), .Q(CNT_num), .clk(clock_2_out), .clr(RST));  // open: load, D, carry, preset
  MIPS_Regifile mips_regifile_1 (
    .Din(RDin), .Clk(CLK), .R1(mips_regifile_1_r1), .R2(mips_regifile_1_r2), .WE(RegWrite),
    .W_num(multiplexer_16_out), .R1_num(ID_R1_num), .R2_num(ID_R2_num));
  assign CLK = nand_1_out ? undriven : 1'bz;  // Controlled_Buffer controlled_buffer_1
  and and_3 (and_3_out, ~Equal, Syscall);  // AND_Gate
  Pull_Resistor #(.pull(1)) pull_resistor_1 (.node(CLK));
  or or_4 (or_4_out, RST, LoadUse, nop);
  ID_EX id_ex_1 (
    .jr_in(\单周期硬布线控制器_1_jr ), .R1_in(mips_regifile_1_r1), .Eimm_in(multiplexer_6_out),
    .jmp_in(\单周期硬布线控制器_1_jmp ), .beq_in(\单周期硬布线控制器_1_beq ), .R2_in(mips_regifile_1_r2),
    .bne_in(\单周期硬布线控制器_1_bne ), .Address_in({ID_PC2[31:28], ID_IR[25:6], ID_Func, 2'b00}),
    .memtogeg_in(\单周期硬布线控制器_1_memtoreg ), .memwrite_in(\单周期硬布线控制器_1_memwrite ), .pcr_in(ID_PC),
    .shamt_in(ID_IR[10:6]), .AluOp_in(\单周期硬布线控制器_1_alu_op ), .AluSrcB_in(\单周期硬布线控制器_1_alu_src ),
    .RegWrite_in(\单周期硬布线控制器_1_regwrite ), .pc_in(ID_PC2), .JAL_in(\单周期硬布线控制器_1_jal ), .RegDst_in(ID_RegDst),
    .ir_in({ID_IR, ID_Func}), .Eimm_out(id_ex_1_eimm_out), .R2_out(id_ex_1_r2_out),
    .Address_out(id_ex_1_address_out), .pcr_out(EX_PC), .shamt_in_2(id_ex_1_shamt_in_2), .pc_out(EX_PC2),
    .ir_out(EX_IR), .Rest(or_4_out), .CLK(CLK), .Enable(run), .halt_in(and_3_out),
    .syscall_in(\单周期硬布线控制器_1_syscall ), .jr_out(JR), .jmp_out(JMP), .beq_out(id_ex_1_beq_out),
    .bne_out(id_ex_1_bne_out), .memtogeg_out(id_ex_1_memtogeg_out), .memwrite_out(id_ex_1_memwrite_out),
    .AluOp_out(id_ex_1_aluop_out), .AluSrcB_out(id_ex_1_alusrcb_out), .RegWrite_out(EX_RegWrite),
    .JAL_out(id_ex_1_jal_out), .RegDst_out(id_ex_1_regdst_out), .halt_out(id_ex_1_halt_out),
    .syscall_out(Syscall), .R1_out(id_ex_1_r1_out), .W__in(multiplexer_5_out), .W__IN_2(EX_WriteReg_num),
    .SLLV_in(\单周期硬布线控制器_1_sllv ), .SLLV_out(SLLV_EX), .BLEZ_in(\单周期硬布线控制器_1_blez ), .BLEZ_out(BLEZ_EX),
    .LBU_in(\单周期硬布线控制器_1_lbu ), .LBU_out(LBU_EX));
  or or_5 (or_5_out, run, Go);
  and and_4 (and_4_out, LoadUse, run);
  Counter #(.width(16), .max('hffff), .behavior("old")) counter_2 (
    .count(or_5_out), .Q(\总周期数 ), .clk(CLK), .clr(RST));  // open: load, D, carry, preset
  Counter #(.width(16), .max('hffff), .behavior("old")) counter_3 (
    .count(and_4_out), .Q(\LoadUse次数 ), .clk(CLK), .clr(RST));  // open: load, D, carry, preset
  Multiplexer #(.select(2), .width(32), .enable("false")) multiplexer_7 (
    .in0(id_ex_1_r1_out), .in1(WB_Alu), .in2(WB_MD), .in3(MEM_Alu), .out(a0), .sel(R1_Forward));
  Multiplexer #(.select(2), .width(32), .enable("false")) multiplexer_8 (
    .in0(id_ex_1_r2_out), .in1(WB_Alu), .in2(WB_MD), .in3(MEM_Alu), .out(multiplexer_8_out), .sel(R2_Forward));
  // Probe on EX_PC2
  or or_6 (Branch, and_5_out, and_7_out, and_8_out);
  and and_5 (and_5_out, id_ex_1_beq_out, mips_alu_1_equal);
  Multiplexer #(.width(32), .enable("false")) multiplexer_9 (
    .in0(multiplexer_8_out), .in1(id_ex_1_eimm_out), .out(multiplexer_9_out), .sel(id_ex_1_alusrcb_out));
  Multiplexer #(.width(32), .enable("false")) multiplexer_10 (
    .in0(multiplexer_9_out), .in1({32{1'b0}}), .out(multiplexer_10_out), .sel(BLEZ_EX));
  Shifter #(.width(32)) shifter_1 (.in(id_ex_1_eimm_out), .\dist (5'b00010), .out(shifter_1_out));
  and and_6 (and_6_out, Equal, Syscall);
  and and_7 (and_7_out, id_ex_1_bne_out, ~mips_alu_1_equal);  // AND_Gate
  // Probe on R1_Forward
  MIPS_ALU mips_alu_1 (
    .X(a0), .Y(multiplexer_10_out), .AluOP(id_ex_1_aluop_out), .Equal(mips_alu_1_equal),
    .Result(mips_alu_1_result), .shamt(multiplexer_11_out));  // open: Result_2
  Multiplexer #(.width(5), .enable("false")) multiplexer_11 (
    .in0(id_ex_1_shamt_in_2), .in1(a0[4:0]), .out(multiplexer_11_out), .sel(SLLV_EX));
  Adder #(.width(32)) adder_2 (.a(shifter_1_out), .b(EX_PC2), .out(adder_2_out));  // open: cin, cout
  // Probe on adder_2_out
  Register #(.width(32), .Select("low")) register_3 (.D(a0), .en(and_6_out), .Q(LedData), .clk(CLK), .clr(RST));
  or or_7 (nop, Branch, JR, JMP);
  Comparator #(.width(32)) comparator_2 (.a(32'h1), .b(mips_alu_1_result), .eq(comparator_2_eq));  // open: gt, lt
  or or_8 (or_8_out, comparator_2_eq, mips_alu_1_equal);
  Comparator #(.width(32)) comparator_3 (.a(multiplexer_10_out), .b(32'h22), .eq(Equal));  // open: gt, lt
  and and_8 (and_8_out, BLEZ_EX, or_8_out);
  EX_MEM ex_mem_1 (
    .MemtoReg_in(id_ex_1_memtogeg_out), .AluResult_in(mips_alu_1_result),
    .MemWrite_int(id_ex_1_memwrite_out), .R2_in(multiplexer_8_out), .RegWtire_in(EX_RegWrite),
    .PCr_in(EX_PC), .JAL_in(id_ex_1_jal_out), .RegDst_in(id_ex_1_regdst_out), .IR_in(EX_IR),
    .syscall_in(Syscall), .PC_in(EX_PC2), .halt_in(id_ex_1_halt_out), .MemtoReg_out(ex_mem_1_memtoreg_out),
    .AluResult_out(MEM_Alu), .MemWrite_out(MemWrite), .R2_out(MDin), .RegWtire_out(MEM_RegWrite),
    .PCr_out(M_PC), .JAL_out(ex_mem_1_jal_out), .RegDst_out(ex_mem_1_regdst_out), .IR_out(MEM_IR),
    .syscall_out(ex_mem_1_syscall_out), .PC_out(MEM_PC2), .halt_out(ex_mem_1_halt_out), .Reset(RST),
    .CLK(CLK), .Enable(run), .W__in(EX_WriteReg_num), .W__IN_2(MEM_WriteReg_num), .LBU_in(LBU_EX),
    .LBU_out(LBU_M));
  Counter #(.width(16), .max('hffff), .behavior("old")) counter_4 (
    .count(JMP), .Q(\无条件分支数 ), .clk(CLK), .clr(RST));  // open: load, D, carry, preset
  Adder #(.width(16)) adder_3 (.a(\无条件分支数 ), .b(\条件分支成功数 ), .out(adder_3_out));  // open: cin, cout
  Multiplier #(.width(16)) multiplier_1 (.a(adder_3_out), .b(16'h2), .out(multiplier_1_out));  // open: cin, cout
  Counter #(.width(16), .max('hffff), .behavior("old")) counter_5 (
    .count(Branch), .Q(\条件分支成功数 ), .clk(CLK), .clr(RST));  // open: load, D, carry, preset
  Adder #(.width(16)) adder_4 (.a(multiplier_1_out), .b(\LoadUse次数 ), .out(\插入气泡数 ));  // open: cin, cout
  RAM #(.addrWidth(10), .dataWidth(32), .bus("separate"), .Select("high")) ram_1 (
    .addr(MEM_Alu[11:2]), .din(MDin), .data({ram_1_data_4, ram_1_data_3, ram_1_data_2, ram_1_data}),
    .str(MemWrite), .clk(CLK), .clr(RST));  // open: sel, ld
  Multiplexer #(.select(2), .width(8), .enable("false")) multiplexer_12 (
    .in0(ram_1_data), .in1(ram_1_data_2), .in2(ram_1_data_3), .in3(ram_1_data_4), .out(multiplexer_12_out),
    .sel(MEM_Alu[1:0]));
  assign bit_extender_3_out = {{24{1'b0}}, multiplexer_12_out};  // Bit_Extender bit_extender_3
  MEM_WB mem_wb_1 (
    .AluResult_in(MEM_Alu), .MemtoReg_in(ex_mem_1_memtoreg_out), .MemD_in(multiplexer_13_out),
    .RegWtire_in(MEM_RegWrite), .PCr_in(M_PC), .JAL_in(ex_mem_1_jal_out), .RegDst_in(ex_mem_1_regdst_out),
    .IR_in(MEM_IR), .syscall_in(ex_mem_1_syscall_out), .PC_in(MEM_PC2), .halt_in(ex_mem_1_halt_out),
    .AluResult_out(WB_Alu), .MemtoReg_out(MemtoReg), .MemD_out(WB_MD), .RegWtire_out(RegWrite),
    .PCr_out(WB_PC), .JAL_out(JAL), .RegDst_out(RegDst), .IR_out(WB_IR), .syscall_out(sys),
    .PC_out(mem_wb_1_pc_out), .halt_out(mem_wb_1_halt_out), .Reset(RST), .CLK(CLK), .Enable(run),
    .W__in(MEM_WriteReg_num), .LBU_in(LBU_M), .LBU_out(LBU_W), .go(Go));  // open: W__IN_2
  Multiplexer #(.width(32), .enable("false")) multiplexer_13 (
    .in0({ram_1_data_4, ram_1_data_3, ram_1_data_2, ram_1_data}), .in1(bit_extender_3_out),
    .out(multiplexer_13_out), .sel(LBU_M));
  not not_1 (run, mem_wb_1_halt_out);
  Multiplexer #(.width(32), .enable("false")) multiplexer_14 (
    .in0(WB_Alu), .in1(WB_MD), .out(multiplexer_14_out), .sel(MemtoReg));
  Multiplexer #(.width(5), .enable("false")) multiplexer_15 (
    .in0(WB_IR[20:16]), .in1(WB_IR[15:11]), .out(multiplexer_15_out), .sel(RegDst));
  Multiplexer #(.width(5), .enable("false")) multiplexer_16 (
    .in0(multiplexer_15_out), .in1({5{1'b1}}), .out(multiplexer_16_out), .sel(JAL));
  assign bit_extender_4_out = {{24{1'b0}}, multiplexer_17_out};  // Bit_Extender bit_extender_4
  Multiplexer #(.select(2), .width(8), .enable("false")) multiplexer_17 (
    .in0(undriven_2[7:0]), .in1(undriven_2[15:8]), .in2(undriven_2[23:16]), .in3(undriven_2[31:24]),
    .out(multiplexer_17_out), .sel(undriven_3));
  Multiplexer #(.width(32), .enable("false")) multiplexer_18 (
    .in0(undriven_2), .in1(bit_extender_4_out), .sel(LBU_W));  // open: out
  Multiplexer #(.width(32), .enable("false")) multiplexer_19 (
    .in0(multiplexer_14_out), .in1(mem_wb_1_pc_out), .out(RDin), .sel(JAL));

  // Other names for the same wires on the sheet: ID_IR[5:0] = ID_Func; EX_OP[5:0] = EX_IR[31:26];
  //   ID_OP[5:0] = ID_IR[31:26]; MEM_OP[5:0] = MEM_IR[31:26]; MEM_PC[31:0] = M_PC

  // Notes on the sheet:
  //   中断源
  //   时空图监测，可删除
  //   中断等待指示
  //   数码管输出
  //   指令字
  //   contents of rom_1 (hex, n*v repeats v):
  //   20110001 8000c05 20110001 20120002 20130003 8000c09 20110001 20120002 20130003 8000c0d 20110001
  //   20120002 20130003 8000c11 20110001 20120002 20130003 c000cf6 20100001 20110001 118fc0 112020
  //   20020022 c 118882 12200001 8000c15 112020 20020022 c 20110001 118880 112020 20020022 c 12200001
  //   8000c1f 20110001 118fc0 112020 20020022 c 1188c3 112020 20020022 c 118903 112020 20020022 c 118903
  //   112020 20020022 c 118903 112020 20020022 c 118903 112020 20020022 c 118903 112020 20020022 c 118903
  //   112020 20020022 c 118903 112020 20020022 c 20100001 109fc0 139fc3 8021 2012000c 24160003 26100001
  //   3210000f 20080008 20090001 139900 2709825 132020 20020022 c 1094022 1500fff9 22100001 2018000f
  //   2188024 108700 20080008 20090001 139902 2709825 132021 20020022 c 1094022 1500fff9 108702 2c9b022
  //   12c00001 8000c50 4020 1084027 84400 3508ffff 82021 20020022 c 2010ffff 20110000 ae300000 22100001
  //   22310004 ae300000 22100001 22310004 ae300000 22100001 22310004 ae300000 22100001 22310004 ae300000
  //   22100001 22310004 ae300000 22100001 22310004 ae300000 22100001 22310004 ae300000 22100001 22310004
  //   ae300000 22100001 22310004 ae300000 22100001 22310004 ae300000 22100001 22310004 ae300000 22100001
  //   22310004 ae300000 22100001 22310004 ae300000 22100001 22310004 ae300000 22100001 22310004 ae300000
  //   22100001 22310004 22100001 8020 2011003c 8e130000 8e340000 274402a 11000002 ae330000 ae140000
  //   2231fffc 1611fff8 102020 20020022 c 22100004 2011003c 1611fff2 20020032 c 20080001 20090003 20110876
  //   112020 20020022 c 200b0008 1118804 1318804 112020 20020022 c 216bffff 1560fff9 20020032 c 2008ffff
  //   20117777 112020 20020022 c 200b0010 3a31ffff 112020 20020022 c 216bffff 1560fffa 20020032 c 20090000
  //   200b0010 34118483 20120404 118c00 129400 36318281 22520404 ad310000 2328820 21290004 216bffff
  //   1560fffb 200b0020 20090000 91310000 112020 20020022 c 21290001 216bffff 1560fff9 20020032 c 2011fff1
  //   112020 20020022 c 22310001 1a20fffb 20020032 c 20100000 22100001 102020 20020022 c 22100002 102020
  //   20020022 c 22100003 102020 20020022 c 22100004 102020 20020022 c 22100005 102020 20020022 c 22100006
  //   102020 20020022 c 22100007 102020 20020022 c 22100008 102020 20020022 20020022 c 3e00008
  //   OP
  //   Func
  //   rs
  //   rt
  //   rd
  //   shamt
  //   imm16
  //   控制位
  //   (PC+4)U4+imm26<<2
  //   流水调试日志用
  //   暂停节拍，不能为0
  //   Beq
  //   JMP
  //   JR
  //   Bne
  //   OP
  //   JAL
  //   Func
  //   Syscall
  //   戳工具置1进入计数暂停模式，ctrl+k时钟自动运行到对应节拍暂停
  //   ctrl+k关闭时钟连续运行，将控制位置零，进入单步调试模式调试
  //   MemToReg
  //   MemWrite
  //   AluOP
  //   AluSrcB
  //   RegWrite
  //   RegDst
  //   可计数暂停的时钟源
  //   为方便自动评测，需要输出流水线各段保存的PC值，注意是PC不是PC+4，另外ID段寄存器写入信息，Mem段内存写入信息也要输出
  //   rt
  //   rd
endmodule

module \中断按键参考电路  (
  input  \同步清零信号 ,
  output \与中断屏蔽位与 
);

  wire \_1号中断_out , and_1_out, clock_1_out, d_ff_1_q, or_1_out, or_2_out;

  Clock clock_1 (.out(clock_1_out));
  Button \_1号中断  (.out(\_1号中断_out ));
  LED \_1号中断等待指示灯  (.in(or_1_out));
  or or_1 (or_1_out, \与中断屏蔽位与 , d_ff_1_q);
  D_Flip_Flop #(.Pre_Clr_Positions("LEGACY"), .enable("true"), .NewFFLayout("false")) d_ff_1 (
    .clk(\_1号中断_out ), .D(1'b1), .Q(d_ff_1_q), .reset(\与中断屏蔽位与 ));  // open: Qn, preset, en
  or or_2 (or_2_out, d_ff_1_q, \与中断屏蔽位与 );
  and and_1 (and_1_out, or_2_out, ~\同步清零信号 );  // AND_Gate
  D_Flip_Flop #(.Pre_Clr_Positions("LEGACY"), .enable("true"), .NewFFLayout("false")) IR1 (
    .clk(clock_1_out), .D(and_1_out), .Q(\与中断屏蔽位与 ));  // open: Qn, preset, en, reset

  // Notes on the sheet:
  //   中断信号采样参考电路
  //   Reset 
endmodule

module \单周期MIPS_单级中断  (
  input  IR1,
  input  IR2,
  input  IR3,
  output RegWrite,
  output MemWrite,
  output [31:0] PC,
  output [31:0] IR,
  output [31:0] RDin,
  output [31:0] MDin,
  output [31:0] LedData
);

  wire and_1_out, and_2_out, and_3_out, and_4_out, and_5_out, and_6_out, and_7_out, and_8_out, and_9_out,
       and_10_out, BLEZ, Branch, CLK, comparator_1_eq, comparator_2_eq, comparator_3_eq, comparator_4_eq,
       comparator_5_eq, comparator_6_eq, controlled_inverter_1_out, controlled_inverter_2_out,
       controlled_inverter_3_out, d_ff_1_q, d_ff_2_q, d_ff_3_q, ERET, Go, halt, IR1_q, IR1_t, IR2_q, IR2_t,
       IR3_q, IR3_t, IRA, IRB, IRC, JAL, LBU, LedOut, mips_alu_1_equal, multiplexer_4_out, not_1_out,
       not_2_out, or_4_out, or_5_out, or_6_out, or_7_out, or_8_out, or_12_out, or_13_out,
       priority_encoder_1_gs, RST, SignedExt, SLLV, Syscall, W1, W2, W3, \中断状态_q , \单周期硬布线控制器_1_alu_src ,
       \单周期硬布线控制器_1_beq , \单周期硬布线控制器_1_bne , \单周期硬布线控制器_1_jmp , \单周期硬布线控制器_1_jr , \单周期硬布线控制器_1_memtoreg ,
       \单周期硬布线控制器_1_regdst ;
  wire [1:0] IR_now, multiplexer_11_out, priority_encoder_1_out;
  wire [3:0] \单周期硬布线控制器_1_alu_op ;
  wire [4:0] mips_probe_1_p2, mips_regifile_1_r1, multiplexer_8_out, multiplexer_9_out, multiplexer_12_out,
       multiplexer_16_out;
  wire [7:0] multiplexer_18_out;
  wire [15:0] \总周期数 ;
  wire [27:0] adder_1_out;
  wire [31:0] adder_2_out, bit_extender_1_out, bit_extender_2_out, bit_extender_3_out, EPC_q,
       mips_alu_1_result, multiplexer_1_out, multiplexer_2_out, multiplexer_5_out, multiplexer_6_out,
       multiplexer_13_out, multiplexer_14_out, multiplexer_15_out, multiplexer_17_out, multiplexer_19_out,
       nextPC, PCout, ram_1_data, shifter_1_out;
  wire [31:5] mips_regifile_1_r1_2;
  wire [31:28] adder_1_out_2;

  Clock clock_1 (.out(CLK));
  Button _1 (.out(IRA));
  Button _2 (.out(IRB));
  Button _3 (.out(IRC));
  Button \u_继续运行  (.out(Go));
  LED led_1 (.in(W1));
  LED led_2 (.in(W2));
  LED led_3 (.in(W3));
  Hex_Digit_Display hex_digit_display_1 (.value(LedData[31:28]));  // open: dp
  Comparator #(.width(16)) comparator_1 (.a(16'h23b), .b(\总周期数 ), .eq(comparator_1_eq));  // open: gt, lt
  Comparator #(.width(16)) comparator_2 (.a(\总周期数 ), .b(16'h1), .eq(comparator_2_eq));  // open: gt, lt
  Comparator #(.width(16)) comparator_3 (.a(\总周期数 ), .b(16'h4), .eq(comparator_3_eq));  // open: gt, lt
  Comparator #(.width(16)) comparator_4 (.a(\总周期数 ), .b(16'h7), .eq(comparator_4_eq));  // open: gt, lt
  or or_1 (W1, IR1_q, d_ff_1_q);
  or or_2 (W2, IR2_q, d_ff_2_q);
  or or_3 (W3, IR3_q, d_ff_3_q);
  Hex_Digit_Display hex_digit_display_2 (.value(LedData[23:20]));  // open: dp
  Hex_Digit_Display hex_digit_display_3 (.value(LedData[27:24]));  // open: dp
  or or_4 (or_4_out, comparator_1_eq, comparator_2_eq);
  assign controlled_inverter_1_out = or_4_out ? ~CLK : 1'bz;  // Controlled_Inverter controlled_inverter_1
  assign controlled_inverter_2_out = comparator_3_eq ? ~CLK : 1'bz;  // Controlled_Inverter controlled_inverter_2
  assign controlled_inverter_3_out = comparator_4_eq ? ~CLK : 1'bz;  // Controlled_Inverter controlled_inverter_3
  D_Flip_Flop #(.Pre_Clr_Positions("LEGACY"), .enable("true"), .NewFFLayout("false")) d_ff_1 (
    .clk(IR1_t), .D(1'b1), .Q(d_ff_1_q), .reset(IR1_q));  // open: Qn, preset, en
  D_Flip_Flop #(.Pre_Clr_Positions("LEGACY"), .enable("true"), .NewFFLayout("false")) d_ff_2 (
    .clk(IR2_t), .D(1'b1), .Q(d_ff_2_q), .reset(IR2_q));  // open: Qn, preset, en
  D_Flip_Flop #(.Pre_Clr_Positions("LEGACY"), .enable("true"), .NewFFLayout("false")) d_ff_3 (
    .clk(IR3_t), .D(1'b1), .Q(d_ff_3_q), .reset(IR3_q));  // open: Qn, preset, en
  Hex_Digit_Display hex_digit_display_4 (.value(LedData[15:12]));  // open: dp
  Hex_Digit_Display hex_digit_display_5 (.value(LedData[19:16]));  // open: dp
  Pull_Resistor pull_resistor_1 (.node(controlled_inverter_1_out));
  Pull_Resistor pull_resistor_2 (.node(controlled_inverter_2_out));
  Pull_Resistor pull_resistor_3 (.node(controlled_inverter_3_out));
  or or_5 (or_5_out, d_ff_1_q, IR1_q);
  or or_6 (or_6_out, d_ff_2_q, IR2_q);
  or or_7 (or_7_out, d_ff_3_q, IR3_q);
  Hex_Digit_Display hex_digit_display_6 (.value(LedData[11:8]));  // open: dp
  Hex_Digit_Display hex_digit_display_7 (.value(LedData[7:4]));  // open: dp
  // Probe on \总周期数 
  Multiplexer #(.width(32), .enable("false")) multiplexer_1 (
    .in0({adder_1_out_2, adder_1_out}), .in1(adder_2_out), .out(multiplexer_1_out), .sel(Branch));
  and and_1 (and_1_out, ERET, IR_now[0], ~IR_now[1]);  // AND_Gate
  and and_2 (and_2_out, ERET, ~IR_now[0], IR_now[1]);  // AND_Gate
  and and_3 (and_3_out, ERET, IR_now[0], IR_now[1]);
  Hex_Digit_Display hex_digit_display_8 (.value(LedData[3:0]));  // open: dp
  Multiplexer #(.width(32), .enable("false")) multiplexer_2 (
    .in0(multiplexer_1_out), .in1({adder_1_out_2, IR[25:0], 2'b00}), .out(multiplexer_2_out),
    .sel(\单周期硬布线控制器_1_jmp ));
  Multiplexer #(.width(32), .enable("false")) multiplexer_3 (
    .in0(multiplexer_2_out), .in1({mips_regifile_1_r1_2, mips_regifile_1_r1}), .out(nextPC),
    .sel(\单周期硬布线控制器_1_jr ));
  or or_8 (or_8_out, not_1_out, Go);
  not not_1 (not_1_out, halt);
  and and_4 (and_4_out, or_5_out, ~and_1_out);  // AND_Gate
  and and_5 (and_5_out, or_6_out, ~and_2_out);  // AND_Gate
  and and_6 (and_6_out, or_7_out, ~and_3_out);  // AND_Gate
  Button button_1 (.out(RST));
  Register #(.width(32), .Select("low")) u_PC (.D(PCout), .en(or_8_out), .Q(PC), .clk(CLK), .clr(RST));
  D_Flip_Flop #(.Pre_Clr_Positions("LEGACY"), .enable("true"), .NewFFLayout("false")) u_IR1 (
    .clk(CLK), .D(and_4_out), .Q(IR1_q));  // open: Qn, preset, en, reset
  D_Flip_Flop #(.Pre_Clr_Positions("LEGACY"), .enable("true"), .NewFFLayout("false")) u_IR2 (
    .clk(CLK), .D(and_5_out), .Q(IR2_q));  // open: Qn, preset, en, reset
  D_Flip_Flop #(.Pre_Clr_Positions("LEGACY"), .enable("true"), .NewFFLayout("false")) u_IR3 (
    .clk(CLK), .D(and_6_out), .Q(IR3_q));  // open: Qn, preset, en, reset
  or or_9 (IR1_t, IR1, IRA);
  not not_2 (not_2_out, halt);
  Counter #(.width(16), .max('hffff)) counter_1 (
    .count(not_2_out), .Q(\总周期数 ), .clk(CLK), .clr(RST));  // open: load, D, carry, preset, down
  Priority_Encoder #(.select(2)) priority_encoder_1 (
    .in0(1'b1), .in1(IR1_q), .in2(IR2_q), .in3(IR3_q), .out(priority_encoder_1_out),
    .gs(priority_encoder_1_gs));  // open: en_out, en_in
  or or_10 (IR2_t, IR2, IRB);
  Adder #(.width(32)) adder_1 (.a(PC), .b(32'h4), .out({adder_1_out_2, adder_1_out}));  // open: cin, cout
  // Probe on priority_encoder_1_out
  // Probe on IR[5:0]
  ROM #(.addrWidth(10), .dataWidth(32), .Select("high")) rom_1 (.addr(PC[11:2]), .data(IR));
  Multiplexer #(.select(2), .enable("false")) multiplexer_4 (
    .in0(1'b0), .in1(priority_encoder_1_gs), .in2(priority_encoder_1_gs), .in3(priority_encoder_1_gs),
    .out(multiplexer_4_out), .sel(priority_encoder_1_out));
  or or_11 (IR3_t, IR3, IRC);
  // Probe on IR[31:26]
  // Mips_Probe mips_probe_1: pin names not known; wires that end beside it: IR, mips_probe_1_p2
  Multiplexer #(.width(32), .enable("false")) multiplexer_5 (
    .in0(nextPC), .in1(multiplexer_6_out), .out(multiplexer_5_out), .sel(and_7_out));
  Multiplexer #(.select(2), .width(32), .enable("false")) multiplexer_6 (
    .in0(nextPC), .in1(32'h30ac), .in2(32'h3150), .in3(32'h31f4), .out(multiplexer_6_out),
    .sel(priority_encoder_1_out));
  and and_7 (and_7_out, multiplexer_4_out, ~\中断状态_q );  // AND_Gate
  Register #(.width(32), .Select("low")) EPC (.D(nextPC), .en(and_7_out), .Q(EPC_q), .clk(CLK));  // open: clr
  Register #(.width(1), .Select("low")) \u_中断状态  (.D(1'b1), .en(and_7_out), .Q(\中断状态_q ), .clk(CLK), .clr(ERET));
  \单周期硬布线控制器  \u_单周期硬布线控制器_1  (
    .Func(IR[5:0]), .OP(IR[31:26]), .ALU_OP(\单周期硬布线控制器_1_alu_op ), .MemToReg(\单周期硬布线控制器_1_memtoreg ),
    .MemWrite(MemWrite), .ALU_SRC(\单周期硬布线控制器_1_alu_src ), .RegWrite(RegWrite), .SysCALL(Syscall),
    .SignedExt(SignedExt), .RegDst(\单周期硬布线控制器_1_regdst ), .JR(\单周期硬布线控制器_1_jr ), .JMP(\单周期硬布线控制器_1_jmp ),
    .Beq(\单周期硬布线控制器_1_beq ), .JAL(JAL), .Bne(\单周期硬布线控制器_1_bne ), .SLLV(SLLV), .BLEZ(BLEZ), .LBU(LBU),
    .ERET(ERET), .MF(IR[25:21]));  // open: MFC0, MTC0
  Multiplexer #(.width(5), .enable("false")) multiplexer_7 (
    .in0(IR[25:21]), .in1(5'b00010), .out(mips_probe_1_p2), .sel(Syscall));
  Multiplexer #(.width(5), .enable("false")) multiplexer_8 (
    .in0(IR[20:16]), .in1(5'b00100), .out(multiplexer_8_out), .sel(Syscall));
  Multiplexer #(.width(5), .enable("false")) multiplexer_9 (
    .in0(IR[20:16]), .in1(IR[15:11]), .out(multiplexer_9_out), .sel(\单周期硬布线控制器_1_regdst ));
  assign bit_extender_1_out = {{16{1'b0}}, IR[15:0]};  // Bit_Extender bit_extender_1
  assign bit_extender_2_out = {{16{IR[15]}}, IR[15:0]};  // Bit_Extender bit_extender_2
  Multiplexer #(.width(32), .enable("false")) multiplexer_10 (
    .in0(multiplexer_5_out), .in1(EPC_q), .out(PCout), .sel(ERET));
  Multiplexer #(.width(2), .enable("false")) multiplexer_11 (
    .in0(priority_encoder_1_out), .in1(2'b00), .out(multiplexer_11_out), .sel(ERET));
  or or_12 (or_12_out, and_7_out, ERET);
  Multiplexer #(.width(5), .enable("false")) multiplexer_12 (
    .in0(multiplexer_9_out), .in1({5{1'b1}}), .out(multiplexer_12_out), .sel(JAL));
  Multiplexer #(.width(32), .enable("false")) multiplexer_13 (
    .in0(bit_extender_1_out), .in1(bit_extender_2_out), .out(multiplexer_13_out), .sel(SignedExt));
  Shifter #(.width(32)) shifter_1 (.in(bit_extender_2_out), .\dist (5'b00010), .out(shifter_1_out));
  Register #(.width(2), .Select("low")) cause (
    .D(multiplexer_11_out), .en(or_12_out), .Q(IR_now), .clk(CLK));  // open: clr
  Adder #(.width(32)) adder_2 (
    .a(shifter_1_out), .b({adder_1_out_2, adder_1_out}), .out(adder_2_out));  // open: cin, cout
  MIPS_Regifile mips_regifile_1 (
    .Din(RDin), .Clk(CLK), .R1({mips_regifile_1_r1_2, mips_regifile_1_r1}), .R2(MDin), .WE(RegWrite),
    .W_num(multiplexer_12_out), .R1_num(mips_probe_1_p2), .R2_num(multiplexer_8_out));
  Multiplexer #(.width(32), .enable("false")) multiplexer_14 (
    .in0(MDin), .in1(multiplexer_13_out), .out(multiplexer_14_out), .sel(\单周期硬布线控制器_1_alu_src ));
  Multiplexer #(.width(32), .enable("false")) multiplexer_15 (
    .in0(multiplexer_14_out), .in1({32{1'b0}}), .out(multiplexer_15_out), .sel(BLEZ));
  Multiplexer #(.width(5), .enable("false")) multiplexer_16 (
    .in0(IR[10:6]), .in1(mips_regifile_1_r1), .out(multiplexer_16_out), .sel(SLLV));
  MIPS_ALU mips_alu_1 (
    .X({mips_regifile_1_r1_2, mips_regifile_1_r1}), .Y(multiplexer_15_out), .AluOP(\单周期硬布线控制器_1_alu_op ),
    .Equal(mips_alu_1_equal), .Result(mips_alu_1_result), .shamt(multiplexer_16_out));  // open: Result_2
  // Probe on multiplexer_16_out
  Comparator #(.width(32)) comparator_5 (.a(32'h1), .b(mips_alu_1_result), .eq(comparator_5_eq));  // open: gt, lt
  Comparator #(.width(32)) comparator_6 (
    .a(32'h22), .b({mips_regifile_1_r1_2, mips_regifile_1_r1}), .eq(comparator_6_eq));  // open: gt, lt
  // Probe on mips_alu_1_result
  Register #(.width(32), .Select("low")) LedReg (.D(MDin), .en(LedOut), .Q(LedData), .clk(CLK), .clr(RST));
  or or_13 (or_13_out, mips_alu_1_equal, comparator_5_eq);
  and and_8 (and_8_out, or_13_out, BLEZ);
  and and_9 (and_9_out, mips_alu_1_equal, \单周期硬布线控制器_1_beq );
  and and_10 (and_10_out, ~mips_alu_1_equal, \单周期硬布线控制器_1_bne );  // AND_Gate
  and and_11 (halt, Syscall, ~comparator_6_eq);  // AND_Gate
  and and_12 (LedOut, Syscall, comparator_6_eq);
  or or_14 (Branch, and_8_out, and_9_out, and_10_out);
  RAM #(.addrWidth(10), .dataWidth(32), .bus("separate"), .Select("high")) ram_1 (
    .addr(mips_alu_1_result[11:2]), .din(MDin), .data(ram_1_data), .str(MemWrite), .clk(CLK), .clr(RST));  // open: sel, ld
  Multiplexer #(.width(32), .enable("false")) multiplexer_17 (
    .in0(mips_alu_1_result), .in1(ram_1_data), .out(multiplexer_17_out), .sel(\单周期硬布线控制器_1_memtoreg ));
  assign bit_extender_3_out = {{24{1'b0}}, multiplexer_18_out};  // Bit_Extender bit_extender_3
  Multiplexer #(.select(2), .width(8), .enable("false")) multiplexer_18 (
    .in0(multiplexer_17_out[7:0]), .in1(multiplexer_17_out[15:8]), .in2(multiplexer_17_out[23:16]),
    .in3(multiplexer_17_out[31:24]), .out(multiplexer_18_out), .sel(mips_alu_1_result[1:0]));
  Multiplexer #(.width(32), .enable("false")) multiplexer_19 (
    .in0(multiplexer_17_out), .in1(bit_extender_3_out), .out(multiplexer_19_out), .sel(LBU));
  Multiplexer #(.width(32), .enable("false")) multiplexer_20 (
    .in0(multiplexer_19_out), .in1({adder_1_out_2, adder_1_out}), .out(RDin), .sel(JAL));

  // Other names for the same wires on the sheet: OP[5:0] = IR[31:26]

  // Notes on the sheet:
  //   中断源
  //   中断等待指示
  //   总复位信号应将除ROM以外所有存储组件全部清零
  //   单级中断测试信号模拟器
  //   数码管输出
  //   数码管输出应该用寄存器锁存，否则显示数据只能一闪而过
  //   jump
  //   jr
  //   Reset 
  //   Reset 
  //   Reset 
  //   指令存储器
  //   contents of rom_1 (hex, n*v repeats v):
  //   201d07d0 20100001 109fc0 139fc3 8021 2012000c 24160008 26100001 3210000f 20080008 20090001 139900
  //   2709825 132020 20020022 c 1094022 1500fff9 22100001 2018000f 2188024 108700 20080008 20090001 139902
  //   2709825 132021 20020022 c 1094022 1500fff9 108702 2c9b022 12c00001 8000c07 4020 1084027 84400
  //   3508ffff 82021 20020022 c 8000c01 afa20000 23bd0004 afa40000 23bd0004 afb00000 23bd0004 afb30000
  //   23bd0004 afb40000 23bd0004 afb50000 23bd0004 afb60000 23bd0004 20160001 20140003 20150001 168020
  //   108100 2149825 132020 20020022 c 1600fffa 295a022 1680fff7 23bdfffc 8fb60000 23bdfffc 8fb50000
  //   23bdfffc 8fb40000 23bdfffc 8fb30000 23bdfffc 8fb00000 23bdfffc 8fa40000 23bdfffc 8fa20000 42000018
  //   afa20000 23bd0004 afa40000 23bd0004 afb00000 23bd0004 afb30000 23bd0004 afb40000 23bd0004 afb50000
  //   23bd0004 afb60000 23bd0004 20160002 20140003 20150001 168020 108100 2149825 132020 20020022 c
  //   1600fffa 295a022 1680fff7 23bdfffc 8fb60000 23bdfffc 8fb50000 23bdfffc 8fb40000 23bdfffc 8fb30000
  //   23bdfffc 8fb00000 23bdfffc 8fa40000 23bdfffc 8fa20000 42000018 afa20000 23bd0004 afa40000 23bd0004
  //   afb00000 23bd0004 afb30000 23bd0004 afb40000 23bd0004 afb50000 23bd0004 afb60000 23bd0004 20160003
  //   20140003 20150001 168020 108100 2149825 132020 20020022 c 1600fffa 295a022 1680fff7 23bdfffc
  //   8fb60000 23bdfffc 8fb50000 23bdfffc 8fb40000 23bdfffc 8fb30000 23bdfffc 8fb00000 23bdfffc 8fa40000
  //   23bdfffc 8fa20000 42000018
  //   关中断信号
  //   OP
  //   Func
  //   rs
  //   指令字
  //   rt
  //   rd
  //   shamt
  //   imm16
  //   imm26
  //   Beq
  //   JMP
  //   JR
  //   Bne
  //   OP
  //   JAL
  //   Func
  //   RegDst
  //   为方便自动评测，需要输出PC，IR，寄存器堆写如数据RDin
  //   MemToReg
  //   MemWrite
  //   AluOP
  //   AluSrcB
  //   RegWrite
  //   RAM写使能MemWrite、RAM写入数据MDin等信号
  //   PC+4+imm16<<2
endmodule

module \单周期MIPS_多级中断  (
  input  IR1,
  input  IR2,
  input  IR3,
  output RegWrite,
  output MemWrite,
  output [31:0] PC,
  output [31:0] IR,
  output [31:0] RDin,
  output [31:0] MDin,
  output [31:0] LedData
);

  wire and_1_out, and_2_out, and_3_out, and_7_out, and_8_out, and_9_out, and_12_out, and_13_out, and_15_out,
       and_16_out, and_17_out, BLEZ, Branch, CLK, comparator_1_eq, comparator_2_eq, comparator_3_eq,
       comparator_4_eq, comparator_5_gt, comparator_6_eq, comparator_7_eq, d_ff_1_q, d_ff_2_q, d_ff_3_q,
       decoder_1_out1, decoder_1_out2, decoder_1_out3, ERET, Go, halt, \IE_0为开中断_q , \IE_0为开中断_qn , IE_in,
       INT, IR1_t, ir1_t_t, IR2_t, ir2_t_t, IR3_t, ir3_t_t, IRA, IRB, IRC, JAL, LBU, LedOut, MFC0,
       mips_alu_1_equal, MTC0, multiplexer_15_out, not_1_out, not_2_out, or_1_out, or_5_out, or_6_out,
       or_7_out, or_11_out, or_13_out, or_14_out, priority_encoder_1_gs, priority_encoder_2_out,
       priority_encoder_3_out, pull_resistor_1_node, RST, Rst1, Rst2, Rst3, SignedExt, SLLV, Syscall, W1, W2,
       W3, \单周期硬布线控制器_1_alu_src , \单周期硬布线控制器_1_beq , \单周期硬布线控制器_1_bne , \单周期硬布线控制器_1_jmp , \单周期硬布线控制器_1_jr ,
       \单周期硬布线控制器_1_memtoreg , \单周期硬布线控制器_1_regdst ;
  wire [1:0] IR_now, priority_encoder_1_out;
  wire [1:1] IE_sell;
  wire [3:0] \单周期硬布线控制器_1_alu_op ;
  wire [4:0] mips_probe_1_p2, multiplexer_5_out, multiplexer_6_out, multiplexer_7_out, multiplexer_12_out;
  wire [7:0] multiplexer_16_out;
  wire [15:0] \总周期数 ;
  wire [27:0] adder_1_out;
  wire [31:0] adder_2_out, bit_extender_1_out, bit_extender_2_out, bit_extender_3_out, demultiplexer_1_out0,
       EPC_q, mips_alu_1_result, mips_regifile_1_r1, multiplexer_1_out, multiplexer_2_out, multiplexer_8_out,
       multiplexer_10_out, multiplexer_11_out, multiplexer_13_out, multiplexer_14_out, multiplexer_17_out,
       multiplexer_18_out, multiplexer_19_out, multiplexer_20_out, multiplexer_23_out, nextPC, PCout,
       ram_1_data, shifter_1_out, siteData;
  wire [31:1] demultiplexer_1_out1;
  wire [31:28] adder_1_out_2;

  Clock clock_1 (.out(CLK));
  Button _1 (.out(IRA));
  Button _2 (.out(IRB));
  Button _3 (.out(IRC));
  Button \u_继续运行  (.out(Go));
  LED led_1 (.in(W1));
  LED led_2 (.in(W2));
  LED led_3 (.in(W3));
  Multiplexer #(.width(32), .enable("false")) multiplexer_1 (
    .in0({adder_1_out_2, adder_1_out}), .in1(adder_2_out), .out(multiplexer_1_out), .sel(Branch));
  Hex_Digit_Display hex_digit_display_1 (.value(LedData[31:28]));  // open: dp
  Multiplexer #(.width(32), .enable("false")) multiplexer_2 (
    .in0(multiplexer_1_out), .in1({adder_1_out_2, IR[25:0], 2'b00}), .out(multiplexer_2_out),
    .sel(\单周期硬布线控制器_1_jmp ));
  Hex_Digit_Display hex_digit_display_2 (.value(LedData[27:24]));  // open: dp
  Hex_Digit_Display hex_digit_display_3 (.value(LedData[23:20]));  // open: dp
  Button button_1 (.out(RST));
  Multiplexer #(.width(32), .enable("false")) multiplexer_3 (
    .in0(multiplexer_2_out), .in1(mips_regifile_1_r1), .out(nextPC), .sel(\单周期硬布线控制器_1_jr ));
  or or_1 (or_1_out, not_1_out, Go);
  not not_1 (not_1_out, halt);
  or or_2 (W1, ir1_t_t, d_ff_1_q);
  or or_3 (W2, ir2_t_t, d_ff_2_q);
  or or_4 (W3, ir3_t_t, d_ff_3_q);
  Hex_Digit_Display hex_digit_display_4 (.value(LedData[19:16]));  // open: dp
  Hex_Digit_Display hex_digit_display_5 (.value(LedData[15:12]));  // open: dp
  not not_2 (not_2_out, halt);
  Register #(.width(32), .Select("low")) u_PC (.D(PCout), .en(or_1_out), .Q(PC), .clk(CLK), .clr(RST));
  D_Flip_Flop #(.Pre_Clr_Positions("LEGACY"), .enable("true"), .NewFFLayout("false")) d_ff_1 (
    .clk(IR1_t), .D(1'b1), .Q(d_ff_1_q), .reset(ir1_t_t));  // open: Qn, preset, en
  D_Flip_Flop #(.Pre_Clr_Positions("LEGACY"), .enable("true"), .NewFFLayout("false")) d_ff_2 (
    .clk(IR2_t), .D(1'b1), .Q(d_ff_2_q), .reset(ir2_t_t));  // open: Qn, preset, en
  D_Flip_Flop #(.Pre_Clr_Positions("LEGACY"), .enable("true"), .NewFFLayout("false")) d_ff_3 (
    .clk(IR3_t), .D(1'b1), .Q(d_ff_3_q), .reset(ir3_t_t));  // open: Qn, preset, en
  Hex_Digit_Display hex_digit_display_6 (.value(LedData[11:8]));  // open: dp
  Hex_Digit_Display hex_digit_display_7 (.value(LedData[7:4]));  // open: dp
  // Probe on \总周期数 
  Counter #(.width(16), .max('hffff)) counter_1 (
    .count(not_2_out), .Q(\总周期数 ), .clk(CLK), .clr(RST));  // open: load, D, carry, preset, down
  Adder #(.width(32)) adder_1 (.a(PC), .b(32'h4), .out({adder_1_out_2, adder_1_out}));  // open: cin, cout
  or or_5 (or_5_out, d_ff_1_q, ir1_t_t);
  or or_6 (or_6_out, d_ff_2_q, ir2_t_t);
  or or_7 (or_7_out, d_ff_3_q, ir3_t_t);
  Hex_Digit_Display hex_digit_display_8 (.value(LedData[3:0]));  // open: dp
  // Probe on IR[5:0]
  // Probe on IR[31:26]
  // Mips_Probe mips_probe_1: pin names not known; wires that end beside it: IR, mips_probe_1_p2
  ROM #(.addrWidth(10), .dataWidth(32), .Select("high")) rom_1 (.addr(PC[11:2]), .data(IR));
  and and_1 (and_1_out, or_5_out, ~Rst1);  // AND_Gate
  and and_2 (and_2_out, or_6_out, ~Rst2);  // AND_Gate
  and and_3 (and_3_out, or_7_out, ~Rst3);  // AND_Gate
  or or_8 (IR1_t, IR1, IRA);
  D_Flip_Flop #(.Pre_Clr_Positions("LEGACY"), .enable("true"), .NewFFLayout("false")) u_IR1 (
    .clk(CLK), .D(and_1_out), .Q(ir1_t_t));  // open: Qn, preset, en, reset
  D_Flip_Flop #(.Pre_Clr_Positions("LEGACY"), .enable("true"), .NewFFLayout("false")) u_IR2 (
    .clk(CLK), .D(and_2_out), .Q(ir2_t_t));  // open: Qn, preset, en, reset
  D_Flip_Flop #(.Pre_Clr_Positions("LEGACY"), .enable("true"), .NewFFLayout("false")) u_IR3 (
    .clk(CLK), .D(and_3_out), .Q(ir3_t_t));  // open: Qn, preset, en, reset
  or or_9 (IR2_t, IR2, IRB);
  assign bit_extender_1_out = {{16{1'b0}}, IR[15:0]};  // Bit_Extender bit_extender_1
  assign bit_extender_2_out = {{16{IR[15]}}, IR[15:0]};  // Bit_Extender bit_extender_2
  \单周期硬布线控制器  \u_单周期硬布线控制器_1  (
    .Func(IR[5:0]), .OP(IR[31:26]), .ALU_OP(\单周期硬布线控制器_1_alu_op ), .MemToReg(\单周期硬布线控制器_1_memtoreg ),
    .MemWrite(MemWrite), .ALU_SRC(\单周期硬布线控制器_1_alu_src ), .RegWrite(RegWrite), .SysCALL(Syscall),
    .SignedExt(SignedExt), .RegDst(\单周期硬布线控制器_1_regdst ), .JR(\单周期硬布线控制器_1_jr ), .JMP(\单周期硬布线控制器_1_jmp ),
    .Beq(\单周期硬布线控制器_1_beq ), .JAL(JAL), .Bne(\单周期硬布线控制器_1_bne ), .SLLV(SLLV), .BLEZ(BLEZ), .LBU(LBU),
    .ERET(ERET), .MFC0(MFC0), .MTC0(MTC0), .MF(IR[25:21]));
  Multiplexer #(.width(5), .enable("false")) multiplexer_4 (
    .in0(IR[25:21]), .in1(5'b00010), .out(mips_probe_1_p2), .sel(Syscall));
  Multiplexer #(.width(5), .enable("false")) multiplexer_5 (
    .in0(IR[20:16]), .in1(5'b00100), .out(multiplexer_5_out), .sel(Syscall));
  Multiplexer #(.width(5), .enable("false")) multiplexer_6 (
    .in0(IR[20:16]), .in1(IR[15:11]), .out(multiplexer_6_out), .sel(\单周期硬布线控制器_1_regdst ));
  Multiplexer #(.width(5), .enable("false")) multiplexer_7 (
    .in0(multiplexer_6_out), .in1({5{1'b1}}), .out(multiplexer_7_out), .sel(JAL));
  Multiplexer #(.width(32), .enable("false")) multiplexer_8 (
    .in0(bit_extender_1_out), .in1(bit_extender_2_out), .out(multiplexer_8_out), .sel(SignedExt));
  or or_10 (IR3_t, IR3, IRC);
  Multiplexer #(.width(32), .enable("false")) multiplexer_9 (
    .in0(multiplexer_18_out), .in1(siteData), .out(RDin), .sel(MFC0));
  Shifter #(.width(32)) shifter_1 (.in(bit_extender_2_out), .\dist (5'b00010), .out(shifter_1_out));
  Decoder #(.select(2), .enable("false")) decoder_1 (
    .out1(decoder_1_out1), .out2(decoder_1_out2), .out3(decoder_1_out3), .sel(IR_now));  // open: out0
  MIPS_Regifile mips_regifile_1 (
    .Din(RDin), .Clk(CLK), .R1(mips_regifile_1_r1), .R2(MDin), .WE(RegWrite), .W_num(multiplexer_7_out),
    .R1_num(mips_probe_1_p2), .R2_num(multiplexer_5_out));
  Adder #(.width(32)) adder_2 (
    .a(shifter_1_out), .b({adder_1_out_2, adder_1_out}), .out(adder_2_out));  // open: cin, cout
  Multiplexer #(.width(32), .enable("false")) multiplexer_10 (
    .in0(MDin), .in1(multiplexer_8_out), .out(multiplexer_10_out), .sel(\单周期硬布线控制器_1_alu_src ));
  and and_4 (Rst1, decoder_1_out1, ERET);
  and and_5 (Rst2, decoder_1_out2, ERET);
  and and_6 (Rst3, decoder_1_out3, ERET);
  Multiplexer #(.width(32), .enable("false")) multiplexer_11 (
    .in0(multiplexer_10_out), .in1({32{1'b0}}), .out(multiplexer_11_out), .sel(BLEZ));
  Multiplexer #(.width(5), .enable("false")) multiplexer_12 (
    .in0(IR[10:6]), .in1(mips_regifile_1_r1[4:0]), .out(multiplexer_12_out), .sel(SLLV));
  MIPS_ALU mips_alu_1 (
    .X(mips_regifile_1_r1), .Y(multiplexer_11_out), .AluOP(\单周期硬布线控制器_1_alu_op ), .Equal(mips_alu_1_equal),
    .Result(mips_alu_1_result), .shamt(multiplexer_12_out));  // open: Result_2
  Priority_Encoder #(.select(2)) priority_encoder_1 (
    .in0(1'b0), .in1(ir1_t_t), .in2(ir2_t_t), .in3(ir3_t_t), .out(priority_encoder_1_out),
    .gs(priority_encoder_1_gs));  // open: en_out, en_in
  // Probe on mips_alu_1_result
  // Probe on multiplexer_12_out
  // Probe on priority_encoder_1_out
  Comparator #(.width(5)) comparator_1 (.a(IR[15:11]), .b(5'b01110), .eq(comparator_1_eq));  // open: gt, lt
  Comparator #(.width(5)) comparator_2 (.a(IR[15:11]), .b(5'b01100), .eq(comparator_2_eq));  // open: gt, lt
  or or_11 (or_11_out, mips_alu_1_equal, comparator_3_eq);
  Comparator #(.width(32)) comparator_3 (.a(32'h1), .b(mips_alu_1_result), .eq(comparator_3_eq));  // open: gt, lt
  Comparator #(.width(32)) comparator_4 (.a(32'h22), .b(mips_regifile_1_r1), .eq(comparator_4_eq));  // open: gt, lt
  Register #(.width(32), .Select("low")) LedReg (.D(MDin), .en(LedOut), .Q(LedData), .clk(CLK), .clr(RST));
  // Probe on IR_now
  stack stack_1 (.INPUT(priority_encoder_1_out), .clk(CLK), .\int (INT), .eret(ERET), .out_5(IR_now));
  and and_7 (and_7_out, or_11_out, BLEZ);
  and and_8 (and_8_out, mips_alu_1_equal, \单周期硬布线控制器_1_beq );
  and and_9 (and_9_out, ~mips_alu_1_equal, \单周期硬布线控制器_1_bne );  // AND_Gate
  and and_10 (halt, Syscall, ~comparator_4_eq);  // AND_Gate
  and and_11 (LedOut, Syscall, comparator_4_eq);
  Multiplexer #(.select(2), .width(32), .enable("false")) multiplexer_13 (
    .in1(32'h30ac), .in2(32'h3174), .in3(32'h323c), .out(multiplexer_13_out), .sel(priority_encoder_1_out));  // open: in0
  and and_12 (and_12_out, comparator_1_eq, MTC0);
  and and_13 (and_13_out, comparator_2_eq, MTC0);
  or or_12 (Branch, and_7_out, and_8_out, and_9_out);
  RAM #(.addrWidth(10), .dataWidth(32), .bus("separate"), .Select("high")) ram_1 (
    .addr(mips_alu_1_result[11:2]), .din(MDin), .data(ram_1_data), .str(MemWrite), .clk(CLK), .clr(RST));  // open: sel, ld
  Pull_Resistor pull_resistor_1 (.node(pull_resistor_1_node));
  Priority_Encoder #(.select(1)) priority_encoder_2 (
    .in0(and_12_out), .in1(and_13_out), .out(priority_encoder_2_out));  // open: gs, en_out, en_in
  Multiplexer #(.width(32), .enable("false")) multiplexer_14 (
    .in0(mips_alu_1_result), .in1(ram_1_data), .out(multiplexer_14_out), .sel(\单周期硬布线控制器_1_memtoreg ));
  Multiplexer #(.select(2), .enable("false")) multiplexer_15 (
    .in0(1'b1), .in1(1'b0), .in2(IE_in), .out(multiplexer_15_out), .sel({IE_sell[1], ERET}));  // open: in3
  Pull_Resistor pull_resistor_2 (.node(IE_sell[1]));
  Decoder #(.enable("false")) decoder_2 (.out0(pull_resistor_1_node), .out1(IE_sell[1]), .sel(priority_encoder_2_out));
  Demultiplexer #(.width(32), .enable("false")) demultiplexer_1 (
    .out0(demultiplexer_1_out0), .out1({demultiplexer_1_out1, IE_in}), .in(MDin), .sel(priority_encoder_2_out));
  Multiplexer #(.select(2), .width(8), .enable("false")) multiplexer_16 (
    .in0(multiplexer_14_out[7:0]), .in1(multiplexer_14_out[15:8]), .in2(multiplexer_14_out[23:16]),
    .in3(multiplexer_14_out[31:24]), .out(multiplexer_16_out), .sel(mips_alu_1_result[1:0]));
  Comparator #(.width(2), .mode("unsigned")) comparator_5 (
    .a(priority_encoder_1_out), .b(IR_now), .gt(comparator_5_gt));  // open: eq, lt
  or or_13 (or_13_out, IE_sell[1], INT, ERET);
  Pull_Resistor pull_resistor_3 (.node(IE_in));
  Multiplexer #(.width(32), .enable("false")) multiplexer_17 (
    .in0(multiplexer_14_out), .in1(bit_extender_3_out), .out(multiplexer_17_out), .sel(LBU));
  assign bit_extender_3_out = {{24{1'b0}}, multiplexer_16_out};  // Bit_Extender bit_extender_3
  and and_14 (INT, comparator_5_gt, and_15_out);
  and and_15 (and_15_out, priority_encoder_1_gs, \IE_0为开中断_qn );
  D_Flip_Flop #(.Pre_Clr_Positions("LEGACY"), .enable("true"), .NewFFLayout("false")) \IE_0为开中断  (
    .clk(CLK), .D(multiplexer_15_out), .Q(\IE_0为开中断_q ), .Qn(\IE_0为开中断_qn ), .en(or_13_out));  // open: preset, reset
  Multiplexer #(.width(32), .enable("false")) multiplexer_18 (
    .in0(multiplexer_17_out), .in1({adder_1_out_2, adder_1_out}), .out(multiplexer_18_out), .sel(JAL));
  Multiplexer #(.width(32), .enable("false")) multiplexer_19 (
    .in0(nextPC), .in1(multiplexer_13_out), .out(multiplexer_19_out), .sel(INT));
  Multiplexer #(.width(32), .enable("false")) multiplexer_20 (
    .in0(nextPC), .in1(demultiplexer_1_out0), .out(multiplexer_20_out), .sel(pull_resistor_1_node));
  Register #(.width(32), .Select("low")) EPC (
    .D(multiplexer_20_out), .en(or_14_out), .Q(EPC_q), .clk(CLK));  // open: clr
  or or_14 (or_14_out, INT, pull_resistor_1_node);
  Multiplexer #(.width(32), .enable("false")) multiplexer_21 (
    .in0(multiplexer_19_out), .in1(EPC_q), .out(PCout), .sel(ERET));
  Comparator #(.width(5)) comparator_6 (.a(IR[15:11]), .b(5'b01110), .eq(comparator_6_eq));  // open: gt, lt
  Comparator #(.width(5)) comparator_7 (.a(IR[15:11]), .b(5'b01100), .eq(comparator_7_eq));  // open: gt, lt
  and and_16 (and_16_out, comparator_6_eq, MFC0);
  and and_17 (and_17_out, comparator_7_eq, MFC0);
  Multiplexer #(.width(32), .enable("false")) multiplexer_22 (
    .in0(EPC_q), .in1(multiplexer_23_out), .out(siteData), .sel(priority_encoder_3_out));
  Multiplexer #(.width(32), .enable("false")) multiplexer_23 (
    .in0({32{1'b0}}), .in1(32'h1), .out(multiplexer_23_out), .sel(\IE_0为开中断_q ));
  Priority_Encoder #(.select(1)) priority_encoder_3 (
    .in0(and_16_out), .in1(and_17_out), .out(priority_encoder_3_out));  // open: gs, en_out, en_in

  // Other names for the same wires on the sheet: Rd[4:0] = IR[15:11]; IE_sell[0] = ERET; OP[5:0] = IR[31:26];
  //   R2[31:0] = MDin

  // Notes on the sheet:
  //   中断源
  //   中断等待指示
  //   总复位信号应将除ROM以外所有存储组件全部清零
  //   jump
  //   jr
  //   数码管输出
  //   数码管输出应该用寄存器锁存，否则显示数据只能一闪而过
  //   指令存储器
  //   指令字
  //   contents of rom_1 (hex, n*v repeats v):
  //   201d07d0 20100001 109fc0 139fc3 8021 2012000c 24160008 26100001 3210000f 20080008 20090001 139900
  //   2709825 132020 20020022 c 1094022 1500fff9 22100001 2018000f 2188024 108700 20080008 20090001 139902
  //   2709825 132021 20020022 c 1094022 1500fff9 108702 2c9b022 12c00001 8000c07 4020 1084027 84400
  //   3508ffff 82021 20020022 c 8000c01 afa20000 23bd0004 afa40000 23bd0004 afb00000 23bd0004 afb30000
  //   23bd0004 afb40000 23bd0004 afb50000 23bd0004 afb60000 23bd0004 40167000 afb60000 23bd0004 40806000
  //   20160001 20140003 20150001 168020 108100 2149825 132020 20020022 c 1600fffa 295a022 1680fff7
  //   20160001 40966000 23bdfffc 8fb60000 40967000 23bdfffc 8fb60000 23bdfffc 8fb50000 23bdfffc 8fb40000
  //   23bdfffc 8fb30000 23bdfffc 8fb00000 23bdfffc 8fa40000 23bdfffc 8fa20000 42000018 afa20000 23bd0004
  //   afa40000 23bd0004 afb00000 23bd0004 afb30000 23bd0004 afb40000 23bd0004 afb50000 23bd0004 afb60000
  //   23bd0004 40167000 afb60000 23bd0004 40806000 20160002 20140003 20150001 168020 108100 2149825 132020
  //   20020022 c 1600fffa 295a022 1680fff7 20160001 40966000 23bdfffc 8fb60000 40967000 23bdfffc 8fb60000
  //   23bdfffc 8fb50000 23bdfffc 8fb40000 23bdfffc 8fb30000 23bdfffc 8fb00000 23bdfffc 8fa40000 23bdfffc
  //   8fa20000 42000018 afa20000 23bd0004 afa40000 23bd0004 afb00000 23bd0004 afb30000 23bd0004 afb40000
  //   23bd0004 afb50000 23bd0004 afb60000 23bd0004 40167000 afb60000 23bd0004 40806000 20160003 20140003
  //   20150001 168020 108100 2149825 132020 20020022 c 1600fffa 295a022 1680fff7 20160001 40966000
  //   23bdfffc 8fb60000 40967000 23bdfffc 8fb60000 23bdfffc 8fb50000 23bdfffc 8fb40000 23bdfffc 8fb30000
  //   23bdfffc 8fb00000 23bdfffc 8fa40000 23bdfffc 8fa20000 42000018
  //   imm26
  //   Reset 
  //   Reset 
  //   Reset 
  //   OP
  //   Func
  //   rs
  //   rt
  //   rd
  //   shamt
  //   imm16
  //   JMP
  //   JR
  //   OP
  //   Func
  //   Beq
  //   Bne
  //   MemToReg
  //   MemWrite
  //   AluOP
  //   AluSrcB
  //   RegWrite
  //   JAL
  //   RegDst
  //   PC+4+imm16<<2
  //   为方便自动评测，需要输出PC，IR，寄存器堆写如数据RDin
  //   RAM写使能MemWrite、RAM写入数据MDin等信号
  //   cp0 14 EPC
  //   cp0 12 IE
  //   mtc0,改变EPC的值
  //   mtc0,改变IE的值
  //   中断响应阶段，值为0，应该关中断，将IE置为1
  //   ERET时，值为1，应该开中断，将IE置为0
  //   mtc0时，值为2，将IE置为对应的值
  //   cp0 14 EPC
  //   cp0 12 IE
endmodule

module \流水线中断  (
  output RegWrite,
  output MemWrite,
  output [31:0] IF_PC,
  output [31:0] ID_PC,
  output [31:0] EX_PC,
  output [31:0] M_PC,
  output [31:0] WB_PC,
  output [31:0] RDin,
  output [31:0] MDin,
  output [31:0] LedData
);

  wire and_1_out, and_2_out, and_3_out, and_4_out, and_5_out, and_6_out, and_7_out, and_8_out, and_9_out,
       and_10_out, and_11_out, and_12_out, and_13_out, and_14_out, BLEZ_EX, Branch, CLK, clock_2_out,
       comparator_1_eq, comparator_1_lt, comparator_2_eq, d_ff_1_q, d_ff_2_q, d_ff_3_q, d_ff_4_q, Equal,
       ERET, ex_mem_1_halt_out, ex_mem_1_jal_out, ex_mem_1_memtoreg_out, ex_mem_1_regdst_out,
       ex_mem_1_syscall_out, EX_RegWrite, Go, id_ex_1_alusrcb_out, id_ex_1_beq_out, id_ex_1_bne_out,
       id_ex_1_halt_out, id_ex_1_jal_out, id_ex_1_memtogeg_out, id_ex_1_memwrite_out, id_ex_1_regdst_out,
       ID_RegDst, IE, IR1, IR1_q, IR2, IR2_q, IR3, IR3_q, JAL, JMP, JR, LBU_EX, LBU_M, LBU_W, LoadUse,
       MEM_RegWrite, mem_wb_1_halt_out, MemtoReg, mips_alu_1_equal, multiplexer_18_out, nand_1_out, nop,
       or_1_out, or_2_out, or_4_out, or_5_out, or_8_out, or_12_out, or_13_out, or_14_out, or_15_out,
       priority_encoder_1_gs, RegDst, RST, run, SignedExt, SLLV_EX, sys, Syscall, undriven, W1, W2, W3,
       \中断状态_q , \单周期硬布线控制器_1_alu_src , \单周期硬布线控制器_1_beq , \单周期硬布线控制器_1_blez , \单周期硬布线控制器_1_bne ,
       \单周期硬布线控制器_1_jal , \单周期硬布线控制器_1_jmp , \单周期硬布线控制器_1_jr , \单周期硬布线控制器_1_lbu , \单周期硬布线控制器_1_memtoreg ,
       \单周期硬布线控制器_1_memwrite , \单周期硬布线控制器_1_regwrite , \单周期硬布线控制器_1_sllv , \单周期硬布线控制器_1_syscall ,
       \重定向数据相关检测_1_loaduse ;
  wire [1:0] IR_now, multiplexer_24_out, priority_encoder_1_out, R1_Forward, R2_Forward, undriven_3,
       \重定向数据相关检测_1_r1_forward , \重定向数据相关检测_1_r2_forward ;
  wire [3:0] id_ex_1_aluop_out, \单周期硬布线控制器_1_alu_op ;
  wire [4:0] EX_WriteReg_num, id_ex_1_shamt_in_2, ID_R1_num, ID_R2_num, MEM_WriteReg_num, multiplexer_2_out,
       multiplexer_5_out, multiplexer_11_out, multiplexer_15_out, multiplexer_16_out;
  wire [5:0] ID_Func;
  wire [7:0] multiplexer_12_out, multiplexer_17_out, ram_1_data, ram_1_data_2, ram_1_data_3, ram_1_data_4;
  wire [12:0] CNT_num;
  wire [15:0] adder_3_out, \LoadUse次数 , multiplier_1_out, \总周期数 , \插入气泡数 , \无条件分支数 , \条件分支成功数 ;
  wire [31:0] a0, adder_1_out, adder_2_out, bit_extender_1_out, bit_extender_2_out, bit_extender_3_out,
       bit_extender_4_out, EPC_q, EX_IR, EX_PC2, id_ex_1_address_out, id_ex_1_eimm_out, id_ex_1_r1_out,
       id_ex_1_r2_out, ID_PC2, IF_IR, MEM_Alu, MEM_IR, MEM_PC2, mem_wb_1_pc_out, mips_alu_1_result,
       mips_regifile_1_r1, mips_regifile_1_r2, multiplexer_6_out, multiplexer_8_out, multiplexer_9_out,
       multiplexer_10_out, multiplexer_13_out, multiplexer_14_out, multiplexer_20_out, multiplexer_21_out,
       nextPC, PCout, shifter_1_out, undriven_2, WB_Alu, WB_IR, WB_MD;
  wire [31:6] ID_IR;

  Button \u_总复位  (.out(RST));
  Button _1 (.out(IR1));
  Button _2 (.out(IR2));
  Button _3 (.out(IR3));
  // Probe on \总周期数 
  // Probe on \总周期数 
  Button \u_继续运行  (.out(Go));
  LED led_1 (.in(W1));
  LED led_2 (.in(W2));
  LED led_3 (.in(W3));
  Hex_Digit_Display hex_digit_display_1 (.value(LedData[31:28]));  // open: dp
  // Probe on IF_PC[19:0]
  // Mips_Probe mips_probe_1: pin names not known; wires that end beside it: IF_IR
  Multiplexer #(.select(3), .width(32), .enable("false")) multiplexer_1 (
    .in0(adder_1_out), .in1({32{1'b0}}), .in2(id_ex_1_address_out), .in3(id_ex_1_r1_out), .in4(adder_2_out),
    .in5({32{1'b0}}), .in6({32{1'b0}}), .in7({32{1'b0}}), .out(nextPC), .sel({Branch, JMP, JR}));
  or or_1 (or_1_out, run, Go);
  Hex_Digit_Display hex_digit_display_2 (.value(LedData[23:20]));  // open: dp
  Hex_Digit_Display hex_digit_display_3 (.value(LedData[27:24]));  // open: dp
  // Probe on ID_PC[19:0]
  // Mips_Probe mips_probe_2: pin names not known; wires that end beside it: {ID_IR, ID_Func}
  Register #(.width(32), .Select("low")) PC (.D(PCout), .en(and_1_out), .Q(IF_PC), .clk(CLK), .clr(RST));
  and and_1 (and_1_out, or_1_out, ~LoadUse);  // AND_Gate
  Hex_Digit_Display hex_digit_display_4 (.value(LedData[15:12]));  // open: dp
  Hex_Digit_Display hex_digit_display_5 (.value(LedData[19:16]));  // open: dp
  // Probe on IF_PC
  Hex_Digit_Display hex_digit_display_6 (.value(LedData[7:4]));  // open: dp
  Hex_Digit_Display hex_digit_display_7 (.value(LedData[11:8]));  // open: dp
  Clock clock_1 (.out(CLK));
  // Probe on EX_PC[19:0]
  // Mips_Probe mips_probe_3: pin names not known; wires that end beside it: EX_IR
  // Probe on ID_PC
  Adder #(.width(32)) adder_1 (.a(IF_PC), .b(32'h4), .out(adder_1_out));  // open: cin, cout
  Hex_Digit_Display hex_digit_display_8 (.value(LedData[3:0]));  // open: dp
  // Probe on EX_PC
  ROM #(.addrWidth(10), .dataWidth(32), .Select("high")) rom_1 (.addr(IF_PC[11:2]), .data(IF_IR));
  and and_2 (and_2_out, ~LoadUse, run);  // AND_Gate
  // Probe on \总周期数 
  // Probe on M_PC[19:0]
  // Mips_Probe mips_probe_4: pin names not known; wires that end beside it: MEM_IR
  // Probe on M_PC
  \重定向数据相关检测  \u_重定向数据相关检测_1  (
    .ID_OP(ID_IR[31:26]), .ID_FUNC(ID_Func), .ID_R1_num(ID_R1_num), .ID_R2_num(ID_R2_num),
    .EX_WriteReg_num(EX_WriteReg_num), .MEM_WriteReg_num(MEM_WriteReg_num), .EX_RegWrite(EX_RegWrite),
    .MEM_RegWrite(MEM_RegWrite), .EX_OP(EX_IR[31:26]), .MEM_OP(MEM_IR[31:26]),
    .LoadUse(\重定向数据相关检测_1_loaduse ), .R1_Forward(\重定向数据相关检测_1_r1_forward ),
    .R2_Forward(\重定向数据相关检测_1_r2_forward ));
  or or_2 (or_2_out, ERET, RST, nop, IE);
  IF_ID if_id_1 (
    .ir_in(IF_IR), .pcr_in(IF_PC), .pc_in(adder_1_out), .ir_out({ID_IR, ID_Func}), .pcr_out(ID_PC),
    .pc_out(ID_PC2), .Reset(or_2_out), .CLK(CLK), .Enable(and_2_out));
  // Probe on \总周期数 
  // Probe on \无条件分支数 
  // Probe on \条件分支成功数 
  // Probe on \插入气泡数 
  // Probe on \LoadUse次数 
  // Probe on WB_PC
  // Probe on IF_PC[11:0]
  // Probe on WB_PC[19:0]
  // Mips_Probe mips_probe_5: pin names not known; wires that end beside it: WB_IR
  Register #(.width(2), .Select("low")) register_1 (
    .D(\重定向数据相关检测_1_r1_forward ), .Q(R1_Forward), .clk(CLK), .clr(RST));  // open: en
  Register #(.width(2), .Select("low")) register_2 (
    .D(\重定向数据相关检测_1_r2_forward ), .Q(R2_Forward), .clk(CLK), .clr(RST));  // open: en
  // Probe on ID_PC[11:0]
  // Probe on EX_PC[11:0]
  Multiplexer #(.width(5), .enable("false")) multiplexer_2 (
    .in0(ID_IR[20:16]), .in1(ID_IR[15:11]), .out(multiplexer_2_out), .sel(ID_RegDst));
  assign bit_extender_1_out = {{16{1'b0}}, {ID_IR[15:6], ID_Func}};  // Bit_Extender bit_extender_1
  assign bit_extender_2_out = {{16{ID_IR[15]}}, {ID_IR[15:6], ID_Func}};  // Bit_Extender bit_extender_2
  // Probe on M_PC[11:0]
  D_Flip_Flop #(.trigger("high"), .Pre_Clr_Positions("LEGACY"), .enable("true"), .NewFFLayout("false")) d_ff_1 (.Q(d_ff_1_q));  // open: clk, D, Qn, preset, en, reset
  // Probe on 13'h340
  or or_3 (LoadUse, LBU_M, LBU_EX, \重定向数据相关检测_1_loaduse );
  \单周期硬布线控制器  \u_单周期硬布线控制器_1  (
    .Func(ID_Func), .OP(ID_IR[31:26]), .ALU_OP(\单周期硬布线控制器_1_alu_op ), .MemToReg(\单周期硬布线控制器_1_memtoreg ),
    .MemWrite(\单周期硬布线控制器_1_memwrite ), .ALU_SRC(\单周期硬布线控制器_1_alu_src ), .RegWrite(\单周期硬布线控制器_1_regwrite ),
    .SysCALL(\单周期硬布线控制器_1_syscall ), .SignedExt(SignedExt), .RegDst(ID_RegDst), .JR(\单周期硬布线控制器_1_jr ),
    .JMP(\单周期硬布线控制器_1_jmp ), .Beq(\单周期硬布线控制器_1_beq ), .JAL(\单周期硬布线控制器_1_jal ), .Bne(\单周期硬布线控制器_1_bne ),
    .SLLV(\单周期硬布线控制器_1_sllv ), .BLEZ(\单周期硬布线控制器_1_blez ), .LBU(\单周期硬布线控制器_1_lbu ), .ERET(ERET));  // open: MFC0, MTC0, MF
  Multiplexer #(.width(5), .enable("false")) multiplexer_3 (
    .in0(ID_IR[25:21]), .in1(5'b00100), .out(ID_R1_num), .sel(\单周期硬布线控制器_1_syscall ));
  Multiplexer #(.width(5), .enable("false")) multiplexer_4 (
    .in0(ID_IR[20:16]), .in1(5'b00010), .out(ID_R2_num), .sel(\单周期硬布线控制器_1_syscall ));
  Multiplexer #(.width(5), .enable("false")) multiplexer_5 (
    .in0(multiplexer_2_out), .in1({5{1'b1}}), .out(multiplexer_5_out), .sel(\单周期硬布线控制器_1_jal ));
  Multiplexer #(.width(32), .enable("false")) multiplexer_6 (
    .in0(bit_extender_1_out), .in1(bit_extender_2_out), .out(multiplexer_6_out), .sel(SignedExt));
  // Probe on WB_PC[11:0]
  Comparator #(.width(13)) comparator_1 (
    .a(CNT_num), .b(13'h340), .eq(comparator_1_eq), .lt(comparator_1_lt));  // open: gt
  Clock clock_2 (.out(clock_2_out));
  // Probe on multiplexer_6_out
  nand nand_1 (nand_1_out, d_ff_1_q, comparator_1_eq);
  Counter #(.width(13), .max('h1fff), .ongoal("stay"), .behavior("old")) counter_1 (
    .count(comparator_1_lt), .Q(CNT_num), .clk(clock_2_out), .clr(RST));  // open: load, D, carry, preset
  MIPS_Regifile mips_regifile_1 (
    .Din(RDin), .Clk(CLK), .R1(mips_regifile_1_r1), .R2(mips_regifile_1_r2), .WE(RegWrite),
    .W_num(multiplexer_16_out), .R1_num(ID_R1_num), .R2_num(ID_R2_num));
  assign CLK = nand_1_out ? undriven : 1'bz;  // Controlled_Buffer controlled_buffer_1
  and and_3 (and_3_out, ~Equal, Syscall);  // AND_Gate
  Pull_Resistor #(.pull(1)) pull_resistor_1 (.node(CLK));
  or or_4 (or_4_out, IE, RST, LoadUse, nop);
  ID_EX id_ex_1 (
    .jr_in(\单周期硬布线控制器_1_jr ), .R1_in(mips_regifile_1_r1), .Eimm_in(multiplexer_6_out),
    .jmp_in(\单周期硬布线控制器_1_jmp ), .beq_in(\单周期硬布线控制器_1_beq ), .R2_in(mips_regifile_1_r2),
    .bne_in(\单周期硬布线控制器_1_bne ), .Address_in({ID_PC2[31:28], ID_IR[25:6], ID_Func, 2'b00}),
    .memtogeg_in(\单周期硬布线控制器_1_memtoreg ), .memwrite_in(\单周期硬布线控制器_1_memwrite ), .pcr_in(ID_PC),
    .shamt_in(ID_IR[10:6]), .AluOp_in(\单周期硬布线控制器_1_alu_op ), .AluSrcB_in(\单周期硬布线控制器_1_alu_src ),
    .RegWrite_in(\单周期硬布线控制器_1_regwrite ), .pc_in(ID_PC2), .JAL_in(\单周期硬布线控制器_1_jal ), .RegDst_in(ID_RegDst),
    .ir_in({ID_IR, ID_Func}), .Eimm_out(id_ex_1_eimm_out), .R2_out(id_ex_1_r2_out),
    .Address_out(id_ex_1_address_out), .pcr_out(EX_PC), .shamt_in_2(id_ex_1_shamt_in_2), .pc_out(EX_PC2),
    .ir_out(EX_IR), .Rest(or_4_out), .CLK(CLK), .Enable(run), .halt_in(and_3_out),
    .syscall_in(\单周期硬布线控制器_1_syscall ), .jr_out(JR), .jmp_out(JMP), .beq_out(id_ex_1_beq_out),
    .bne_out(id_ex_1_bne_out), .memtogeg_out(id_ex_1_memtogeg_out), .memwrite_out(id_ex_1_memwrite_out),
    .AluOp_out(id_ex_1_aluop_out), .AluSrcB_out(id_ex_1_alusrcb_out), .RegWrite_out(EX_RegWrite),
    .JAL_out(id_ex_1_jal_out), .RegDst_out(id_ex_1_regdst_out), .halt_out(id_ex_1_halt_out),
    .syscall_out(Syscall), .R1_out(id_ex_1_r1_out), .W__in(multiplexer_5_out), .W__IN_2(EX_WriteReg_num),
    .SLLV_in(\单周期硬布线控制器_1_sllv ), .SLLV_out(SLLV_EX), .BLEZ_in(\单周期硬布线控制器_1_blez ), .BLEZ_out(BLEZ_EX),
    .LBU_in(\单周期硬布线控制器_1_lbu ), .LBU_out(LBU_EX));
  or or_5 (or_5_out, run, Go);
  and and_4 (and_4_out, LoadUse, run);
  Counter #(.width(16), .max('hffff), .behavior("old")) counter_2 (
    .count(or_5_out), .Q(\总周期数 ), .clk(CLK), .clr(RST));  // open: load, D, carry, preset
  Counter #(.width(16), .max('hffff), .behavior("old")) counter_3 (
    .count(and_4_out), .Q(\LoadUse次数 ), .clk(CLK), .clr(RST));  // open: load, D, carry, preset
  Multiplexer #(.select(2), .width(32), .enable("false")) multiplexer_7 (
    .in0(id_ex_1_r1_out), .in1(WB_Alu), .in2(WB_MD), .in3(MEM_Alu), .out(a0), .sel(R1_Forward));
  Multiplexer #(.select(2), .width(32), .enable("false")) multiplexer_8 (
    .in0(id_ex_1_r2_out), .in1(WB_Alu), .in2(WB_MD), .in3(MEM_Alu), .out(multiplexer_8_out), .sel(R2_Forward));
  // Probe on EX_PC2
  or or_6 (Branch, and_5_out, and_7_out, and_8_out);
  and and_5 (and_5_out, id_ex_1_beq_out, mips_alu_1_equal);
  Multiplexer #(.width(32), .enable("false")) multiplexer_9 (
    .in0(multiplexer_8_out), .in1(id_ex_1_eimm_out), .out(multiplexer_9_out), .sel(id_ex_1_alusrcb_out));
  Multiplexer #(.width(32), .enable("false")) multiplexer_10 (
    .in0(multiplexer_9_out), .in1({32{1'b0}}), .out(multiplexer_10_out), .sel(BLEZ_EX));
  Shifter #(.width(32)) shifter_1 (.in(id_ex_1_eimm_out), .\dist (5'b00010), .out(shifter_1_out));
  and and_6 (and_6_out, Equal, Syscall);
  and and_7 (and_7_out, id_ex_1_bne_out, ~mips_alu_1_equal);  // AND_Gate
  // Probe on R1_Forward
  MIPS_ALU mips_alu_1 (
    .X(a0), .Y(multiplexer_10_out), .AluOP(id_ex_1_aluop_out), .Equal(mips_alu_1_equal),
    .Result(mips_alu_1_result), .shamt(multiplexer_11_out));  // open: Result_2
  Multiplexer #(.width(5), .enable("false")) multiplexer_11 (
    .in0(id_ex_1_shamt_in_2), .in1(a0[4:0]), .out(multiplexer_11_out), .sel(SLLV_EX));
  Adder #(.width(32)) adder_2 (.a(shifter_1_out), .b(EX_PC2), .out(adder_2_out));  // open: cin, cout
  // Probe on adder_2_out
  Register #(.width(32), .Select("low")) register_3 (.D(a0), .en(and_6_out), .Q(LedData), .clk(CLK), .clr(RST));
  or or_7 (nop, Branch, JR, JMP);
  Comparator #(.width(32)) comparator_2 (.a(32'h1), .b(mips_alu_1_result), .eq(comparator_2_eq));  // open: gt, lt
  or or_8 (or_8_out, comparator_2_eq, mips_alu_1_equal);
  Comparator #(.width(32)) comparator_3 (.a(multiplexer_10_out), .b(32'h22), .eq(Equal));  // open: gt, lt
  and and_8 (and_8_out, BLEZ_EX, or_8_out);
  EX_MEM ex_mem_1 (
    .MemtoReg_in(id_ex_1_memtogeg_out), .AluResult_in(mips_alu_1_result),
    .MemWrite_int(id_ex_1_memwrite_out), .R2_in(multiplexer_8_out), .RegWtire_in(EX_RegWrite),
    .PCr_in(EX_PC), .JAL_in(id_ex_1_jal_out), .RegDst_in(id_ex_1_regdst_out), .IR_in(EX_IR),
    .syscall_in(Syscall), .PC_in(EX_PC2), .halt_in(id_ex_1_halt_out), .MemtoReg_out(ex_mem_1_memtoreg_out),
    .AluResult_out(MEM_Alu), .MemWrite_out(MemWrite), .R2_out(MDin), .RegWtire_out(MEM_RegWrite),
    .PCr_out(M_PC), .JAL_out(ex_mem_1_jal_out), .RegDst_out(ex_mem_1_regdst_out), .IR_out(MEM_IR),
    .syscall_out(ex_mem_1_syscall_out), .PC_out(MEM_PC2), .halt_out(ex_mem_1_halt_out), .Reset(RST),
    .CLK(CLK), .Enable(run), .W__in(EX_WriteReg_num), .W__IN_2(MEM_WriteReg_num), .LBU_in(LBU_EX),
    .LBU_out(LBU_M));
  Counter #(.width(16), .max('hffff), .behavior("old")) counter_4 (
    .count(JMP), .Q(\无条件分支数 ), .clk(CLK), .clr(RST));  // open: load, D, carry, preset
  Adder #(.width(16)) adder_3 (.a(\无条件分支数 ), .b(\条件分支成功数 ), .out(adder_3_out));  // open: cin, cout
  Multiplier #(.width(16)) multiplier_1 (.a(adder_3_out), .b(16'h2), .out(multiplier_1_out));  // open: cin, cout
  Counter #(.width(16), .max('hffff), .behavior("old")) counter_5 (
    .count(Branch), .Q(\条件分支成功数 ), .clk(CLK), .clr(RST));  // open: load, D, carry, preset
  Adder #(.width(16)) adder_4 (.a(multiplier_1_out), .b(\LoadUse次数 ), .out(\插入气泡数 ));  // open: cin, cout
  RAM #(.addrWidth(10), .dataWidth(32), .bus("separate"), .Select("high")) ram_1 (
    .addr(MEM_Alu[11:2]), .din(MDin), .data({ram_1_data_4, ram_1_data_3, ram_1_data_2, ram_1_data}),
    .str(MemWrite), .clk(CLK), .clr(RST));  // open: sel, ld
  Multiplexer #(.select(2), .width(8), .enable("false")) multiplexer_12 (
    .in0(ram_1_data), .in1(ram_1_data_2), .in2(ram_1_data_3), .in3(ram_1_data_4), .out(multiplexer_12_out),
    .sel(MEM_Alu[1:0]));
  assign bit_extender_3_out = {{24{1'b0}}, multiplexer_12_out};  // Bit_Extender bit_extender_3
  D_Flip_Flop #(.Pre_Clr_Positions("LEGACY"), .enable("true"), .NewFFLayout("false")) d_ff_2 (
    .clk(IR1), .D(1'b1), .Q(d_ff_2_q), .reset(IR1_q));  // open: Qn, preset, en
  or or_9 (W1, IR1_q, d_ff_2_q);
  D_Flip_Flop #(.Pre_Clr_Positions("LEGACY"), .enable("true"), .NewFFLayout("false")) d_ff_3 (
    .clk(IR2), .D(1'b1), .Q(d_ff_3_q), .reset(IR2_q));  // open: Qn, preset, en
  or or_10 (W2, IR2_q, d_ff_3_q);
  D_Flip_Flop #(.Pre_Clr_Positions("LEGACY"), .enable("true"), .NewFFLayout("false")) d_ff_4 (
    .clk(IR3), .D(1'b1), .Q(d_ff_4_q), .reset(IR3_q));  // open: Qn, preset, en
  or or_11 (W3, IR3_q, d_ff_4_q);
  MEM_WB mem_wb_1 (
    .AluResult_in(MEM_Alu), .MemtoReg_in(ex_mem_1_memtoreg_out), .MemD_in(multiplexer_13_out),
    .RegWtire_in(MEM_RegWrite), .PCr_in(M_PC), .JAL_in(ex_mem_1_jal_out), .RegDst_in(ex_mem_1_regdst_out),
    .IR_in(MEM_IR), .syscall_in(ex_mem_1_syscall_out), .PC_in(MEM_PC2), .halt_in(ex_mem_1_halt_out),
    .AluResult_out(WB_Alu), .MemtoReg_out(MemtoReg), .MemD_out(WB_MD), .RegWtire_out(RegWrite),
    .PCr_out(WB_PC), .JAL_out(JAL), .RegDst_out(RegDst), .IR_out(WB_IR), .syscall_out(sys),
    .PC_out(mem_wb_1_pc_out), .halt_out(mem_wb_1_halt_out), .Reset(RST), .CLK(CLK), .Enable(run),
    .W__in(MEM_WriteReg_num), .LBU_in(LBU_M), .LBU_out(LBU_W));  // open: W__IN_2, go
  Multiplexer #(.width(32), .enable("false")) multiplexer_13 (
    .in0({ram_1_data_4, ram_1_data_3, ram_1_data_2, ram_1_data}), .in1(bit_extender_3_out),
    .out(multiplexer_13_out), .sel(LBU_M));
  or or_12 (or_12_out, d_ff_2_q, IR1_q);
  or or_13 (or_13_out, d_ff_3_q, IR2_q);
  or or_14 (or_14_out, d_ff_4_q, IR3_q);
  not not_1 (run, mem_wb_1_halt_out);
  Multiplexer #(.width(32), .enable("false")) multiplexer_14 (
    .in0(WB_Alu), .in1(WB_MD), .out(multiplexer_14_out), .sel(MemtoReg));
  and and_9 (and_9_out, or_12_out, ~and_10_out);  // AND_Gate
  and and_10 (and_10_out, ERET, IR_now[0], ~IR_now[1]);  // AND_Gate
  and and_11 (and_11_out, or_13_out, ~and_12_out);  // AND_Gate
  and and_12 (and_12_out, ERET, ~IR_now[0], IR_now[1]);  // AND_Gate
  and and_13 (and_13_out, or_14_out, ~and_14_out);  // AND_Gate
  and and_14 (and_14_out, ERET, IR_now[0], IR_now[1]);
  Multiplexer #(.width(5), .enable("false")) multiplexer_15 (
    .in0(WB_IR[20:16]), .in1(WB_IR[15:11]), .out(multiplexer_15_out), .sel(RegDst));
  D_Flip_Flop #(.Pre_Clr_Positions("LEGACY"), .enable("true"), .NewFFLayout("false")) u_IR1 (
    .clk(CLK), .D(and_9_out), .Q(IR1_q));  // open: Qn, preset, en, reset
  D_Flip_Flop #(.Pre_Clr_Positions("LEGACY"), .enable("true"), .NewFFLayout("false")) u_IR2 (
    .clk(CLK), .D(and_11_out), .Q(IR2_q));  // open: Qn, preset, en, reset
  D_Flip_Flop #(.Pre_Clr_Positions("LEGACY"), .enable("true"), .NewFFLayout("false")) u_IR3 (
    .clk(CLK), .D(and_13_out), .Q(IR3_q));  // open: Qn, preset, en, reset
  Multiplexer #(.width(5), .enable("false")) multiplexer_16 (
    .in0(multiplexer_15_out), .in1({5{1'b1}}), .out(multiplexer_16_out), .sel(JAL));
  Priority_Encoder #(.select(2)) priority_encoder_1 (
    .in0(1'b1), .in1(IR1_q), .in2(IR2_q), .in3(IR3_q), .out(priority_encoder_1_out),
    .gs(priority_encoder_1_gs));  // open: en_out, en_in
  Multiplexer #(.select(2), .width(8), .enable("false")) multiplexer_17 (
    .in0(undriven_2[7:0]), .in1(undriven_2[15:8]), .in2(undriven_2[23:16]), .in3(undriven_2[31:24]),
    .out(multiplexer_17_out), .sel(undriven_3));
  assign bit_extender_4_out = {{24{1'b0}}, multiplexer_17_out};  // Bit_Extender bit_extender_4
  // Probe on priority_encoder_1_out
  Multiplexer #(.select(2), .enable("false")) multiplexer_18 (
    .in0(1'b0), .in1(priority_encoder_1_gs), .in2(priority_encoder_1_gs), .in3(priority_encoder_1_gs),
    .out(multiplexer_18_out), .sel(priority_encoder_1_out));
  Multiplexer #(.width(32), .enable("false")) multiplexer_19 (
    .in0(undriven_2), .in1(bit_extender_4_out), .sel(LBU_W));  // open: out
  Multiplexer #(.width(32), .enable("false")) multiplexer_20 (
    .in0(nextPC), .in1(multiplexer_21_out), .out(multiplexer_20_out), .sel(IE));
  Multiplexer #(.select(2), .width(32), .enable("false")) multiplexer_21 (
    .in0(nextPC), .in1(32'h30ac), .in2(32'h3150), .in3(32'h31f4), .out(multiplexer_21_out),
    .sel(priority_encoder_1_out));
  and and_15 (IE, multiplexer_18_out, ~\中断状态_q );  // AND_Gate
  Multiplexer #(.width(32), .enable("false")) multiplexer_22 (
    .in0(multiplexer_14_out), .in1(mem_wb_1_pc_out), .out(RDin), .sel(JAL));
  Register #(.width(32), .Select("low")) EPC (.D(ID_PC), .en(IE), .Q(EPC_q), .clk(CLK));  // open: clr
  or or_15 (or_15_out, IE, ERET);
  Register #(.width(1), .Select("low")) \u_中断状态  (.D(1'b1), .en(IE), .Q(\中断状态_q ), .clk(CLK), .clr(ERET));
  // Probe on PCout
  Multiplexer #(.width(32), .enable("false")) multiplexer_23 (
    .in0(multiplexer_20_out), .in1(EPC_q), .out(PCout), .sel(ERET));
  Multiplexer #(.width(2), .enable("false")) multiplexer_24 (
    .in0(priority_encoder_1_out), .in1(2'b00), .out(multiplexer_24_out), .sel(ERET));
  Register #(.width(2), .Select("low")) cause (
    .D(multiplexer_24_out), .en(or_15_out), .Q(IR_now), .clk(CLK));  // open: clr

  // Other names for the same wires on the sheet: ID_IR[5:0] = ID_Func; EX_OP[5:0] = EX_IR[31:26];
  //   ID_OP[5:0] = ID_IR[31:26]; MEM_OP[5:0] = MEM_IR[31:26]; MEM_PC[31:0] = M_PC

  // Notes on the sheet:
  //   中断源
  //   时空图监测，可删除
  //   中断等待指示
  //   数码管输出
  //   指令字
  //   contents of rom_1 (hex, n*v repeats v):
  //   201d07d0 20100001 109fc0 139fc3 8021 2012000c 24160008 26100001 3210000f 20080008 20090001 139900
  //   2709825 132020 20020022 c 1094022 1500fff9 22100001 2018000f 2188024 108700 20080008 20090001 139902
  //   2709825 132021 20020022 c 1094022 1500fff9 108702 2c9b022 12c00001 8000c07 4020 1084027 84400
  //   3508ffff 82021 20020022 c 8000c01 afa20000 23bd0004 afa40000 23bd0004 afb00000 23bd0004 afb30000
  //   23bd0004 afb40000 23bd0004 afb50000 23bd0004 afb60000 23bd0004 20160001 20140003 20150001 168020
  //   108100 2149825 132020 20020022 c 1600fffa 295a022 1680fff7 23bdfffc 8fb60000 23bdfffc 8fb50000
  //   23bdfffc 8fb40000 23bdfffc 8fb30000 23bdfffc 8fb00000 23bdfffc 8fa40000 23bdfffc 8fa20000 42000018
  //   afa20000 23bd0004 afa40000 23bd0004 afb00000 23bd0004 afb30000 23bd0004 afb40000 23bd0004 afb50000
  //   23bd0004 afb60000 23bd0004 20160002 20140003 20150001 168020 108100 2149825 132020 20020022 c
  //   1600fffa 295a022 1680fff7 23bdfffc 8fb60000 23bdfffc 8fb50000 23bdfffc 8fb40000 23bdfffc 8fb30000
  //   23bdfffc 8fb00000 23bdfffc 8fa40000 23bdfffc 8fa20000 42000018 afa20000 23bd0004 afa40000 23bd0004
  //   afb00000 23bd0004 afb30000 23bd0004 afb40000 23bd0004 afb50000 23bd0004 afb60000 23bd0004 20160003
  //   20140003 20150001 168020 108100 2149825 132020 20020022 c 1600fffa 295a022 1680fff7 23bdfffc
  //   8fb60000 23bdfffc 8fb50000 23bdfffc 8fb40000 23bdfffc 8fb30000 23bdfffc 8fb00000 23bdfffc 8fa40000
  //   23bdfffc 8fa20000 42000018
  //   OP
  //   Func
  //   rs
  //   rt
  //   rd
  //   shamt
  //   imm16
  //   控制位
  //   (PC+4)U4+imm26<<2
  //   流水调试日志用
  //   暂停节拍，不能为0
  //   Beq
  //   JMP
  //   JR
  //   Bne
  //   OP
  //   JAL
  //   Func
  //   Syscall
  //   戳工具置1进入计数暂停模式，ctrl+k时钟自动运行到对应节拍暂停
  //   ctrl+k关闭时钟连续运行，将控制位置零，进入单步调试模式调试
  //   MemToReg
  //   MemWrite
  //   AluOP
  //   AluSrcB
  //   RegWrite
  //   RegDst
  //   可计数暂停的时钟源
  //   为方便自动评测，需要输出流水线各段保存的PC值，注意是PC不是PC+4，另外ID段寄存器写入信息，Mem段内存写入信息也要输出
  //   rt
  //   rd
  //   Reset 
  //   Reset 
  //   Reset 
endmodule

module \封装正确性测试  (
);

  wire IR1, IR2, IR3, MemW, RegW;
  wire [31:0] EX_PC, ID_PC, IF_PC, IR, LED, MDin, MDinr, MEM_PC, PC, RDin, RDinr, WB_PC;

  \单周期MIPS  \u_单周期mips_1  (
    .RegWrite(RegW), .MemWrite(MemW), .PC(PC), .IR(IR), .RDin(RDin), .MDin(MDin), .LedData(LED));  // open: IR1, IR2, IR3
  \气泡流水线  \u_气泡流水线_1  (
    .RegWrite(RegW), .MemWrite(MemW), .IF_PC(IF_PC), .ID_PC(ID_PC), .EX_PC(EX_PC), .M_PC(MEM_PC),
    .WB_PC(WB_PC), .RDin(RDinr), .MDin(MDinr), .LedData(LED));
  \单周期MIPS_单级中断  \u_单周期mips_单级中断_1  (
    .IR1(IR1), .IR2(IR2), .IR3(IR3), .RegWrite(RegW), .MemWrite(MemW), .PC(PC), .IR(IR), .RDin(RDin),
    .MDin(MDin), .LedData(LED));
  \理想流水线  \u_理想流水线_1  (
    .RegWrite(RegW), .MemWrite(MemW), .IF_PC(IF_PC), .ID_PC(ID_PC), .EX_PC(EX_PC), .M_PC(MEM_PC),
    .WB_PC(WB_PC), .RDin(RDinr), .MDin(MDinr), .LedData(LED));
  \重定向流水线  \u_重定向流水线_1  (
    .RegWrite(RegW), .MemWrite(MemW), .IF_PC(IF_PC), .ID_PC(ID_PC), .EX_PC(EX_PC), .M_PC(MEM_PC),
    .WB_PC(WB_PC), .RDin(RDinr), .MDin(MDinr), .LedData(LED));
  \单周期MIPS_多级中断  \u_单周期mips_多级中断_1  (
    .IR1(IR1), .IR2(IR2), .IR3(IR3), .RegWrite(RegW), .MemWrite(MemW), .PC(PC), .IR(IR), .RDin(RDin),
    .MDin(MDin), .LedData(LED));

  // Notes on the sheet:
  //   单周期封装测试
  //   气泡流水封装测试
  //   单周期+单级中断封装测试
  //   请检查上面封装有无位宽不匹配，引脚标签是否和连接的标签相对应，否则无法在educoder平台上正确测试
  //   理想流水封装测试
  //   重定向流水封装测试
  //   单周期+多级中断封装测试
endmodule

module IF_ID (
  input  [31:0] ir_in,
  input  [31:0] pcr_in,
  input  [31:0] pc_in,
  input  Reset,
  input  CLK,
  input  Enable,
  output [31:0] ir_out,
  output [31:0] pcr_out,
  output [31:0] pc_out
);

  wire [31:0] multiplexer_1_out, multiplexer_2_out, multiplexer_3_out;

  Multiplexer #(.width(32), .enable("false")) multiplexer_1 (
    .in0(ir_in), .in1({32{1'b0}}), .out(multiplexer_1_out), .sel(Reset));
  Multiplexer #(.width(32), .enable("false")) multiplexer_2 (
    .in0(pcr_in), .in1({32{1'b0}}), .out(multiplexer_2_out), .sel(Reset));
  Multiplexer #(.width(32), .enable("false")) multiplexer_3 (
    .in0(pc_in), .in1({32{1'b0}}), .out(multiplexer_3_out), .sel(Reset));
  Register #(.width(32), .Select("low")) register_1 (
    .D(multiplexer_1_out), .en(Enable), .Q(ir_out), .clk(CLK));  // open: clr
  Register #(.width(32), .Select("low")) register_2 (
    .D(multiplexer_2_out), .en(Enable), .Q(pcr_out), .clk(CLK));  // open: clr
  Register #(.width(32), .Select("low")) register_3 (
    .D(multiplexer_3_out), .en(Enable), .Q(pc_out), .clk(CLK));  // open: clr
endmodule

module ID_EX (
  input  jr_in,
  input  [31:0] R1_in,
  input  [31:0] Eimm_in,
  input  jmp_in,
  input  BLEZ_in,
  input  beq_in,
  input  [31:0] R2_in,
  input  LBU_in,
  input  bne_in,
  input  [31:0] Address_in,
  input  memtogeg_in,
  input  memwrite_in,
  input  [31:0] pcr_in,
  input  [4:0] shamt_in,
  input  [3:0] AluOp_in,
  input  AluSrcB_in,
  input  syscall_in,
  input  RegWrite_in,
  input  [31:0] pc_in,
  input  JAL_in,
  input  RegDst_in,
  input  [4:0] W__in,
  input  [31:0] ir_in,
  input  halt_in,
  input  SLLV_in,
  input  Rest,
  input  CLK,
  input  Enable,
  output jr_out,
  output [31:0] R1_out,
  output [31:0] Eimm_out,
  output jmp_out,
  output BLEZ_out,
  output beq_out,
  output [31:0] R2_out,
  output LBU_out,
  output bne_out,
  output [31:0] Address_out,
  output memtogeg_out,
  output memwrite_out,
  output [31:0] pcr_out,
  output [4:0] shamt_in_2,
  output [3:0] AluOp_out,
  output AluSrcB_out,
  output syscall_out,
  output RegWrite_out,
  output [31:0] pc_out,
  output JAL_out,
  output RegDst_out,
  output [4:0] W__IN_2,
  output [31:0] ir_out,
  output halt_out,
  output SLLV_out
);

  wire multiplexer_1_out, multiplexer_2_out, multiplexer_3_out, multiplexer_4_out, multiplexer_5_out,
       multiplexer_6_out, multiplexer_8_out, multiplexer_9_out, multiplexer_10_out, multiplexer_11_out,
       multiplexer_12_out, multiplexer_21_out, multiplexer_23_out, multiplexer_24_out, multiplexer_25_out;
  wire [3:0] multiplexer_7_out;
  wire [4:0] multiplexer_20_out, multiplexer_22_out;
  wire [31:0] multiplexer_13_out, multiplexer_14_out, multiplexer_15_out, multiplexer_16_out,
       multiplexer_17_out, multiplexer_18_out, multiplexer_19_out;

  Multiplexer #(.enable("false")) multiplexer_1 (.in0(jr_in), .in1(1'b0), .out(multiplexer_1_out), .sel(Rest));
  Multiplexer #(.enable("false")) multiplexer_2 (.in0(jmp_in), .in1(1'b0), .out(multiplexer_2_out), .sel(Rest));
  Multiplexer #(.enable("false")) multiplexer_3 (.in0(beq_in), .in1(1'b0), .out(multiplexer_3_out), .sel(Rest));
  Multiplexer #(.enable("false")) multiplexer_4 (.in0(bne_in), .in1(1'b0), .out(multiplexer_4_out), .sel(Rest));
  Multiplexer #(.enable("false")) multiplexer_5 (.in0(memtogeg_in), .in1(1'b0), .out(multiplexer_5_out), .sel(Rest));
  Multiplexer #(.enable("false")) multiplexer_6 (.in0(memwrite_in), .in1(1'b0), .out(multiplexer_6_out), .sel(Rest));
  Multiplexer #(.width(4), .enable("false")) multiplexer_7 (
    .in0(AluOp_in), .in1(4'b0000), .out(multiplexer_7_out), .sel(Rest));
  Multiplexer #(.enable("false")) multiplexer_8 (.in0(AluSrcB_in), .in1(1'b0), .out(multiplexer_8_out), .sel(Rest));
  Multiplexer #(.enable("false")) multiplexer_9 (.in0(RegWrite_in), .in1(1'b0), .out(multiplexer_9_out), .sel(Rest));
  Multiplexer #(.enable("false")) multiplexer_10 (.in0(JAL_in), .in1(1'b0), .out(multiplexer_10_out), .sel(Rest));
  Multiplexer #(.enable("false")) multiplexer_11 (.in0(RegDst_in), .in1(1'b0), .out(multiplexer_11_out), .sel(Rest));
  Multiplexer #(.enable("false")) multiplexer_12 (.in0(halt_in), .in1(1'b0), .out(multiplexer_12_out), .sel(Rest));
  Register #(.width(1), .Select("low")) register_1 (
    .D(multiplexer_1_out), .en(Enable), .Q(jr_out), .clk(CLK));  // open: clr
  Register #(.width(1), .Select("low")) register_2 (
    .D(multiplexer_2_out), .en(Enable), .Q(jmp_out), .clk(CLK));  // open: clr
  Register #(.width(1), .Select("low")) register_3 (
    .D(multiplexer_3_out), .en(Enable), .Q(beq_out), .clk(CLK));  // open: clr
  Register #(.width(1), .Select("low")) register_4 (
    .D(multiplexer_4_out), .en(Enable), .Q(bne_out), .clk(CLK));  // open: clr
  Register #(.width(1), .Select("low")) register_5 (
    .D(multiplexer_5_out), .en(Enable), .Q(memtogeg_out), .clk(CLK));  // open: clr
  Register #(.width(1), .Select("low")) register_6 (
    .D(multiplexer_6_out), .en(Enable), .Q(memwrite_out), .clk(CLK));  // open: clr
  Register #(.width(4), .Select("low")) register_7 (
    .D(multiplexer_7_out), .en(Enable), .Q(AluOp_out), .clk(CLK));  // open: clr
  Register #(.width(1), .Select("low")) register_8 (
    .D(multiplexer_8_out), .en(Enable), .Q(AluSrcB_out), .clk(CLK));  // open: clr
  Register #(.width(1), .Select("low")) register_9 (
    .D(multiplexer_9_out), .en(Enable), .Q(RegWrite_out), .clk(CLK));  // open: clr
  Register #(.width(1), .Select("low")) register_10 (
    .D(multiplexer_10_out), .en(Enable), .Q(JAL_out), .clk(CLK));  // open: clr
  Register #(.width(1), .Select("low")) register_11 (
    .D(multiplexer_11_out), .en(Enable), .Q(RegDst_out), .clk(CLK));  // open: clr
  Register #(.width(1), .Select("low")) register_12 (
    .D(multiplexer_12_out), .en(Enable), .Q(halt_out), .clk(CLK));  // open: clr
  Multiplexer #(.width(32), .enable("false")) multiplexer_13 (
    .in0(R1_in), .in1({32{1'b0}}), .out(multiplexer_13_out), .sel(Rest));
  Multiplexer #(.width(32), .enable("false")) multiplexer_14 (
    .in0(R2_in), .in1({32{1'b0}}), .out(multiplexer_14_out), .sel(Rest));
  Multiplexer #(.width(32), .enable("false")) multiplexer_15 (
    .in0(pcr_in), .in1({32{1'b0}}), .out(multiplexer_15_out), .sel(Rest));
  Multiplexer #(.width(32), .enable("false")) multiplexer_16 (
    .in0(pc_in), .in1({32{1'b0}}), .out(multiplexer_16_out), .sel(Rest));
  Multiplexer #(.width(32), .enable("false")) multiplexer_17 (
    .in0(ir_in), .in1({32{1'b0}}), .out(multiplexer_17_out), .sel(Rest));
  Register #(.width(32), .Select("low")) register_13 (
    .D(multiplexer_13_out), .en(Enable), .Q(R1_out), .clk(CLK));  // open: clr
  Register #(.width(32), .Select("low")) register_14 (
    .D(multiplexer_14_out), .en(Enable), .Q(R2_out), .clk(CLK));  // open: clr
  Register #(.width(32), .Select("low")) register_15 (
    .D(multiplexer_15_out), .en(Enable), .Q(pcr_out), .clk(CLK));  // open: clr
  Register #(.width(32), .Select("low")) register_16 (
    .D(multiplexer_16_out), .en(Enable), .Q(pc_out), .clk(CLK));  // open: clr
  Register #(.width(32), .Select("low")) register_17 (
    .D(multiplexer_17_out), .en(Enable), .Q(ir_out), .clk(CLK));  // open: clr
  Multiplexer #(.width(32), .enable("false")) multiplexer_18 (
    .in0(Eimm_in), .in1({32{1'b0}}), .out(multiplexer_18_out), .sel(Rest));
  Multiplexer #(.width(32), .enable("false")) multiplexer_19 (
    .in0(Address_in), .in1({32{1'b0}}), .out(multiplexer_19_out), .sel(Rest));
  Multiplexer #(.width(5), .enable("false")) multiplexer_20 (
    .in0(shamt_in), .in1({5{1'b0}}), .out(multiplexer_20_out), .sel(Rest));
  Multiplexer #(.enable("false")) multiplexer_21 (.in0(syscall_in), .in1(1'b0), .out(multiplexer_21_out), .sel(Rest));
  Multiplexer #(.width(5), .enable("false")) multiplexer_22 (
    .in0(W__in), .in1({5{1'b0}}), .out(multiplexer_22_out), .sel(Rest));
  Multiplexer #(.enable("false")) multiplexer_23 (.in0(SLLV_in), .in1(1'b0), .out(multiplexer_23_out), .sel(Rest));
  Register #(.width(32), .Select("low")) register_18 (
    .D(multiplexer_18_out), .en(Enable), .Q(Eimm_out), .clk(CLK));  // open: clr
  Register #(.width(32), .Select("low")) register_19 (
    .D(multiplexer_19_out), .en(Enable), .Q(Address_out), .clk(CLK));  // open: clr
  Register #(.width(5), .Select("low")) register_20 (
    .D(multiplexer_20_out), .en(Enable), .Q(shamt_in_2), .clk(CLK));  // open: clr
  Register #(.width(1), .Select("low")) register_21 (
    .D(multiplexer_21_out), .en(Enable), .Q(syscall_out), .clk(CLK));  // open: clr
  Register #(.width(5), .Select("low")) register_22 (
    .D(multiplexer_22_out), .en(Enable), .Q(W__IN_2), .clk(CLK));  // open: clr
  Register #(.width(1), .Select("low")) register_23 (
    .D(multiplexer_23_out), .en(Enable), .Q(SLLV_out), .clk(CLK));  // open: clr
  Multiplexer #(.enable("false")) multiplexer_24 (.in0(BLEZ_in), .in1(1'b0), .out(multiplexer_24_out), .sel(Rest));
  Multiplexer #(.enable("false")) multiplexer_25 (.in0(LBU_in), .in1(1'b0), .out(multiplexer_25_out), .sel(Rest));
  Register #(.width(1), .Select("low")) register_24 (
    .D(multiplexer_24_out), .en(Enable), .Q(BLEZ_out), .clk(CLK));  // open: clr
  Register #(.width(1), .Select("low")) register_25 (
    .D(multiplexer_25_out), .en(Enable), .Q(LBU_out), .clk(CLK));  // open: clr
endmodule

module EX_MEM (
  input  MemtoReg_in,
  input  [31:0] AluResult_in,
  input  MemWrite_int,
  input  [31:0] R2_in,
  input  RegWtire_in,
  input  [31:0] PCr_in,
  input  JAL_in,
  input  RegDst_in,
  input  [31:0] IR_in,
  input  syscall_in,
  input  [31:0] PC_in,
  input  halt_in,
  input  [4:0] W__in,
  input  LBU_in,
  input  Reset,
  input  CLK,
  input  Enable,
  output MemtoReg_out,
  output [31:0] AluResult_out,
  output MemWrite_out,
  output [31:0] R2_out,
  output RegWtire_out,
  output [31:0] PCr_out,
  output JAL_out,
  output RegDst_out,
  output [31:0] IR_out,
  output syscall_out,
  output [31:0] PC_out,
  output halt_out,
  output [4:0] W__IN_2,
  output LBU_out
);

  wire multiplexer_1_out, multiplexer_2_out, multiplexer_3_out, multiplexer_4_out, multiplexer_5_out,
       multiplexer_6_out, multiplexer_7_out, multiplexer_8_out;
  wire [4:0] multiplexer_14_out;
  wire [31:0] multiplexer_9_out, multiplexer_10_out, multiplexer_11_out, multiplexer_12_out,
       multiplexer_13_out;

  Multiplexer #(.enable("false")) multiplexer_1 (.in0(MemtoReg_in), .in1(1'b0), .out(multiplexer_1_out), .sel(Reset));
  Multiplexer #(.enable("false")) multiplexer_2 (.in0(MemWrite_int), .in1(1'b0), .out(multiplexer_2_out), .sel(Reset));
  Multiplexer #(.enable("false")) multiplexer_3 (.in0(RegWtire_in), .in1(1'b0), .out(multiplexer_3_out), .sel(Reset));
  Multiplexer #(.enable("false")) multiplexer_4 (.in0(JAL_in), .in1(1'b0), .out(multiplexer_4_out), .sel(Reset));
  Multiplexer #(.enable("false")) multiplexer_5 (.in0(RegDst_in), .in1(1'b0), .out(multiplexer_5_out), .sel(Reset));
  Multiplexer #(.enable("false")) multiplexer_6 (.in0(syscall_in), .in1(1'b0), .out(multiplexer_6_out), .sel(Reset));
  Multiplexer #(.enable("false")) multiplexer_7 (.in0(halt_in), .in1(1'b0), .out(multiplexer_7_out), .sel(Reset));
  Multiplexer #(.enable("false")) multiplexer_8 (.in0(LBU_in), .in1(1'b0), .out(multiplexer_8_out), .sel(Reset));
  Register #(.width(1), .Select("low")) register_1 (
    .D(multiplexer_1_out), .en(Enable), .Q(MemtoReg_out), .clk(CLK));  // open: clr
  Register #(.width(1), .Select("low")) register_2 (
    .D(multiplexer_2_out), .en(Enable), .Q(MemWrite_out), .clk(CLK));  // open: clr
  Register #(.width(1), .Select("low")) register_3 (
    .D(multiplexer_3_out), .en(Enable), .Q(RegWtire_out), .clk(CLK));  // open: clr
  Register #(.width(1), .Select("low")) register_4 (
    .D(multiplexer_4_out), .en(Enable), .Q(JAL_out), .clk(CLK));  // open: clr
  Register #(.width(1), .Select("low")) register_5 (
    .D(multiplexer_5_out), .en(Enable), .Q(RegDst_out), .clk(CLK));  // open: clr
  Register #(.width(1), .Select("low")) register_6 (
    .D(multiplexer_6_out), .en(Enable), .Q(syscall_out), .clk(CLK));  // open: clr
  Register #(.width(1), .Select("low")) register_7 (
    .D(multiplexer_7_out), .en(Enable), .Q(halt_out), .clk(CLK));  // open: clr
  Register #(.width(1), .Select("low")) register_8 (
    .D(multiplexer_8_out), .en(Enable), .Q(LBU_out), .clk(CLK));  // open: clr
  Multiplexer #(.width(32), .enable("false")) multiplexer_9 (
    .in0(AluResult_in), .in1({32{1'b0}}), .out(multiplexer_9_out), .sel(Reset));
  Multiplexer #(.width(32), .enable("false")) multiplexer_10 (
    .in0(R2_in), .in1({32{1'b0}}), .out(multiplexer_10_out), .sel(Reset));
  Multiplexer #(.width(32), .enable("false")) multiplexer_11 (
    .in0(PCr_in), .in1({32{1'b0}}), .out(multiplexer_11_out), .sel(Reset));
  Multiplexer #(.width(32), .enable("false")) multiplexer_12 (
    .in0(IR_in), .in1({32{1'b0}}), .out(multiplexer_12_out), .sel(Reset));
  Multiplexer #(.width(32), .enable("false")) multiplexer_13 (
    .in0(PC_in), .in1({32{1'b0}}), .out(multiplexer_13_out), .sel(Reset));
  Multiplexer #(.width(5), .enable("false")) multiplexer_14 (
    .in0(W__in), .in1({5{1'b0}}), .out(multiplexer_14_out), .sel(Reset));
  Register #(.width(32), .Select("low")) register_9 (
    .D(multiplexer_9_out), .en(Enable), .Q(AluResult_out), .clk(CLK));  // open: clr
  Register #(.width(32), .Select("low")) register_10 (
    .D(multiplexer_10_out), .en(Enable), .Q(R2_out), .clk(CLK));  // open: clr
  Register #(.width(32), .Select("low")) register_11 (
    .D(multiplexer_11_out), .en(Enable), .Q(PCr_out), .clk(CLK));  // open: clr
  Register #(.width(32), .Select("low")) register_12 (
    .D(multiplexer_12_out), .en(Enable), .Q(IR_out), .clk(CLK));  // open: clr
  Register #(.width(32), .Select("low")) register_13 (
    .D(multiplexer_13_out), .en(Enable), .Q(PC_out), .clk(CLK));  // open: clr
  Register #(.width(5), .Select("low")) register_14 (
    .D(multiplexer_14_out), .en(Enable), .Q(W__IN_2), .clk(CLK));  // open: clr
endmodule

module MEM_WB (
  input  [31:0] AluResult_in,
  input  MemtoReg_in,
  input  [31:0] MemD_in,
  input  RegWtire_in,
  input  [31:0] PCr_in,
  input  JAL_in,
  input  RegDst_in,
  input  [31:0] IR_in,
  input  syscall_in,
  input  go,
  input  [31:0] PC_in,
  input  halt_in,
  input  [4:0] W__in,
  input  LBU_in,
  input  Reset,
  input  CLK,
  input  Enable,
  output [31:0] AluResult_out,
  output MemtoReg_out,
  output [31:0] MemD_out,
  output RegWtire_out,
  output [31:0] PCr_out,
  output JAL_out,
  output RegDst_out,
  output [31:0] IR_out,
  output syscall_out,
  output [31:0] PC_out,
  output halt_out,
  output [4:0] W__IN_2,
  output LBU_out
);

  wire multiplexer_1_out, multiplexer_2_out, multiplexer_3_out, multiplexer_4_out, multiplexer_5_out,
       multiplexer_6_out, multiplexer_7_out;
  wire [4:0] multiplexer_13_out;
  wire [31:0] multiplexer_8_out, multiplexer_9_out, multiplexer_10_out, multiplexer_11_out,
       multiplexer_12_out;

  Multiplexer #(.enable("false")) multiplexer_1 (.in0(MemtoReg_in), .in1(1'b0), .out(multiplexer_1_out), .sel(Reset));
  Multiplexer #(.enable("false")) multiplexer_2 (.in0(RegWtire_in), .in1(1'b0), .out(multiplexer_2_out), .sel(Reset));
  Multiplexer #(.enable("false")) multiplexer_3 (.in0(JAL_in), .in1(1'b0), .out(multiplexer_3_out), .sel(Reset));
  Multiplexer #(.enable("false")) multiplexer_4 (.in0(RegDst_in), .in1(1'b0), .out(multiplexer_4_out), .sel(Reset));
  Multiplexer #(.enable("false")) multiplexer_5 (.in0(syscall_in), .in1(1'b0), .out(multiplexer_5_out), .sel(Reset));
  Multiplexer #(.enable("false")) multiplexer_6 (.in0(halt_in), .in1(1'b0), .out(multiplexer_6_out), .sel(Reset));
  Multiplexer #(.enable("false")) multiplexer_7 (.in0(LBU_in), .in1(1'b0), .out(multiplexer_7_out), .sel(Reset));
  Register #(.width(1), .Select("low")) register_1 (
    .D(multiplexer_1_out), .en(Enable), .Q(MemtoReg_out), .clk(CLK));  // open: clr
  Register #(.width(1), .Select("low")) register_2 (
    .D(multiplexer_2_out), .en(Enable), .Q(RegWtire_out), .clk(CLK));  // open: clr
  Register #(.width(1), .Select("low")) register_3 (
    .D(multiplexer_3_out), .en(Enable), .Q(JAL_out), .clk(CLK));  // open: clr
  Register #(.width(1), .Select("low")) register_4 (
    .D(multiplexer_4_out), .en(Enable), .Q(RegDst_out), .clk(CLK));  // open: clr
  Register #(.width(1), .Select("low")) register_5 (
    .D(multiplexer_5_out), .en(Enable), .Q(syscall_out), .clk(CLK));  // open: clr
  Register #(.width(1), .Select("low")) register_6 (
    .D(multiplexer_6_out), .en(Enable), .Q(halt_out), .clk(CLK), .clr(go));
  Register #(.width(1), .Select("low")) register_7 (
    .D(multiplexer_7_out), .en(Enable), .Q(LBU_out), .clk(CLK));  // open: clr
  Multiplexer #(.width(32), .enable("false")) multiplexer_8 (
    .in0(AluResult_in), .in1({32{1'b0}}), .out(multiplexer_8_out), .sel(Reset));
  Multiplexer #(.width(32), .enable("false")) multiplexer_9 (
    .in0(MemD_in), .in1({32{1'b0}}), .out(multiplexer_9_out), .sel(Reset));
  Multiplexer #(.width(32), .enable("false")) multiplexer_10 (
    .in0(PCr_in), .in1({32{1'b0}}), .out(multiplexer_10_out), .sel(Reset));
  Multiplexer #(.width(32), .enable("false")) multiplexer_11 (
    .in0(IR_in), .in1({32{1'b0}}), .out(multiplexer_11_out), .sel(Reset));
  Multiplexer #(.width(32), .enable("false")) multiplexer_12 (
    .in0(PC_in), .in1({32{1'b0}}), .out(multiplexer_12_out), .sel(Reset));
  Multiplexer #(.width(5), .enable("false")) multiplexer_13 (
    .in0(W__in), .in1({5{1'b0}}), .out(multiplexer_13_out), .sel(Reset));
  Register #(.width(32), .Select("low")) register_8 (
    .D(multiplexer_8_out), .en(Enable), .Q(AluResult_out), .clk(CLK));  // open: clr
  Register #(.width(32), .Select("low")) register_9 (
    .D(multiplexer_9_out), .en(Enable), .Q(MemD_out), .clk(CLK));  // open: clr
  Register #(.width(32), .Select("low")) register_10 (
    .D(multiplexer_10_out), .en(Enable), .Q(PCr_out), .clk(CLK));  // open: clr
  Register #(.width(32), .Select("low")) register_11 (
    .D(multiplexer_11_out), .en(Enable), .Q(IR_out), .clk(CLK));  // open: clr
  Register #(.width(32), .Select("low")) register_12 (
    .D(multiplexer_12_out), .en(Enable), .Q(PC_out), .clk(CLK));  // open: clr
  Register #(.width(5), .Select("low")) register_13 (
    .D(multiplexer_13_out), .en(Enable), .Q(W__IN_2), .clk(CLK));  // open: clr
endmodule
module \源寄存器使用情况  (
  input  OP0,
  input  OP1,
  input  OP2,
  input  OP3,
  input  OP4,
  input  OP5,
  input  F0,
  input  F1,
  input  F2,
  input  F3,
  input  F4,
  input  F5,
  output R1_Used,
  output R2_Used
);

  wire and_1_out, and_2_out, and_3_out, and_4_out, and_5_out, and_6_out, and_7_out, and_8_out, and_9_out,
       and_10_out, and_11_out, and_12_out, and_13_out, and_14_out, and_15_out, and_16_out, and_17_out,
       and_18_out, and_19_out, and_20_out, and_21_out, and_22_out, and_23_out, and_24_out, and_25_out,
       and_26_out, and_27_out, and_28_out, and_29_out, and_30_out, and_31_out, and_32_out, and_33_out,
       and_34_out, and_35_out, and_36_out, and_37_out, and_38_out, and_39_out, and_40_out, and_41_out,
       and_42_out, not_1_out, not_2_out, not_3_out, not_4_out, not_5_out, not_6_out, not_7_out, not_8_out,
       not_9_out, not_10_out, not_11_out, not_12_out, not_13_out, not_14_out, not_15_out, not_16_out,
       not_17_out, not_18_out, not_19_out, not_20_out, not_21_out, not_22_out, not_23_out, not_24_out,
       not_25_out, not_26_out, not_27_out, not_28_out, not_29_out, not_30_out, not_31_out, not_32_out,
       not_33_out, not_34_out, not_35_out, not_36_out, not_37_out, not_38_out, not_39_out, not_40_out,
       not_41_out, not_42_out, not_43_out, not_44_out, not_45_out, not_46_out, not_47_out, not_48_out,
       not_49_out, not_50_out, not_51_out, not_52_out, not_53_out, not_54_out, not_55_out, not_56_out,
       not_57_out, not_58_out, not_59_out, not_60_out, not_61_out, not_62_out, not_63_out, not_64_out,
       not_65_out, not_66_out, not_67_out, not_68_out, not_69_out, not_70_out, not_71_out, not_72_out,
       not_73_out, not_74_out, not_75_out, not_76_out, not_77_out, not_78_out, not_79_out, not_80_out,
       not_81_out, not_82_out, not_83_out, not_84_out, not_85_out, not_86_out, not_87_out, not_88_out,
       not_89_out, not_90_out, not_91_out, not_92_out, not_93_out, not_94_out, not_95_out, not_96_out,
       not_97_out, not_98_out, not_99_out, not_100_out, not_101_out, not_102_out, not_103_out, not_104_out,
       not_105_out, not_106_out, not_107_out, not_108_out, not_109_out, not_110_out, not_111_out,
       not_112_out, not_113_out, not_114_out, not_115_out, not_116_out, not_117_out, not_118_out,
       not_119_out, not_120_out, not_121_out, not_122_out, not_123_out, not_124_out, not_125_out,
       not_126_out, not_127_out, not_128_out, not_129_out, not_130_out, not_131_out, not_132_out,
       not_133_out, not_134_out, not_135_out, not_136_out, not_137_out, not_138_out, not_139_out,
       not_140_out, not_141_out, not_142_out, not_143_out, not_144_out, not_145_out, not_146_out,
       not_147_out, not_148_out, not_149_out, not_150_out, not_151_out, not_152_out, not_153_out,
       not_154_out, not_155_out, not_156_out, not_157_out, not_158_out, not_159_out, not_160_out,
       not_161_out, not_162_out, not_163_out, not_164_out, not_165_out, not_166_out, not_167_out,
       not_168_out, not_169_out, not_170_out, not_171_out, not_172_out, not_173_out, not_174_out,
       not_175_out, not_176_out, not_177_out, not_178_out, not_179_out, not_180_out, not_181_out,
       not_182_out, not_183_out, not_184_out, not_185_out, not_186_out, not_187_out, not_188_out,
       not_189_out, not_190_out, not_191_out, not_192_out, not_193_out, not_194_out, not_195_out,
       not_196_out, not_197_out, not_198_out, not_199_out, not_200_out, not_201_out, not_202_out,
       not_203_out, not_204_out, not_205_out, not_206_out, not_207_out, not_208_out, not_209_out,
       not_210_out, not_211_out, not_212_out, not_213_out, not_214_out, not_215_out, not_216_out,
       not_217_out, not_218_out, not_219_out, not_220_out, not_221_out, not_222_out, not_223_out,
       not_224_out, not_225_out, not_226_out, not_227_out, not_228_out, not_229_out, not_230_out,
       not_231_out, not_232_out, not_233_out, not_234_out, not_235_out, not_236_out, not_237_out,
       not_238_out, not_239_out, not_240_out, not_241_out, not_242_out, not_243_out, not_244_out,
       not_245_out, not_246_out, not_247_out, not_248_out, not_249_out, not_250_out, not_251_out,
       not_252_out, not_253_out, not_254_out, not_255_out, not_256_out, not_257_out, not_258_out,
       not_259_out, not_260_out, not_261_out, not_262_out, not_263_out, not_264_out, not_265_out,
       not_266_out, not_267_out, not_268_out, not_269_out, not_270_out, not_271_out, not_272_out,
       not_273_out, not_274_out, not_275_out, not_276_out, not_277_out, not_278_out, not_279_out,
       not_280_out, not_281_out, not_282_out, not_283_out, not_284_out, not_285_out, not_286_out,
       not_287_out, not_288_out, not_289_out, not_290_out, not_291_out, not_292_out, not_293_out,
       not_294_out, not_295_out, not_296_out, not_297_out, not_298_out, not_299_out, not_300_out,
       not_301_out, not_302_out, not_303_out, not_304_out, not_305_out, not_306_out, not_307_out,
       not_308_out, not_309_out, not_310_out, not_311_out, not_312_out, not_313_out, not_314_out,
       not_315_out, not_316_out, not_317_out, not_318_out, not_319_out, not_320_out, not_321_out,
       not_322_out, not_323_out, not_324_out, not_325_out;

  not not_1 (not_1_out, OP5);
  not not_2 (not_2_out, OP4);
  not not_3 (not_3_out, OP3);
  not not_4 (not_4_out, OP2);
  not not_5 (not_5_out, OP1);
  not not_6 (not_6_out, OP0);
  not not_7 (not_7_out, F5);
  not not_8 (not_8_out, F4);
  not not_9 (not_9_out, F3);
  not not_10 (not_10_out, F2);
  not not_11 (not_11_out, F1);
  not not_12 (not_12_out, F0);
  not not_13 (not_13_out, OP5);
  not not_14 (not_14_out, OP4);
  not not_15 (not_15_out, OP3);
  not not_16 (not_16_out, OP2);
  not not_17 (not_17_out, OP1);
  not not_18 (not_18_out, OP0);
  not not_19 (not_19_out, F5);
  not not_20 (not_20_out, F4);
  not not_21 (not_21_out, F3);
  not not_22 (not_22_out, F2);
  not not_23 (not_23_out, OP5);
  not not_24 (not_24_out, OP4);
  not not_25 (not_25_out, OP3);
  not not_26 (not_26_out, OP2);
  not not_27 (not_27_out, OP1);
  not not_28 (not_28_out, OP0);
  not not_29 (not_29_out, F5);
  not not_30 (not_30_out, F4);
  not not_31 (not_31_out, F3);
  not not_32 (not_32_out, F2);
  not not_33 (not_33_out, F0);
  not not_34 (not_34_out, OP5);
  not not_35 (not_35_out, OP4);
  not not_36 (not_36_out, OP3);
  not not_37 (not_37_out, OP2);
  not not_38 (not_38_out, OP1);
  not not_39 (not_39_out, OP0);
  not not_40 (not_40_out, F4);
  not not_41 (not_41_out, F3);
  not not_42 (not_42_out, F2);
  not not_43 (not_43_out, F1);
  not not_44 (not_44_out, F0);
  not not_45 (not_45_out, OP5);
  not not_46 (not_46_out, OP4);
  not not_47 (not_47_out, OP3);
  not not_48 (not_48_out, OP2);
  not not_49 (not_49_out, OP1);
  not not_50 (not_50_out, OP0);
  not not_51 (not_51_out, F4);
  not not_52 (not_52_out, F3);
  not not_53 (not_53_out, F2);
  not not_54 (not_54_out, F1);
  not not_55 (not_55_out, OP5);
  not not_56 (not_56_out, OP4);
  not not_57 (not_57_out, OP3);
  not not_58 (not_58_out, OP2);
  not not_59 (not_59_out, OP1);
  not not_60 (not_60_out, OP0);
  not not_61 (not_61_out, F4);
  not not_62 (not_62_out, F3);
  not not_63 (not_63_out, F2);
  not not_64 (not_64_out, F0);
  not not_65 (not_65_out, OP5);
  not not_66 (not_66_out, OP4);
  not not_67 (not_67_out, OP3);
  not not_68 (not_68_out, OP2);
  not not_69 (not_69_out, OP1);
  not not_70 (not_70_out, OP0);
  not not_71 (not_71_out, F4);
  not not_72 (not_72_out, F3);
  not not_73 (not_73_out, F1);
  not not_74 (not_74_out, F0);
  not not_75 (not_75_out, OP5);
  not not_76 (not_76_out, OP4);
  not not_77 (not_77_out, OP3);
  not not_78 (not_78_out, OP2);
  not not_79 (not_79_out, OP1);
  not not_80 (not_80_out, OP0);
  not not_81 (not_81_out, F4);
  not not_82 (not_82_out, F3);
  not not_83 (not_83_out, F1);
  not not_84 (not_84_out, OP5);
  not not_85 (not_85_out, OP4);
  not not_86 (not_86_out, OP3);
  not not_87 (not_87_out, OP2);
  not not_88 (not_88_out, OP1);
  not not_89 (not_89_out, OP0);
  not not_90 (not_90_out, F4);
  not not_91 (not_91_out, F3);
  not not_92 (not_92_out, OP5);
  not not_93 (not_93_out, OP4);
  not not_94 (not_94_out, OP3);
  not not_95 (not_95_out, OP2);
  not not_96 (not_96_out, OP1);
  not not_97 (not_97_out, OP0);
  not not_98 (not_98_out, F4);
  not not_99 (not_99_out, F2);
  not not_100 (not_100_out, F0);
  not not_101 (not_101_out, OP5);
  not not_102 (not_102_out, OP4);
  not not_103 (not_103_out, OP3);
  not not_104 (not_104_out, OP2);
  not not_105 (not_105_out, OP1);
  not not_106 (not_106_out, OP0);
  not not_107 (not_107_out, F4);
  not not_108 (not_108_out, F2);
  not not_109 (not_109_out, OP5);
  not not_110 (not_110_out, OP4);
  not not_111 (not_111_out, OP3);
  not not_112 (not_112_out, OP2);
  not not_113 (not_113_out, OP1);
  not not_114 (not_114_out, OP0);
  not not_115 (not_115_out, F5);
  not not_116 (not_116_out, F4);
  not not_117 (not_117_out, F2);
  not not_118 (not_118_out, F1);
  not not_119 (not_119_out, F0);
  not not_120 (not_120_out, OP5);
  not not_121 (not_121_out, OP4);
  not not_122 (not_122_out, OP3);
  not not_123 (not_123_out, OP2);
  not not_124 (not_124_out, OP1);
  not not_125 (not_125_out, OP0);
  not not_126 (not_126_out, F5);
  not not_127 (not_127_out, F4);
  not not_128 (not_128_out, F1);
  not not_129 (not_129_out, F0);
  not not_130 (not_130_out, OP5);
  not not_131 (not_131_out, OP4);
  not not_132 (not_132_out, OP3);
  not not_133 (not_133_out, OP1);
  not not_134 (not_134_out, OP0);
  not not_135 (not_135_out, OP5);
  not not_136 (not_136_out, OP4);
  not not_137 (not_137_out, OP3);
  not not_138 (not_138_out, OP1);
  not not_139 (not_139_out, OP5);
  not not_140 (not_140_out, OP4);
  not not_141 (not_141_out, OP2);
  not not_142 (not_142_out, OP1);
  not not_143 (not_143_out, OP0);
  not not_144 (not_144_out, OP5);
  not not_145 (not_145_out, OP4);
  not not_146 (not_146_out, OP1);
  not not_147 (not_147_out, OP0);
  not not_148 (not_148_out, OP5);
  not not_149 (not_149_out, OP4);
  not not_150 (not_150_out, OP2);
  not not_151 (not_151_out, OP1);
  not not_152 (not_152_out, OP5);
  not not_153 (not_153_out, OP4);
  not not_154 (not_154_out, OP2);
  not not_155 (not_155_out, OP0);
  not not_156 (not_156_out, OP5);
  not not_157 (not_157_out, OP4);
  not not_158 (not_158_out, OP1);
  not not_159 (not_159_out, OP4);
  not not_160 (not_160_out, OP3);
  not not_161 (not_161_out, OP2);
  not not_162 (not_162_out, OP4);
  not not_163 (not_163_out, OP2);
  not not_164 (not_164_out, OP5);
  not not_165 (not_165_out, OP4);
  not not_166 (not_166_out, OP3);
  not not_167 (not_167_out, OP0);
  not not_168 (not_168_out, OP5);
  not not_169 (not_169_out, OP4);
  not not_170 (not_170_out, OP0);
  not not_171 (not_171_out, OP5);
  not not_172 (not_172_out, OP4);
  not not_173 (not_173_out, OP3);
  not not_174 (not_174_out, OP2);
  not not_175 (not_175_out, OP1);
  not not_176 (not_176_out, OP0);
  not not_177 (not_177_out, F5);
  not not_178 (not_178_out, F4);
  not not_179 (not_179_out, F3);
  not not_180 (not_180_out, F1);
  not not_181 (not_181_out, F0);
  not not_182 (not_182_out, OP4);
  not not_183 (not_183_out, OP3);
  not not_184 (not_184_out, OP1);
  not not_185 (not_185_out, OP0);
  not not_186 (not_186_out, OP5);
  not not_187 (not_187_out, OP4);
  not not_188 (not_188_out, OP3);
  not not_189 (not_189_out, OP2);
  not not_190 (not_190_out, OP1);
  not not_191 (not_191_out, OP0);
  not not_192 (not_192_out, F5);
  not not_193 (not_193_out, F4);
  not not_194 (not_194_out, F3);
  not not_195 (not_195_out, F2);
  not not_196 (not_196_out, F1);
  not not_197 (not_197_out, F0);
  not not_198 (not_198_out, OP5);
  not not_199 (not_199_out, OP4);
  not not_200 (not_200_out, OP3);
  not not_201 (not_201_out, OP2);
  not not_202 (not_202_out, OP1);
  not not_203 (not_203_out, OP0);
  not not_204 (not_204_out, F5);
  not not_205 (not_205_out, F4);
  not not_206 (not_206_out, F3);
  not not_207 (not_207_out, F2);
  not not_208 (not_208_out, OP5);
  not not_209 (not_209_out, OP4);
  not not_210 (not_210_out, OP3);
  not not_211 (not_211_out, OP2);
  not not_212 (not_212_out, OP1);
  not not_213 (not_213_out, OP0);
  not not_214 (not_214_out, F5);
  not not_215 (not_215_out, F4);
  not not_216 (not_216_out, F3);
  not not_217 (not_217_out, F2);
  not not_218 (not_218_out, F0);
  not not_219 (not_219_out, OP5);
  not not_220 (not_220_out, OP4);
  not not_221 (not_221_out, OP3);
  not not_222 (not_222_out, OP2);
  not not_223 (not_223_out, OP1);
  not not_224 (not_224_out, OP0);
  not not_225 (not_225_out, F4);
  not not_226 (not_226_out, F3);
  not not_227 (not_227_out, F2);
  not not_228 (not_228_out, F1);
  not not_229 (not_229_out, F0);
  not not_230 (not_230_out, OP5);
  not not_231 (not_231_out, OP4);
  not not_232 (not_232_out, OP3);
  not not_233 (not_233_out, OP2);
  not not_234 (not_234_out, OP1);
  not not_235 (not_235_out, OP0);
  not not_236 (not_236_out, F4);
  not not_237 (not_237_out, F3);
  not not_238 (not_238_out, F2);
  not not_239 (not_239_out, F1);
  not not_240 (not_240_out, OP5);
  not not_241 (not_241_out, OP4);
  not not_242 (not_242_out, OP3);
  not not_243 (not_243_out, OP2);
  not not_244 (not_244_out, OP1);
  not not_245 (not_245_out, OP0);
  not not_246 (not_246_out, F4);
  not not_247 (not_247_out, F3);
  not not_248 (not_248_out, F2);
  not not_249 (not_249_out, F0);
  not not_250 (not_250_out, OP5);
  not not_251 (not_251_out, OP4);
  not not_252 (not_252_out, OP3);
  not not_253 (not_253_out, OP2);
  not not_254 (not_254_out, OP1);
  not not_255 (not_255_out, OP0);
  not not_256 (not_256_out, F4);
  not not_257 (not_257_out, F3);
  not not_258 (not_258_out, F1);
  not not_259 (not_259_out, F0);
  not not_260 (not_260_out, OP5);
  not not_261 (not_261_out, OP4);
  not not_262 (not_262_out, OP3);
  not not_263 (not_263_out, OP2);
  not not_264 (not_264_out, OP1);
  not not_265 (not_265_out, OP0);
  not not_266 (not_266_out, F4);
  not not_267 (not_267_out, F3);
  not not_268 (not_268_out, F1);
  not not_269 (not_269_out, OP5);
  not not_270 (not_270_out, OP4);
  not not_271 (not_271_out, OP3);
  not not_272 (not_272_out, OP2);
  not not_273 (not_273_out, OP1);
  not not_274 (not_274_out, OP0);
  not not_275 (not_275_out, F4);
  not not_276 (not_276_out, F3);
  not not_277 (not_277_out, OP5);
  not not_278 (not_278_out, OP4);
  not not_279 (not_279_out, OP3);
  not not_280 (not_280_out, OP2);
  not not_281 (not_281_out, OP1);
  not not_282 (not_282_out, OP0);
  not not_283 (not_283_out, F4);
  not not_284 (not_284_out, F2);
  not not_285 (not_285_out, F0);
  not not_286 (not_286_out, OP5);
  not not_287 (not_287_out, OP4);
  not not_288 (not_288_out, OP3);
  not not_289 (not_289_out, OP2);
  not not_290 (not_290_out, OP1);
  not not_291 (not_291_out, OP0);
  not not_292 (not_292_out, F4);
  not not_293 (not_293_out, F2);
  not not_294 (not_294_out, OP5);
  not not_295 (not_295_out, OP4);
  not not_296 (not_296_out, OP3);
  not not_297 (not_297_out, OP2);
  not not_298 (not_298_out, OP1);
  not not_299 (not_299_out, OP0);
  not not_300 (not_300_out, F5);
  not not_301 (not_301_out, F4);
  not not_302 (not_302_out, F1);
  not not_303 (not_303_out, F0);
  not not_304 (not_304_out, OP5);
  not not_305 (not_305_out, OP4);
  not not_306 (not_306_out, OP3);
  not not_307 (not_307_out, OP1);
  not not_308 (not_308_out, OP0);
  not not_309 (not_309_out, OP5);
  not not_310 (not_310_out, OP4);
  not not_311 (not_311_out, OP3);
  not not_312 (not_312_out, OP1);
  not not_313 (not_313_out, OP4);
  not not_314 (not_314_out, OP2);
  not not_315 (not_315_out, OP5);
  not not_316 (not_316_out, OP4);
  not not_317 (not_317_out, OP3);
  not not_318 (not_318_out, OP2);
  not not_319 (not_319_out, OP1);
  not not_320 (not_320_out, OP0);
  not not_321 (not_321_out, F5);
  not not_322 (not_322_out, F4);
  not not_323 (not_323_out, F3);
  not not_324 (not_324_out, F1);
  not not_325 (not_325_out, F0);
  and and_1 (and_1_out, not_1_out, not_2_out, not_3_out, not_4_out, not_5_out, not_6_out, not_7_out, not_8_out, not_9_out, not_10_out, not_11_out, not_12_out);
  and and_2 (and_2_out, not_13_out, not_14_out, not_15_out, not_16_out, not_17_out, not_18_out, not_19_out, not_20_out, not_21_out, not_22_out, F1, F0);
  and and_3 (and_3_out, not_23_out, not_24_out, not_25_out, not_26_out, not_27_out, not_28_out, not_29_out, not_30_out, not_31_out, not_32_out, F1, not_33_out);
  and and_4 (and_4_out, not_34_out, not_35_out, not_36_out, not_37_out, not_38_out, not_39_out, F5, not_40_out, not_41_out, not_42_out, not_43_out, not_44_out);
  and and_5 (and_5_out, not_45_out, not_46_out, not_47_out, not_48_out, not_49_out, not_50_out, F5, not_51_out, not_52_out, not_53_out, not_54_out, F0);
  and and_6 (and_6_out, not_55_out, not_56_out, not_57_out, not_58_out, not_59_out, not_60_out, F5, not_61_out, not_62_out, not_63_out, F1, not_64_out);
  and and_7 (and_7_out, not_65_out, not_66_out, not_67_out, not_68_out, not_69_out, not_70_out, F5, not_71_out, not_72_out, F2, not_73_out, not_74_out);
  and and_8 (and_8_out, not_75_out, not_76_out, not_77_out, not_78_out, not_79_out, not_80_out, F5, not_81_out, not_82_out, F2, not_83_out, F0);
  and and_9 (and_9_out, not_84_out, not_85_out, not_86_out, not_87_out, not_88_out, not_89_out, F5, not_90_out, not_91_out, F2, F1, F0);
  and and_10 (and_10_out, not_92_out, not_93_out, not_94_out, not_95_out, not_96_out, not_97_out, F5, not_98_out, F3, not_99_out, F1, not_100_out);
  and and_11 (and_11_out, not_101_out, not_102_out, not_103_out, not_104_out, not_105_out, not_106_out, F5, not_107_out, F3, not_108_out, F1, F0);
  and and_12 (and_12_out, not_109_out, not_110_out, not_111_out, not_112_out, not_113_out, not_114_out, not_115_out, not_116_out, F3, not_117_out, not_118_out, not_119_out);
  and and_13 (and_13_out, not_120_out, not_121_out, not_122_out, not_123_out, not_124_out, not_125_out, not_126_out, not_127_out, F3, F2, not_128_out, not_129_out);
  and and_14 (and_14_out, not_130_out, not_131_out, not_132_out, OP2, not_133_out, not_134_out);
  and and_15 (and_15_out, not_135_out, not_136_out, not_137_out, OP2, not_138_out, OP0);
  and and_16 (and_16_out, not_139_out, not_140_out, OP3, not_141_out, not_142_out, not_143_out);
  and and_17 (and_17_out, not_144_out, not_145_out, OP3, OP2, not_146_out, not_147_out);
  and and_18 (and_18_out, not_148_out, not_149_out, OP3, not_150_out, not_151_out, OP0);
  and and_19 (and_19_out, not_152_out, not_153_out, OP3, not_154_out, OP1, not_155_out);
  and and_20 (and_20_out, not_156_out, not_157_out, OP3, OP2, not_158_out, OP0);
  and and_21 (and_21_out, OP5, not_159_out, not_160_out, not_161_out, OP1, OP0);
  and and_22 (and_22_out, OP5, not_162_out, OP3, not_163_out, OP1, OP0);
  and and_23 (and_23_out, not_164_out, not_165_out, not_166_out, OP2, OP1, not_167_out);
  and and_24 (and_24_out, not_168_out, not_169_out, OP3, OP2, OP1, not_170_out);
  and and_25 (and_25_out, not_171_out, not_172_out, not_173_out, not_174_out, not_175_out, not_176_out, not_177_out, not_178_out, not_179_out, F2, not_180_out, not_181_out);
  and and_26 (and_26_out, OP5, not_182_out, not_183_out, OP2, not_184_out, not_185_out);
  and and_27 (and_27_out, not_186_out, not_187_out, not_188_out, not_189_out, not_190_out, not_191_out, not_192_out, not_193_out, not_194_out, not_195_out, not_196_out, not_197_out);
  and and_28 (and_28_out, not_198_out, not_199_out, not_200_out, not_201_out, not_202_out, not_203_out, not_204_out, not_205_out, not_206_out, not_207_out, F1, F0);
  and and_29 (and_29_out, not_208_out, not_209_out, not_210_out, not_211_out, not_212_out, not_213_out, not_214_out, not_215_out, not_216_out, not_217_out, F1, not_218_out);
  and and_30 (and_30_out, not_219_out, not_220_out, not_221_out, not_222_out, not_223_out, not_224_out, F5, not_225_out, not_226_out, not_227_out, not_228_out, not_229_out);
  and and_31 (and_31_out, not_230_out, not_231_out, not_232_out, not_233_out, not_234_out, not_235_out, F5, not_236_out, not_237_out, not_238_out, not_239_out, F0);
  and and_32 (and_32_out, not_240_out, not_241_out, not_242_out, not_243_out, not_244_out, not_245_out, F5, not_246_out, not_247_out, not_248_out, F1, not_249_out);
  and and_33 (and_33_out, not_250_out, not_251_out, not_252_out, not_253_out, not_254_out, not_255_out, F5, not_256_out, not_257_out, F2, not_258_out, not_259_out);
  and and_34 (and_34_out, not_260_out, not_261_out, not_262_out, not_263_out, not_264_out, not_265_out, F5, not_266_out, not_267_out, F2, not_268_out, F0);
  and and_35 (and_35_out, not_269_out, not_270_out, not_271_out, not_272_out, not_273_out, not_274_out, F5, not_275_out, not_276_out, F2, F1, F0);
  and and_36 (and_36_out, not_277_out, not_278_out, not_279_out, not_280_out, not_281_out, not_282_out, F5, not_283_out, F3, not_284_out, F1, not_285_out);
  and and_37 (and_37_out, not_286_out, not_287_out, not_288_out, not_289_out, not_290_out, not_291_out, F5, not_292_out, F3, not_293_out, F1, F0);
  and and_38 (and_38_out, not_294_out, not_295_out, not_296_out, not_297_out, not_298_out, not_299_out, not_300_out, not_301_out, F3, F2, not_302_out, not_303_out);
  and and_39 (and_39_out, not_304_out, not_305_out, not_306_out, OP2, not_307_out, not_308_out);
  and and_40 (and_40_out, not_309_out, not_310_out, not_311_out, OP2, not_312_out, OP0);
  and and_41 (and_41_out, OP5, not_313_out, OP3, not_314_out, OP1, OP0);
  and and_42 (and_42_out, not_315_out, not_316_out, not_317_out, not_318_out, not_319_out, not_320_out, not_321_out, not_322_out, not_323_out, F2, not_324_out, not_325_out);
  or or_1 (R1_Used, and_1_out, and_2_out, and_3_out, and_4_out, and_5_out, and_6_out, and_7_out, and_8_out, and_9_out, and_10_out, and_11_out, and_12_out, and_13_out, and_14_out, and_15_out, and_16_out, and_17_out, and_18_out, and_19_out, and_20_out, and_21_out, and_22_out, and_23_out, and_24_out, and_25_out, and_26_out);
  or or_2 (R2_Used, and_27_out, and_28_out, and_29_out, and_30_out, and_31_out, and_32_out, and_33_out, and_34_out, and_35_out, and_36_out, and_37_out, and_38_out, and_39_out, and_40_out, and_41_out, and_42_out);
endmodule

// 数据冲突检测
module \气泡数据相关检测  (
  input  [5:0] ID_OP,
  input  [5:0] ID_FUNC,
  input  [4:0] ID_R1_num,
  input  [4:0] ID_R2_num,
  input  [4:0] EX_WriteReg_num,
  input  [4:0] MEM_WriteReg_num,
  input  EX_RegWrite,
  input  MEM_RegWrite,
  output DataConflict
);

  wire and_1_out, and_2_out, and_3_out, and_4_out, and_5_out, and_6_out, comparator_1_eq, comparator_2_eq,
       comparator_3_eq, comparator_4_eq, comparator_5_eq, comparator_6_eq, comparator_7_eq, comparator_8_eq,
       not_1_out, not_2_out, not_3_out, not_4_out, or_1_out, or_2_out, \源寄存器使用情况_1_r1_used ,
       \源寄存器使用情况_1_r2_used ;

  Comparator #(.width(5)) comparator_1 (.a({5{1'b0}}), .b(EX_WriteReg_num), .eq(comparator_1_eq));  // open: gt, lt
  Comparator #(.width(5)) comparator_2 (.a({5{1'b0}}), .b(MEM_WriteReg_num), .eq(comparator_2_eq));  // open: gt, lt
  Comparator #(.width(5)) comparator_3 (.a({5{1'b0}}), .b(EX_WriteReg_num), .eq(comparator_3_eq));  // open: gt, lt
  Comparator #(.width(5)) comparator_4 (.a({5{1'b0}}), .b(MEM_WriteReg_num), .eq(comparator_4_eq));  // open: gt, lt
  not not_1 (not_1_out, comparator_1_eq);
  Comparator #(.width(5)) comparator_5 (.a(EX_WriteReg_num), .b(ID_R1_num), .eq(comparator_5_eq));  // open: gt, lt
  Comparator #(.width(5)) comparator_6 (.a(ID_R1_num), .b(MEM_WriteReg_num), .eq(comparator_6_eq));  // open: gt, lt
  not not_2 (not_2_out, comparator_2_eq);
  not not_3 (not_3_out, comparator_3_eq);
  Comparator #(.width(5)) comparator_7 (.a(EX_WriteReg_num), .b(ID_R2_num), .eq(comparator_7_eq));  // open: gt, lt
  Comparator #(.width(5)) comparator_8 (.a(ID_R2_num), .b(MEM_WriteReg_num), .eq(comparator_8_eq));  // open: gt, lt
  not not_4 (not_4_out, comparator_4_eq);
  and and_1 (and_1_out, not_1_out, EX_RegWrite, comparator_5_eq);
  and and_2 (and_2_out, comparator_6_eq, MEM_RegWrite, not_2_out);
  \源寄存器使用情况  \u_源寄存器使用情况_1  (
    .OP0(ID_OP[0]), .OP1(ID_OP[1]), .OP2(ID_OP[2]), .OP3(ID_OP[3]), .OP4(ID_OP[4]), .OP5(ID_OP[5]),
    .F0(ID_FUNC[0]), .F1(ID_FUNC[1]), .F2(ID_FUNC[2]), .F3(ID_FUNC[3]), .F4(ID_FUNC[4]), .F5(ID_FUNC[5]),
    .R1_Used(\源寄存器使用情况_1_r1_used ), .R2_Used(\源寄存器使用情况_1_r2_used ));
  and and_3 (and_3_out, not_3_out, EX_RegWrite, comparator_7_eq);
  and and_4 (and_4_out, comparator_8_eq, MEM_RegWrite, not_4_out);
  or or_1 (or_1_out, and_1_out, and_2_out);
  or or_2 (or_2_out, and_3_out, and_4_out);
  and and_5 (and_5_out, or_1_out, \源寄存器使用情况_1_r1_used );
  and and_6 (and_6_out, \源寄存器使用情况_1_r2_used , or_2_out);
  or or_3 (DataConflict, and_5_out, and_6_out);
endmodule

module \测试  (
  output [31:0] out_1
);

  MIPS_ALU mips_alu_1 (.X({32{1'b1}}), .Y(32'h2), .Result(out_1));  // open: AluOP, Equal, Result_2, shamt
endmodule

// AIDSB
module SBAID (
  input  [1:0] SubAddr,
  output s0,
  output s1,
  output s2,
  output s3
);

  wire not_1_out, not_2_out, not_3_out, not_4_out;

  not not_1 (not_1_out, SubAddr[1]);
  not not_2 (not_2_out, SubAddr[0]);
  not not_3 (not_3_out, SubAddr[1]);
  not not_4 (not_4_out, SubAddr[0]);
  and and_1 (s3, SubAddr[1], SubAddr[0]);
  and and_2 (s0, not_1_out, not_2_out);
  and and_3 (s1, not_3_out, SubAddr[0]);
  and and_4 (s2, SubAddr[1], not_4_out);
endmodule

// 重定向数据相关
module \重定向数据相关检测  (
  input  [5:0] ID_OP,
  input  [5:0] ID_FUNC,
  input  [4:0] ID_R1_num,
  input  [4:0] ID_R2_num,
  input  [4:0] EX_WriteReg_num,
  input  [4:0] MEM_WriteReg_num,
  input  EX_RegWrite,
  input  MEM_RegWrite,
  input  [5:0] EX_OP,
  input  [5:0] MEM_OP,
  output LoadUse,
  output [1:0] R1_Forward,
  output [1:0] R2_Forward
);

  wire and_1_out, and_2_out, and_3_out, and_4_out, and_5_out, and_6_out, and_7_out, and_8_out, and_10_out,
       and_11_out, comparator_1_eq, comparator_2_eq, comparator_3_eq, comparator_4_eq, comparator_5_eq,
       comparator_6_eq, comparator_7_eq, comparator_8_eq, comparator_9_eq, comparator_10_eq, not_1_out,
       not_2_out, not_3_out, not_4_out, or_1_out, R1_Used, R2_Used;
  wire [1:0] priority_encoder_1_out, priority_encoder_2_out;

  \源寄存器使用情况  \u_源寄存器使用情况_1  (
    .OP0(ID_OP[0]), .OP1(ID_OP[1]), .OP2(ID_OP[2]), .OP3(ID_OP[3]), .OP4(ID_OP[4]), .OP5(ID_OP[5]),
    .F0(ID_FUNC[0]), .F1(ID_FUNC[1]), .F2(ID_FUNC[2]), .F3(ID_FUNC[3]), .F4(ID_FUNC[4]), .F5(ID_FUNC[5]),
    .R1_Used(R1_Used), .R2_Used(R2_Used));
  Comparator #(.width(5)) comparator_1 (.a({5{1'b0}}), .b(EX_WriteReg_num), .eq(comparator_1_eq));  // open: gt, lt
  Comparator #(.width(5)) comparator_2 (.a({5{1'b0}}), .b(MEM_WriteReg_num), .eq(comparator_2_eq));  // open: gt, lt
  Comparator #(.width(5)) comparator_3 (.a({5{1'b0}}), .b(EX_WriteReg_num), .eq(comparator_3_eq));  // open: gt, lt
  Comparator #(.width(5)) comparator_4 (.a({5{1'b0}}), .b(MEM_WriteReg_num), .eq(comparator_4_eq));  // open: gt, lt
  not not_1 (not_1_out, comparator_1_eq);
  Comparator #(.width(5)) comparator_5 (.a(EX_WriteReg_num), .b(ID_R1_num), .eq(comparator_5_eq));  // open: gt, lt
  Comparator #(.width(5)) comparator_6 (.a(ID_R1_num), .b(MEM_WriteReg_num), .eq(comparator_6_eq));  // open: gt, lt
  not not_2 (not_2_out, comparator_2_eq);
  not not_3 (not_3_out, comparator_3_eq);
  Comparator #(.width(5)) comparator_7 (.a(EX_WriteReg_num), .b(ID_R2_num), .eq(comparator_7_eq));  // open: gt, lt
  Comparator #(.width(5)) comparator_8 (.a(ID_R2_num), .b(MEM_WriteReg_num), .eq(comparator_8_eq));  // open: gt, lt
  not not_4 (not_4_out, comparator_4_eq);
  and and_1 (and_1_out, not_1_out, EX_RegWrite, comparator_5_eq);
  and and_2 (and_2_out, comparator_6_eq, MEM_RegWrite, not_2_out);
  and and_3 (and_3_out, not_3_out, EX_RegWrite, comparator_7_eq);
  and and_4 (and_4_out, comparator_8_eq, MEM_RegWrite, not_4_out);
  and and_5 (and_5_out, and_1_out, R1_Used);
  and and_6 (and_6_out, R1_Used, and_2_out);
  and and_7 (and_7_out, and_3_out, R2_Used);
  and and_8 (and_8_out, R2_Used, and_4_out);
  or or_1 (or_1_out, and_5_out, and_7_out);
  Comparator #(.width(6)) comparator_9 (.a(EX_OP), .b(6'b100011), .eq(comparator_9_eq));  // open: gt, lt
  and and_9 (LoadUse, or_1_out, comparator_9_eq);
  Comparator #(.width(6)) comparator_10 (.a(6'b100011), .b(MEM_OP), .eq(comparator_10_eq));  // open: gt, lt
  and and_10 (and_10_out, and_6_out, comparator_10_eq);
  and and_11 (and_11_out, comparator_10_eq, and_8_out);
  Priority_Encoder #(.select(2)) priority_encoder_1 (
    .in0(1'b1), .in1(and_6_out), .in2(and_10_out), .in3(and_5_out), .out(priority_encoder_1_out));  // open: gs, en_out, en_in
  Multiplexer #(.width(2), .enable("false")) multiplexer_1 (
    .in0(priority_encoder_1_out), .out(R1_Forward), .sel(LoadUse));  // open: in1
  Priority_Encoder #(.select(2)) priority_encoder_2 (
    .in0(1'b1), .in1(and_8_out), .in2(and_11_out), .in3(and_7_out), .out(priority_encoder_2_out));  // open: gs, en_out, en_in
  Multiplexer #(.width(2), .enable("false")) multiplexer_2 (
    .in0(priority_encoder_2_out), .out(R2_Forward), .sel(LoadUse));  // open: in1

  // Notes on the sheet:
  //   lw
  //   lw
  //   ID段和MEM段数据相关且MEM段指令不是lw，需要接通WB.ALU
  //   ID段和MEM段数据相关且MEM段的指令为lw，需要接通WB.MemData
  //   ID段和EX段数据相关,需要接通MEM.ALU
  //   ID段和MEM段数据相关且MEM段指令不是lw，需要接通WB.ALU
  //   ID段和MEM段数据相关且MEM段的指令为lw，需要接通WB.MemData
  //   ID段和EX段数据相关,需要接通MEM.ALU
endmodule

module stack (
  input  [1:0] INPUT,
  input  clk,
  input  \int ,
  input  eret,
  output [1:0] out_5
);

  wire and_1_out, and_2_out, and_3_out, or_1_out, stack1_1_s0, stack1_1_s1, stack1_1_s2;
  wire [1:0] counter_1_q, demultiplexer_1_out0, demultiplexer_1_out1, demultiplexer_1_out2, s0_q, s1_q, s2_q,
       subtractor_1_out;

  Demultiplexer #(.select(2), .width(2), .enable("false")) demultiplexer_1 (
    .out0(demultiplexer_1_out0), .out1(demultiplexer_1_out1), .out2(demultiplexer_1_out2), .in(INPUT),
    .sel(counter_1_q));  // open: out3
  or or_1 (or_1_out, \int , eret);
  Counter #(.width(2), .max('h3)) counter_1 (
    .count(or_1_out), .Q(counter_1_q), .clk(clk), .down(eret));  // open: load, D, carry, clr, preset
  stack1 stack1_1 (.I1(counter_1_q[1]), .I0(counter_1_q[0]), .S0(stack1_1_s0), .S1(stack1_1_s1), .S2(stack1_1_s2));
  Register #(.width(2), .Select("low")) s0 (
    .D(demultiplexer_1_out0), .en(and_1_out), .Q(s0_q), .clk(clk));  // open: clr
  and and_1 (and_1_out, \int , stack1_1_s0);
  and and_2 (and_2_out, stack1_1_s1, \int );
  Register #(.width(2), .Select("low")) s1 (
    .D(demultiplexer_1_out1), .en(and_2_out), .Q(s1_q), .clk(clk));  // open: clr
  and and_3 (and_3_out, stack1_1_s2, \int );
  Register #(.width(2), .Select("low")) s2 (
    .D(demultiplexer_1_out2), .en(and_3_out), .Q(s2_q), .clk(clk));  // open: clr
  Multiplexer #(.select(2), .width(2), .enable("false")) multiplexer_1 (
    .in0(s0_q), .in1(s1_q), .in2(s2_q), .in3(2'b00), .out(out_5), .sel(subtractor_1_out));
  Subtractor #(.width(2)) subtractor_1 (.a(counter_1_q), .b(2'b01), .out(subtractor_1_out));  // open: bin, bout
endmodule

module stack1 (
  input  I1,
  input  I0,
  output S0,
  output S1,
  output S2
);

  wire not_1_out, not_2_out, not_3_out, not_4_out;

  not not_1 (not_1_out, I1);
  not not_2 (not_2_out, I0);
  not not_3 (not_3_out, I1);
  not not_4 (not_4_out, I0);
  and and_1 (S0, not_1_out, not_2_out);
  and and_2 (S1, not_3_out, I0);
  and and_3 (S2, I1, not_4_out);
endmodule
