// Logisim project cpu21-riscv.circ as structural Verilog: 19 circuits, main circuit ◇单周期RISC-V
module \单周期RISC_V  (
  input  IR1,
  input  IR2,
  input  IR3,
  output RegWrite,
  output MemWrite,
  output [31:0] PC,
  output [31:0] IR,
  output [31:0] RDin,
  output [31:0] MDin,
  output [31:0] LedData
);

  wire alu_1_equal, alu_1_out_6, and_2_out, and_3_out, and_4_out, and_6_out, beq, CLK, clock_2_out,
       comparator_1_eq, comparator_2_eq, comparator_3_eq, comparator_4_eq, comparator_4_lt, d_ff_1_q, ecall,
       Go, halt, IR1_t, IR2_t, IR3_t, IRA, IRB, IRC, jal, jalr, lb, nand_1_out, not_1_out, not_2_out,
       or_4_out, or_6_out, RST, W1, W2, W3, \单周期硬布线控制器_1_alu_src , \单周期硬布线控制器_1_beq , \单周期硬布线控制器_1_blt ,
       \单周期硬布线控制器_1_bne , \单周期硬布线控制器_1_memtoreg , \单周期硬布线控制器_1_s_type ;
  wire [1:0] priority_encoder_1_out;
  wire [3:0] \单周期硬布线控制器_1_alu_op ;
  wire [4:0] multiplexer_2_out, multiplexer_3_out, multiplexer_4_out;
  wire [7:0] multiplexer_8_out;
  wire [9:0] bit_extender_1_out, dataaddr, shifter_4_out;
  wire [12:0] CNT_num;
  wire [15:0] \总周期数 ;
  wire [31:0] adder_1_out, adder_2_out, adder_3_out, alu_1_result, and_5_out, bit_extender_2_out,
       bit_extender_3_out, bit_extender_4_out, bit_extender_5_out, bit_extender_7_out, multiplexer_1_out,
       multiplexer_5_out, multiplexer_6_out, multiplexer_9_out, multiplexer_10_out, PC_q, R1, ram_1_data,
       shifter_2_out, shifter_3_out, shifter_5_out, shifter_6_out;

  Clock #(.highDuration(1), .lowDuration(1)) clock_1 ();  // open: out
  Button _1 (.out(IRA));
  Button _2 (.out(IRB));
  Button _3 (.out(IRC));
  Button button_1 (.out(RST));
  Button \u_继续运行  (.out(Go));
  LED #(.active("true")) led_1 (.in(W1));
  LED #(.active("true")) led_2 (.in(W2));
  LED #(.active("true")) led_3 (.in(W3));
  not not_1 (not_1_out, halt);
  Hex_Digit_Display hex_digit_display_1 (.value(LedData[31:28]));  // open: dp
  Register #(.width(32), .trigger("rising"), .Select("low")) u_PC (
    .D(multiplexer_1_out), .en(not_1_out), .Q(PC_q), .clk(CLK), .clr(RST));
  // Probe on multiplexer_1_out
  Priority_Encoder #(.select(2), .disabled("Z")) priority_encoder_1 (
    .in0(1'b1), .in1(jal), .in2(jalr), .in3(beq), .out(priority_encoder_1_out));  // open: gs, en_out, en_in
  Hex_Digit_Display hex_digit_display_2 (.value(LedData[23:20]));  // open: dp
  Hex_Digit_Display hex_digit_display_3 (.value(LedData[27:24]));  // open: dp
  // Probe on PC
  Shifter #(.width(32), .shift("ll")) shifter_1 (.in(PC_q), .\dist (5'b00010), .out(PC));
  Bit_Extender #(.in_width(32), .out_width(10), .\type ("sign")) bit_extender_1 (.in(PC_q), .out(bit_extender_1_out));
  Adder #(.width(32)) adder_1 (.a(PC_q), .b(32'h1), .out(adder_1_out));  // open: cin, cout
  Multiplexer #(.select(2), .width(32), .disabled("Z"), .enable("false")) multiplexer_1 (
    .in0(adder_1_out), .in1(adder_3_out), .in2(shifter_5_out), .in3(adder_2_out), .out(multiplexer_1_out),
    .sel(priority_encoder_1_out));
  Hex_Digit_Display hex_digit_display_4 (.value(LedData[19:16]));  // open: dp
  Hex_Digit_Display hex_digit_display_5 (.value(LedData[15:12]));  // open: dp
  // RiscV_Probe riscv_probe_1: pin names not known; wires that end beside it: {32{1'b0}}, IR
  Hex_Digit_Display hex_digit_display_6 (.value(LedData[11:8]));  // open: dp
  Hex_Digit_Display hex_digit_display_7 (.value(LedData[7:4]));  // open: dp
  // Probe on \总周期数 
  Comparator #(.width(32), .mode("twosComplement")) comparator_1 (
    .a({32{1'b0}}), .b(IR), .eq(comparator_1_eq));  // open: gt, lt
  ROM #(.addrWidth(10), .dataWidth(32), .Select("high")) rom_1 (.addr(bit_extender_1_out), .data(IR));
  Comparator #(.width(32), .mode("twosComplement")) comparator_2 (
    .a(MDin), .b(32'ha), .eq(comparator_2_eq));  // open: gt, lt
  Hex_Digit_Display hex_digit_display_8 (.value(LedData[3:0]));  // open: dp
  // Probe on IR
  \单周期硬布线控制器  \u_单周期硬布线控制器_1  (
    .Funct({IR[30], IR[25], IR[14:12]}), .OP(IR[6:2]), .ALU_OP(\单周期硬布线控制器_1_alu_op ),
    .MemToReg(\单周期硬布线控制器_1_memtoreg ), .MemWrite(MemWrite), .ALU_SRC(\单周期硬布线控制器_1_alu_src ),
    .RegWrite(RegWrite), .ecall(ecall), .S_type(\单周期硬布线控制器_1_s_type ), .Jalr(jalr), .Beq(\单周期硬布线控制器_1_beq ),
    .JAL(jal), .Bne(\单周期硬布线控制器_1_bne ), .LB(lb), .BLT(\单周期硬布线控制器_1_blt ), .IR_0(comparator_1_eq));  // open: CSRRCI, URET, CSRRSI
  Multiplexer #(.select(1), .width(5), .disabled("Z"), .enable("false")) multiplexer_2 (
    .in0(IR[19:15]), .in1(5'b01010), .out(multiplexer_2_out), .sel(ecall));
  Multiplexer #(.select(1), .width(5), .disabled("Z"), .enable("false")) multiplexer_3 (
    .in0(IR[24:20]), .in1(5'b10001), .out(multiplexer_3_out), .sel(ecall));
  assign bit_extender_2_out = {{20{IR[31]}}, IR[31:20]};  // Bit_Extender bit_extender_2
  assign bit_extender_3_out = {{20{IR[31]}}, {IR[31:25], IR[11:7]}};  // Bit_Extender bit_extender_3
  and and_1 (halt, comparator_2_eq, ~Go, ecall);  // AND_Gate
  or or_1 (IR1_t, IR1, IRA);
  Multiplexer #(.select(1), .width(5), .disabled("Z"), .enable("false")) multiplexer_4 (
    .in0(multiplexer_3_out), .in1(IR[11:7]), .out(multiplexer_4_out), .sel(\单周期硬布线控制器_1_s_type ));
  Multiplexer #(.select(1), .width(32), .disabled("Z"), .enable("false")) multiplexer_5 (
    .in0(bit_extender_2_out), .in1(bit_extender_3_out), .out(multiplexer_5_out), .sel(MemWrite));
  assign bit_extender_4_out = {{20{IR[31]}}, {IR[31], IR[7], IR[30:25], IR[11:8]}};  // Bit_Extender bit_extender_4
  Shifter #(.width(32), .shift("ar")) shifter_2 (.in(bit_extender_4_out), .\dist (5'b00001), .out(shifter_2_out));
  assign bit_extender_5_out = {{12{IR[31]}}, {IR[31], IR[19:12], IR[20], IR[30:21]}};  // Bit_Extender bit_extender_5
  or or_2 (IR2_t, IR2, IRB);
  Regifile regifile_1 (
    .Din(RDin), .Clk(CLK), .R1(R1), .R2(MDin), .WE(RegWrite), .W_num(multiplexer_4_out),
    .R1_num(multiplexer_2_out), .R2_num(multiplexer_3_out));
  Adder #(.width(32)) adder_2 (.a(shifter_2_out), .b(PC_q), .out(adder_2_out));  // open: cin, cout
  Shifter #(.width(32), .shift("ar")) shifter_3 (.in(bit_extender_5_out), .\dist (5'b00001), .out(shifter_3_out));
  Adder #(.width(32)) adder_3 (.a(shifter_3_out), .b(PC_q), .out(adder_3_out));  // open: cin, cout
  Register #(.width(32), .trigger("rising"), .Select("low")) register_1 (
    .D(R1), .en(ecall), .Q(LedData), .clk(CLK), .clr(RST));
  or or_3 (IR3_t, IR3, IRC);
  Multiplexer #(.select(1), .width(32), .disabled("Z"), .enable("false")) multiplexer_6 (
    .in0(MDin), .in1(multiplexer_5_out), .out(multiplexer_6_out), .sel(\单周期硬布线控制器_1_alu_src ));
  and and_2 (and_2_out, \单周期硬布线控制器_1_blt , alu_1_out_6);
  and and_3 (and_3_out, \单周期硬布线控制器_1_beq , alu_1_equal);
  and and_4 (and_4_out, \单周期硬布线控制器_1_bne , ~alu_1_equal);  // AND_Gate
  ALU alu_1 (
    .X(R1), .Y(multiplexer_6_out), .AluOP(\单周期硬布线控制器_1_alu_op ), .Equal(alu_1_equal), .Result(alu_1_result),
    .out_6(alu_1_out_6));  // open: Result_2, out_4
  Shifter #(.width(10), .shift("lr")) shifter_4 (.in(dataaddr), .\dist (4'b0010), .out(shifter_4_out));
  Bit_Extender #(.in_width(32), .out_width(10), .\type ("sign")) bit_extender_6 (.in(alu_1_result), .out(dataaddr));
  Multiplexer #(.select(1), .width(32), .disabled("Z"), .enable("false")) multiplexer_7 (
    .in0(multiplexer_10_out), .in1(shifter_6_out), .out(RDin), .sel(or_4_out));
  or or_4 (or_4_out, jal, jalr);
  assign and_5_out = alu_1_result & 32'hfffffffe;  // AND_Gate and_5, 32 bits wide
  Shifter #(.width(32), .shift("ar")) shifter_5 (.in(and_5_out), .\dist (5'b00010), .out(shifter_5_out));
  or or_5 (beq, and_2_out, and_3_out, and_4_out);
  // Probe on \单周期硬布线控制器_1_alu_op 
  Comparator #(.width(32), .mode("twosComplement")) comparator_3 (
    .a(MDin), .b(32'ha), .eq(comparator_3_eq));  // open: gt, lt
  RAM #(.addrWidth(10), .dataWidth(32), .bus("separate"), .Select("high")) ram_1 (
    .addr(shifter_4_out), .din(MDin), .data(ram_1_data), .str(MemWrite), .clk(CLK), .clr(RST));  // open: sel, ld
  and and_6 (and_6_out, comparator_3_eq, ecall);
  not not_2 (not_2_out, Go);
  Multiplexer #(.select(2), .width(8), .disabled("Z"), .enable("false")) multiplexer_8 (
    .in0(ram_1_data[7:0]), .in1(ram_1_data[15:8]), .in2(ram_1_data[23:16]), .in3(ram_1_data[31:24]),
    .out(multiplexer_8_out), .sel(dataaddr[1:0]));
  and and_7 (halt, and_6_out, not_2_out);
  assign bit_extender_7_out = {{24{multiplexer_8_out[7]}}, multiplexer_8_out};  // Bit_Extender bit_extender_7
  Shifter #(.width(32), .shift("ll")) shifter_6 (.in(adder_1_out), .\dist (5'b00010), .out(shifter_6_out));
  D_Flip_Flop #(.trigger("high"), .Pre_Clr_Positions("LEGACY"), .NegatePresetClear("false"), .enable("true"), .NewFFLayout("false")) d_ff_1 (.Q(d_ff_1_q));  // open: clk, D, Qn, preset, en, reset
  // Probe on 13'h120
  Multiplexer #(.select(1), .width(32), .disabled("Z"), .enable("false")) multiplexer_9 (
    .in0(ram_1_data), .in1(bit_extender_7_out), .out(multiplexer_9_out), .sel(lb));
  Comparator #(.width(13), .mode("twosComplement")) comparator_4 (
    .a(CNT_num), .b(13'h120), .eq(comparator_4_eq), .lt(comparator_4_lt));  // open: gt
  Clock #(.highDuration(1), .lowDuration(1)) clock_2 (.out(clock_2_out));
  Counter #(.width(13), .max('h1fff), .ongoal("stay"), .trigger("rising"), .behavior("old")) counter_1 (
    .count(comparator_4_lt), .Q(CNT_num), .clk(clock_2_out), .clr(RST));  // open: load, D, carry, preset
  Multiplexer #(.select(1), .width(32), .disabled("Z"), .enable("false")) multiplexer_10 (
    .in0(alu_1_result), .in1(multiplexer_9_out), .out(multiplexer_10_out), .sel(\单周期硬布线控制器_1_memtoreg ));
  nand nand_1 (nand_1_out, d_ff_1_q, comparator_4_eq);
  assign CLK = nand_1_out ? clock_2_out : 1'bz;  // Controlled_Buffer controlled_buffer_1
  Pull_Resistor #(.pull(1)) pull_resistor_1 (.node(CLK));
  Counter #(.width(16), .max('hffff), .ongoal("stay"), .trigger("rising"), .behavior("old")) counter_2 (
    .D(\总周期数 ), .Q(\总周期数 ), .clk(or_6_out), .clr(RST));  // open: load, count, carry, preset
  or or_6 (or_6_out, halt, CLK);

  // Other names for the same wires on the sheet: R2[31:0] = MDin

  // Notes on the sheet:
  //   中断源
  //   中断等待指示
  //   总复位信号应将除ROM以外所有存储组件全部清零
  //   数码管输出
  //   指令存储器
  //   数码管输出应该用寄存器锁存，否则显示数据只能一闪而过
  //   指令字
  //   contents of rom_1 (hex, n*v repeats v):
  //   100493 100006f 100493 200913 300993 100006f 100493 200913 300993 100006f 100493 200913 300993
  //   100006f 100493 200913 300993 3b8000ef 100413 100493 1f49493 900533 2200893 73 24d493 48463 fedff06f
  //   900533 2200893 73 100493 249493 900533 2200893 73 48463 fedff06f 100493 1f49493 900533 2200893 73
  //   4034d493 900533 2200893 73 4044d493 900533 2200893 73 4044d493 900533 2200893 73 4044d493 900533
  //   2200893 73 4044d493 900533 2200893 73 4044d493 900533 2200893 73 4044d493 900533 2200893 73 4044d493
  //   900533 2200893 73 100413 1f41993 41f9d993 433 c00913 300b13 140413 f47413 800293 100313 499993
  //   89e9b3 1300533 2200893 73 406282b3 fe0294e3 140413 f00f93 1f47433 1c41413 800293 100313 49d993
  //   89e9b3 1300533 2200893 73 406282b3 fe0294e3 1c45413 406b0b33 b0463 f95ff06f 2b3 fff2c293 829293
  //   ff2e293 500533 2200893 73 fff00413 493 84a023 140413 448493 84a023 140413 448493 84a023 140413
  //   448493 84a023 140413 448493 84a023 140413 448493 84a023 140413 448493 84a023 140413 448493 84a023
  //   140413 448493 84a023 140413 448493 84a023 140413 448493 84a023 140413 448493 84a023 140413 448493
  //   84a023 140413 448493 84a023 140413 448493 84a023 140413 448493 84a023 140413 448493 140413 433
  //   3c00493 42983 4aa03 149a2b3 28663 134a023 1442023 ffc48493 fe9412e3 800533 2200893 73 440413 3c00493
  //   fc9416e3 a00893 73 fff00293 7700493 849493 7748493 900533 2200893 73 1000e13 54c4b3 900533 2200893
  //   73 fffe0e13 fe0e16e3 a00893 73 fff00293 313 1900413 841413 9700493 940533 2200893 73 5484b3 494b313
  //   fe0306e3 a00893 73 313 1000e13 8400493 849493 8348493 400913 891913 490913 849493 8248493 849493
  //   8148493 891913 490913 891913 490913 932023 12484b3 430313 fffe0e13 fe0e18e3 2000e13 313 30483 900533
  //   2200893 73 130313 fffe0e13 fe0e14e3 a00893 73 ff100493 900533 2200893 73 148493 fe04c8e3 a00893 73
  //   a00893 73 413 140413 800533 2200893 73 240413 800533 2200893 73 340413 800533 2200893 73 440413
  //   800533 2200893 73 540413 800533 2200893 73 640413 800533 2200893 73 740413 800533 2200893 73 840413
  //   800533 2200893 2200893 73 8067
  //   Beq
  //   Bne
  //   MemToReg
  //   MemWrite
  //   AluOP
  //   AluSrcB
  //   RegWrite
  //   为方便自动评测，需要输出PC，IR，寄存器堆写如数据RDin
  //   数据存储器
  //   RAM写使能MemWrite、RAM写入数据MDin等信号
  //   控制位
  //   暂停节拍，不能为0
  //   戳工具置1进入计数暂停模式，ctrl+k时钟自动运行到对应节拍暂停
  //   ctrl+k关闭时钟连续运行，将控制位置零，进入单步调试模式调试
  //   用这个时钟源需要去掉电路中的其他时钟源
  //   可计数暂停的时钟源
endmodule

// 单周期硬布线控制器
module \单周期硬布线控制器  (
  input  [4:0] OP,
  input  [4:0] Funct,
  input  IR_0,
  output [3:0] ALU_OP,
  output MemToReg,
  output ALU_SRC,
  output MemWrite,
  output RegWrite,
  output ecall,
  output Beq,
  output S_type,
  output Bne,
  output Jalr,
  output JAL,
  output BLT,
  output LB,
  output URET,
  output CSRRCI,
  output CSRRSI
);

  wire not_1_out, \控制信号自动生成_1_alu_src , \控制信号自动生成_1_lb , \控制信号自动生成_1_memtoreg , \控制信号自动生成_1_regwrite ,
       \控制信号自动生成_1_s_type ;

  not not_1 (not_1_out, IR_0);
  \运算控制器自动生成  \u_运算控制器自动生成_1  (
    .OP2(OP[0]), .OP3(OP[1]), .OP4(OP[2]), .OP5(OP[3]), .OP6(OP[4]), .F12(Funct[0]), .F13(Funct[1]),
    .F14(Funct[2]), .F25(Funct[3]), .F30(Funct[4]), .S0(ALU_OP[0]), .S1(ALU_OP[1]), .S2(ALU_OP[2]),
    .S3(ALU_OP[3]));
  \控制信号自动生成  \u_控制信号自动生成_1  (
    .OP2(OP[0]), .OP3(OP[1]), .MemToReg(\控制信号自动生成_1_memtoreg ), .OP4(OP[2]), .OP5(OP[3]), .OP6(OP[4]),
    .F12(Funct[0]), .MemWrite(MemWrite), .F13(Funct[1]), .F14(Funct[2]), .F25(Funct[3]), .F30(Funct[4]),
    .ALU_SRC(\控制信号自动生成_1_alu_src ), .RegWrite(\控制信号自动生成_1_regwrite ), .ecall(ecall),
    .S_Type(\控制信号自动生成_1_s_type ), .BEQ(Beq), .BNE(Bne), .JALR(Jalr), .JAL(JAL), .LB(\控制信号自动生成_1_lb ),
    .BLT(BLT), .URET(URET), .CSRRCI(CSRRCI), .CSRRSI(CSRRSI));
  and and_1 (MemToReg, not_1_out, \控制信号自动生成_1_memtoreg );
  and and_2 (ALU_SRC, \控制信号自动生成_1_alu_src , not_1_out);
  and and_3 (RegWrite, \控制信号自动生成_1_regwrite , not_1_out);
  and and_4 (S_type, \控制信号自动生成_1_s_type , not_1_out);
  and and_5 (LB, \控制信号自动生成_1_lb , not_1_out);

  // Other names for the same wires on the sheet: OP_CODE[4:0] = OP

  // Notes on the sheet:
  //   运算器控制器，根据指令生成运算器功能选择信号
  //   控制信号生成，产生数据通路需要的其他控制信号
endmodule

// 运算器控制器
module \运算控制器自动生成  (
  input  OP2,
  input  OP3,
  input  OP4,
  input  OP5,
  input  OP6,
  input  F12,
  input  F13,
  input  F14,
  input  F25,
  input  F30,
  output S0,
  output S1,
  output S2,
  output S3
);

  wire and_1_out, and_2_out, and_3_out, and_4_out, and_5_out, and_6_out, and_7_out, and_8_out, and_9_out,
       and_10_out, and_11_out, and_12_out, and_13_out, and_14_out, and_15_out, and_16_out, and_17_out,
       and_18_out, and_19_out, and_20_out, and_21_out, and_22_out, and_23_out, and_24_out, and_25_out,
       and_26_out, and_27_out, and_28_out, and_29_out, and_30_out, and_31_out, and_32_out, and_33_out,
       and_34_out, and_35_out, and_36_out, and_37_out, and_38_out, and_39_out, and_40_out, and_41_out,
       and_42_out, and_43_out, and_44_out, and_45_out, and_46_out, and_47_out, and_48_out, and_49_out,
       and_50_out, and_51_out, and_52_out, and_53_out, not_1_out, not_2_out, not_3_out, not_4_out, not_5_out,
       not_6_out, not_7_out, not_8_out, not_9_out, not_10_out, not_11_out, not_12_out, not_13_out,
       not_14_out, not_15_out, not_16_out, not_17_out, not_18_out, not_19_out, not_20_out, not_21_out,
       not_22_out, not_23_out, not_24_out, not_25_out, not_26_out, not_27_out, not_28_out, not_29_out,
       not_30_out, not_31_out, not_32_out, not_33_out, not_34_out, not_35_out, not_36_out, not_37_out,
       not_38_out, not_39_out, not_40_out, not_41_out, not_42_out, not_43_out, not_44_out, not_45_out,
       not_46_out, not_47_out, not_48_out, not_49_out, not_50_out, not_51_out, not_52_out, not_53_out,
       not_54_out, not_55_out, not_56_out, not_57_out, not_58_out, not_59_out, not_60_out, not_61_out,
       not_62_out, not_63_out, not_64_out, not_65_out, not_66_out, not_67_out, not_68_out, not_69_out,
       not_70_out, not_71_out, not_72_out, not_73_out, not_74_out, not_75_out, not_76_out, not_77_out,
       not_78_out, not_79_out, not_80_out, not_81_out, not_82_out, not_83_out, not_84_out, not_85_out,
       not_86_out, not_87_out, not_88_out, not_89_out, not_90_out, not_91_out, not_92_out, not_93_out,
       not_94_out, not_95_out, not_96_out, not_97_out, not_98_out, not_99_out, not_100_out, not_101_out,
       not_102_out, not_103_out, not_104_out, not_105_out, not_106_out, not_107_out, not_108_out,
       not_109_out, not_110_out, not_111_out, not_112_out, not_113_out, not_114_out, not_115_out,
       not_116_out, not_117_out, not_118_out, not_119_out, not_120_out, not_121_out, not_122_out,
       not_123_out, not_124_out, not_125_out, not_126_out, not_127_out, not_128_out, not_129_out,
       not_130_out, not_131_out, not_132_out, not_133_out, not_134_out, not_135_out, not_136_out,
       not_137_out, not_138_out, not_139_out, not_140_out, not_141_out, not_142_out, not_143_out,
       not_144_out, not_145_out, not_146_out, not_147_out, not_148_out, not_149_out, not_150_out,
       not_151_out, not_152_out, not_153_out, not_154_out, not_155_out, not_156_out, not_157_out,
       not_158_out, not_159_out, not_160_out, not_161_out, not_162_out, not_163_out, not_164_out,
       not_165_out, not_166_out, not_167_out, not_168_out, not_169_out, not_170_out, not_171_out,
       not_172_out, not_173_out, not_174_out, not_175_out, not_176_out, not_177_out, not_178_out,
       not_179_out, not_180_out, not_181_out, not_182_out, not_183_out, not_184_out, not_185_out,
       not_186_out, not_187_out, not_188_out, not_189_out, not_190_out, not_191_out, not_192_out,
       not_193_out, not_194_out, not_195_out, not_196_out, not_197_out, not_198_out, not_199_out,
       not_200_out, not_201_out, not_202_out, not_203_out, not_204_out, not_205_out, not_206_out,
       not_207_out, not_208_out, not_209_out, not_210_out, not_211_out, not_212_out, not_213_out,
       not_214_out, not_215_out, not_216_out, not_217_out, not_218_out, not_219_out, not_220_out,
       not_221_out, not_222_out, not_223_out, not_224_out, not_225_out, not_226_out, not_227_out,
       not_228_out, not_229_out, not_230_out, not_231_out, not_232_out, not_233_out, not_234_out,
       not_235_out, not_236_out, not_237_out, not_238_out, not_239_out, not_240_out, not_241_out,
       not_242_out, not_243_out, not_244_out, not_245_out, not_246_out, not_247_out, not_248_out,
       not_249_out, not_250_out, not_251_out, not_252_out, not_253_out, not_254_out, not_255_out,
       not_256_out, not_257_out, not_258_out, not_259_out, not_260_out, not_261_out, not_262_out,
       not_263_out, not_264_out, not_265_out, not_266_out, not_267_out, not_268_out, not_269_out,
       not_270_out, not_271_out, not_272_out, not_273_out, not_274_out, not_275_out, not_276_out,
       not_277_out, not_278_out, not_279_out, not_280_out, not_281_out, not_282_out, not_283_out,
       not_284_out, not_285_out, not_286_out, not_287_out, not_288_out, not_289_out, not_290_out,
       not_291_out, not_292_out, not_293_out;

  not not_1 (not_1_out, F30);
  not not_2 (not_2_out, F25);
  not not_3 (not_3_out, F14);
  not not_4 (not_4_out, F13);
  not not_5 (not_5_out, F12);
  not not_6 (not_6_out, OP6);
  not not_7 (not_7_out, OP3);
  not not_8 (not_8_out, OP2);
  not not_9 (not_9_out, F30);
  not not_10 (not_10_out, F25);
  not not_11 (not_11_out, OP6);
  not not_12 (not_12_out, OP3);
  not not_13 (not_13_out, OP2);
  not not_14 (not_14_out, F30);
  not not_15 (not_15_out, F25);
  not not_16 (not_16_out, F14);
  not not_17 (not_17_out, F12);
  not not_18 (not_18_out, OP6);
  not not_19 (not_19_out, OP3);
  not not_20 (not_20_out, OP2);
  not not_21 (not_21_out, F14);
  not not_22 (not_22_out, F13);
  not not_23 (not_23_out, F12);
  not not_24 (not_24_out, OP6);
  not not_25 (not_25_out, OP5);
  not not_26 (not_26_out, OP3);
  not not_27 (not_27_out, OP2);
  not not_28 (not_28_out, OP6);
  not not_29 (not_29_out, OP5);
  not not_30 (not_30_out, OP3);
  not not_31 (not_31_out, OP2);
  not not_32 (not_32_out, F13);
  not not_33 (not_33_out, F12);
  not not_34 (not_34_out, OP6);
  not not_35 (not_35_out, OP5);
  not not_36 (not_36_out, OP3);
  not not_37 (not_37_out, OP2);
  not not_38 (not_38_out, F14);
  not not_39 (not_39_out, F12);
  not not_40 (not_40_out, OP6);
  not not_41 (not_41_out, OP5);
  not not_42 (not_42_out, OP3);
  not not_43 (not_43_out, OP2);
  not not_44 (not_44_out, F25);
  not not_45 (not_45_out, F13);
  not not_46 (not_46_out, OP6);
  not not_47 (not_47_out, OP5);
  not not_48 (not_48_out, OP3);
  not not_49 (not_49_out, OP2);
  not not_50 (not_50_out, F14);
  not not_51 (not_51_out, F12);
  not not_52 (not_52_out, OP6);
  not not_53 (not_53_out, OP5);
  not not_54 (not_54_out, OP4);
  not not_55 (not_55_out, OP3);
  not not_56 (not_56_out, OP2);
  not not_57 (not_57_out, F14);
  not not_58 (not_58_out, F12);
  not not_59 (not_59_out, OP6);
  not not_60 (not_60_out, OP4);
  not not_61 (not_61_out, OP3);
  not not_62 (not_62_out, OP2);
  not not_63 (not_63_out, F14);
  not not_64 (not_64_out, F13);
  not not_65 (not_65_out, F12);
  not not_66 (not_66_out, OP4);
  not not_67 (not_67_out, OP3);
  not not_68 (not_68_out, OP2);
  not not_69 (not_69_out, F14);
  not not_70 (not_70_out, F13);
  not not_71 (not_71_out, OP4);
  not not_72 (not_72_out, OP3);
  not not_73 (not_73_out, OP2);
  not not_74 (not_74_out, OP4);
  not not_75 (not_75_out, F14);
  not not_76 (not_76_out, F13);
  not not_77 (not_77_out, F12);
  not not_78 (not_78_out, OP4);
  not not_79 (not_79_out, OP3);
  not not_80 (not_80_out, OP3);
  not not_81 (not_81_out, OP2);
  not not_82 (not_82_out, F30);
  not not_83 (not_83_out, F25);
  not not_84 (not_84_out, F13);
  not not_85 (not_85_out, F12);
  not not_86 (not_86_out, OP6);
  not not_87 (not_87_out, OP3);
  not not_88 (not_88_out, OP2);
  not not_89 (not_89_out, F14);
  not not_90 (not_90_out, F13);
  not not_91 (not_91_out, F12);
  not not_92 (not_92_out, OP6);
  not not_93 (not_93_out, OP5);
  not not_94 (not_94_out, OP4);
  not not_95 (not_95_out, OP3);
  not not_96 (not_96_out, OP2);
  not not_97 (not_97_out, F13);
  not not_98 (not_98_out, F12);
  not not_99 (not_99_out, OP4);
  not not_100 (not_100_out, OP3);
  not not_101 (not_101_out, OP2);
  not not_102 (not_102_out, F25);
  not not_103 (not_103_out, F14);
  not not_104 (not_104_out, F13);
  not not_105 (not_105_out, F12);
  not not_106 (not_106_out, OP6);
  not not_107 (not_107_out, OP3);
  not not_108 (not_108_out, OP2);
  not not_109 (not_109_out, F30);
  not not_110 (not_110_out, F25);
  not not_111 (not_111_out, OP6);
  not not_112 (not_112_out, OP3);
  not not_113 (not_113_out, OP2);
  not not_114 (not_114_out, F30);
  not not_115 (not_115_out, F25);
  not not_116 (not_116_out, F14);
  not not_117 (not_117_out, F12);
  not not_118 (not_118_out, OP6);
  not not_119 (not_119_out, OP3);
  not not_120 (not_120_out, OP2);
  not not_121 (not_121_out, OP6);
  not not_122 (not_122_out, OP5);
  not not_123 (not_123_out, OP3);
  not not_124 (not_124_out, OP2);
  not not_125 (not_125_out, F14);
  not not_126 (not_126_out, F12);
  not not_127 (not_127_out, OP6);
  not not_128 (not_128_out, OP5);
  not not_129 (not_129_out, OP3);
  not not_130 (not_130_out, OP2);
  not not_131 (not_131_out, F30);
  not not_132 (not_132_out, F25);
  not not_133 (not_133_out, F13);
  not not_134 (not_134_out, OP6);
  not not_135 (not_135_out, OP5);
  not not_136 (not_136_out, OP3);
  not not_137 (not_137_out, OP2);
  not not_138 (not_138_out, F14);
  not not_139 (not_139_out, F13);
  not not_140 (not_140_out, F12);
  not not_141 (not_141_out, OP4);
  not not_142 (not_142_out, OP3);
  not not_143 (not_143_out, OP2);
  not not_144 (not_144_out, F14);
  not not_145 (not_145_out, F13);
  not not_146 (not_146_out, OP4);
  not not_147 (not_147_out, OP3);
  not not_148 (not_148_out, OP2);
  not not_149 (not_149_out, OP3);
  not not_150 (not_150_out, OP2);
  not not_151 (not_151_out, F13);
  not not_152 (not_152_out, F12);
  not not_153 (not_153_out, OP4);
  not not_154 (not_154_out, OP3);
  not not_155 (not_155_out, OP2);
  not not_156 (not_156_out, F30);
  not not_157 (not_157_out, F25);
  not not_158 (not_158_out, F14);
  not not_159 (not_159_out, F13);
  not not_160 (not_160_out, F12);
  not not_161 (not_161_out, OP6);
  not not_162 (not_162_out, OP3);
  not not_163 (not_163_out, OP2);
  not not_164 (not_164_out, F25);
  not not_165 (not_165_out, F14);
  not not_166 (not_166_out, F13);
  not not_167 (not_167_out, F12);
  not not_168 (not_168_out, OP6);
  not not_169 (not_169_out, OP3);
  not not_170 (not_170_out, OP2);
  not not_171 (not_171_out, F30);
  not not_172 (not_172_out, F25);
  not not_173 (not_173_out, OP6);
  not not_174 (not_174_out, OP3);
  not not_175 (not_175_out, OP2);
  not not_176 (not_176_out, F30);
  not not_177 (not_177_out, F25);
  not not_178 (not_178_out, F14);
  not not_179 (not_179_out, OP6);
  not not_180 (not_180_out, OP3);
  not not_181 (not_181_out, OP2);
  not not_182 (not_182_out, F14);
  not not_183 (not_183_out, F13);
  not not_184 (not_184_out, F12);
  not not_185 (not_185_out, OP6);
  not not_186 (not_186_out, OP5);
  not not_187 (not_187_out, OP3);
  not not_188 (not_188_out, OP2);
  not not_189 (not_189_out, OP6);
  not not_190 (not_190_out, OP5);
  not not_191 (not_191_out, OP3);
  not not_192 (not_192_out, OP2);
  not not_193 (not_193_out, F14);
  not not_194 (not_194_out, F12);
  not not_195 (not_195_out, OP6);
  not not_196 (not_196_out, OP5);
  not not_197 (not_197_out, OP4);
  not not_198 (not_198_out, OP3);
  not not_199 (not_199_out, OP2);
  not not_200 (not_200_out, F14);
  not not_201 (not_201_out, F12);
  not not_202 (not_202_out, OP6);
  not not_203 (not_203_out, OP4);
  not not_204 (not_204_out, OP3);
  not not_205 (not_205_out, OP2);
  not not_206 (not_206_out, OP4);
  not not_207 (not_207_out, F14);
  not not_208 (not_208_out, F13);
  not not_209 (not_209_out, F12);
  not not_210 (not_210_out, OP4);
  not not_211 (not_211_out, OP3);
  not not_212 (not_212_out, OP3);
  not not_213 (not_213_out, OP2);
  not not_214 (not_214_out, F14);
  not not_215 (not_215_out, OP6);
  not not_216 (not_216_out, OP5);
  not not_217 (not_217_out, OP3);
  not not_218 (not_218_out, OP2);
  not not_219 (not_219_out, F14);
  not not_220 (not_220_out, F13);
  not not_221 (not_221_out, F12);
  not not_222 (not_222_out, OP6);
  not not_223 (not_223_out, OP5);
  not not_224 (not_224_out, OP4);
  not not_225 (not_225_out, OP3);
  not not_226 (not_226_out, OP2);
  not not_227 (not_227_out, F30);
  not not_228 (not_228_out, F25);
  not not_229 (not_229_out, F12);
  not not_230 (not_230_out, OP6);
  not not_231 (not_231_out, OP3);
  not not_232 (not_232_out, OP2);
  not not_233 (not_233_out, F30);
  not not_234 (not_234_out, F25);
  not not_235 (not_235_out, F14);
  not not_236 (not_236_out, F12);
  not not_237 (not_237_out, OP6);
  not not_238 (not_238_out, OP3);
  not not_239 (not_239_out, OP2);
  not not_240 (not_240_out, F30);
  not not_241 (not_241_out, F25);
  not not_242 (not_242_out, F14);
  not not_243 (not_243_out, OP6);
  not not_244 (not_244_out, OP3);
  not not_245 (not_245_out, OP2);
  not not_246 (not_246_out, F12);
  not not_247 (not_247_out, OP6);
  not not_248 (not_248_out, OP5);
  not not_249 (not_249_out, OP3);
  not not_250 (not_250_out, OP2);
  not not_251 (not_251_out, F13);
  not not_252 (not_252_out, F12);
  not not_253 (not_253_out, OP6);
  not not_254 (not_254_out, OP5);
  not not_255 (not_255_out, OP3);
  not not_256 (not_256_out, OP2);
  not not_257 (not_257_out, F14);
  not not_258 (not_258_out, F12);
  not not_259 (not_259_out, OP6);
  not not_260 (not_260_out, OP5);
  not not_261 (not_261_out, OP3);
  not not_262 (not_262_out, OP2);
  not not_263 (not_263_out, F14);
  not not_264 (not_264_out, F13);
  not not_265 (not_265_out, F12);
  not not_266 (not_266_out, OP4);
  not not_267 (not_267_out, OP3);
  not not_268 (not_268_out, OP2);
  not not_269 (not_269_out, F14);
  not not_270 (not_270_out, F13);
  not not_271 (not_271_out, OP4);
  not not_272 (not_272_out, OP3);
  not not_273 (not_273_out, OP2);
  not not_274 (not_274_out, F12);
  not not_275 (not_275_out, OP3);
  not not_276 (not_276_out, OP2);
  not not_277 (not_277_out, F30);
  not not_278 (not_278_out, F25);
  not not_279 (not_279_out, F13);
  not not_280 (not_280_out, F12);
  not not_281 (not_281_out, OP6);
  not not_282 (not_282_out, OP3);
  not not_283 (not_283_out, OP2);
  not not_284 (not_284_out, F14);
  not not_285 (not_285_out, OP6);
  not not_286 (not_286_out, OP5);
  not not_287 (not_287_out, OP3);
  not not_288 (not_288_out, OP2);
  not not_289 (not_289_out, F13);
  not not_290 (not_290_out, F12);
  not not_291 (not_291_out, OP4);
  not not_292 (not_292_out, OP3);
  not not_293 (not_293_out, OP2);
  and and_1 (and_1_out, not_1_out, not_2_out, not_3_out, not_4_out, not_5_out, not_6_out, OP5, OP4, not_7_out, not_8_out);
  and and_2 (and_2_out, not_9_out, not_10_out, F14, F13, F12, not_11_out, OP5, OP4, not_12_out, not_13_out);
  and and_3 (and_3_out, not_14_out, not_15_out, not_16_out, F13, not_17_out, not_18_out, OP5, OP4, not_19_out, not_20_out);
  and and_4 (and_4_out, not_21_out, not_22_out, not_23_out, not_24_out, not_25_out, OP4, not_26_out, not_27_out);
  and and_5 (and_5_out, F14, F13, F12, not_28_out, not_29_out, OP4, not_30_out, not_31_out);
  and and_6 (and_6_out, F14, not_32_out, not_33_out, not_34_out, not_35_out, OP4, not_36_out, not_37_out);
  and and_7 (and_7_out, not_38_out, F13, not_39_out, not_40_out, not_41_out, OP4, not_42_out, not_43_out);
  and and_8 (and_8_out, F30, not_44_out, F14, not_45_out, F12, not_46_out, not_47_out, OP4, not_48_out, not_49_out);
  and and_9 (and_9_out, not_50_out, F13, not_51_out, not_52_out, not_53_out, not_54_out, not_55_out, not_56_out);
  and and_10 (and_10_out, not_57_out, F13, not_58_out, not_59_out, OP5, not_60_out, not_61_out, not_62_out);
  and and_11 (and_11_out, not_63_out, not_64_out, not_65_out, OP6, OP5, not_66_out, not_67_out, not_68_out);
  and and_12 (and_12_out, not_69_out, not_70_out, F12, OP6, OP5, not_71_out, not_72_out, not_73_out);
  and and_13 (and_13_out, OP6, OP5, not_74_out, OP3, OP2);
  and and_14 (and_14_out, not_75_out, not_76_out, not_77_out, OP6, OP5, not_78_out, not_79_out, OP2);
  and and_15 (and_15_out, F14, F13, F12, OP6, OP5, OP4, not_80_out, not_81_out);
  and and_16 (and_16_out, not_82_out, not_83_out, F14, not_84_out, not_85_out, not_86_out, OP5, OP4, not_87_out, not_88_out);
  and and_17 (and_17_out, not_89_out, not_90_out, not_91_out, not_92_out, not_93_out, not_94_out, not_95_out, not_96_out);
  and and_18 (and_18_out, F14, not_97_out, not_98_out, OP6, OP5, not_99_out, not_100_out, not_101_out);
  and and_19 (and_19_out, F30, not_102_out, not_103_out, not_104_out, not_105_out, not_106_out, OP5, OP4, not_107_out, not_108_out);
  and and_20 (and_20_out, not_109_out, not_110_out, F14, F13, F12, not_111_out, OP5, OP4, not_112_out, not_113_out);
  and and_21 (and_21_out, not_114_out, not_115_out, not_116_out, F13, not_117_out, not_118_out, OP5, OP4, not_119_out, not_120_out);
  and and_22 (and_22_out, F14, F13, F12, not_121_out, not_122_out, OP4, not_123_out, not_124_out);
  and and_23 (and_23_out, not_125_out, F13, not_126_out, not_127_out, not_128_out, OP4, not_129_out, not_130_out);
  and and_24 (and_24_out, not_131_out, not_132_out, F14, not_133_out, F12, not_134_out, not_135_out, OP4, not_136_out, not_137_out);
  and and_25 (and_25_out, not_138_out, not_139_out, not_140_out, OP6, OP5, not_141_out, not_142_out, not_143_out);
  and and_26 (and_26_out, not_144_out, not_145_out, F12, OP6, OP5, not_146_out, not_147_out, not_148_out);
  and and_27 (and_27_out, F14, F13, F12, OP6, OP5, OP4, not_149_out, not_150_out);
  and and_28 (and_28_out, F14, not_151_out, not_152_out, OP6, OP5, not_153_out, not_154_out, not_155_out);
  and and_29 (and_29_out, not_156_out, not_157_out, not_158_out, not_159_out, not_160_out, not_161_out, OP5, OP4, not_162_out, not_163_out);
  and and_30 (and_30_out, F30, not_164_out, not_165_out, not_166_out, not_167_out, not_168_out, OP5, OP4, not_169_out, not_170_out);
  and and_31 (and_31_out, not_171_out, not_172_out, F14, F13, F12, not_173_out, OP5, OP4, not_174_out, not_175_out);
  and and_32 (and_32_out, not_176_out, not_177_out, not_178_out, F13, F12, not_179_out, OP5, OP4, not_180_out, not_181_out);
  and and_33 (and_33_out, not_182_out, not_183_out, not_184_out, not_185_out, not_186_out, OP4, not_187_out, not_188_out);
  and and_34 (and_34_out, F14, F13, F12, not_189_out, not_190_out, OP4, not_191_out, not_192_out);
  and and_35 (and_35_out, not_193_out, F13, not_194_out, not_195_out, not_196_out, not_197_out, not_198_out, not_199_out);
  and and_36 (and_36_out, not_200_out, F13, not_201_out, not_202_out, OP5, not_203_out, not_204_out, not_205_out);
  and and_37 (and_37_out, OP6, OP5, not_206_out, OP3, OP2);
  and and_38 (and_38_out, not_207_out, not_208_out, not_209_out, OP6, OP5, not_210_out, not_211_out, OP2);
  and and_39 (and_39_out, F14, F13, F12, OP6, OP5, OP4, not_212_out, not_213_out);
  and and_40 (and_40_out, not_214_out, F13, F12, not_215_out, not_216_out, OP4, not_217_out, not_218_out);
  and and_41 (and_41_out, not_219_out, not_220_out, not_221_out, not_222_out, not_223_out, not_224_out, not_225_out, not_226_out);
  and and_42 (and_42_out, not_227_out, not_228_out, F14, F13, not_229_out, not_230_out, OP5, OP4, not_231_out, not_232_out);
  and and_43 (and_43_out, not_233_out, not_234_out, not_235_out, F13, not_236_out, not_237_out, OP5, OP4, not_238_out, not_239_out);
  and and_44 (and_44_out, not_240_out, not_241_out, not_242_out, F13, F12, not_243_out, OP5, OP4, not_244_out, not_245_out);
  and and_45 (and_45_out, F14, F13, not_246_out, not_247_out, not_248_out, OP4, not_249_out, not_250_out);
  and and_46 (and_46_out, F14, not_251_out, not_252_out, not_253_out, not_254_out, OP4, not_255_out, not_256_out);
  and and_47 (and_47_out, not_257_out, F13, not_258_out, not_259_out, not_260_out, OP4, not_261_out, not_262_out);
  and and_48 (and_48_out, not_263_out, not_264_out, not_265_out, OP6, OP5, not_266_out, not_267_out, not_268_out);
  and and_49 (and_49_out, not_269_out, not_270_out, F12, OP6, OP5, not_271_out, not_272_out, not_273_out);
  and and_50 (and_50_out, F14, F13, not_274_out, OP6, OP5, OP4, not_275_out, not_276_out);
  and and_51 (and_51_out, not_277_out, not_278_out, F14, not_279_out, not_280_out, not_281_out, OP5, OP4, not_282_out, not_283_out);
  and and_52 (and_52_out, not_284_out, F13, F12, not_285_out, not_286_out, OP4, not_287_out, not_288_out);
  and and_53 (and_53_out, F14, not_289_out, not_290_out, OP6, OP5, not_291_out, not_292_out, not_293_out);
  or or_1 (S0, and_1_out, and_2_out, and_3_out, and_4_out, and_5_out, and_6_out, and_7_out, and_8_out, and_9_out, and_10_out, and_11_out, and_12_out, and_13_out, and_14_out, and_15_out, and_16_out, and_17_out, and_18_out);
  or or_2 (S1, and_19_out, and_20_out, and_21_out, and_22_out, and_23_out, and_24_out, and_25_out, and_26_out, and_27_out, and_28_out);
  or or_3 (S2, and_29_out, and_30_out, and_31_out, and_32_out, and_33_out, and_34_out, and_35_out, and_36_out, and_37_out, and_38_out, and_39_out, and_40_out, and_41_out);
  or or_4 (S3, and_42_out, and_43_out, and_44_out, and_45_out, and_46_out, and_47_out, and_48_out, and_49_out, and_50_out, and_51_out, and_52_out, and_53_out);
endmodule

// 控制信号生成
module \控制信号自动生成  (
  input  OP2,
  input  OP3,
  input  OP4,
  input  OP5,
  input  OP6,
  input  F12,
  input  F13,
  input  F14,
  input  F25,
  input  F30,
  output MemToReg,
  output MemWrite,
  output ALU_SRC,
  output RegWrite,
  output ecall,
  output S_Type,
  output BEQ,
  output BNE,
  output JALR,
  output JAL,
  output LB,
  output BLT,
  output URET,
  output CSRRCI,
  output CSRRSI
);

  wire and_3_out, and_4_out, and_5_out, and_6_out, and_7_out, and_8_out, and_9_out, and_10_out, and_11_out,
       and_12_out, and_13_out, and_14_out, and_15_out, and_16_out, and_17_out, and_18_out, and_19_out,
       and_21_out, and_22_out, and_23_out, and_24_out, and_25_out, and_26_out, and_27_out, and_28_out,
       and_29_out, and_30_out, and_31_out, not_1_out, not_2_out, not_3_out, not_4_out, not_5_out, not_6_out,
       not_7_out, not_8_out, not_9_out, not_10_out, not_11_out, not_12_out, not_13_out, not_14_out,
       not_15_out, not_16_out, not_17_out, not_18_out, not_19_out, not_20_out, not_21_out, not_22_out,
       not_23_out, not_24_out, not_25_out, not_26_out, not_27_out, not_28_out, not_29_out, not_30_out,
       not_31_out, not_32_out, not_33_out, not_34_out, not_35_out, not_36_out, not_37_out, not_38_out,
       not_39_out, not_40_out, not_41_out, not_42_out, not_43_out, not_44_out, not_45_out, not_46_out,
       not_47_out, not_48_out, not_49_out, not_50_out, not_51_out, not_52_out, not_53_out, not_54_out,
       not_55_out, not_56_out, not_57_out, not_58_out, not_59_out, not_60_out, not_61_out, not_62_out,
       not_63_out, not_64_out, not_65_out, not_66_out, not_67_out, not_68_out, not_69_out, not_70_out,
       not_71_out, not_72_out, not_73_out, not_74_out, not_75_out, not_76_out, not_77_out, not_78_out,
       not_79_out, not_80_out, not_81_out, not_82_out, not_83_out, not_84_out, not_85_out, not_86_out,
       not_87_out, not_88_out, not_89_out, not_90_out, not_91_out, not_92_out, not_93_out, not_94_out,
       not_95_out, not_96_out, not_97_out, not_98_out, not_99_out, not_100_out, not_101_out, not_102_out,
       not_103_out, not_104_out, not_105_out, not_106_out, not_107_out, not_108_out, not_109_out,
       not_110_out, not_111_out, not_112_out, not_113_out, not_114_out, not_115_out, not_116_out,
       not_117_out, not_118_out, not_119_out, not_120_out, not_121_out, not_122_out, not_123_out,
       not_124_out, not_125_out, not_126_out, not_127_out, not_128_out, not_129_out, not_130_out,
       not_131_out, not_132_out, not_133_out, not_134_out, not_135_out, not_136_out, not_137_out,
       not_138_out, not_139_out, not_140_out, not_141_out, not_142_out, not_143_out, not_144_out,
       not_145_out, not_146_out, not_147_out, not_148_out, not_149_out, not_150_out, not_151_out,
       not_152_out, not_153_out, not_154_out, not_155_out, not_156_out, not_157_out, not_158_out,
       not_159_out, not_160_out, not_161_out, not_162_out, not_163_out, not_164_out, not_165_out,
       not_166_out, not_167_out, not_168_out, not_169_out, not_170_out, not_171_out, not_172_out,
       not_173_out, not_174_out, not_175_out, not_176_out, not_177_out, not_178_out, not_179_out,
       not_180_out, not_181_out, not_182_out, not_183_out, not_184_out, not_185_out, not_186_out,
       not_187_out, not_188_out, not_189_out, not_190_out, not_191_out, not_192_out, not_193_out,
       not_194_out, not_195_out, not_196_out, not_197_out, not_198_out, not_199_out, not_200_out,
       not_201_out, not_202_out, not_203_out, not_204_out, not_205_out;

  not not_1 (not_1_out, OP2);
  not not_2 (not_2_out, OP3);
  not not_3 (not_3_out, OP4);
  not not_4 (not_4_out, OP5);
  not not_5 (not_5_out, OP6);
  not not_6 (not_6_out, F12);
  not not_7 (not_7_out, F14);
  not not_8 (not_8_out, OP2);
  not not_9 (not_9_out, OP3);
  not not_10 (not_10_out, OP4);
  not not_11 (not_11_out, OP6);
  not not_12 (not_12_out, F12);
  not not_13 (not_13_out, F14);
  not not_14 (not_14_out, OP2);
  not not_15 (not_15_out, OP3);
  not not_16 (not_16_out, OP5);
  not not_17 (not_17_out, OP6);
  not not_18 (not_18_out, F12);
  not not_19 (not_19_out, F14);
  not not_20 (not_20_out, OP2);
  not not_21 (not_21_out, OP3);
  not not_22 (not_22_out, OP4);
  not not_23 (not_23_out, OP6);
  not not_24 (not_24_out, F12);
  not not_25 (not_25_out, F14);
  not not_26 (not_26_out, OP2);
  not not_27 (not_27_out, OP3);
  not not_28 (not_28_out, OP5);
  not not_29 (not_29_out, OP6);
  not not_30 (not_30_out, F12);
  not not_31 (not_31_out, OP2);
  not not_32 (not_32_out, OP3);
  not not_33 (not_33_out, OP5);
  not not_34 (not_34_out, OP6);
  not not_35 (not_35_out, F25);
  not not_36 (not_36_out, F30);
  not not_37 (not_37_out, OP2);
  not not_38 (not_38_out, OP3);
  not not_39 (not_39_out, OP5);
  not not_40 (not_40_out, OP6);
  not not_41 (not_41_out, F25);
  not not_42 (not_42_out, OP2);
  not not_43 (not_43_out, OP3);
  not not_44 (not_44_out, OP5);
  not not_45 (not_45_out, OP6);
  not not_46 (not_46_out, OP3);
  not not_47 (not_47_out, OP4);
  not not_48 (not_48_out, F12);
  not not_49 (not_49_out, F13);
  not not_50 (not_50_out, F14);
  not not_51 (not_51_out, OP2);
  not not_52 (not_52_out, OP3);
  not not_53 (not_53_out, OP5);
  not not_54 (not_54_out, OP6);
  not not_55 (not_55_out, F12);
  not not_56 (not_56_out, F14);
  not not_57 (not_57_out, OP2);
  not not_58 (not_58_out, OP3);
  not not_59 (not_59_out, OP5);
  not not_60 (not_60_out, OP6);
  not not_61 (not_61_out, F12);
  not not_62 (not_62_out, OP2);
  not not_63 (not_63_out, OP3);
  not not_64 (not_64_out, OP5);
  not not_65 (not_65_out, OP6);
  not not_66 (not_66_out, F25);
  not not_67 (not_67_out, F30);
  not not_68 (not_68_out, OP2);
  not not_69 (not_69_out, OP3);
  not not_70 (not_70_out, OP6);
  not not_71 (not_71_out, F12);
  not not_72 (not_72_out, F13);
  not not_73 (not_73_out, F14);
  not not_74 (not_74_out, F25);
  not not_75 (not_75_out, OP2);
  not not_76 (not_76_out, OP3);
  not not_77 (not_77_out, OP6);
  not not_78 (not_78_out, F12);
  not not_79 (not_79_out, F25);
  not not_80 (not_80_out, F30);
  not not_81 (not_81_out, OP2);
  not not_82 (not_82_out, OP3);
  not not_83 (not_83_out, OP5);
  not not_84 (not_84_out, OP6);
  not not_85 (not_85_out, F25);
  not not_86 (not_86_out, OP2);
  not not_87 (not_87_out, OP3);
  not not_88 (not_88_out, OP5);
  not not_89 (not_89_out, OP6);
  not not_90 (not_90_out, OP2);
  not not_91 (not_91_out, OP3);
  not not_92 (not_92_out, OP6);
  not not_93 (not_93_out, F25);
  not not_94 (not_94_out, F30);
  not not_95 (not_95_out, OP4);
  not not_96 (not_96_out, F12);
  not not_97 (not_97_out, F13);
  not not_98 (not_98_out, F14);
  not not_99 (not_99_out, OP4);
  not not_100 (not_100_out, OP2);
  not not_101 (not_101_out, OP3);
  not not_102 (not_102_out, F12);
  not not_103 (not_103_out, F13);
  not not_104 (not_104_out, F14);
  not not_105 (not_105_out, F25);
  not not_106 (not_106_out, F30);
  not not_107 (not_107_out, OP2);
  not not_108 (not_108_out, OP3);
  not not_109 (not_109_out, OP5);
  not not_110 (not_110_out, OP6);
  not not_111 (not_111_out, F12);
  not not_112 (not_112_out, F14);
  not not_113 (not_113_out, F25);
  not not_114 (not_114_out, F30);
  not not_115 (not_115_out, OP2);
  not not_116 (not_116_out, OP3);
  not not_117 (not_117_out, OP5);
  not not_118 (not_118_out, OP6);
  not not_119 (not_119_out, F12);
  not not_120 (not_120_out, F14);
  not not_121 (not_121_out, OP2);
  not not_122 (not_122_out, OP3);
  not not_123 (not_123_out, OP5);
  not not_124 (not_124_out, OP6);
  not not_125 (not_125_out, F12);
  not not_126 (not_126_out, OP2);
  not not_127 (not_127_out, OP3);
  not not_128 (not_128_out, OP5);
  not not_129 (not_129_out, OP6);
  not not_130 (not_130_out, F25);
  not not_131 (not_131_out, F30);
  not not_132 (not_132_out, OP2);
  not not_133 (not_133_out, OP3);
  not not_134 (not_134_out, OP6);
  not not_135 (not_135_out, F12);
  not not_136 (not_136_out, F13);
  not not_137 (not_137_out, F14);
  not not_138 (not_138_out, F25);
  not not_139 (not_139_out, OP2);
  not not_140 (not_140_out, OP3);
  not not_141 (not_141_out, OP6);
  not not_142 (not_142_out, F12);
  not not_143 (not_143_out, F25);
  not not_144 (not_144_out, F30);
  not not_145 (not_145_out, OP2);
  not not_146 (not_146_out, OP3);
  not not_147 (not_147_out, OP5);
  not not_148 (not_148_out, OP6);
  not not_149 (not_149_out, F25);
  not not_150 (not_150_out, OP2);
  not not_151 (not_151_out, OP3);
  not not_152 (not_152_out, OP5);
  not not_153 (not_153_out, OP6);
  not not_154 (not_154_out, OP2);
  not not_155 (not_155_out, OP3);
  not not_156 (not_156_out, OP6);
  not not_157 (not_157_out, F25);
  not not_158 (not_158_out, F30);
  not not_159 (not_159_out, OP4);
  not not_160 (not_160_out, F12);
  not not_161 (not_161_out, F13);
  not not_162 (not_162_out, F14);
  not not_163 (not_163_out, OP4);
  not not_164 (not_164_out, OP2);
  not not_165 (not_165_out, OP3);
  not not_166 (not_166_out, OP4);
  not not_167 (not_167_out, F12);
  not not_168 (not_168_out, F13);
  not not_169 (not_169_out, F14);
  not not_170 (not_170_out, OP2);
  not not_171 (not_171_out, OP3);
  not not_172 (not_172_out, OP4);
  not not_173 (not_173_out, F13);
  not not_174 (not_174_out, F14);
  not not_175 (not_175_out, OP3);
  not not_176 (not_176_out, OP4);
  not not_177 (not_177_out, F12);
  not not_178 (not_178_out, F13);
  not not_179 (not_179_out, F14);
  not not_180 (not_180_out, OP4);
  not not_181 (not_181_out, OP2);
  not not_182 (not_182_out, OP3);
  not not_183 (not_183_out, OP4);
  not not_184 (not_184_out, OP5);
  not not_185 (not_185_out, OP6);
  not not_186 (not_186_out, F12);
  not not_187 (not_187_out, F13);
  not not_188 (not_188_out, F14);
  not not_189 (not_189_out, OP2);
  not not_190 (not_190_out, OP3);
  not not_191 (not_191_out, OP4);
  not not_192 (not_192_out, F12);
  not not_193 (not_193_out, F13);
  not not_194 (not_194_out, OP2);
  not not_195 (not_195_out, OP3);
  not not_196 (not_196_out, F12);
  not not_197 (not_197_out, F13);
  not not_198 (not_198_out, F14);
  not not_199 (not_199_out, F25);
  not not_200 (not_200_out, F30);
  not not_201 (not_201_out, OP2);
  not not_202 (not_202_out, OP3);
  not not_203 (not_203_out, OP2);
  not not_204 (not_204_out, OP3);
  not not_205 (not_205_out, F12);
  and and_1 (MemToReg, not_1_out, not_2_out, not_3_out, not_4_out, not_5_out, not_6_out, not_7_out);
  and and_2 (MemWrite, not_8_out, not_9_out, not_10_out, OP5, not_11_out, not_12_out, F13, not_13_out);
  and and_3 (and_3_out, not_14_out, not_15_out, not_16_out, not_17_out, not_18_out, not_19_out);
  and and_4 (and_4_out, not_20_out, not_21_out, not_22_out, not_23_out, not_24_out, F13, not_25_out);
  and and_5 (and_5_out, not_26_out, not_27_out, OP4, not_28_out, not_29_out, not_30_out);
  and and_6 (and_6_out, not_31_out, not_32_out, OP4, not_33_out, not_34_out, not_35_out, not_36_out);
  and and_7 (and_7_out, not_37_out, not_38_out, OP4, not_39_out, not_40_out, F14, not_41_out);
  and and_8 (and_8_out, not_42_out, not_43_out, OP4, not_44_out, not_45_out, F13);
  and and_9 (and_9_out, OP2, not_46_out, not_47_out, OP5, OP6, not_48_out, not_49_out, not_50_out);
  and and_10 (and_10_out, not_51_out, not_52_out, not_53_out, not_54_out, not_55_out, not_56_out);
  and and_11 (and_11_out, not_57_out, not_58_out, OP4, not_59_out, not_60_out, not_61_out);
  and and_12 (and_12_out, not_62_out, not_63_out, OP4, not_64_out, not_65_out, not_66_out, not_67_out);
  and and_13 (and_13_out, not_68_out, not_69_out, OP4, not_70_out, not_71_out, not_72_out, not_73_out, not_74_out);
  and and_14 (and_14_out, not_75_out, not_76_out, OP4, not_77_out, not_78_out, not_79_out, not_80_out);
  and and_15 (and_15_out, not_81_out, not_82_out, OP4, not_83_out, not_84_out, F14, not_85_out);
  and and_16 (and_16_out, not_86_out, not_87_out, OP4, not_88_out, not_89_out, F13);
  and and_17 (and_17_out, not_90_out, not_91_out, OP4, not_92_out, F13, not_93_out, not_94_out);
  and and_18 (and_18_out, OP2, not_95_out, OP5, OP6, not_96_out, not_97_out, not_98_out);
  and and_19 (and_19_out, OP2, OP3, not_99_out, OP5, OP6);
  and and_20 (ecall, not_100_out, not_101_out, OP4, OP5, OP6, not_102_out, not_103_out, not_104_out, not_105_out, not_106_out);
  and and_21 (and_21_out, not_107_out, not_108_out, not_109_out, not_110_out, not_111_out, not_112_out, not_113_out, not_114_out);
  and and_22 (and_22_out, not_115_out, not_116_out, not_117_out, not_118_out, not_119_out, F13, not_120_out);
  and and_23 (and_23_out, not_121_out, not_122_out, OP4, not_123_out, not_124_out, not_125_out);
  and and_24 (and_24_out, not_126_out, not_127_out, OP4, not_128_out, not_129_out, not_130_out, not_131_out);
  and and_25 (and_25_out, not_132_out, not_133_out, OP4, not_134_out, not_135_out, not_136_out, not_137_out, not_138_out);
  and and_26 (and_26_out, not_139_out, not_140_out, OP4, not_141_out, not_142_out, not_143_out, not_144_out);
  and and_27 (and_27_out, not_145_out, not_146_out, OP4, not_147_out, not_148_out, F14, not_149_out);
  and and_28 (and_28_out, not_150_out, not_151_out, OP4, not_152_out, not_153_out, F13);
  and and_29 (and_29_out, not_154_out, not_155_out, OP4, not_156_out, F13, not_157_out, not_158_out);
  and and_30 (and_30_out, OP2, not_159_out, OP5, OP6, not_160_out, not_161_out, not_162_out);
  and and_31 (and_31_out, OP2, OP3, not_163_out, OP5, OP6);
  and and_32 (BEQ, not_164_out, not_165_out, not_166_out, OP5, OP6, not_167_out, not_168_out, not_169_out);
  and and_33 (BNE, not_170_out, not_171_out, not_172_out, OP5, OP6, F12, not_173_out, not_174_out);
  and and_34 (JALR, OP2, not_175_out, not_176_out, OP5, OP6, not_177_out, not_178_out, not_179_out);
  and and_35 (JAL, OP2, OP3, not_180_out, OP5, OP6);
  and and_36 (LB, not_181_out, not_182_out, not_183_out, not_184_out, not_185_out, not_186_out, not_187_out, not_188_out);
  and and_37 (BLT, not_189_out, not_190_out, not_191_out, OP5, OP6, not_192_out, not_193_out, F14);
  and and_38 (URET, not_194_out, not_195_out, OP4, OP5, OP6, not_196_out, not_197_out, not_198_out, not_199_out, not_200_out);
  and and_39 (CSRRCI, not_201_out, not_202_out, OP4, OP5, OP6, F12, F13, F14);
  and and_40 (CSRRSI, not_203_out, not_204_out, OP4, OP5, OP6, not_205_out, F13, F14);
  or or_1 (ALU_SRC, and_3_out, and_4_out, and_5_out, and_6_out, and_7_out, and_8_out, and_9_out);
  or or_2 (RegWrite, and_10_out, and_11_out, and_12_out, and_13_out, and_14_out, and_15_out, and_16_out, and_17_out, and_18_out, and_19_out);
  or or_3 (S_Type, and_21_out, and_22_out, and_23_out, and_24_out, and_25_out, and_26_out, and_27_out, and_28_out, and_29_out, and_30_out, and_31_out);
endmodule

// ALU
module ALU (
  input  [31:0] X,
  input  [31:0] Y,
  input  [3:0] AluOP,
  output out_4,
  output Equal,
  output out_6,
  output [31:0] Result,
  output [31:0] Result_2
);

  wire [0:0] comparator_1_lt, comparator_2_lt;
  wire [31:0] adder_1_out, AND_out, divider_1_out, divider_1_rem, multiplier_1_cout, multiplier_1_out,
       NOR_out, OR_out, shifter_1_out, shifter_2_out, shifter_3_out, subtractor_1_out, XOR_out;

  assign AND_out = X & Y;  // AND_Gate AND, 32 bits wide
  assign OR_out = X | Y;  // OR_Gate OR, 32 bits wide
  Shifter #(.width(32), .shift("ll")) shifter_1 (.in(X), .\dist (Y[4:0]), .out(shifter_1_out));
  Shifter #(.width(32), .shift("ar")) shifter_2 (.in(X), .\dist (Y[4:0]), .out(shifter_2_out));
  Shifter #(.width(32), .shift("lr")) shifter_3 (.in(X), .\dist (Y[4:0]), .out(shifter_3_out));
  Multiplier #(.width(32)) multiplier_1 (.a(X), .b(Y), .out(multiplier_1_out), .cout(multiplier_1_cout));  // open: cin
  Divider #(.width(32)) divider_1 (.a(X), .b(Y), .out(divider_1_out), .rem(divider_1_rem));  // open: upper
  Adder #(.width(32)) adder_1 (.a(X), .b(Y), .out(adder_1_out));  // open: cin, cout
  Subtractor #(.width(32)) subtractor_1 (.a(X), .b(Y), .out(subtractor_1_out));  // open: bin, bout
  assign XOR_out = X ^ Y;  // XOR_Gate XOR, 32 bits wide
  assign NOR_out = ~(X | Y);  // NOR_Gate NOR, 32 bits wide
  Comparator #(.width(32), .mode("twosComplement")) comparator_1 (
    .a(X), .b(Y), .eq(Equal), .lt(comparator_1_lt[0]));  // open: gt
  Comparator #(.width(32), .mode("unsigned")) comparator_2 (.a(X), .b(Y), .lt(comparator_2_lt[0]));  // open: gt, eq
  Multiplexer #(.select(4), .width(32), .disabled("Z"), .enable("false")) multiplexer_1 (
    .in0(shifter_1_out), .in1(shifter_2_out), .in2(shifter_3_out), .in3(multiplier_1_out),
    .in4(divider_1_out), .in5(adder_1_out), .in6(subtractor_1_out), .in7(AND_out), .in8(OR_out),
    .in9(XOR_out), .in10(NOR_out), .in11({{31{1'b0}}, comparator_1_lt[0]}),
    .in12({{31{1'b0}}, comparator_2_lt[0]}), .in13({32{1'b0}}), .in14({32{1'b0}}), .in15({32{1'b0}}),
    .out(Result), .sel(AluOP));
  Multiplexer #(.select(4), .width(32), .disabled("Z"), .enable("false")) multiplexer_2 (
    .in0({32{1'b0}}), .in1({32{1'b0}}), .in2({32{1'b0}}), .in3(multiplier_1_cout), .in4(divider_1_rem),
    .in5({32{1'b0}}), .in6({32{1'b0}}), .in7({32{1'b0}}), .in8({32{1'b0}}), .in9({32{1'b0}}),
    .in10({32{1'b0}}), .in11({32{1'b0}}), .in12({32{1'b0}}), .in13({32{1'b0}}), .in14({32{1'b0}}),
    .in15({32{1'b0}}), .out(Result_2), .sel(AluOP));
  Multiplexer #(.select(4), .width(1), .disabled("Z"), .enable("false")) multiplexer_3 (
    .in0(1'b0), .in1(1'b0), .in2(1'b0), .in3(1'b0), .in4(1'b0), .in5(1'b0), .in6(1'b0), .in7(1'b0),
    .in8(1'b0), .in9(1'b0), .in10(1'b0), .in11(comparator_1_lt[0]), .in12(comparator_2_lt[0]), .in13(1'b0),
    .in14(1'b0), .in15(1'b0), .out(out_6), .sel(AluOP));
  not not_1 (out_4, out_6);

  // Other names for the same wires on the sheet: Result2[31:0] = Result_2; S[3:0] = AluOP; tunnel = out_6;
  //   tunnel_t = out_4

  // Notes on the sheet:
  //   不要改变此引脚区域内容，也不要改变ALU封装形式
  //   输入引脚
  //   输出引脚
endmodule

module Regifile (
  input  [31:0] Din,
  input  Clk,
  input  WE,
  input  [4:0] R1_num,
  input  [4:0] W_num,
  input  [4:0] R2_num,
  output [31:0] R1,
  output [31:0] R2
);

  // RegisterFile registerfile_1: pin names not known; wires that end beside it: Din, Clk, WE, W_num, R1_num, R2_num, R1, R2
endmodule

module \单周期_单级中断  (
  input  IR1,
  input  IR2,
  input  IR3,
  input  IR4,
  input  IR5,
  input  IR6,
  input  IR7,
  input  IR8,
  input  IR9,
  input  IR10,
  input  IR11,
  input  IR12,
  input  IR13,
  output [3:0] out_14,
  output [6:0] X,
  output Win1,
  output Win2,
  output [6:0] Y,
  output [15:0] IMA
);

  wire alu_1_equal, alu_1_out_6, and_1_out, and_2_out, and_3_out, and_4_out, and_5_out, and_6_out, and_7_out,
       and_8_out, and_9_out, and_10_out, and_11_out, and_12_out, and_13_out, and_14_out, and_15_out,
       and_16_out, and_18_out, and_20_out, beq, CLK, clock_2_out, comparator_1_eq, comparator_2_eq,
       comparator_2_lt, comparator_3_eq, comparator_4_gt, comparator_5_lt, d_ff_1_q, d_ff_2_q, d_ff_3_q,
       d_ff_4_q, d_ff_5_q, d_ff_6_q, d_ff_7_q, d_ff_8_q, d_ff_9_q, d_ff_10_q, d_ff_11_q, d_ff_12_q,
       d_ff_13_q, d_ff_14_q, d_ff_15_q, d_ff_15_qn, demultiplexer_2_out1, demultiplexer_2_out2,
       demultiplexer_2_out3, demultiplexer_2_out4, demultiplexer_2_out5, demultiplexer_2_out6,
       demultiplexer_2_out7, demultiplexer_2_out8, demultiplexer_2_out9, demultiplexer_2_out10,
       demultiplexer_2_out12, demultiplexer_2_out13, ecall, Go, halt, IR1_2_q, IR1_3_q, IR1_4_q, IR1_5_q,
       IR1_6_q, IR1_7_q, IR1_8_q, IR1_9_q, IR1_10_q, IR1_11_q, IR1_12_q, IR1_13_q, IR1_q, jal, jalr, lb,
       MemWrite, nand_1_out, not_1_out, or_14_out, or_15_out, or_16_out, or_17_out, or_18_out, or_19_out,
       or_20_out, or_21_out, or_22_out, or_23_out, or_24_out, or_25_out, or_26_out, or_27_out, or_28_out,
       or_30_out, or_31_out, register_4_q, RegWrite, RST, uret, W1, W2, W3, W4, W5, W6, W7, W8, W9, W10, W11,
       W12, W13, \单周期硬布线控制器_1_alu_src , \单周期硬布线控制器_1_beq , \单周期硬布线控制器_1_blt , \单周期硬布线控制器_1_bne ,
       \单周期硬布线控制器_1_ecall , \单周期硬布线控制器_1_memtoreg , \单周期硬布线控制器_1_s_type , \单周期硬布线控制器_1_uret ,
       \系统调用选择_1_加载初始界面 , \系统调用选择_1_加载地图 , \系统调用选择_1_消除一个木块 , \系统调用选择_1_移动 , \系统调用选择_2_加载初始界面 ,
       \系统调用选择_2_加载地图 , \系统调用选择_2_消除一个木块 , \系统调用选择_2_移动 ;
  wire [1:0] bit_extender_9_out, priority_encoder_1_out, xor_1_out;
  wire [2:0] multiplexer_13_out, priority_encoder_3_out;
  wire [3:0] bit_extender_7_out, bit_extender_8_out, multiplexer_8_out, register_1_q, \单周期硬布线控制器_1_alu_op ;
  wire [4:0] multiplexer_2_out, multiplexer_3_out, W_num;
  wire [6:0] \像素删除逻辑_1_xout , \像素删除逻辑_1_yout , \像素移动逻辑_1_xout , \像素移动逻辑_1_yout , \初始界面加载_1_xout ,
       \初始界面加载_1_yout , \地图加载_1_xout , \地图加载_1_yout , \坐标运算逻辑_1_x , \坐标运算逻辑_1_y , \坐标运算逻辑_2_x , \坐标运算逻辑_2_y ,
       \坐标运算逻辑_3_x , \坐标运算逻辑_3_y ;
  wire [9:0] bit_extender_1_out, bit_extender_10_out, dataaddr;
  wire [12:0] CNT_num;
  wire [15:0] \像素移动逻辑_1_ima , \初始界面加载_1_ima , \地图加载_1_ima , \总周期数 ;
  wire [31:0] adder_1_out, adder_2_out, adder_3_out, alu_1_result, and_17_out, bit_extender_2_out,
       bit_extender_3_out, bit_extender_4_out, bit_extender_5_out, IR, LedData, MDin, multiplexer_5_out,
       multiplexer_6_out, multiplexer_9_out, multiplexer_10_out, multiplexer_11_out, multiplexer_12_out,
       multiplexer_14_out, multiplexer_15_out, PC, PC0, PC_q, PCnext, R1, ram_1_data, RDin, register_2_q,
       register_3_q, shifter_2_out, shifter_3_out, shifter_4_out, shifter_5_out, shifter_6_out,
       \寄存器内容备份_1_输出结果 , \寄存器内容备份_2_输出结果 , \寄存器内容备份_3_输出结果 , \寄存器内容备份_4_输出结果 , \寄存器内容备份_5_输出结果 ;

  Clock #(.highDuration(1), .lowDuration(1)) clock_1 ();  // open: out
  Button _1 ();  // open: out
  Button _2 ();  // open: out
  Button _3 ();  // open: out
  Button \u_继续运行  (.out(Go));
  LED #(.active("true")) led_1 (.in(W1));
  LED #(.active("true")) led_2 (.in(W2));
  LED #(.active("true")) led_3 (.in(W3));
  Hex_Digit_Display hex_digit_display_1 (.value(LedData[31:28]));  // open: dp
  Hex_Digit_Display hex_digit_display_2 (.value(LedData[27:24]));  // open: dp
  Hex_Digit_Display hex_digit_display_3 (.value(LedData[23:20]));  // open: dp
  not not_1 (not_1_out, halt);
  Priority_Encoder #(.select(2), .disabled("Z")) priority_encoder_1 (
    .in0(1'b1), .in1(jal), .in2(jalr), .in3(beq), .out(priority_encoder_1_out));  // open: gs, en_out, en_in
  Hex_Digit_Display hex_digit_display_4 (.value(LedData[15:12]));  // open: dp
  Hex_Digit_Display hex_digit_display_5 (.value(LedData[19:16]));  // open: dp
  Register #(.width(32), .trigger("rising"), .Select("low")) u_PC (
    .D(PCnext), .en(not_1_out), .Q(PC_q), .clk(CLK), .clr(RST));
  // Probe on PC0
  Multiplexer #(.select(2), .width(32), .disabled("Z"), .enable("false")) multiplexer_1 (
    .in0(adder_1_out), .in1(adder_3_out), .in2(shifter_4_out), .in3(adder_2_out), .out(PC0),
    .sel(priority_encoder_1_out));
  Hex_Digit_Display hex_digit_display_6 (.value(LedData[11:8]));  // open: dp
  Hex_Digit_Display hex_digit_display_7 (.value(LedData[7:4]));  // open: dp
  // Probe on \总周期数 
  // Probe on PC
  Shifter #(.width(32), .shift("ll")) shifter_1 (.in(PC_q), .\dist (5'b00010), .out(PC));
  Bit_Extender #(.in_width(32), .out_width(10), .\type ("sign")) bit_extender_1 (.in(PC_q), .out(bit_extender_1_out));
  Adder #(.width(32)) adder_1 (.a(PC_q), .b(32'h1), .out(adder_1_out));  // open: cin, cout
  Hex_Digit_Display hex_digit_display_8 (.value(LedData[3:0]));  // open: dp
  Comparator #(.width(32), .mode("twosComplement")) comparator_1 (
    .a({32{1'b0}}), .b(IR), .eq(comparator_1_eq));  // open: gt, lt
  // RiscV_Probe riscv_probe_1: pin names not known; wires that end beside it: {32{1'b0}}, IR
  Demultiplexer #(.select(1), .width(1), .tristate("false"), .disabled("Z"), .enable("false")) demultiplexer_1 (
    .out0(ecall), .out1(uret), .in(\单周期硬布线控制器_1_uret ), .sel(IR[21]));
  ROM #(.addrWidth(10), .dataWidth(32), .Select("high")) rom_1 (.addr(bit_extender_1_out), .data(IR));
  or or_1 (W1, IR1_q, d_ff_1_q);
  or or_2 (W2, IR1_2_q, d_ff_2_q);
  or or_3 (W3, IR1_3_q, d_ff_3_q);
  or or_4 (W4, IR1_4_q, d_ff_4_q);
  or or_5 (W5, IR1_5_q, d_ff_5_q);
  or or_6 (W6, IR1_6_q, d_ff_6_q);
  or or_7 (W7, IR1_7_q, d_ff_7_q);
  or or_8 (W8, IR1_8_q, d_ff_8_q);
  or or_9 (W9, IR1_9_q, d_ff_9_q);
  or or_10 (W10, IR1_10_q, d_ff_10_q);
  or or_11 (W11, IR1_11_q, d_ff_11_q);
  or or_12 (W12, IR1_12_q, d_ff_12_q);
  or or_13 (W13, IR1_13_q, d_ff_13_q);
  D_Flip_Flop #(.trigger("rising"), .Pre_Clr_Positions("LEGACY"), .NegatePresetClear("false"), .enable("true"), .NewFFLayout("false")) d_ff_1 (
    .clk(IR1), .D(1'b1), .Q(d_ff_1_q), .reset(IR1_q));  // open: Qn, preset, en
  D_Flip_Flop #(.trigger("rising"), .Pre_Clr_Positions("LEGACY"), .NegatePresetClear("false"), .enable("true"), .NewFFLayout("false")) d_ff_2 (
    .clk(IR2), .D(1'b1), .Q(d_ff_2_q), .reset(IR1_2_q));  // open: Qn, preset, en
  D_Flip_Flop #(.trigger("rising"), .Pre_Clr_Positions("LEGACY"), .NegatePresetClear("false"), .enable("true"), .NewFFLayout("false")) d_ff_3 (
    .clk(IR3), .D(1'b1), .Q(d_ff_3_q), .reset(IR1_3_q));  // open: Qn, preset, en
  D_Flip_Flop #(.trigger("rising"), .Pre_Clr_Positions("LEGACY"), .NegatePresetClear("false"), .enable("true"), .NewFFLayout("false")) d_ff_4 (
    .clk(IR4), .D(1'b1), .Q(d_ff_4_q), .reset(IR1_4_q));  // open: Qn, preset, en
  D_Flip_Flop #(.trigger("rising"), .Pre_Clr_Positions("LEGACY"), .NegatePresetClear("false"), .enable("true"), .NewFFLayout("false")) d_ff_5 (
    .clk(IR5), .D(1'b1), .Q(d_ff_5_q), .reset(IR1_5_q));  // open: Qn, preset, en
  D_Flip_Flop #(.trigger("rising"), .Pre_Clr_Positions("LEGACY"), .NegatePresetClear("false"), .enable("true"), .NewFFLayout("false")) d_ff_6 (
    .clk(IR6), .D(1'b1), .Q(d_ff_6_q), .reset(IR1_6_q));  // open: Qn, preset, en
  D_Flip_Flop #(.trigger("rising"), .Pre_Clr_Positions("LEGACY"), .NegatePresetClear("false"), .enable("true"), .NewFFLayout("false")) d_ff_7 (
    .clk(IR7), .D(1'b1), .Q(d_ff_7_q), .reset(IR1_7_q));  // open: Qn, preset, en
  D_Flip_Flop #(.trigger("rising"), .Pre_Clr_Positions("LEGACY"), .NegatePresetClear("false"), .enable("true"), .NewFFLayout("false")) d_ff_8 (
    .clk(IR8), .D(1'b1), .Q(d_ff_8_q), .reset(IR1_8_q));  // open: Qn, preset, en
  D_Flip_Flop #(.trigger("rising"), .Pre_Clr_Positions("LEGACY"), .NegatePresetClear("false"), .enable("true"), .NewFFLayout("false")) d_ff_9 (
    .clk(IR9), .D(1'b1), .Q(d_ff_9_q), .reset(IR1_9_q));  // open: Qn, preset, en
  D_Flip_Flop #(.trigger("rising"), .Pre_Clr_Positions("LEGACY"), .NegatePresetClear("false"), .enable("true"), .NewFFLayout("false")) d_ff_10 (
    .clk(IR10), .D(1'b1), .Q(d_ff_10_q), .reset(IR1_10_q));  // open: Qn, preset, en
  D_Flip_Flop #(.trigger("rising"), .Pre_Clr_Positions("LEGACY"), .NegatePresetClear("false"), .enable("true"), .NewFFLayout("false")) d_ff_11 (
    .clk(IR11), .D(1'b1), .Q(d_ff_11_q), .reset(IR1_11_q));  // open: Qn, preset, en
  D_Flip_Flop #(.trigger("rising"), .Pre_Clr_Positions("LEGACY"), .NegatePresetClear("false"), .enable("true"), .NewFFLayout("false")) d_ff_12 (
    .clk(IR12), .D(1'b1), .Q(d_ff_12_q), .reset(IR1_12_q));  // open: Qn, preset, en
  D_Flip_Flop #(.trigger("rising"), .Pre_Clr_Positions("LEGACY"), .NegatePresetClear("false"), .enable("true"), .NewFFLayout("false")) d_ff_13 (
    .clk(IR13), .D(1'b1), .Q(d_ff_13_q), .reset(IR1_13_q));  // open: Qn, preset, en
  \单周期硬布线控制器  \u_单周期硬布线控制器_1  (
    .Funct({IR[30], IR[25], IR[14:12]}), .OP(IR[6:2]), .ALU_OP(\单周期硬布线控制器_1_alu_op ),
    .MemToReg(\单周期硬布线控制器_1_memtoreg ), .MemWrite(MemWrite), .ALU_SRC(\单周期硬布线控制器_1_alu_src ),
    .RegWrite(RegWrite), .ecall(\单周期硬布线控制器_1_ecall ), .S_type(\单周期硬布线控制器_1_s_type ), .Jalr(jalr),
    .Beq(\单周期硬布线控制器_1_beq ), .JAL(jal), .Bne(\单周期硬布线控制器_1_bne ), .LB(lb), .BLT(\单周期硬布线控制器_1_blt ),
    .URET(\单周期硬布线控制器_1_uret ), .IR_0(comparator_1_eq));  // open: CSRRCI, CSRRSI
  Multiplexer #(.select(1), .width(5), .disabled("Z"), .enable("false")) multiplexer_2 (
    .in0(IR[19:15]), .in1(5'b01010), .out(multiplexer_2_out), .sel(\单周期硬布线控制器_1_ecall ));
  Multiplexer #(.select(1), .width(5), .disabled("Z"), .enable("false")) multiplexer_3 (
    .in0(IR[24:20]), .in1(5'b10001), .out(multiplexer_3_out), .sel(\单周期硬布线控制器_1_ecall ));
  assign bit_extender_2_out = {{20{IR[31]}}, IR[31:20]};  // Bit_Extender bit_extender_2
  assign bit_extender_3_out = {{20{IR[31]}}, {IR[31:25], IR[11:7]}};  // Bit_Extender bit_extender_3
  assign bit_extender_4_out = {{20{IR[31]}}, {IR[31], IR[7], IR[30:25], IR[11:8]}};  // Bit_Extender bit_extender_4
  or or_14 (or_14_out, d_ff_1_q, IR1_q);
  or or_15 (or_15_out, d_ff_2_q, IR1_2_q);
  or or_16 (or_16_out, d_ff_3_q, IR1_3_q);
  or or_17 (or_17_out, d_ff_4_q, IR1_4_q);
  or or_18 (or_18_out, d_ff_5_q, IR1_5_q);
  or or_19 (or_19_out, d_ff_6_q, IR1_6_q);
  or or_20 (or_20_out, d_ff_7_q, IR1_7_q);
  or or_21 (or_21_out, d_ff_8_q, IR1_8_q);
  or or_22 (or_22_out, d_ff_9_q, IR1_9_q);
  or or_23 (or_23_out, d_ff_10_q, IR1_10_q);
  or or_24 (or_24_out, d_ff_11_q, IR1_11_q);
  or or_25 (or_25_out, d_ff_12_q, IR1_12_q);
  or or_26 (or_26_out, d_ff_13_q, IR1_13_q);
  Multiplexer #(.select(1), .width(5), .disabled("Z"), .enable("false")) multiplexer_4 (
    .in0(multiplexer_3_out), .in1(IR[11:7]), .out(W_num), .sel(\单周期硬布线控制器_1_s_type ));
  Multiplexer #(.select(1), .width(32), .disabled("Z"), .enable("false")) multiplexer_5 (
    .in0(bit_extender_2_out), .in1(bit_extender_3_out), .out(multiplexer_5_out), .sel(MemWrite));
  Shifter #(.width(32), .shift("ar")) shifter_2 (.in(bit_extender_4_out), .\dist (5'b00001), .out(shifter_2_out));
  assign bit_extender_5_out = {{12{IR[31]}}, {IR[31], IR[19:12], IR[20], IR[30:21]}};  // Bit_Extender bit_extender_5
  and and_1 (and_1_out, or_14_out, ~or_31_out);  // AND_Gate
  and and_2 (and_2_out, or_15_out, ~or_31_out);  // AND_Gate
  and and_3 (and_3_out, or_16_out, ~or_31_out);  // AND_Gate
  and and_4 (and_4_out, or_17_out, ~or_31_out);  // AND_Gate
  and and_5 (and_5_out, or_18_out, ~or_31_out);  // AND_Gate
  and and_6 (and_6_out, or_19_out, ~or_31_out);  // AND_Gate
  and and_7 (and_7_out, or_20_out, ~or_31_out);  // AND_Gate
  and and_8 (and_8_out, or_21_out, ~or_31_out);  // AND_Gate
  and and_9 (and_9_out, or_22_out, ~or_31_out);  // AND_Gate
  and and_10 (and_10_out, or_23_out, ~or_31_out);  // AND_Gate
  and and_11 (and_11_out, or_24_out, ~demultiplexer_2_out12);  // AND_Gate
  and and_12 (and_12_out, or_25_out, ~demultiplexer_2_out12);  // AND_Gate
  and and_13 (and_13_out, or_26_out, ~demultiplexer_2_out13);  // AND_Gate
  Regifile regifile_1 (
    .Din(RDin), .Clk(CLK), .R1(R1), .R2(MDin), .WE(RegWrite), .W_num(W_num), .R1_num(multiplexer_2_out),
    .R2_num(multiplexer_3_out));
  Adder #(.width(32)) adder_2 (.a(shifter_2_out), .b(PC_q), .out(adder_2_out));  // open: cin, cout
  Shifter #(.width(32), .shift("ar")) shifter_3 (.in(bit_extender_5_out), .\dist (5'b00001), .out(shifter_3_out));
  Adder #(.width(32)) adder_3 (.a(shifter_3_out), .b(PC_q), .out(adder_3_out));  // open: cin, cout
  D_Flip_Flop #(.trigger("rising"), .Pre_Clr_Positions("LEGACY"), .NegatePresetClear("false"), .enable("true"), .NewFFLayout("false")) u_IR1 (
    .clk(CLK), .D(and_1_out), .Q(IR1_q), .reset(RST));  // open: Qn, preset, en
  D_Flip_Flop #(.trigger("rising"), .Pre_Clr_Positions("LEGACY"), .NegatePresetClear("false"), .enable("true"), .NewFFLayout("false")) IR1_2 (
    .clk(CLK), .D(and_2_out), .Q(IR1_2_q), .reset(RST));  // open: Qn, preset, en
  D_Flip_Flop #(.trigger("rising"), .Pre_Clr_Positions("LEGACY"), .NegatePresetClear("false"), .enable("true"), .NewFFLayout("false")) IR1_3 (
    .clk(CLK), .D(and_3_out), .Q(IR1_3_q), .reset(RST));  // open: Qn, preset, en
  D_Flip_Flop #(.trigger("rising"), .Pre_Clr_Positions("LEGACY"), .NegatePresetClear("false"), .enable("true"), .NewFFLayout("false")) IR1_4 (
    .clk(CLK), .D(and_4_out), .Q(IR1_4_q), .reset(RST));  // open: Qn, preset, en
  D_Flip_Flop #(.trigger("rising"), .Pre_Clr_Positions("LEGACY"), .NegatePresetClear("false"), .enable("true"), .NewFFLayout("false")) IR1_5 (
    .clk(CLK), .D(and_5_out), .Q(IR1_5_q), .reset(RST));  // open: Qn, preset, en
  D_Flip_Flop #(.trigger("rising"), .Pre_Clr_Positions("LEGACY"), .NegatePresetClear("false"), .enable("true"), .NewFFLayout("false")) IR1_6 (
    .clk(CLK), .D(and_6_out), .Q(IR1_6_q), .reset(RST));  // open: Qn, preset, en
  D_Flip_Flop #(.trigger("rising"), .Pre_Clr_Positions("LEGACY"), .NegatePresetClear("false"), .enable("true"), .NewFFLayout("false")) IR1_7 (
    .clk(CLK), .D(and_7_out), .Q(IR1_7_q), .reset(RST));  // open: Qn, preset, en
  D_Flip_Flop #(.trigger("rising"), .Pre_Clr_Positions("LEGACY"), .NegatePresetClear("false"), .enable("true"), .NewFFLayout("false")) IR1_8 (
    .clk(CLK), .D(and_8_out), .Q(IR1_8_q), .reset(RST));  // open: Qn, preset, en
  D_Flip_Flop #(.trigger("rising"), .Pre_Clr_Positions("LEGACY"), .NegatePresetClear("false"), .enable("true"), .NewFFLayout("false")) IR1_9 (
    .clk(CLK), .D(and_9_out), .Q(IR1_9_q), .reset(RST));  // open: Qn, preset, en
  D_Flip_Flop #(.trigger("rising"), .Pre_Clr_Positions("LEGACY"), .NegatePresetClear("false"), .enable("true"), .NewFFLayout("false")) IR1_10 (
    .clk(CLK), .D(and_10_out), .Q(IR1_10_q), .reset(RST));  // open: Qn, preset, en
  D_Flip_Flop #(.trigger("rising"), .Pre_Clr_Positions("LEGACY"), .NegatePresetClear("false"), .enable("true"), .NewFFLayout("false")) IR1_11 (
    .clk(CLK), .D(and_11_out), .Q(IR1_11_q), .reset(RST));  // open: Qn, preset, en
  D_Flip_Flop #(.trigger("rising"), .Pre_Clr_Positions("LEGACY"), .NegatePresetClear("false"), .enable("true"), .NewFFLayout("false")) IR1_12 (
    .clk(CLK), .D(and_12_out), .Q(IR1_12_q), .reset(RST));  // open: Qn, preset, en
  D_Flip_Flop #(.trigger("rising"), .Pre_Clr_Positions("LEGACY"), .NegatePresetClear("false"), .enable("true"), .NewFFLayout("false")) IR1_13 (
    .clk(CLK), .D(and_13_out), .Q(IR1_13_q), .reset(RST));  // open: Qn, preset, en
  Multiplexer #(.select(1), .width(32), .disabled("Z"), .enable("false")) multiplexer_6 (
    .in0(MDin), .in1(multiplexer_5_out), .out(multiplexer_6_out), .sel(\单周期硬布线控制器_1_alu_src ));
  ALU alu_1 (
    .X(R1), .Y(multiplexer_6_out), .AluOP(\单周期硬布线控制器_1_alu_op ), .Equal(alu_1_equal), .Result(alu_1_result),
    .out_6(alu_1_out_6));  // open: Result_2, out_4
  and and_14 (and_14_out, \单周期硬布线控制器_1_blt , alu_1_out_6);
  and and_15 (and_15_out, \单周期硬布线控制器_1_beq , alu_1_equal);
  and and_16 (and_16_out, \单周期硬布线控制器_1_bne , ~alu_1_equal);  // AND_Gate
  Bit_Extender #(.in_width(32), .out_width(10), .\type ("sign")) bit_extender_6 (.in(alu_1_result), .out(dataaddr));
  assign and_17_out = alu_1_result & 32'hfffffffe;  // AND_Gate and_17, 32 bits wide
  Multiplexer #(.select(1), .width(32), .disabled("Z"), .enable("false")) multiplexer_7 (
    .in0(multiplexer_9_out), .in1(shifter_5_out), .out(RDin), .sel(or_27_out));
  or or_27 (or_27_out, jal, jalr);
  Shifter #(.width(32), .shift("ar")) shifter_4 (.in(and_17_out), .\dist (5'b00010), .out(shifter_4_out));
  or or_28 (or_28_out, IR1_7_q, IR1_8_q, IR1_9_q, IR1_10_q, IR1_5_q, IR1_q, IR1_3_q, IR1_4_q, IR1_6_q, IR1_2_q, IR1_11_q, IR1_12_q, IR1_13_q);
  or or_29 (beq, and_14_out, and_15_out, and_16_out);
  // Probe on \单周期硬布线控制器_1_alu_op 
  // RiscV_Probe riscv_probe_2: pin names not known; wires that end beside it: IR
  Priority_Encoder #(.select(4), .disabled("Z")) priority_encoder_2 (
    .in0(1'b1), .in1(IR1_q), .in2(IR1_2_q), .in3(IR1_3_q), .in4(IR1_4_q), .in5(IR1_5_q), .in6(IR1_6_q),
    .in7(IR1_7_q), .in8(IR1_8_q), .in9(IR1_9_q), .in10(IR1_10_q), .in11(IR1_11_q), .in12(IR1_12_q),
    .in13(IR1_13_q), .out(out_14));  // open: in14, in15, gs, en_out, en_in
  RAM #(.addrWidth(10), .dataWidth(32), .bus("separate"), .Select("high")) ram_1 (
    .addr(dataaddr), .din(MDin), .data(ram_1_data), .str(MemWrite), .clk(CLK), .clr(RST));  // open: sel, ld
  D_Flip_Flop #(.trigger("high"), .Pre_Clr_Positions("LEGACY"), .NegatePresetClear("false"), .enable("true"), .NewFFLayout("false")) d_ff_14 (.Q(d_ff_14_q));  // open: clk, D, Qn, preset, en, reset
  // Probe on 13'hba
  Shifter #(.width(32), .shift("ll")) shifter_5 (.in(adder_1_out), .\dist (5'b00010), .out(shifter_5_out));
  Comparator #(.width(13), .mode("twosComplement")) comparator_2 (
    .a(CNT_num), .b(13'hba), .eq(comparator_2_eq), .lt(comparator_2_lt));  // open: gt
  Clock #(.highDuration(1), .lowDuration(1)) clock_2 (.out(clock_2_out));
  and and_18 (and_18_out, or_28_out, d_ff_15_qn);
  nand nand_1 (nand_1_out, d_ff_14_q, comparator_2_eq);
  Counter #(.width(13), .max('h1fff), .ongoal("stay"), .trigger("rising"), .behavior("old")) counter_1 (
    .count(comparator_2_lt), .Q(CNT_num), .clk(clock_2_out), .clr(RST));  // open: load, D, carry, preset
  Shifter #(.width(32), .shift("ll")) shifter_6 (.in(PC0), .\dist (5'b00010), .out(shifter_6_out));
  D_Flip_Flop #(.trigger("rising"), .Pre_Clr_Positions("LEGACY"), .NegatePresetClear("false"), .enable("true"), .NewFFLayout("false")) d_ff_15 (
    .clk(CLK), .D(and_18_out), .Q(d_ff_15_q), .Qn(d_ff_15_qn), .en(d_ff_15_qn), .reset(or_30_out));  // open: preset
  or or_30 (or_30_out, RST, uret);
  assign CLK = nand_1_out ? clock_2_out : 1'bz;  // Controlled_Buffer controlled_buffer_1
  Multiplexer #(.select(1), .width(4), .disabled("Z"), .enable("false")) multiplexer_8 (
    .in0(out_14), .in1(4'b0000), .out(multiplexer_8_out), .sel(d_ff_15_q));
  Register #(.width(4), .trigger("rising"), .Select("low")) register_1 (
    .D(out_14), .Q(register_1_q), .clk(d_ff_15_q));  // open: en, clr
  Demultiplexer #(.select(4), .width(1), .tristate("false"), .disabled("Z"), .enable("false")) demultiplexer_2 (
    .out1(demultiplexer_2_out1), .out2(demultiplexer_2_out2), .out3(demultiplexer_2_out3),
    .out4(demultiplexer_2_out4), .out5(demultiplexer_2_out5), .out6(demultiplexer_2_out6),
    .out7(demultiplexer_2_out7), .out8(demultiplexer_2_out8), .out9(demultiplexer_2_out9),
    .out10(demultiplexer_2_out10), .out12(demultiplexer_2_out12), .out13(demultiplexer_2_out13), .in(uret),
    .sel(register_1_q));  // open: out0, out11, out14, out15
  Multiplexer #(.select(1), .width(32), .disabled("Z"), .enable("false")) multiplexer_9 (
    .in0(alu_1_result), .in1(ram_1_data), .out(multiplexer_9_out), .sel(\单周期硬布线控制器_1_memtoreg ));
  Pull_Resistor #(.pull(1)) pull_resistor_1 (.node(CLK));
  Button button_1 (.out(RST));
  Multiplexer #(.select(4), .width(32), .disabled("Z"), .enable("false")) multiplexer_10 (
    .in0(shifter_6_out), .in1(32'h38d0), .in2(32'h3968), .in3(32'h39f0), .in4(32'h3a78), .in5(32'h391c),
    .in6(32'h39ac), .in7(32'h3a34), .in8(32'h3ac4), .in9(32'h3b10), .in10(32'h3b30), .in12(32'h3e70),
    .in13(32'h30c8), .out(multiplexer_10_out), .sel(multiplexer_8_out));  // open: in11, in14, in15
  Register #(.width(32), .trigger("rising"), .Select("low")) register_2 (
    .D(shifter_6_out), .en(d_ff_15_qn), .Q(register_2_q), .clk(CLK), .clr(RST));
  or or_31 (or_31_out, demultiplexer_2_out10, demultiplexer_2_out1, demultiplexer_2_out2, demultiplexer_2_out3, demultiplexer_2_out4, demultiplexer_2_out5, demultiplexer_2_out6, demultiplexer_2_out7, demultiplexer_2_out8, demultiplexer_2_out9);
  Counter #(.width(16), .max('hffff), .ongoal("stay"), .trigger("rising"), .behavior("old")) counter_2 (
    .D(\总周期数 ), .Q(\总周期数 ), .clk(CLK), .clr(RST));  // open: load, count, carry, preset
  Multiplexer #(.select(1), .width(32), .disabled("Z"), .enable("false")) multiplexer_11 (
    .in0(multiplexer_10_out), .in1(register_2_q), .out(multiplexer_11_out), .sel(uret));
  Register #(.width(32), .trigger("rising"), .Select("low")) register_3 (
    .D(R1), .en(ecall), .Q(register_3_q), .clk(CLK), .clr(RST));
  Multiplexer #(.select(1), .width(32), .disabled("Z"), .enable("false")) multiplexer_12 (
    .in0({32{1'b0}}), .in1(R1), .out(multiplexer_12_out), .sel(ecall));
  Shifter #(.width(32), .shift("lr")) shifter_7 (.in(multiplexer_11_out), .\dist (5'b00010), .out(PCnext));
  Comparator #(.width(32), .mode("twosComplement")) comparator_3 (
    .a(MDin), .b(32'ha), .eq(comparator_3_eq));  // open: gt, lt
  and and_19 (halt, comparator_3_eq, ecall);
  Comparator #(.width(4), .mode("twosComplement")) comparator_4 (
    .a(out_14), .b(4'b0000), .gt(comparator_4_gt));  // open: eq, lt
  Comparator #(.width(4), .mode("twosComplement")) comparator_5 (
    .a(out_14), .b(4'b0101), .lt(comparator_5_lt));  // open: gt, eq
  Bit_Extender #(.in_width(32), .out_width(4), .\type ("zero")) bit_extender_7 (
    .in(register_3_q), .out(bit_extender_7_out));
  Bit_Extender #(.in_width(32), .out_width(4), .\type ("zero")) bit_extender_8 (
    .in(multiplexer_12_out), .out(bit_extender_8_out));
  \系统调用选择  \u_系统调用选择_1  (
    .\中断信息 (bit_extender_7_out), .\加载地图 (\系统调用选择_1_加载地图 ), .\加载初始界面 (\系统调用选择_1_加载初始界面 ),
    .\移动 (\系统调用选择_1_移动 ), .\消除一个木块 (\系统调用选择_1_消除一个木块 ));  // open: win2, win1, 消除两个木块
  \系统调用选择  \u_系统调用选择_2  (
    .\中断信息 (bit_extender_8_out), .\加载地图 (\系统调用选择_2_加载地图 ), .\加载初始界面 (\系统调用选择_2_加载初始界面 ),
    .\移动 (\系统调用选择_2_移动 ), .win2(Win1), .win1(Win2), .\消除一个木块 (\系统调用选择_2_消除一个木块 ));  // open: 消除两个木块
  and and_20 (and_20_out, comparator_4_gt, comparator_5_lt);
  \寄存器内容备份  \u_寄存器内容备份_1  (
    .\写入数据 (RDin), .Clk(CLK), .regwrite(RegWrite), .\常量序号 (5'b10110), .\变量序号 (W_num),
    .\输出结果 (\寄存器内容备份_1_输出结果 ));
  \寄存器内容备份  \u_寄存器内容备份_2  (
    .\写入数据 (RDin), .Clk(CLK), .regwrite(RegWrite), .\常量序号 (5'b10101), .\变量序号 (W_num),
    .\输出结果 (\寄存器内容备份_2_输出结果 ));
  \寄存器内容备份  \u_寄存器内容备份_3  (
    .\写入数据 (RDin), .Clk(CLK), .regwrite(RegWrite), .\常量序号 (5'b01001), .\变量序号 (W_num),
    .\输出结果 (\寄存器内容备份_3_输出结果 ));
  \寄存器内容备份  \u_寄存器内容备份_4  (
    .\写入数据 (RDin), .Clk(CLK), .regwrite(RegWrite), .\常量序号 (5'b01000), .\变量序号 (W_num),
    .\输出结果 (\寄存器内容备份_4_输出结果 ));
  \寄存器内容备份  \u_寄存器内容备份_5  (
    .\写入数据 (RDin), .Clk(CLK), .regwrite(RegWrite), .\常量序号 (5'b11100), .\变量序号 (W_num),
    .\输出结果 (\寄存器内容备份_5_输出结果 ));
  Register #(.width(1), .trigger("rising"), .Select("low")) register_4 (
    .D(and_20_out), .en(ecall), .Q(register_4_q), .clk(CLK));  // open: clr
  Priority_Encoder #(.select(3), .disabled("Z")) priority_encoder_3 (
    .in0(1'b1), .in1(\系统调用选择_1_加载地图 ), .in2(\系统调用选择_1_加载初始界面 ), .in3(\系统调用选择_1_移动 ), .in4(\系统调用选择_1_消除一个木块 ),
    .out(priority_encoder_3_out));  // open: in5, in6, in7, gs, en_out, en_in
  Multiplexer #(.select(1), .width(3), .disabled("Z"), .enable("false")) multiplexer_13 (
    .in0(3'b100), .in1(3'b011), .out(multiplexer_13_out), .sel(register_4_q));
  Multiplexer #(.select(1), .width(32), .disabled("Z"), .enable("false")) multiplexer_14 (
    .in0(\寄存器内容备份_1_输出结果 ), .in1(\寄存器内容备份_2_输出结果 ), .out(multiplexer_14_out), .sel(register_4_q));
  Bit_Extender #(.in_width(32), .out_width(2), .\type ("zero")) bit_extender_9 (
    .in(multiplexer_14_out), .out(bit_extender_9_out));
  Multiplexer #(.select(1), .width(32), .disabled("Z"), .enable("false")) multiplexer_15 (
    .in0(\寄存器内容备份_3_输出结果 ), .in1(\寄存器内容备份_4_输出结果 ), .out(multiplexer_15_out), .sel(register_4_q));
  Bit_Extender #(.in_width(32), .out_width(10), .\type ("zero")) bit_extender_10 (
    .in(\寄存器内容备份_5_输出结果 ), .out(bit_extender_10_out));
  assign xor_1_out = bit_extender_9_out ^ 2'b01;  // XOR_Gate xor_1, 2 bits wide
  \坐标运算逻辑  \u_坐标运算逻辑_1  (.in_1(multiplexer_15_out[9:0]), .x(\坐标运算逻辑_1_x ), .y(\坐标运算逻辑_1_y ));
  \坐标运算逻辑  \u_坐标运算逻辑_2  (.in_1(multiplexer_15_out[19:10]), .x(\坐标运算逻辑_2_x ), .y(\坐标运算逻辑_2_y ));
  \坐标运算逻辑  \u_坐标运算逻辑_3  (.in_1(bit_extender_10_out), .x(\坐标运算逻辑_3_x ), .y(\坐标运算逻辑_3_y ));
  \初始界面加载  \u_初始界面加载_1  (
    .star(\系统调用选择_2_加载初始界面 ), .clk(CLK), .ima(\初始界面加载_1_ima ), .Xout(\初始界面加载_1_xout ), .Yout(\初始界面加载_1_yout ));  // open: stop, end
  \地图加载  \u_地图加载_1  (
    .star(\系统调用选择_2_加载地图 ), .clk(CLK), .ima(\地图加载_1_ima ), .Xout(\地图加载_1_xout ), .Yout(\地图加载_1_yout ));  // open: stop
  \像素移动逻辑  \u_像素移动逻辑_1  (
    .star(\系统调用选择_2_移动 ), .clk(CLK), .choose(multiplexer_13_out), .X0(\坐标运算逻辑_2_x ), .Y0(\坐标运算逻辑_2_y ),
    .X1(\坐标运算逻辑_1_x ), .Y1(\坐标运算逻辑_1_y ), .dir(xor_1_out), .xout(\像素移动逻辑_1_xout ), .yout(\像素移动逻辑_1_yout ),
    .ima(\像素移动逻辑_1_ima ));  // open: end, stop
  \像素删除逻辑  \u_像素删除逻辑_1  (
    .star(\系统调用选择_2_消除一个木块 ), .clk(CLK), .num(7'b0000110), .X(\坐标运算逻辑_3_x ), .Y(\坐标运算逻辑_3_y ),
    .Xout(\像素删除逻辑_1_xout ), .Yout(\像素删除逻辑_1_yout ));  // open: stop
  Multiplexer #(.select(3), .width(7), .disabled("Z"), .enable("false")) multiplexer_16 (
    .in0({7{1'b0}}), .in1(\地图加载_1_xout ), .in2(\初始界面加载_1_xout ), .in3(\像素移动逻辑_1_xout ),
    .in4(\像素删除逻辑_1_xout ), .out(X), .sel(priority_encoder_3_out));  // open: in5, in6, in7
  Multiplexer #(.select(3), .width(7), .disabled("Z"), .enable("false")) multiplexer_17 (
    .in0({7{1'b0}}), .in1(\地图加载_1_yout ), .in2(\初始界面加载_1_yout ), .in3(\像素移动逻辑_1_yout ),
    .in4(\像素删除逻辑_1_yout ), .out(Y), .sel(priority_encoder_3_out));  // open: in5, in6, in7
  Multiplexer #(.select(3), .width(16), .disabled("Z"), .enable("false")) multiplexer_18 (
    .in0({16{1'b0}}), .in1(\地图加载_1_ima ), .in2(\初始界面加载_1_ima ), .in3(\像素移动逻辑_1_ima ), .in4({16{1'b0}}),
    .out(IMA), .sel(priority_encoder_3_out));  // open: in5, in6, in7
  // LCD_Video lcd_video_1: pin names not known; wires that end beside it: CLK, 1'b1, X, Y, IMA

  // Other names for the same wires on the sheet: Enum[3:0] = out_14; R2[31:0] = MDin

  // Notes on the sheet:
  //   中断源
  //   中断等待指示
  //   数码管输出
  //   数码管输出应该用寄存器锁存，否则显示数据只能一闪而过
  //   指令存储器
  //   指令字
  //   contents of rom_1 (hex, n*v repeats v):
  //   49*13 f3dff06f 300913 993 129a023 913 129a123 129a223 129a323 190913 129a423 129a523 913 129a623
  //   129a723 190913 129a823 129a923 913 129aa23 129ab23 129ac23 129ad23 129ae23 129af23 329a023 329a123
  //   190913 329a223 329a323 913 2898993 129a023 129a123 129a223 129a323 190913 129a423 129a523 913
  //   129a623 129a723 190913 129a823 129a923 913 129aa23 129ab23 129ac23 129ad23 129ae23 129af23 329a023
  //   329a123 190913 329a223 329a323 913 2898993 129a023 129a123 129a223 129a323 190913 129a423 129a523
  //   913 129a623 129a723 190913 129a823 129a923 913 129aa23 129ab23 129ac23 129ad23 129ae23 129af23
  //   329a023 329a123 329a223 329a323 2898993 129a023 129a123 129a223 129a323 190913 129a423 129a523 913
  //   129a623 129a723 190913 129a823 129a923 913 129aa23 129ab23 129ac23 129ad23 129ae23 129af23 329a023
  //   329a123 329a223 329a323 2898993 129a023 129a123 129a223 129a323 290913 129a423 129a523 129a623
  //   129a723 129a823 129a923 913 129aa23 129ab23 129ac23 129ad23 129ae23 129af23 329a023 329a123 329a223
  //   329a323 2898993 129a023 129a123 190913 129a223 129a323 190913 129a423 129a523 129a623 129a723
  //   129a823 129a923 913 129aa23 129ab23 129ac23 129ad23 129ae23 129af23 190913 329a023 329a123 913
  //   329a223 329a323 2898993 129a023 129a123 190913 129a223 129a323 913 129a423 129a523 129a623 129a723
  //   129a823 129a923 129aa23 129ab23 129ac23 129ad23 129ae23 129af23 190913 329a023 329a123 913 329a223
  //   329a323 2898993 129a023 129a123 129a223 129a323 129a423 129a523 129a623 129a723 129a823 129a923
  //   129aa23 129ab23 129ac23 129ad23 129ae23 129af23 329a023 329a123 329a223 329a323 2898993 129a023
  //   129a123 129a223 129a323 190913 129a423 129a523 913 129a623 129a723 129a823 129a923 129aa23 129ab23
  //   129ac23 129ad23 190913 129ae23 129af23 913 329a023 329a123 329a223 329a323 2898993 129a023 129a123
  //   129a223 129a323 190913 129a423 129a523 913 129a623 129a723 129a823 290913 129a923 129aa23 913
  //   129ab23 129ac23 129ad23 190913 129ae23 129af23 913 329a023 329a123 329a223 329a323 2898993 129a023
  //   129a123 129a223 129a323 190913 129a423 129a523 913 129a623 129a723 129a823 290913 129a923 129aa23
  //   913 129ab23 129ac23 129ad23 190913 129ae23 129af23 913 329a023 329a123 329a223 329a323 2898993
  //   129a023 129a123 129a223 129a323 190913 129a423 129a523 913 129a623 129a723 129a823 129a923 129aa23
  //   129ab23 129ac23 129ad23 190913 129ae23 129af23 913 329a023 329a123 329a223 329a323 2898993 129a023
  //   129a123 129a223 129a323 129a423 129a523 129a623 129a723 129a823 129a923 129aa23 129ab23 129ac23
  //   129ad23 129ae23 129af23 329a023 329a123 329a223 329a323 2898993 129a023 129a123 129a223 129a323
  //   129a423 129a523 129a623 129a723 129a823 129a923 129aa23 129ab23 129ac23 129ad23 129ae23 129af23
  //   190913 329a023 329a123 913 329a223 329a323 2898993 129a023 129a123 129a223 129a323 129a423 129a523
  //   129a623 129a723 129a823 129a923 290913 129aa23 129ab23 129ac23 129ad23 129ae23 129af23 100913
  //   329a023 329a123 913 329a223 329a323 2898993 129a023 129a123 129a223 129a323 129a423 129a523 129a623
  //   129a723 129a823 129a923 290913 129aa23 129ab23 129ac23 129ad23 129ae23 129af23 913 329a023 329a123
  //   329a223 329a323 2898993 129a023 129a123 129a223 129a323 129a423 129a523 129a623 129a723 129a823
  //   129a923 190913 129aa23 129ab23 913 129ac23 129ad23 190913 129ae23 129af23 913 329a023 329a123
  //   329a223 329a323 2898993 129a023 129a123 129a223 129a323 129a423 129a523 129a623 129a723 129a823
  //   129a923 190913 129aa23 129ab23 913 129ac23 129ad23 190913 129ae23 129af23 913 329a023 329a123
  //   329a223 329a323 190913 2898993 129a023 129a123 913 129a223 129a323 129a423 129a523 129a623 129a723
  //   129a823 129a923 190913 129aa23 129ab23 913 129ac23 129ad23 190913 129ae23 129af23 913 329a023
  //   329a123 490913 329a223 913 329a323 190913 2898993 129a023 129a123 913 129a223 129a323 129a423
  //   129a523 129a623 129a723 129a823 129a923 190913 129aa23 129ab23 913 129ac23 129ad23 190913 129ae23
  //   129af23 913 329a023 329a123 329a223 329a323 200513 2200893 73 413 2f400493 300a93 300b13 b93 c13 c93
  //   d13 200073 3ff47413 100a93 2800a13 414409b3 9a903 26091663 29a903 26091263 913 1242023 41440a33
  //   a41413 1440433 300913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
  //   Beq
  //   Bne
  //   MemToReg
  //   MemWrite
  //   AluOP
  //   AluSrcB
  //   RegWrite
  //   Reset 
  //   Reset 
  //   Reset 
  //   Reset 
  //   Reset 
  //   Reset 
  //   Reset 
  //   Reset 
  //   Reset 
  //   Reset 
  //   Reset 
  //   Reset 
  //   Reset 
  //   为方便自动评测，需要输出PC，IR，寄存器堆写如数据RDin
  //   RAM写使能MemWrite、RAM写入数据MDin等信号
  //   数据存储器
  //   控制位
  //   暂停节拍，不能为0
  //   戳工具置1进入计数暂停模式，ctrl+k时钟自动运行到对应节拍暂停
  //   可计数暂停的时钟源
endmodule
module \单周期_多级中断  (
  input  IR1,
  input  IR2,
  input  IR3,
  output RegWrite,
  output MemWrite,
  output [31:0] PC,
  output [31:0] IR,
  output [31:0] RDin,
  output [31:0] MDin,
  output [31:0] LedData
);

  wire alu_1_equal, alu_1_out_6, and_1_out, and_2_out, and_3_out, and_4_out, and_5_out, and_6_out, and_8_out,
       and_9_out, and_10_out, and_11_out, and_12_out, beq, CLK, clock_2_out, comparator_1_eq,
       comparator_2_eq, comparator_3_eq, comparator_4_eq, comparator_5_eq, comparator_6_eq, comparator_7_gt,
       comparator_8_eq, comparator_8_lt, comparator_9_eq, csrrci, csrrsi, d_ff_1_q, d_ff_2_q, d_ff_3_q,
       d_ff_4_q, d_ff_5_q, d_ff_6_qn, d_ff_7_q, decoder_1_out0, decoder_1_out1, decoder_1_out2,
       demultiplexer_2_out1, demultiplexer_2_out2, demultiplexer_2_out3, ecall, Go, halt, IR1_2_q, IR1_3_q,
       IR1_q, IR1_t, IR2_t, IR3_t, IRA, IRB, IRC, jal, jalr, lb, nand_1_out, not_1_out, or_1_out, or_2_out,
       or_8_out, or_9_out, or_10_out, or_12_out, or_14_out, or_15_out, RST, uret, W1, W2, W3,
       \单周期硬布线控制器_1_alu_src , \单周期硬布线控制器_1_beq , \单周期硬布线控制器_1_blt , \单周期硬布线控制器_1_bne , \单周期硬布线控制器_1_ecall ,
       \单周期硬布线控制器_1_memtoreg , \单周期硬布线控制器_1_s_type , \单周期硬布线控制器_1_uret ;
  wire [1:0] counter_2_q, demultiplexer_3_out0, demultiplexer_3_out1, demultiplexer_3_out2, \int ,
       multiplexer_11_out, priority_encoder_1_out, priority_encoder_2_out, register_1_q, register_2_q,
       register_3_q;
  wire [3:0] \单周期硬布线控制器_1_alu_op ;
  wire [4:0] multiplexer_2_out, multiplexer_3_out, multiplexer_4_out;
  wire [7:0] multiplexer_8_out;
  wire [9:0] bit_extender_1_out, dataaddr, shifter_4_out;
  wire [12:0] CNT_num;
  wire [15:0] \总周期数 ;
  wire [31:0] adder_1_out, adder_2_out, adder_3_out, alu_1_result, and_7_out, bit_extender_2_out,
       bit_extender_3_out, bit_extender_4_out, bit_extender_5_out, bit_extender_7_out, demultiplexer_4_out0,
       demultiplexer_4_out1, demultiplexer_4_out2, multiplexer_5_out, multiplexer_6_out, multiplexer_9_out,
       multiplexer_10_out, multiplexer_12_out, multiplexer_14_out, PC0, PC_q, PCnext, R1, ram_1_data,
       register_4_q, register_5_q, register_6_q, shifter_2_out, shifter_3_out, shifter_5_out, shifter_6_out;

  Clock #(.highDuration(1), .lowDuration(1)) clock_1 ();  // open: out
  Button _1 ();  // open: out
  Button _2 ();  // open: out
  Button _3 ();  // open: out
  Button \u_继续运行  (.out(Go));
  LED #(.active("true")) led_1 (.in(W1));
  LED #(.active("true")) led_2 (.in(W2));
  LED #(.active("true")) led_3 (.in(W3));
  Button _1_2 ();  // open: out
  Button _2_2 ();  // open: out
  Button _3_2 ();  // open: out
  Hex_Digit_Display hex_digit_display_1 (.value(LedData[31:28]));  // open: dp
  LED #(.active("true")) led_4 (.in(W1));
  LED #(.active("true")) led_5 (.in(W2));
  LED #(.active("true")) led_6 (.in(W3));
  Comparator #(.width(16), .mode("twosComplement")) comparator_1 (
    .a(16'h258), .b(\总周期数 ), .eq(comparator_1_eq));  // open: gt, lt
  Comparator #(.width(16), .mode("twosComplement")) comparator_2 (
    .a(\总周期数 ), .b(16'h1), .eq(comparator_2_eq));  // open: gt, lt
  Comparator #(.width(16), .mode("twosComplement")) comparator_3 (
    .a(\总周期数 ), .b(16'h4), .eq(comparator_3_eq));  // open: gt, lt
  Comparator #(.width(16), .mode("twosComplement")) comparator_4 (
    .a(\总周期数 ), .b(16'h7), .eq(comparator_4_eq));  // open: gt, lt
  Comparator #(.width(16), .mode("twosComplement")) comparator_5 (
    .a(\总周期数 ), .b(16'h241), .eq(comparator_5_eq));  // open: gt, lt
  not not_1 (not_1_out, halt);
  Hex_Digit_Display hex_digit_display_2 (.value(LedData[27:24]));  // open: dp
  Hex_Digit_Display hex_digit_display_3 (.value(LedData[23:20]));  // open: dp
  or or_1 (or_1_out, comparator_1_eq, comparator_2_eq);
  assign IRA = or_1_out ? ~CLK : 1'bz;  // Controlled_Inverter controlled_inverter_1
  assign IRB = comparator_3_eq ? ~CLK : 1'bz;  // Controlled_Inverter controlled_inverter_2
  or or_2 (or_2_out, comparator_4_eq, comparator_5_eq);
  assign IRC = or_2_out ? ~CLK : 1'bz;  // Controlled_Inverter controlled_inverter_3
  Register #(.width(32), .trigger("rising"), .Select("low")) u_PC (
    .D(PCnext), .en(not_1_out), .Q(PC_q), .clk(CLK), .clr(RST));
  // Probe on PC0
  Priority_Encoder #(.select(2), .disabled("Z")) priority_encoder_1 (
    .in0(1'b1), .in1(jal), .in2(jalr), .in3(beq), .out(priority_encoder_1_out));  // open: gs, en_out, en_in
  Hex_Digit_Display hex_digit_display_4 (.value(LedData[15:12]));  // open: dp
  Hex_Digit_Display hex_digit_display_5 (.value(LedData[19:16]));  // open: dp
  Pull_Resistor #(.pull(0)) pull_resistor_1 (.node(IRA));
  Pull_Resistor #(.pull(0)) pull_resistor_2 (.node(IRB));
  Pull_Resistor #(.pull(0)) pull_resistor_3 (.node(IRC));
  // Probe on PC
  Shifter #(.width(32), .shift("ll")) shifter_1 (.in(PC_q), .\dist (5'b00010), .out(PC));
  Bit_Extender #(.in_width(32), .out_width(10), .\type ("sign")) bit_extender_1 (.in(PC_q), .out(bit_extender_1_out));
  Adder #(.width(32)) adder_1 (.a(PC_q), .b(32'h1), .out(adder_1_out));  // open: cin, cout
  Multiplexer #(.select(2), .width(32), .disabled("Z"), .enable("false")) multiplexer_1 (
    .in0(adder_1_out), .in1(adder_3_out), .in2(shifter_5_out), .in3(adder_2_out), .out(PC0),
    .sel(priority_encoder_1_out));
  Hex_Digit_Display hex_digit_display_6 (.value(LedData[7:4]));  // open: dp
  Hex_Digit_Display hex_digit_display_7 (.value(LedData[11:8]));  // open: dp
  // Probe on \总周期数 
  // RiscV_Probe riscv_probe_1: pin names not known; wires that end beside it: {32{1'b0}}, IR
  Hex_Digit_Display hex_digit_display_8 (.value(LedData[3:0]));  // open: dp
  Comparator #(.width(32), .mode("twosComplement")) comparator_6 (
    .a({32{1'b0}}), .b(IR), .eq(comparator_6_eq));  // open: gt, lt
  Demultiplexer #(.select(1), .width(1), .tristate("false"), .disabled("Z"), .enable("false")) demultiplexer_1 (
    .out0(ecall), .out1(uret), .in(\单周期硬布线控制器_1_uret ), .sel(IR[21]));
  ROM #(.addrWidth(10), .dataWidth(32), .Select("high")) rom_1 (.addr(bit_extender_1_out), .data(IR));
  or or_3 (IR1_t, IR1, IRA);
  D_Flip_Flop #(.trigger("rising"), .Pre_Clr_Positions("LEGACY"), .NegatePresetClear("false"), .enable("true"), .NewFFLayout("false")) d_ff_1 (
    .clk(IRA), .D(1'b1), .Q(d_ff_1_q), .reset(IR1_q));  // open: Qn, preset, en
  or or_4 (W1, IR1_q, d_ff_1_q);
  D_Flip_Flop #(.trigger("rising"), .Pre_Clr_Positions("LEGACY"), .NegatePresetClear("false"), .enable("true"), .NewFFLayout("false")) d_ff_2 (
    .clk(IRB), .D(1'b1), .Q(d_ff_2_q), .reset(IR1_2_q));  // open: Qn, preset, en
  or or_5 (W2, IR1_2_q, d_ff_2_q);
  D_Flip_Flop #(.trigger("rising"), .Pre_Clr_Positions("LEGACY"), .NegatePresetClear("false"), .enable("true"), .NewFFLayout("false")) d_ff_3 (
    .clk(IRC), .D(1'b1), .Q(d_ff_3_q), .reset(IR1_3_q));  // open: Qn, preset, en
  or or_6 (W3, IR1_3_q, d_ff_3_q);
  \单周期硬布线控制器  \u_单周期硬布线控制器_1  (
    .Funct({IR[30], IR[25], IR[14:12]}), .OP(IR[6:2]), .ALU_OP(\单周期硬布线控制器_1_alu_op ),
    .MemToReg(\单周期硬布线控制器_1_memtoreg ), .MemWrite(MemWrite), .ALU_SRC(\单周期硬布线控制器_1_alu_src ),
    .RegWrite(RegWrite), .ecall(\单周期硬布线控制器_1_ecall ), .S_type(\单周期硬布线控制器_1_s_type ), .Jalr(jalr),
    .Beq(\单周期硬布线控制器_1_beq ), .JAL(jal), .Bne(\单周期硬布线控制器_1_bne ), .LB(lb), .CSRRCI(csrrci),
    .BLT(\单周期硬布线控制器_1_blt ), .URET(\单周期硬布线控制器_1_uret ), .CSRRSI(csrrsi), .IR_0(comparator_6_eq));
  Multiplexer #(.select(1), .width(5), .disabled("Z"), .enable("false")) multiplexer_2 (
    .in0(IR[19:15]), .in1(5'b01010), .out(multiplexer_2_out), .sel(\单周期硬布线控制器_1_ecall ));
  Multiplexer #(.select(1), .width(5), .disabled("Z"), .enable("false")) multiplexer_3 (
    .in0(IR[24:20]), .in1(5'b10001), .out(multiplexer_3_out), .sel(\单周期硬布线控制器_1_ecall ));
  assign bit_extender_2_out = {{20{IR[31]}}, IR[31:20]};  // Bit_Extender bit_extender_2
  assign bit_extender_3_out = {{20{IR[31]}}, {IR[31:25], IR[11:7]}};  // Bit_Extender bit_extender_3
  or or_7 (IR2_t, IR2, IRB);
  or or_8 (or_8_out, d_ff_1_q, IR1_q);
  or or_9 (or_9_out, d_ff_2_q, IR1_2_q);
  or or_10 (or_10_out, d_ff_3_q, IR1_3_q);
  Multiplexer #(.select(1), .width(5), .disabled("Z"), .enable("false")) multiplexer_4 (
    .in0(multiplexer_3_out), .in1(IR[11:7]), .out(multiplexer_4_out), .sel(\单周期硬布线控制器_1_s_type ));
  Multiplexer #(.select(1), .width(32), .disabled("Z"), .enable("false")) multiplexer_5 (
    .in0(bit_extender_2_out), .in1(bit_extender_3_out), .out(multiplexer_5_out), .sel(MemWrite));
  assign bit_extender_4_out = {{20{IR[31]}}, {IR[31], IR[7], IR[30:25], IR[11:8]}};  // Bit_Extender bit_extender_4
  Shifter #(.width(32), .shift("ar")) shifter_2 (.in(bit_extender_4_out), .\dist (5'b00001), .out(shifter_2_out));
  assign bit_extender_5_out = {{12{IR[31]}}, {IR[31], IR[19:12], IR[20], IR[30:21]}};  // Bit_Extender bit_extender_5
  Regifile regifile_1 (
    .Din(RDin), .Clk(CLK), .R1(R1), .R2(MDin), .WE(RegWrite), .W_num(multiplexer_4_out),
    .R1_num(multiplexer_2_out), .R2_num(multiplexer_3_out));
  Adder #(.width(32)) adder_2 (.a(shifter_2_out), .b(PC_q), .out(adder_2_out));  // open: cin, cout
  Shifter #(.width(32), .shift("ar")) shifter_3 (.in(bit_extender_5_out), .\dist (5'b00001), .out(shifter_3_out));
  Adder #(.width(32)) adder_3 (.a(shifter_3_out), .b(PC_q), .out(adder_3_out));  // open: cin, cout
  or or_11 (IR3_t, IR3, IRC);
  and and_1 (and_1_out, or_8_out, ~demultiplexer_2_out1);  // AND_Gate
  and and_2 (and_2_out, or_9_out, ~demultiplexer_2_out2);  // AND_Gate
  and and_3 (and_3_out, or_10_out, ~demultiplexer_2_out3);  // AND_Gate
  D_Flip_Flop #(.trigger("rising"), .Pre_Clr_Positions("LEGACY"), .NegatePresetClear("false"), .enable("true"), .NewFFLayout("false")) u_IR1 (
    .clk(CLK), .D(and_1_out), .Q(IR1_q), .reset(RST));  // open: Qn, preset, en
  D_Flip_Flop #(.trigger("rising"), .Pre_Clr_Positions("LEGACY"), .NegatePresetClear("false"), .enable("true"), .NewFFLayout("false")) IR1_2 (
    .clk(CLK), .D(and_2_out), .Q(IR1_2_q), .reset(RST));  // open: Qn, preset, en
  D_Flip_Flop #(.trigger("rising"), .Pre_Clr_Positions("LEGACY"), .NegatePresetClear("false"), .enable("true"), .NewFFLayout("false")) IR1_3 (
    .clk(CLK), .D(and_3_out), .Q(IR1_3_q), .reset(RST));  // open: Qn, preset, en
  Multiplexer #(.select(1), .width(32), .disabled("Z"), .enable("false")) multiplexer_6 (
    .in0(MDin), .in1(multiplexer_5_out), .out(multiplexer_6_out), .sel(\单周期硬布线控制器_1_alu_src ));
  and and_4 (and_4_out, \单周期硬布线控制器_1_blt , alu_1_out_6);
  and and_5 (and_5_out, \单周期硬布线控制器_1_beq , alu_1_equal);
  and and_6 (and_6_out, \单周期硬布线控制器_1_bne , ~alu_1_equal);  // AND_Gate
  ALU alu_1 (
    .X(R1), .Y(multiplexer_6_out), .AluOP(\单周期硬布线控制器_1_alu_op ), .Equal(alu_1_equal), .Result(alu_1_result),
    .out_6(alu_1_out_6));  // open: Result_2, out_4
  Priority_Encoder #(.select(2), .disabled("Z")) priority_encoder_2 (
    .in0(1'b1), .in1(IR1_q), .in2(IR1_2_q), .in3(IR1_3_q), .out(priority_encoder_2_out));  // open: gs, en_out, en_in
  D_Flip_Flop #(.trigger("rising"), .Pre_Clr_Positions("LEGACY"), .NegatePresetClear("false"), .enable("false"), .NewFFLayout("false")) d_ff_4 (
    .clk(CLK), .D(csrrci), .Q(d_ff_4_q), .reset(RST));  // open: Qn, preset
  D_Flip_Flop #(.trigger("rising"), .Pre_Clr_Positions("LEGACY"), .NegatePresetClear("false"), .enable("false"), .NewFFLayout("false")) d_ff_5 (
    .clk(CLK), .D(csrrsi), .Q(d_ff_5_q), .reset(RST));  // open: Qn, preset
  Shifter #(.width(10), .shift("lr")) shifter_4 (.in(dataaddr), .\dist (4'b0010), .out(shifter_4_out));
  Bit_Extender #(.in_width(32), .out_width(10), .\type ("sign")) bit_extender_6 (.in(alu_1_result), .out(dataaddr));
  Multiplexer #(.select(1), .width(32), .disabled("Z"), .enable("false")) multiplexer_7 (
    .in0(multiplexer_10_out), .in1(shifter_6_out), .out(RDin), .sel(or_12_out));
  or or_12 (or_12_out, jal, jalr);
  assign and_7_out = alu_1_result & 32'hfffffffe;  // AND_Gate and_7, 32 bits wide
  Shifter #(.width(32), .shift("ar")) shifter_5 (.in(and_7_out), .\dist (5'b00010), .out(shifter_5_out));
  and and_8 (and_8_out, and_9_out, d_ff_6_qn);
  or or_13 (beq, and_4_out, and_5_out, and_6_out);
  // Probe on \单周期硬布线控制器_1_alu_op 
  D_Flip_Flop #(.trigger("rising"), .Pre_Clr_Positions("LEGACY"), .NegatePresetClear("false"), .enable("true"), .NewFFLayout("false")) d_ff_6 (
    .clk(CLK), .D(and_8_out), .Qn(d_ff_6_qn), .preset(d_ff_4_q), .en(d_ff_6_qn), .reset(or_14_out));  // open: Q
  or or_14 (or_14_out, RST, d_ff_5_q, uret);
  RAM #(.addrWidth(10), .dataWidth(32), .bus("separate"), .Select("high")) ram_1 (
    .addr(shifter_4_out), .din(MDin), .data(ram_1_data), .str(MemWrite), .clk(CLK), .clr(RST));  // open: sel, ld
  Comparator #(.width(2), .mode("unsigned")) comparator_7 (
    .a(priority_encoder_2_out), .b(\int ), .gt(comparator_7_gt));  // open: eq, lt
  Demultiplexer #(.select(2), .width(1), .tristate("false"), .disabled("Z"), .enable("false")) demultiplexer_2 (
    .out1(demultiplexer_2_out1), .out2(demultiplexer_2_out2), .out3(demultiplexer_2_out3), .in(uret),
    .sel(\int ));  // open: out0
  Multiplexer #(.select(2), .width(8), .disabled("Z"), .enable("false")) multiplexer_8 (
    .in0(ram_1_data[7:0]), .in1(ram_1_data[15:8]), .in2(ram_1_data[23:16]), .in3(ram_1_data[31:24]),
    .out(multiplexer_8_out), .sel(dataaddr[1:0]));
  D_Flip_Flop #(.trigger("high"), .Pre_Clr_Positions("LEGACY"), .NegatePresetClear("false"), .enable("true"), .NewFFLayout("false")) d_ff_7 (.Q(d_ff_7_q));  // open: clk, D, Qn, preset, en, reset
  // Probe on 13'hba
  and and_9 (and_9_out, comparator_7_gt, d_ff_6_qn);
  assign bit_extender_7_out = {{24{multiplexer_8_out[7]}}, multiplexer_8_out};  // Bit_Extender bit_extender_7
  Shifter #(.width(32), .shift("ll")) shifter_6 (.in(adder_1_out), .\dist (5'b00010), .out(shifter_6_out));
  Comparator #(.width(13), .mode("twosComplement")) comparator_8 (
    .a(CNT_num), .b(13'hba), .eq(comparator_8_eq), .lt(comparator_8_lt));  // open: gt
  Clock #(.highDuration(1), .lowDuration(1)) clock_2 (.out(clock_2_out));
  or or_15 (or_15_out, and_9_out, uret);
  Multiplexer #(.select(1), .width(32), .disabled("Z"), .enable("false")) multiplexer_9 (
    .in0(ram_1_data), .in1(bit_extender_7_out), .out(multiplexer_9_out), .sel(lb));
  nand nand_1 (nand_1_out, d_ff_7_q, comparator_8_eq);
  Counter #(.width(13), .max('h1fff), .ongoal("stay"), .trigger("rising"), .behavior("old")) counter_1 (
    .count(comparator_8_lt), .Q(CNT_num), .clk(clock_2_out), .clr(RST));  // open: load, D, carry, preset
  Counter #(.width(2), .max('h3), .ongoal("wrap"), .trigger("rising"), .behavior("new")) counter_2 (
    .count(or_15_out), .Q(counter_2_q), .clk(CLK), .clr(RST), .down(uret));  // open: load, D, carry, preset
  assign CLK = nand_1_out ? clock_2_out : 1'bz;  // Controlled_Buffer controlled_buffer_1
  Demultiplexer #(.select(2), .width(2), .tristate("false"), .disabled("Z"), .enable("false")) demultiplexer_3 (
    .out0(demultiplexer_3_out0), .out1(demultiplexer_3_out1), .out2(demultiplexer_3_out2),
    .in(priority_encoder_2_out), .sel(counter_2_q));  // open: out3
  Demultiplexer #(.select(2), .width(32), .tristate("false"), .disabled("Z"), .enable("false")) demultiplexer_4 (
    .out0(demultiplexer_4_out0), .out1(demultiplexer_4_out1), .out2(demultiplexer_4_out2), .in(PC0),
    .sel(counter_2_q));  // open: out3
  Decoder #(.select(2), .tristate("false"), .disabled("Z"), .enable("false")) decoder_1 (
    .out0(decoder_1_out0), .out1(decoder_1_out1), .out2(decoder_1_out2), .sel(counter_2_q));  // open: out3
  Multiplexer #(.select(1), .width(32), .disabled("Z"), .enable("false")) multiplexer_10 (
    .in0(alu_1_result), .in1(multiplexer_9_out), .out(multiplexer_10_out), .sel(\单周期硬布线控制器_1_memtoreg ));
  Pull_Resistor #(.pull(1)) pull_resistor_4 (.node(CLK));
  Multiplexer #(.select(1), .width(2), .disabled("Z"), .enable("false")) multiplexer_11 (
    .in0(2'b00), .in1(priority_encoder_2_out), .out(multiplexer_11_out), .sel(and_9_out));
  Button button_1 (.out(RST));
  Multiplexer #(.select(2), .width(32), .disabled("Z"), .enable("false")) multiplexer_12 (
    .in0(PC0), .in1(32'hc2b), .in2(32'hc56), .in3(32'hc81), .out(multiplexer_12_out), .sel(multiplexer_11_out));
  and and_10 (and_10_out, and_9_out, decoder_1_out0);
  and and_11 (and_11_out, and_9_out, decoder_1_out1);
  and and_12 (and_12_out, and_9_out, decoder_1_out2);
  Counter #(.width(16), .max('hffff), .ongoal("stay"), .trigger("rising"), .behavior("old")) counter_3 (
    .D(\总周期数 ), .Q(\总周期数 ), .clk(CLK), .clr(RST));  // open: load, count, carry, preset
  Register #(.width(2), .trigger("rising"), .Select("low")) register_1 (
    .D(demultiplexer_3_out0), .en(and_10_out), .Q(register_1_q), .clk(CLK), .clr(RST));
  Register #(.width(2), .trigger("rising"), .Select("low")) register_2 (
    .D(demultiplexer_3_out1), .en(and_11_out), .Q(register_2_q), .clk(CLK), .clr(RST));
  Register #(.width(2), .trigger("rising"), .Select("low")) register_3 (
    .D(demultiplexer_3_out2), .en(and_12_out), .Q(register_3_q), .clk(CLK), .clr(RST));
  Register #(.width(32), .trigger("rising"), .Select("low")) register_4 (
    .D(demultiplexer_4_out0), .en(and_10_out), .Q(register_4_q), .clk(CLK), .clr(RST));
  Register #(.width(32), .trigger("rising"), .Select("low")) register_5 (
    .D(demultiplexer_4_out1), .en(and_11_out), .Q(register_5_q), .clk(CLK), .clr(RST));
  Register #(.width(32), .trigger("rising"), .Select("low")) register_6 (
    .D(demultiplexer_4_out2), .en(and_12_out), .Q(register_6_q), .clk(CLK), .clr(RST));
  Comparator #(.width(32), .mode("twosComplement")) comparator_9 (
    .a(MDin), .b(32'ha), .eq(comparator_9_eq));  // open: gt, lt
  and and_13 (halt, comparator_9_eq, ecall);
  Register #(.width(32), .trigger("rising"), .Select("low")) register_7 (
    .D(R1), .en(ecall), .Q(LedData), .clk(CLK), .clr(RST));
  Multiplexer #(.select(2), .width(2), .disabled("Z"), .enable("false")) multiplexer_13 (
    .in0(2'b00), .in1(register_1_q), .in2(register_2_q), .in3(register_3_q), .out(\int ), .sel(counter_2_q));
  Multiplexer #(.select(2), .width(32), .disabled("Z"), .enable("false")) multiplexer_14 (
    .in0(multiplexer_12_out), .in1(register_4_q), .in2(register_5_q), .in3(register_6_q),
    .out(multiplexer_14_out), .sel(counter_2_q));
  // RiscV_Probe riscv_probe_2: pin names not known; wires that end beside it: IR
  Multiplexer #(.select(1), .width(32), .disabled("Z"), .enable("false")) multiplexer_15 (
    .in0(multiplexer_12_out), .in1(multiplexer_14_out), .out(PCnext), .sel(uret));

  // Other names for the same wires on the sheet: R2[31:0] = MDin

  // Notes on the sheet:
  //   中断源
  //   中断等待指示
  //   总复位信号应将除ROM以外所有存储组件全部清零
  //   多级中断测试信号模拟器
  //   数码管输出
  //   数码管输出应该用寄存器锁存，否则显示数据只能一闪而过
  //   指令存储器
  //   指令字
  //   contents of rom_1 (hex, n*v repeats v):
  //   7d000113 100413 1f41993 41f9d993 433 c00913 800b13 140413 f47413 800293 100313 499993 89e9b3 1300533
  //   2200893 73 406282b3 fe0294e3 140413 f00f93 1f47433 1c41413 800293 100313 49d993 89e9b3 1300533
  //   2200893 73 406282b3 fe0294e3 1c45413 406b0b33 b0463 f95ff06f 2b3 fff2c293 1029293 fff2e293 500533
  //   2200893 73 f5dff06f 1112023 410113 a12023 410113 812023 410113 1312023 410113 1412023 410113 1512023
  //   410113 1612023 410113 40e073 100b13 300a13 100a93 1600433 441413 14469b3 1300533 2200893 73 fe0416e3
  //   415a0a33 fe0a10e3 40f073 ffc10113 12b03 ffc10113 12a83 ffc10113 12a03 ffc10113 12983 ffc10113 12403
  //   ffc10113 12503 ffc10113 12883 200073 1112023 410113 a12023 410113 812023 410113 1312023 410113
  //   1412023 410113 1512023 410113 1612023 410113 40e073 200b13 300a13 100a93 1600433 441413 14469b3
  //   1300533 2200893 73 fe0416e3 415a0a33 fe0a10e3 40f073 ffc10113 12b03 ffc10113 12a83 ffc10113 12a03
  //   ffc10113 12983 ffc10113 12403 ffc10113 12503 ffc10113 12883 200073 1112023 410113 a12023 410113
  //   812023 410113 1312023 410113 1412023 410113 1512023 410113 1612023 410113 40e073 300b13 300a13
  //   100a93 1600433 441413 14469b3 1300533 2200893 73 fe0416e3 415a0a33 fe0a10e3 40f073 ffc10113 12b03
  //   ffc10113 12a83 ffc10113 12a03 ffc10113 12983 ffc10113 12403 ffc10113 12503 ffc10113 12883 200073
  //   Beq
  //   Bne
  //   MemToReg
  //   MemWrite
  //   AluOP
  //   AluSrcB
  //   RegWrite
  //   Reset 
  //   Reset 
  //   Reset 
  //   为方便自动评测，需要输出PC，IR，寄存器堆写如数据RDin
  //   RAM写使能MemWrite、RAM写入数据MDin等信号
  //   数据存储器
  //   控制位
  //   暂停节拍，不能为0
  //   戳工具置1进入计数暂停模式，ctrl+k时钟自动运行到对应节拍暂停
  //   可计数暂停的时钟源
endmodule

module \像素信息获取与计算逻辑  (
  input  star,
  input  [2:0] choose,
  input  clk,
  input  [6:0] x,
  input  [6:0] y,
  input  [1:0] dir,
  output stop,
  output \end ,
  output [15:0] ima,
  output [6:0] Xout,
  output [6:0] Yout
);

  wire comparator_1_eq, comparator_2_eq;
  wire [6:0] adder_1_out, adder_2_out, adder_3_out, adder_4_out, multiplexer_2_out, multiplexer_3_out,
       subtractor_1_out;
  wire [7:0] counter_1_q;
  wire [31:0] \固定砖块信息_data , \子弹信息_data , \木块信息_data , \白色坦克信息_data , \绿色坦克信息_data ;
  wire [31:16] multiplexer_1_out;

  Counter #(.width(8), .max('hff), .ongoal("wrap"), .trigger("rising"), .behavior("new")) counter_1 (
    .count(stop), .Q(counter_1_q), .clk(clk), .clr(star));  // open: load, D, carry, preset, down
  ROM #(.addrWidth(8), .dataWidth(32), .Select("low")) \u_木块信息  (.addr(counter_1_q), .data(\木块信息_data ));
  ROM #(.addrWidth(8), .dataWidth(32), .Select("low")) \u_固定砖块信息  (.addr(counter_1_q), .data(\固定砖块信息_data ));
  ROM #(.addrWidth(8), .dataWidth(32), .Select("low")) \u_白色坦克信息  (.addr(counter_1_q), .data(\白色坦克信息_data ));
  ROM #(.addrWidth(8), .dataWidth(32), .Select("low")) \u_绿色坦克信息  (.addr(counter_1_q), .data(\绿色坦克信息_data ));
  ROM #(.addrWidth(8), .dataWidth(32), .Select("low")) \u_子弹信息  (.addr(counter_1_q), .data(\子弹信息_data ));
  Multiplexer #(.select(3), .width(32), .disabled("Z"), .enable("false")) multiplexer_1 (
    .in0({32{1'b0}}), .in1(\木块信息_data ), .in2(\固定砖块信息_data ), .in3(\白色坦克信息_data ), .in4(\绿色坦克信息_data ),
    .in5(\子弹信息_data ), .in6({32{1'b0}}), .in7({32{1'b0}}), .out({multiplexer_1_out, ima}), .sel(choose));
  Comparator #(.width(3), .mode("twosComplement")) comparator_1 (
    .a(3'b000), .b(choose), .eq(comparator_1_eq));  // open: gt, lt
  Comparator #(.width(32), .mode("twosComplement")) comparator_2 (
    .a({32{1'b0}}), .b({multiplexer_1_out, ima}), .eq(comparator_2_eq));  // open: gt, lt
  Subtractor #(.width(7)) subtractor_1 (
    .a(7'b0001011), .b(multiplexer_1_out[29:23]), .out(subtractor_1_out));  // open: bin, bout
  not not_1 (stop, comparator_2_eq);
  Adder #(.width(7)) adder_1 (.a(x), .b(7'b0000100), .out(adder_1_out));  // open: cin, cout
  Adder #(.width(7)) adder_2 (.a(y), .b(7'b0000100), .out(adder_2_out));  // open: cin, cout
  Register #(.width(1), .trigger("rising"), .Select("low")) register_1 (
    .D(comparator_2_eq), .Q(\end ), .clk(clk), .clr(star));  // open: en
  Multiplexer #(.select(2), .width(7), .disabled("Z"), .enable("false")) multiplexer_2 (
    .in0(multiplexer_1_out[22:16]), .in1(multiplexer_1_out[29:23]), .in2(multiplexer_1_out[22:16]),
    .in3(subtractor_1_out), .out(multiplexer_2_out), .sel(dir));
  Multiplexer #(.select(2), .width(7), .disabled("Z"), .enable("false")) multiplexer_3 (
    .in0(multiplexer_1_out[29:23]), .in1(multiplexer_1_out[22:16]), .in2(subtractor_1_out),
    .in3(multiplexer_1_out[22:16]), .out(multiplexer_3_out), .sel(dir));
  Adder #(.width(7)) adder_3 (.a(multiplexer_2_out), .b(adder_1_out), .out(adder_3_out));  // open: cin, cout
  Adder #(.width(7)) adder_4 (.a(multiplexer_3_out), .b(adder_2_out), .out(adder_4_out));  // open: cin, cout
  Multiplexer #(.select(1), .width(7), .disabled("Z"), .enable("false")) multiplexer_4 (
    .in0(adder_3_out), .in1({7{1'b0}}), .out(Xout), .sel(comparator_1_eq));
  Multiplexer #(.select(1), .width(7), .disabled("Z"), .enable("false")) multiplexer_5 (
    .in0(adder_4_out), .in1({7{1'b0}}), .out(Yout), .sel(comparator_1_eq));

  // Notes on the sheet:
  //   contents of 木块信息 (hex, n*v repeats v):
  //   5940 15560 25940 35940 45940 54d20 805d42 815d41 825d42 835d42 845d42 855101 10050e4 1014ce5 10250e4
  //   10350e4 10450e4 10544c4 18069c2 18169c2 1826de3 18369c2 1846dc2 1855d81 2005d41 2015941 2026182
  //   2035d61 2046141 2055101 2805104 28154e4 2825d44 2835923 2845504 28548e2
  //   contents of 固定砖块信息 (hex, n*v repeats v):
  //   6739 16739 26739 36b5a 46739 55294 806739 817fff 827fff 837fff 846739 854e73 1006739 1017fff 1027fff
  //   1037fff 1046739 1054e73 1806739 1817fff 1827fff 1837fff 1846b5a 1854e73 2006739 2016739 2026739
  //   2036739 2045ad6 2054e73 2805294 2814631 2824a52 2834a52 2844a52 2854e73
  //   contents of 白色坦克信息 (hex, n*v repeats v):
  //   54e73 64a30 b0421 803214 81571a 832108 845ad4 855ef8 860488 870088 891ce7 8a4697 8b2dd0 10029cf
  //   1014ab6 1036739 1046f7a 1056f7c 10600cc 10700cd 1080043 1091cc5 10a3e32 10b2d8e 18039f4 1814a76
  //   1827fde 183739d 1846738 1856b3a 1862df1 1871571 18800ae 1891d90 18a4296 18b31d0 20025ae 2014253
  //   202779c 2036b5a 2045ef6 2056718 2066339 2075af8 208006a 2091d91 20a3613 20b296d 2801d4e 2813e34
  //   282779c 2836b59 2846318 2854654 2865ad6 2876f57 28808ec 2891971 28a31f2 28b214d 3004254 3014eb6
  //   302739c 3036b5a 3044674 30508eb 306633a 3076b59 30800ee 3091971 30a4eb5 30b3a11 380216e 3813e34
  //   382779b 3836f7b 38435f1 38525af 38677dd 3877338 38800ed 389216c 38a3213 38b216e 4003a35 4014a97
  //   4027bdd 4036b5a 4046319 4056739 4065ef7 4076b56 40800f1 4092151 40a42b5 40b31f0 4800cc8 4813a12
  //   482294a 48377bd 48462d5 48562f6 486675a 4874ed9 488006b 4891d2c 48a216f 48b14e9 50056d7 501675a
  //   50335ad 5047fff 50573bf 5061d4d 50704cd 50918c5 50a633a 50b4653 580294a 5812d6b 5840001 5850001
  //   5860024 5870044 5890842 58a2d6b 58b2d6b
  //   contents of 绿色坦克信息 (hex, n*v repeats v):
  //   298a 12a8e 2326f 50041 60c84 91dab a26af b260c 802e8e 811bb0 822373 840400 852169 862a2c 870c21
  //   891de8 8a17ce 8b13af 1001a8e 101174d 1022ace 10315c9 10407ed 1051aad 10611ca 10707ee 1080faf 10915a9
  //   10a1f2f 10b230f 1801e2c 181328a 18222ae 1830dc8 1840349 1851e4b 18619ea 1870708 188032b 1892549
  //   18a2a8e 18b2a6d 2001ead 2011b8e 2021b50 2031927 2040f4c 2051b0d 20619e8 20716ab 2080a6a 2091da9
  //   20a1bb0 20b1b8f 2801e2b 2810eed 2821aac 28324c8 28407ee 2851b0d 28619e9 2870268 2881da9 2891989
  //   28a16cd 28b1a8c 300224c 3012ead 30226cc 3031908 304076c 3051a29 3061dea 30705a7 30825ab 3092569
  //   30a26ce 30b22cd 38016ad 3810f8f 3821f2e 38320e9 3840ea8 3850bad 3860e49 3872dec 3882e0f 38915c9
  //   38a1790 38b1b50 4001a2a 4011e8a 40216aa 40324ea 4040a06 4050bf0 4060e48 4073e72 4083671 4091d47
  //   40a1acb 40b16ac 4802e6e 4813730 48236f0 48324e9 48421cb 4852e2e 4864291 48742b3 4882e0e 4892969
  //   48a4311 48b3af0 50016ad 501136e 502132f 5031507 50429ac 5052ded 5062dcc 5072169 5082d8b 5090dc9
  //   50a0f6f 50b0f4e 5802e2d 5812aef 5822eb0 5830401 5840421 5850401 5860421 5870421 58925cb 58a2aef
  //   58b2aae
  //   contents of 子弹信息 (hex, n*v repeats v):
  //   812529 824e73 836318 84318c 10135ad 1025ef7 103739c 1044e73 1816f7b 1827bde 1837fff 1846739 2013def
  //   20277bd 2036f7b 2042529 2810c63 2823def 283294a 2840421
endmodule

module \地图加载  (
  input  star,
  input  clk,
  output [15:0] ima,
  output stop,
  output [6:0] Xout,
  output [6:0] Yout
);

  wire and_1_out, comparator_1_eq, d_ff_1_q, not_1_out, or_1_out, \像素信息获取与计算逻辑_1_end ;
  wire [2:0] rom_1_data;
  wire [4:0] bit_extender_1_out, divider_1_out, divider_1_rem;
  wire [6:0] bit_extender_2_out, bit_extender_3_out, multiplier_1_out, multiplier_2_out;
  wire [8:0] counter_1_q;

  not not_1 (not_1_out, comparator_1_eq);
  Counter #(.width(9), .max('h1ff), .ongoal("wrap"), .trigger("rising"), .behavior("new")) counter_1 (
    .count(not_1_out), .Q(counter_1_q), .clk(\像素信息获取与计算逻辑_1_end ), .clr(star));  // open: load, D, carry, preset, down
  Comparator #(.width(9), .mode("twosComplement")) comparator_1 (
    .a(9'h191), .b(counter_1_q), .eq(comparator_1_eq));  // open: gt, lt
  assign bit_extender_1_out = {{1{1'b0}}, counter_1_q[8:5]};  // Bit_Extender bit_extender_1
  Divider #(.width(5)) divider_1 (
    .a(counter_1_q[4:0]), .b(5'b10100), .out(divider_1_out), .upper(bit_extender_1_out), .rem(divider_1_rem));
  or or_1 (or_1_out, \像素信息获取与计算逻辑_1_end , star);
  D_Flip_Flop #(.trigger("rising"), .Pre_Clr_Positions("LEGACY"), .NegatePresetClear("false"), .enable("true"), .NewFFLayout("false")) d_ff_1 (
    .Q(d_ff_1_q), .preset(star), .reset(comparator_1_eq));  // open: clk, D, Qn, en
  assign bit_extender_2_out = {{2{1'b0}}, divider_1_out};  // Bit_Extender bit_extender_2
  assign bit_extender_3_out = {{2{1'b0}}, divider_1_rem};  // Bit_Extender bit_extender_3
  ROM #(.addrWidth(9), .dataWidth(3), .Select("low")) rom_1 (.addr(counter_1_q), .data(rom_1_data));
  and and_1 (and_1_out, d_ff_1_q, clk);
  Multiplier #(.width(7)) multiplier_1 (
    .a(bit_extender_2_out), .b(7'b0000110), .out(multiplier_1_out));  // open: cin, cout
  Multiplier #(.width(7)) multiplier_2 (
    .a(bit_extender_3_out), .b(7'b0000110), .out(multiplier_2_out));  // open: cin, cout
  \像素信息获取与计算逻辑  \u_像素信息获取与计算逻辑_1  (
    .x(multiplier_2_out), .star(or_1_out), .choose(rom_1_data), .clk(and_1_out), .y(multiplier_1_out),
    .dir(2'b00), .\end (\像素信息获取与计算逻辑_1_end ), .ima(ima), .Xout(Xout), .Yout(Yout), .stop(stop));

  // Notes on the sheet:
  //   contents of rom_1 (hex, n*v repeats v):
  //   3 0 0 0 1 1 0 0 1 1 8*0 1 1 4*0 1 1 0 0 1 1 8*0 1 1 4*0 1 1 0 0 1 1 14*0 1 1 0 0 1 1 14*0 6*2 12*0 1
  //   1 6*2 6*0 1 1 4*0 1 1 12*0 1 1 26*0 1 1 8*0 1 1 8*0 1 1 0 0 0 2 2 0 0 0 1 1 8*0 1 1 0 0 0 2 2 0 0 0
  //   1 1 8*0 1 1 8*0 1 1 40*0 1 1 12*0 6*2 1 1 12*0 6*2 14*0 1 1 0 0 1 1 14*0 1 1 0 0 1 1 4*0 1 1 8*0 1 1
  //   0 0 1 1 0 0 4 0 1 1 8*0 1 1 0 0 1 1
endmodule

module \键盘逻辑  (
  input  [6:0] in_1,
  output a,
  output w,
  output s,
  output d,
  output f,
  output h,
  output u,
  output j,
  output k,
  output l
);

  Comparator #(.width(7), .mode("twosComplement")) comparator_1 (.a(in_1), .b(7'b1100001), .eq(a));  // open: gt, lt
  Comparator #(.width(7), .mode("twosComplement")) comparator_2 (.a(in_1), .b(7'b1110111), .eq(w));  // open: gt, lt
  Comparator #(.width(7), .mode("twosComplement")) comparator_3 (.a(in_1), .b(7'b1110011), .eq(s));  // open: gt, lt
  Comparator #(.width(7), .mode("twosComplement")) comparator_4 (.a(in_1), .b(7'b1100100), .eq(d));  // open: gt, lt
  Comparator #(.width(7), .mode("twosComplement")) comparator_5 (.a(in_1), .b(7'b1100110), .eq(f));  // open: gt, lt
  Comparator #(.width(7), .mode("twosComplement")) comparator_6 (.a(in_1), .b(7'b1101000), .eq(h));  // open: gt, lt
  Comparator #(.width(7), .mode("twosComplement")) comparator_7 (.a(in_1), .b(7'b1110101), .eq(u));  // open: gt, lt
  Comparator #(.width(7), .mode("twosComplement")) comparator_8 (.a(in_1), .b(7'b1101010), .eq(j));  // open: gt, lt
  Comparator #(.width(7), .mode("twosComplement")) comparator_9 (.a(in_1), .b(7'b1101011), .eq(k));  // open: gt, lt
  Comparator #(.width(7), .mode("twosComplement")) comparator_10 (.a(in_1), .b(7'b1101100), .eq(l));  // open: gt, lt
endmodule

module \像素删除逻辑  (
  input  star,
  input  clk,
  input  [6:0] num,
  input  [6:0] X,
  input  [6:0] Y,
  output stop,
  output [6:0] Xout,
  output [6:0] Yout
);

  wire comparator_1_eq, comparator_2_eq, not_1_out;
  wire [6:0] adder_1_out, adder_2_out, divider_1_out, divider_1_rem, subtractor_1_out;
  wire [13:0] counter_1_q;

  Counter #(.width(14), .max('h3fff), .ongoal("wrap"), .trigger("rising"), .behavior("new")) counter_1 (
    .count(not_1_out), .Q(counter_1_q), .clk(clk), .clr(star));  // open: load, D, carry, preset, down
  Subtractor #(.width(7)) subtractor_1 (.a(num), .b(7'b0000001), .out(subtractor_1_out));  // open: bin, bout
  not not_1 (not_1_out, stop);
  Comparator #(.width(7), .mode("twosComplement")) comparator_1 (
    .a(subtractor_1_out), .b(divider_1_out), .eq(comparator_1_eq));  // open: gt, lt
  Divider #(.width(7)) divider_1 (
    .a(counter_1_q[6:0]), .b(num), .out(divider_1_out), .upper(counter_1_q[13:7]), .rem(divider_1_rem));
  Comparator #(.width(7), .mode("twosComplement")) comparator_2 (
    .a(subtractor_1_out), .b(divider_1_rem), .eq(comparator_2_eq));  // open: gt, lt
  Adder #(.width(7)) adder_1 (.a(divider_1_out), .b(X), .out(adder_1_out));  // open: cin, cout
  Adder #(.width(7)) adder_2 (.a(divider_1_rem), .b(Y), .out(adder_2_out));  // open: cin, cout
  and and_1 (stop, comparator_1_eq, comparator_2_eq);
  Adder #(.width(7)) adder_3 (.a(7'b0000100), .b(adder_1_out), .out(Xout));  // open: cin, cout
  Adder #(.width(7)) adder_4 (.a(7'b0000100), .b(adder_2_out), .out(Yout));  // open: cin, cout
endmodule

module \像素移动逻辑  (
  input  star,
  input  clk,
  input  [2:0] choose,
  input  [6:0] X0,
  input  [6:0] Y0,
  input  [6:0] X1,
  input  [6:0] Y1,
  input  [1:0] dir,
  output \end ,
  output stop,
  output [6:0] xout,
  output [6:0] yout,
  output [15:0] ima
);

  wire and_1_out, \像素删除逻辑_1_stop ;
  wire [6:0] multiplexer_1_out, \像素信息获取与计算逻辑_1_xout , \像素信息获取与计算逻辑_1_yout , \像素删除逻辑_1_xout , \像素删除逻辑_1_yout ;
  wire [15:0] \像素信息获取与计算逻辑_1_ima ;

  Multiplexer #(.select(3), .width(7), .disabled("Z"), .enable("false")) multiplexer_1 (
    .in0({7{1'b0}}), .in1(7'b0000110), .in2(7'b0000110), .in3(7'b0001100), .in4(7'b0001100),
    .in5(7'b0000110), .in6({7{1'b0}}), .in7({7{1'b0}}), .out(multiplexer_1_out), .sel(choose));
  \像素删除逻辑  \u_像素删除逻辑_1  (
    .star(star), .clk(clk), .num(multiplexer_1_out), .X(X0), .Y(Y0), .stop(\像素删除逻辑_1_stop ),
    .Xout(\像素删除逻辑_1_xout ), .Yout(\像素删除逻辑_1_yout ));
  and and_1 (and_1_out, \像素删除逻辑_1_stop , clk);
  \像素信息获取与计算逻辑  \u_像素信息获取与计算逻辑_1  (
    .x(X1), .star(star), .choose(choose), .clk(and_1_out), .y(Y1), .dir(dir), .\end (\end ),
    .ima(\像素信息获取与计算逻辑_1_ima ), .Xout(\像素信息获取与计算逻辑_1_xout ), .Yout(\像素信息获取与计算逻辑_1_yout ), .stop(stop));
  Multiplexer #(.select(1), .width(7), .disabled("Z"), .enable("false")) multiplexer_2 (
    .in0(\像素删除逻辑_1_xout ), .in1(\像素信息获取与计算逻辑_1_xout ), .out(xout), .sel(\像素删除逻辑_1_stop ));
  Multiplexer #(.select(1), .width(7), .disabled("Z"), .enable("false")) multiplexer_3 (
    .in0(\像素删除逻辑_1_yout ), .in1(\像素信息获取与计算逻辑_1_yout ), .out(yout), .sel(\像素删除逻辑_1_stop ));
  Multiplexer #(.select(1), .width(16), .disabled("Z"), .enable("false")) multiplexer_4 (
    .in0({16{1'b0}}), .in1(\像素信息获取与计算逻辑_1_ima ), .out(ima), .sel(\像素删除逻辑_1_stop ));
endmodule

module \坦克大战  (
);

  wire clock_1_out, or_1_out, or_2_out, \初始界面_out , \开始_out , \键盘逻辑_1_a , \键盘逻辑_1_d , \键盘逻辑_1_f , \键盘逻辑_1_h ,
       \键盘逻辑_1_j , \键盘逻辑_1_k , \键盘逻辑_1_l , \键盘逻辑_1_s , \键盘逻辑_1_u , \键盘逻辑_1_w ;
  wire [1:0] \单周期_单级中断_1_win1 ;
  wire [3:0] register_1_q;
  wire [6:0] keyboard_1_data, \单周期_单级中断_1_x , \单周期_单级中断_1_y ;
  wire [15:0] \单周期_单级中断_1_ima ;

  Clock #(.highDuration(1), .lowDuration(1)) clock_1 (.out(clock_1_out));
  Keyboard #(.Char_bit_width(7), .buflen(32), .trigger("rising")) keyboard_1 (
    .clk(clock_1_out), .re(1'b1), .data(keyboard_1_data));  // open: clr, avail
  Button \u_初始界面  (.out(\初始界面_out ));
  Button \u_开始  (.out(\开始_out ));
  \键盘逻辑  \u_键盘逻辑_1  (
    .in_1(keyboard_1_data), .a(\键盘逻辑_1_a ), .w(\键盘逻辑_1_w ), .s(\键盘逻辑_1_s ), .d(\键盘逻辑_1_d ), .f(\键盘逻辑_1_f ),
    .h(\键盘逻辑_1_h ), .u(\键盘逻辑_1_u ), .j(\键盘逻辑_1_j ), .k(\键盘逻辑_1_k ), .l(\键盘逻辑_1_l ));
  or or_1 (or_1_out, \初始界面_out , \开始_out );
  \单周期_单级中断  \u_单周期_单级中断_1  (
    .IR1(\键盘逻辑_1_w ), .IR2(\键盘逻辑_1_d ), .IR3(\键盘逻辑_1_s ), .IR4(\键盘逻辑_1_a ), .IR5(\键盘逻辑_1_u ),
    .IR6(\键盘逻辑_1_k ), .IR7(\键盘逻辑_1_j ), .IR8(\键盘逻辑_1_h ), .IR9(\键盘逻辑_1_f ), .IR10(\键盘逻辑_1_l ),
    .IR12(\初始界面_out ), .IR13(\开始_out ), .X(\单周期_单级中断_1_x ), .Win1(\单周期_单级中断_1_win1 [0]),
    .Win2(\单周期_单级中断_1_win1 [1]), .Y(\单周期_单级中断_1_y ), .IMA(\单周期_单级中断_1_ima ));  // open: IR11, out_14
  Hex_Digit_Display hex_digit_display_1 (.value(register_1_q));  // open: dp
  Register #(.width(4), .trigger("rising"), .Select("low")) register_1 (
    .D({2'b00, \单周期_单级中断_1_win1 }), .Q(register_1_q), .clk(or_2_out), .clr(or_1_out));  // open: en
  \音频播放  \u_音频播放_1  (.\触发信号 (or_2_out), .rst(or_1_out));
  or or_2 (or_2_out, \单周期_单级中断_1_win1 [0], \单周期_单级中断_1_win1 [1]);
  // LCD_Video lcd_video_1: pin names not known; wires that end beside it: or_1_out, clock_1_out, 1'b1, \单周期_单级中断_1_x , \单周期_单级中断_1_y , \单周期_单级中断_1_ima 
endmodule

module \系统调用选择  (
  input  [3:0] \中断信息 ,
  output \加载地图 ,
  output \加载初始界面 ,
  output \移动 ,
  output win2,
  output win1,
  output \消除一个木块 ,
  output \消除两个木块 
);

  Comparator #(.width(4), .mode("twosComplement")) comparator_1 (.a(\中断信息 ), .b(4'b0010), .eq(\加载地图 ));  // open: gt, lt
  Comparator #(.width(4), .mode("twosComplement")) comparator_2 (
    .a(\中断信息 ), .b(4'b0001), .eq(\加载初始界面 ));  // open: gt, lt
  Comparator #(.width(4), .mode("twosComplement")) comparator_3 (.a(\中断信息 ), .b(4'b0011), .eq(\移动 ));  // open: gt, lt
  Comparator #(.width(4), .mode("twosComplement")) comparator_4 (.a(\中断信息 ), .b(4'b0100), .eq(win2));  // open: gt, lt
  Comparator #(.width(4), .mode("twosComplement")) comparator_5 (.a(\中断信息 ), .b(4'b0101), .eq(win1));  // open: gt, lt
  Comparator #(.width(4), .mode("twosComplement")) comparator_6 (
    .a(\中断信息 ), .b(4'b0110), .eq(\消除一个木块 ));  // open: gt, lt
  Comparator #(.width(4), .mode("twosComplement")) comparator_7 (
    .a(\中断信息 ), .b(4'b0111), .eq(\消除两个木块 ));  // open: gt, lt
endmodule

module \寄存器内容备份  (
  input  [31:0] \写入数据 ,
  input  Clk,
  input  regwrite,
  input  [4:0] \常量序号 ,
  input  [4:0] \变量序号 ,
  output [31:0] \输出结果 
);

  wire and_1_out, comparator_1_eq;

  Comparator #(.width(5), .mode("twosComplement")) comparator_1 (
    .a(\常量序号 ), .b(\变量序号 ), .eq(comparator_1_eq));  // open: gt, lt
  and and_1 (and_1_out, Clk, comparator_1_eq, regwrite);
  Register #(.width(32), .trigger("rising"), .Select("low")) register_1 (
    .D(\写入数据 ), .Q(\输出结果 ), .clk(and_1_out));  // open: en, clr
endmodule

module \坐标运算逻辑  (
  input  [9:0] in_1,
  output [6:0] x,
  output [6:0] y
);

  wire [4:0] divider_1_out, divider_1_rem;
  wire [6:0] bit_extender_1_out, bit_extender_2_out;
  wire [9:0] shifter_1_out;

  Shifter #(.width(10), .shift("lr")) shifter_1 (.in(in_1), .\dist (4'b0001), .out(shifter_1_out));
  Divider #(.width(5)) divider_1 (
    .a(shifter_1_out[4:0]), .b(5'b10100), .out(divider_1_out), .upper(shifter_1_out[9:5]), .rem(divider_1_rem));
  assign bit_extender_1_out = {{2{1'b0}}, divider_1_out};  // Bit_Extender bit_extender_1
  assign bit_extender_2_out = {{2{1'b0}}, divider_1_rem};  // Bit_Extender bit_extender_2
  Multiplier #(.width(7)) multiplier_1 (.a(bit_extender_1_out), .b(7'b0000110), .out(y));  // open: cin, cout
  Multiplier #(.width(7)) multiplier_2 (.a(bit_extender_2_out), .b(7'b0000110), .out(x));  // open: cin, cout
endmodule

module \音频播放  (
  input  \触发信号 ,
  input  rst
);

  wire and_1_out, clock_1_out, comparator_1_eq, comparator_2_gt, not_1_out, not_2_out, or_1_out, play;
  wire [4:0] rom_1_data;
  wire [7:0] adder_1_out, adder_2_out, register_2_q, register_3_q;
  wire [13:0] multiplexer_1_out;
  wire [31:0] counter_1_q;

  not not_1 (not_1_out, play);
  and and_1 (and_1_out, play, comparator_2_gt);
  or or_1 (or_1_out, not_1_out, and_1_out);
  Adder #(.width(8)) adder_1 (.a(register_2_q), .b(8'h1), .out(adder_1_out));  // open: cin, cout
  Clock #(.highDuration(1), .lowDuration(1)) clock_1 (.out(clock_1_out));
  Register #(.width(1), .trigger("rising"), .Select("low")) register_1 (
    .D(\触发信号 ), .en(or_1_out), .Q(play), .clk(clock_1_out), .clr(rst));
  Register #(.width(8), .trigger("rising"), .Select("low")) register_2 (
    .D(adder_1_out), .en(play), .Q(register_2_q), .clk(clock_1_out), .clr(comparator_2_gt));
  Comparator #(.width(8), .mode("twosComplement")) comparator_1 (
    .a(register_2_q), .b({8{1'b1}}), .eq(comparator_1_eq));  // open: gt, lt
  Counter #(.width(32), .max('hffffffff), .ongoal("wrap"), .trigger("rising"), .behavior("new")) counter_1 (
    .D(counter_1_q), .Q(counter_1_q), .clk(clock_1_out), .clr(not_2_out));  // open: load, count, carry, preset, down
  not not_2 (not_2_out, play);
  Adder #(.width(8)) adder_2 (.a(register_3_q), .b(8'h1), .out(adder_2_out));  // open: cin, cout
  Register #(.width(8), .trigger("rising"), .Select("low")) register_3 (
    .D(adder_2_out), .en(comparator_1_eq), .Q(register_3_q), .clk(clock_1_out), .clr(comparator_2_gt));
  Comparator #(.width(32), .mode("twosComplement")) comparator_2 (
    .a(counter_1_q), .b(32'h6000), .gt(comparator_2_gt));  // open: eq, lt
  ROM #(.addrWidth(8), .dataWidth(5), .Select("low")) rom_1 (.addr(register_3_q), .data(rom_1_data));
  Multiplexer #(.select(5), .width(14), .disabled("Z"), .enable("false")) multiplexer_1 (
    .in0({14{1'b1}}), .in1(14'h93), .in2(14'ha5), .in3(14'haf), .in4(14'hc4), .in5(14'hdd), .in6(14'hf8),
    .in7(14'h106), .in8(14'h126), .in9(14'h14a), .in10(14'h15e), .in11(14'h189), .in12(14'h1b9),
    .in13(14'h1ef), .in14(14'h20d), .in15(14'h24d), .in16(14'h295), .in17(14'h2bc), .in18(14'h312),
    .in19(14'h372), .in20(14'h3de), .in21({14{1'b0}}), .out(multiplexer_1_out), .sel(rom_1_data));  // open: in22, in23, in24, in25, in26, in27, in28, in29, in30, in31
  // Buzzer #(.freq_measure("Hz"), .vol_width(7)) buzzer_1: pin names not known; wires that end beside it: multiplexer_1_out, play

  // Notes on the sheet:
  //   contents of rom_1 (hex, n*v repeats v):
  //   0 0 6*1 9 9 c b 6*9 4 4 6 6 a 8 6*7 6 5 7 7 6 5 10*4 3 3 8*4 8 8 b a 6*8 4 4 d d c a 6*9 7 6 5 5 6 3
  //   4*4 21*15
endmodule

module \初始界面加载  (
  input  star,
  input  clk,
  output stop,
  output \end ,
  output [15:0] ima,
  output [6:0] Xout,
  output [6:0] Yout
);

  wire clk_t, comparator_1_eq;
  wire [11:0] counter_1_q;
  wire [31:30] rom_1_data;

  Counter #(.width(12), .max('hfff), .ongoal("wrap"), .trigger("rising"), .behavior("new")) counter_1 (
    .count(stop), .Q(counter_1_q), .clk(clk), .clr(star));  // open: load, D, carry, preset, down
  ROM #(.addrWidth(12), .dataWidth(32), .Select("low")) rom_1 (
    .addr(counter_1_q), .data({rom_1_data, Yout, Xout, ima}));
  Comparator #(.width(32), .mode("twosComplement")) comparator_1 (
    .a({32{1'b0}}), .b({rom_1_data, Yout, Xout, ima}), .eq(comparator_1_eq));  // open: gt, lt
  not not_1 (stop, comparator_1_eq);
  Register #(.width(1), .trigger("rising"), .Select("low")) register_1 (
    .D(comparator_1_eq), .Q(\end ), .clk(clk_t), .clr(star));  // open: en

  // Notes on the sheet:
  //   contents of rom_1 (hex, n*v repeats v):
  //   f90000 fd0000 17b0421 17c2529 1800000 1830000 1850000 1fb0842 1fc39ce 2022108 2030842 20414a5
  //   27c0000 2822d6b 2831ce7 2842d6b 2850842 2f80000 2fb0842 2fc318c 3022d6b 3031ce7 3042d6b 3050842
  //   37b0842 37c2d6b 3822108 3830842 38414a5 3fc0421 4330000 44d0000 47b0842 47c35ad 49e5ef7 49f2108
  //   4ad56b5 4ae14a5 4af1ce7 4b05294 4b44631 4b5318c 4b618c6 4b76f7b 4b835ad 4bb0000 4be5ad6 4bf4e73
  //   4c00421 4c15ef7 4c34631 4c4294a 4c50842 4c65ef7 4c84a52 4c92529 4ca0000 4fa0000 4fb0421 4fc2529
  //   51e4a52 51f0842 5200842 5211084 5220000 5230000 52c294a 52d1ce7 52e56b5 52f3def 5303def 53114a5
  //   5330000 5345ad6 5354a52 5360842 5375294 5390c63 53a0c63 53d0421 53e1084 53f6f7b 5404631 54118c6
  //   5424e73 543294a 5445294 5454e73 5462108 5474e73 5482108 5495ad6 54b0000 5790000 59e4a52 5a06318
  //   5a17fff 5a20c63 5ac39ce 5ad18c6 5ae56b5 5af5294 5b02d6b 5b11ce7 5b46b5a 5b56318 5b60421 5b74e73
  //   5b97fff 5ba6f7b 5be6739 5bf35ad 5c05294 5c10842 5c26318 5c32d6b 5c44e73 5c55ad6 5c61084 5c76739
  //   5c82108 5c95ad6 5cd0000 61e6739 61f18c6 6210842 62d5ef7 62e18c6 62f4210 6303def 6330000 6344e73
  //   63539ce 6361ce7 6376f7b 6382108 6390000 63a0421 63d0c63 63e7fff 63f2d6b 6402108 6414e73 6420842
  //   6435ad6 6442529 645294a 6465294 6485ad6 6492529 69a0000 69e14a5 69f0842 6a50000 6ab0000 6ad1084
  //   6af0000 6b01084 6b40c63 6b50421 6b60421 6b714a5 6b80c63 6be14a5 6bf18c6 6c118c6 6c31084 6c40421
  //   6c61084 6c81084 6c90000 6fd0000 7180000 73d0000 7410000 7460000 7780000 77c0000 8550000 85c0000
  //   8b40000 8ba0001 8bc0000 8c40000 8c70400 8cc0000 8e10001 9290001 9300001 9320400 9330400 93d0000
  //   93e0000 94a0001 94b0001 9520000 9530000 9540000 9550001 95a0000 95b0000 9ab0000 9af0001 9b40400
  //   9b80001 9bc0000 9bd0000 9c30000 9c40001 9ca0001 9cb0001 9d20000 9d30000 9d70401 9d80001 9e20000
  //   9e30020 a2a0000 a2d0000 a360001 a370001 a380001 a390001 a3f0000 a400000 a450000 a490000 a4f0000
  //   a500000 a530000 a610400 aac0400 aad0400 aae0800 aaf0800 ab00800 ab10400 ab20400 ab30400 ab50001
  //   ab60001 ab70400 ab80400 ab90400 aba0400 abb0400 abc0400 abd0400 ac00400 ac10400 ac20400 ac50400
  //   ac60400 ac70400 ac90400 aca0400 acb0800 acc0400 ace0400 ad30000 ad50400 ad60800 ad70400 ada0000
  //   adf0400 ae00800 ae10800 ae20400 b290400 b2b0400 b2c1400 b2d1c00 b2e1c00 b2f2000 b302420 b311800
  //   b322020 b331400 b340400 b360400 b371021 b381c00 b391c00 b3a1820 b3b0800 b3c0400 b3d0400 b3e0c00
  //   b3f1420 b401800 b410c00 b420400 b430400 b440c00 b451400 b461820 b471000 b481420 b491000 b4a1800
  //   b4b0c00 b4c0400 b4d0400 b4e0c00 b4f1400 b501821 b510800 b530400 b540800 b551821 b561c00 b572020
  //   b581400 b590400 b5b0000 b5f0400 b601400 b611c20 b620c00 b630400 b650000 bab0400 bac2ca5 bad620f
  //   bae48e6 baf4ce5 bb065cc bb140c4 bb2660e bb32ca4 bb40400 bb50400 bb60800 bb749ac bb840e6 bb9558a
  //   bba518a bbb1000 bbc0800 bbd0400 bbe28a5 bbf498b bc04527 bc11c00 bc20800 bc30400 bc41000 bc53d07
  //   bc6622f bc71c00 bc84127 bc94127 bca4107 bcb1400 bcc0800 bcd0800 bce1800 bcf4549 bd05a10 bd11000
  //   bd20400 bd30400 bd41821 bd555ce bd640e5 bd7660e bd82882 bd90c00 bdb0000 bde0400 bdf0c00 be04508
  //   be1660f be22062 be30400 c2c45cc c2d7b16 c2e6a2f c2f6e2e c307e91 c316e0e c327af5 c3349cd c340400
  //   c350400 c360c00 c3759ed c386a50 c397691 c3a7671 c3b1800 c3c0800 c3d0400 c3e2884 c3f7292 c406e4f
  //   c412820 c420800 c430400 c441000 c456651 c467ed5 c473061 c484106 c496a70 c4a6a70 c4b1000 c4c0800
  //   c4d0c00 c4e2420 c4f7272 c507717 c511442 c520400 c530400 c541420 c5576d5 c56662f c577ed4 c584547
  //   c591000 c5a0400 c5e0400 c5f1000 c607230 c617ed5 c6234c6 c630800 ca00000 cac1482 cad1c62 cae3d26
  //   caf5dec cb05969 cb138a3 cb22061 cb31862 cb40400 cb50400 cb64dab cb74947 cb84548 cb92c81 cba5d8a
  //   cbb59ac cbc1401 cbd0800 cbe1c20 cbf59ab cc0722f cc14505 cc22042 cc30800 cc41820 cc56631 cc6558b
  //   cc73041 cc82840 cc9622e cca5e0d ccb1000 ccc0c00 ccd1c41 cce558b ccf5ded cd01c62 cd10800 cd20400
  //   cd328e7 cd43928 cd52461 cd62861 cd74106 cd8662f cd934c4 cda0400 cdd0400 cde1000 cdf3d07 ce0722f
  //   ce15969 ce22c83 ce30800 d2b0000 d2d0800 d2e2ca3 d2f59ed d30558a d311c00 d320800 d330400 d350c00
  //   d366a30 d37598b d3834e6 d391000 d3a61cc d3b7251 d3c1c01 d3d0c00 d3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
endmodule
